// Logisim project FL_RISCV_CU.circ as structural Verilog: 67 circuits, main circuit Norb_ALU_8B_CRA
module Norb_ALU_RISCV_ALU (
  input  [6:0] InFunc7,
  input  [2:0] InFunc3,
  input  [31:0] InA,
  input  [31:0] InB,
  output ZERO_FLAG,
  output [31:0] ALU_OUTPUT
);

  wire and_1_out, and_2_out, and_3_out, and_4_out, norb_std_3b_matcher_1_outaeqb,
       norb_std_3b_matcher_2_outaeqb, norb_std_3b_matcher_3_outaeqb, norb_std_3b_matcher_4_outaeqb,
       norb_std_3b_matcher_5_outaeqb, norb_std_3b_matcher_6_outaeqb, norb_std_3b_matcher_7_outaeqb,
       norb_std_3b_matcher_8_outaeqb, norb_std_7b_matcher_1_outaeqb, norb_std_7b_matcher_2_outaeqb,
       norb_std_7b_matcher_3_outaeqb, norb_std_7b_matcher_4_outaeqb;
  wire [4:0] bitselector_1_out, bitselector_2_out, bitselector_3_out;
  wire [31:0] norb_alu_32b_bwl_1_outaandb, norb_alu_32b_bwl_1_outaorb, norb_alu_32b_bwl_1_outaxorb,
       norb_alu_32b_cra_1_outaaddb, norb_alu_32b_crs_1_outasubtractb, norb_alu_32b_sll_1_outshifted,
       norb_alu_32b_slt_1_outflag, norb_alu_32b_sltu_1_outsltu, norb_alu_32b_sra_1_outshifted,
       norb_alu_32b_srl_1_outshifted, norb_std_32b_selector_1_out32b, norb_std_32b_selector_2_out32b,
       norb_std_32b_selector_3_out32b, norb_std_32b_selector_4_out32b, norb_std_32b_selector_5_out32b,
       norb_std_32b_selector_6_out32b, norb_std_32b_selector_7_out32b, norb_std_32b_selector_8_out32b,
       norb_std_32b_selector_9_out32b, norb_std_32b_selector_10_out32b;

  BitSelector #(.group(5), .width(32)) bitselector_1 (.in(InB), .out(bitselector_1_out), .sel(3'b000));
  BitSelector #(.group(5), .width(32)) bitselector_2 (.in(InB), .out(bitselector_2_out), .sel(3'b000));
  BitSelector #(.group(5), .width(32)) bitselector_3 (.in(InB), .out(bitselector_3_out), .sel(3'b000));
  Norb_ALU_32B_CRA norb_alu_32b_cra_1 (
    .InA(InA), .InB(InB), .OutAAddB(norb_alu_32b_cra_1_outaaddb));  // open: FlagOverflow
  Norb_ALU_32B_CRS norb_alu_32b_crs_1 (
    .InA(InA), .InB(InB), .OutASubtractB(norb_alu_32b_crs_1_outasubtractb));  // open: FlagOverflow
  Norb_ALU_32B_SLL norb_alu_32b_sll_1 (
    .InShamt(bitselector_1_out), .InNum(InA), .OutShifted(norb_alu_32b_sll_1_outshifted));
  Norb_ALU_32B_SLT norb_alu_32b_slt_1 (.InA(InA), .InB(InB), .OutFlag(norb_alu_32b_slt_1_outflag));
  Norb_ALU_32B_SLTU norb_alu_32b_sltu_1 (.InA(InA), .InB(InB), .OutSLTU(norb_alu_32b_sltu_1_outsltu));
  Norb_ALU_32B_SRL norb_alu_32b_srl_1 (
    .InShamt(bitselector_2_out), .InNum(InA), .OutShifted(norb_alu_32b_srl_1_outshifted));
  Norb_ALU_32B_SRA norb_alu_32b_sra_1 (
    .InShamt(bitselector_3_out), .InNum(InA), .OutShifted(norb_alu_32b_sra_1_outshifted));
  Norb_ALU_32B_BWL norb_alu_32b_bwl_1 (
    .InA(InA), .InB(InB), .OutAAndB(norb_alu_32b_bwl_1_outaandb), .OutAOrB(norb_alu_32b_bwl_1_outaorb),
    .OutAXorB(norb_alu_32b_bwl_1_outaxorb));
  Norb_STD_7B_Matcher norb_std_7b_matcher_1 (
    .In8B_A(InFunc7), .In8B_B({7{1'b0}}), .OutAEqB(norb_std_7b_matcher_1_outaeqb));
  Norb_STD_3B_Matcher norb_std_3b_matcher_1 (
    .In8B_A(InFunc3), .In8B_B(3'b000), .OutAEqB(norb_std_3b_matcher_1_outaeqb));
  Norb_STD_7B_Matcher norb_std_7b_matcher_2 (
    .In8B_A(InFunc7), .In8B_B(7'b0100000), .OutAEqB(norb_std_7b_matcher_2_outaeqb));
  Norb_STD_3B_Matcher norb_std_3b_matcher_2 (
    .In8B_A(InFunc3), .In8B_B(3'b001), .OutAEqB(norb_std_3b_matcher_2_outaeqb));
  Norb_STD_3B_Matcher norb_std_3b_matcher_3 (.In8B_B(3'b010), .OutAEqB(norb_std_3b_matcher_3_outaeqb));  // open: In8B_A
  Norb_STD_3B_Matcher norb_std_3b_matcher_4 (.In8B_B(3'b011), .OutAEqB(norb_std_3b_matcher_4_outaeqb));  // open: In8B_A
  Norb_STD_7B_Matcher norb_std_7b_matcher_3 (
    .In8B_A(InFunc7), .In8B_B({7{1'b0}}), .OutAEqB(norb_std_7b_matcher_3_outaeqb));
  Norb_STD_3B_Matcher norb_std_3b_matcher_5 (
    .In8B_A(InFunc3), .In8B_B(3'b101), .OutAEqB(norb_std_3b_matcher_5_outaeqb));
  Norb_STD_7B_Matcher norb_std_7b_matcher_4 (
    .In8B_A(InFunc7), .In8B_B(7'b0100000), .OutAEqB(norb_std_7b_matcher_4_outaeqb));
  Norb_STD_3B_Matcher norb_std_3b_matcher_6 (
    .In8B_A(InFunc3), .In8B_B(3'b111), .OutAEqB(norb_std_3b_matcher_6_outaeqb));
  Norb_STD_3B_Matcher norb_std_3b_matcher_7 (
    .In8B_A(InFunc3), .In8B_B(3'b110), .OutAEqB(norb_std_3b_matcher_7_outaeqb));
  Norb_STD_3B_Matcher norb_std_3b_matcher_8 (
    .In8B_A(InFunc3), .In8B_B(3'b100), .OutAEqB(norb_std_3b_matcher_8_outaeqb));
  and and_1 (and_1_out, norb_std_7b_matcher_1_outaeqb, norb_std_3b_matcher_1_outaeqb);
  and and_2 (and_2_out, norb_std_3b_matcher_1_outaeqb, norb_std_7b_matcher_2_outaeqb);
  and and_3 (and_3_out, norb_std_7b_matcher_3_outaeqb, norb_std_3b_matcher_5_outaeqb);
  and and_4 (and_4_out, norb_std_3b_matcher_5_outaeqb, norb_std_7b_matcher_4_outaeqb);
  Norb_STD_32B_Selector norb_std_32b_selector_1 (
    .In32B(norb_alu_32b_cra_1_outaaddb), .InSelect(and_1_out), .Out32B(norb_std_32b_selector_1_out32b));
  Norb_STD_32B_Selector norb_std_32b_selector_2 (
    .In32B(norb_alu_32b_crs_1_outasubtractb), .InSelect(and_2_out), .Out32B(norb_std_32b_selector_2_out32b));
  Norb_STD_32B_Selector norb_std_32b_selector_3 (
    .In32B(norb_alu_32b_sll_1_outshifted), .InSelect(norb_std_3b_matcher_2_outaeqb),
    .Out32B(norb_std_32b_selector_3_out32b));
  Norb_STD_32B_Selector norb_std_32b_selector_4 (
    .In32B(norb_alu_32b_slt_1_outflag), .InSelect(norb_std_3b_matcher_3_outaeqb),
    .Out32B(norb_std_32b_selector_4_out32b));
  Norb_STD_32B_Selector norb_std_32b_selector_5 (
    .In32B(norb_alu_32b_sltu_1_outsltu), .InSelect(norb_std_3b_matcher_4_outaeqb),
    .Out32B(norb_std_32b_selector_5_out32b));
  Norb_STD_32B_Selector norb_std_32b_selector_6 (
    .In32B(norb_alu_32b_srl_1_outshifted), .InSelect(and_3_out), .Out32B(norb_std_32b_selector_6_out32b));
  Norb_STD_32B_Selector norb_std_32b_selector_7 (
    .In32B(norb_alu_32b_sra_1_outshifted), .InSelect(and_4_out), .Out32B(norb_std_32b_selector_7_out32b));
  Norb_STD_32B_Selector norb_std_32b_selector_8 (
    .In32B(norb_alu_32b_bwl_1_outaandb), .InSelect(norb_std_3b_matcher_6_outaeqb),
    .Out32B(norb_std_32b_selector_8_out32b));
  Norb_STD_32B_Selector norb_std_32b_selector_9 (
    .In32B(norb_alu_32b_bwl_1_outaorb), .InSelect(norb_std_3b_matcher_7_outaeqb),
    .Out32B(norb_std_32b_selector_9_out32b));
  Norb_STD_32B_Selector norb_std_32b_selector_10 (
    .In32B(norb_alu_32b_bwl_1_outaxorb), .InSelect(norb_std_3b_matcher_8_outaeqb),
    .Out32B(norb_std_32b_selector_10_out32b));
  assign ALU_OUTPUT = norb_std_32b_selector_1_out32b | norb_std_32b_selector_2_out32b | norb_std_32b_selector_3_out32b | norb_std_32b_selector_4_out32b | norb_std_32b_selector_5_out32b | norb_std_32b_selector_6_out32b | norb_std_32b_selector_7_out32b | norb_std_32b_selector_8_out32b | norb_std_32b_selector_9_out32b | norb_std_32b_selector_10_out32b;  // OR_Gate or_1, 32 bits wide
  Norb_STD_32B_Matcher norb_std_32b_matcher_1 (.In32B_A(ALU_OUTPUT), .In32B_B({32{1'b0}}), .OutAEqB(ZERO_FLAG));
endmodule

module Norb_ALU_8B_CRA (
  input  [7:0] InA,
  input  [7:0] InB,
  input  CarryIn,
  output CarryOverflow,
  output [7:0] OutAPlusB
);

  wire and_1_out, and_2_out, and_3_out, and_4_out, and_5_out, and_6_out, and_7_out, and_8_out, and_9_out,
       and_10_out, and_11_out, and_12_out, and_13_out, and_14_out, and_15_out, and_16_out, or_1_out,
       or_2_out, or_3_out, or_4_out, or_5_out, or_6_out, or_7_out, xor_1_out, xor_3_out, xor_5_out,
       xor_7_out, xor_9_out, xor_11_out, xor_13_out, xor_15_out;

  xor xor_1 (xor_1_out, InA[0], CarryIn);
  and and_1 (and_1_out, InA[0], CarryIn);
  xor xor_2 (OutAPlusB[0], InB[0], xor_1_out);
  and and_2 (and_2_out, InB[0], xor_1_out);
  or or_1 (or_1_out, and_2_out, and_1_out);
  xor xor_3 (xor_3_out, InA[1], or_1_out);
  and and_3 (and_3_out, InA[1], or_1_out);
  xor xor_4 (OutAPlusB[1], InB[1], xor_3_out);
  and and_4 (and_4_out, InB[1], xor_3_out);
  or or_2 (or_2_out, and_4_out, and_3_out);
  xor xor_5 (xor_5_out, InA[2], or_2_out);
  and and_5 (and_5_out, InA[2], or_2_out);
  xor xor_6 (OutAPlusB[2], InB[2], xor_5_out);
  or or_3 (or_3_out, and_6_out, and_5_out);
  and and_6 (and_6_out, InB[2], xor_5_out);
  and and_7 (and_7_out, InA[3], or_3_out);
  xor xor_7 (xor_7_out, InA[3], or_3_out);
  and and_8 (and_8_out, InB[3], xor_7_out);
  xor xor_8 (OutAPlusB[3], InB[3], xor_7_out);
  or or_4 (or_4_out, and_8_out, and_7_out);
  xor xor_9 (xor_9_out, InA[4], or_4_out);
  and and_9 (and_9_out, InA[4], or_4_out);
  xor xor_10 (OutAPlusB[4], InB[4], xor_9_out);
  and and_10 (and_10_out, InB[4], xor_9_out);
  or or_5 (or_5_out, and_10_out, and_9_out);
  xor xor_11 (xor_11_out, InA[5], or_5_out);
  and and_11 (and_11_out, InA[5], or_5_out);
  xor xor_12 (OutAPlusB[5], InB[5], xor_11_out);
  and and_12 (and_12_out, InB[5], xor_11_out);
  or or_6 (or_6_out, and_12_out, and_11_out);
  xor xor_13 (xor_13_out, InA[6], or_6_out);
  and and_13 (and_13_out, InA[6], or_6_out);
  xor xor_14 (OutAPlusB[6], InB[6], xor_13_out);
  and and_14 (and_14_out, InB[6], xor_13_out);
  or or_7 (or_7_out, and_14_out, and_13_out);
  xor xor_15 (xor_15_out, InA[7], or_7_out);
  and and_15 (and_15_out, InA[7], or_7_out);
  xor xor_16 (OutAPlusB[7], InB[7], xor_15_out);
  and and_16 (and_16_out, InB[7], xor_15_out);
  or or_8 (CarryOverflow, and_16_out, and_15_out);

  // Notes on the sheet:
  //   CRA: Carry Ripple Adder
endmodule

module Norb_ALU_8B_CRS (
  input  [7:0] InA,
  input  [7:0] InB,
  input  CarryIn,
  output CarryOverflow,
  output [7:0] OutASubtractB
);

  wire and_1_out, and_2_out, and_3_out, and_4_out, and_5_out, and_6_out, and_7_out, and_8_out, and_9_out,
       and_10_out, and_11_out, and_12_out, and_13_out, and_14_out, and_15_out, and_16_out, not_1_out,
       not_2_out, not_3_out, not_4_out, not_5_out, not_6_out, not_7_out, not_8_out, or_1_out, or_2_out,
       or_3_out, or_4_out, or_5_out, or_6_out, or_7_out, xor_1_out, xor_3_out, xor_5_out, xor_7_out,
       xor_9_out, xor_11_out, xor_13_out, xor_15_out;

  xor xor_1 (xor_1_out, InA[0], CarryIn);
  and and_1 (and_1_out, InA[0], CarryIn);
  xor xor_2 (OutASubtractB[0], not_1_out, xor_1_out);
  and and_2 (and_2_out, not_1_out, xor_1_out);
  or or_1 (or_1_out, and_2_out, and_1_out);
  not not_1 (not_1_out, InB[0]);
  not not_2 (not_2_out, InB[1]);
  not not_3 (not_3_out, InB[2]);
  not not_4 (not_4_out, InB[3]);
  xor xor_3 (xor_3_out, InA[1], or_1_out);
  and and_3 (and_3_out, InA[1], or_1_out);
  not not_5 (not_5_out, InB[4]);
  not not_6 (not_6_out, InB[5]);
  not not_7 (not_7_out, InB[6]);
  not not_8 (not_8_out, InB[7]);
  xor xor_4 (OutASubtractB[1], not_2_out, xor_3_out);
  and and_4 (and_4_out, not_2_out, xor_3_out);
  or or_2 (or_2_out, and_4_out, and_3_out);
  xor xor_5 (xor_5_out, InA[2], or_2_out);
  and and_5 (and_5_out, InA[2], or_2_out);
  xor xor_6 (OutASubtractB[2], not_3_out, xor_5_out);
  or or_3 (or_3_out, and_6_out, and_5_out);
  and and_6 (and_6_out, not_3_out, xor_5_out);
  and and_7 (and_7_out, InA[3], or_3_out);
  xor xor_7 (xor_7_out, InA[3], or_3_out);
  and and_8 (and_8_out, not_4_out, xor_7_out);
  xor xor_8 (OutASubtractB[3], not_4_out, xor_7_out);
  or or_4 (or_4_out, and_8_out, and_7_out);
  xor xor_9 (xor_9_out, InA[4], or_4_out);
  and and_9 (and_9_out, InA[4], or_4_out);
  xor xor_10 (OutASubtractB[4], not_5_out, xor_9_out);
  and and_10 (and_10_out, not_5_out, xor_9_out);
  or or_5 (or_5_out, and_10_out, and_9_out);
  xor xor_11 (xor_11_out, InA[5], or_5_out);
  and and_11 (and_11_out, InA[5], or_5_out);
  xor xor_12 (OutASubtractB[5], not_6_out, xor_11_out);
  and and_12 (and_12_out, not_6_out, xor_11_out);
  or or_6 (or_6_out, and_12_out, and_11_out);
  xor xor_13 (xor_13_out, InA[6], or_6_out);
  and and_13 (and_13_out, InA[6], or_6_out);
  xor xor_14 (OutASubtractB[6], not_7_out, xor_13_out);
  and and_14 (and_14_out, not_7_out, xor_13_out);
  or or_7 (or_7_out, and_14_out, and_13_out);
  xor xor_15 (xor_15_out, InA[7], or_7_out);
  and and_15 (and_15_out, InA[7], or_7_out);
  xor xor_16 (OutASubtractB[7], not_8_out, xor_15_out);
  and and_16 (and_16_out, not_8_out, xor_15_out);
  or or_8 (CarryOverflow, and_16_out, and_15_out);

  // Notes on the sheet:
  //   CarryIn: initial=0x1
  //   CRS: Carry Ripple Subtractor
endmodule

module Norb_ALU_32B_CRA (
  input  [31:0] InA,
  input  [31:0] InB,
  output FlagOverflow,
  output [31:0] OutAAddB
);

  wire norb_alu_8b_cra_1_carryoverflow, norb_alu_8b_cra_2_carryoverflow, norb_alu_8b_cra_3_carryoverflow;
  wire [7:0] norb_alu_8b_cra_1_outaplusb, norb_alu_8b_cra_2_outaplusb, norb_alu_8b_cra_3_outaplusb,
       norb_alu_8b_cra_4_outaplusb, norb_std_32b8b_splitter_1_out0, norb_std_32b8b_splitter_1_out1,
       norb_std_32b8b_splitter_1_out2, norb_std_32b8b_splitter_1_out3, norb_std_32b8b_splitter_2_out0,
       norb_std_32b8b_splitter_2_out1, norb_std_32b8b_splitter_2_out2, norb_std_32b8b_splitter_2_out3;

  Norb_STD_32B8B_Splitter norb_std_32b8b_splitter_1 (
    .In32B(InA), .Out0(norb_std_32b8b_splitter_1_out0), .Out1(norb_std_32b8b_splitter_1_out1),
    .Out2(norb_std_32b8b_splitter_1_out2), .Out3(norb_std_32b8b_splitter_1_out3));
  Norb_STD_32B8B_Splitter norb_std_32b8b_splitter_2 (
    .In32B(InB), .Out0(norb_std_32b8b_splitter_2_out0), .Out1(norb_std_32b8b_splitter_2_out1),
    .Out2(norb_std_32b8b_splitter_2_out2), .Out3(norb_std_32b8b_splitter_2_out3));
  Norb_ALU_8B_CRA norb_alu_8b_cra_1 (
    .InA(norb_std_32b8b_splitter_1_out0), .InB(norb_std_32b8b_splitter_2_out0), .CarryIn(1'b0),
    .CarryOverflow(norb_alu_8b_cra_1_carryoverflow), .OutAPlusB(norb_alu_8b_cra_1_outaplusb));
  Norb_ALU_8B_CRA norb_alu_8b_cra_2 (
    .InA(norb_std_32b8b_splitter_1_out1), .InB(norb_std_32b8b_splitter_2_out1),
    .CarryIn(norb_alu_8b_cra_1_carryoverflow), .CarryOverflow(norb_alu_8b_cra_2_carryoverflow),
    .OutAPlusB(norb_alu_8b_cra_2_outaplusb));
  Norb_ALU_8B_CRA norb_alu_8b_cra_3 (
    .InA(norb_std_32b8b_splitter_1_out2), .InB(norb_std_32b8b_splitter_2_out2),
    .CarryIn(norb_alu_8b_cra_2_carryoverflow), .CarryOverflow(norb_alu_8b_cra_3_carryoverflow),
    .OutAPlusB(norb_alu_8b_cra_3_outaplusb));
  Norb_ALU_8B_CRA norb_alu_8b_cra_4 (
    .InA(norb_std_32b8b_splitter_1_out3), .InB(norb_std_32b8b_splitter_2_out3),
    .CarryIn(norb_alu_8b_cra_3_carryoverflow), .CarryOverflow(FlagOverflow),
    .OutAPlusB(norb_alu_8b_cra_4_outaplusb));
  Norb_STD_8B32B_Splitter norb_std_8b32b_splitter_1 (
    .In0(norb_alu_8b_cra_1_outaplusb), .In1(norb_alu_8b_cra_2_outaplusb), .In2(norb_alu_8b_cra_3_outaplusb),
    .In3(norb_alu_8b_cra_4_outaplusb), .Out32B(OutAAddB));

  // Notes on the sheet:
  //   CRA: Carry Ripple Adder
endmodule

module Norb_ALU_32B_CRS (
  input  [31:0] InA,
  input  [31:0] InB,
  output FlagOverflow,
  output [31:0] OutASubtractB
);

  wire norb_alu_8b_crs_1_carryoverflow, norb_alu_8b_crs_2_carryoverflow, norb_alu_8b_crs_3_carryoverflow;
  wire [7:0] norb_alu_8b_crs_1_outasubtractb, norb_alu_8b_crs_2_outasubtractb,
       norb_alu_8b_crs_3_outasubtractb, norb_alu_8b_crs_4_outasubtractb, norb_std_32b8b_splitter_1_out0,
       norb_std_32b8b_splitter_1_out1, norb_std_32b8b_splitter_1_out2, norb_std_32b8b_splitter_1_out3,
       norb_std_32b8b_splitter_2_out0, norb_std_32b8b_splitter_2_out1, norb_std_32b8b_splitter_2_out2,
       norb_std_32b8b_splitter_2_out3;

  Norb_STD_32B8B_Splitter norb_std_32b8b_splitter_1 (
    .In32B(InA), .Out0(norb_std_32b8b_splitter_1_out0), .Out1(norb_std_32b8b_splitter_1_out1),
    .Out2(norb_std_32b8b_splitter_1_out2), .Out3(norb_std_32b8b_splitter_1_out3));
  Norb_STD_32B8B_Splitter norb_std_32b8b_splitter_2 (
    .In32B(InB), .Out0(norb_std_32b8b_splitter_2_out0), .Out1(norb_std_32b8b_splitter_2_out1),
    .Out2(norb_std_32b8b_splitter_2_out2), .Out3(norb_std_32b8b_splitter_2_out3));
  Norb_ALU_8B_CRS norb_alu_8b_crs_1 (
    .InA(norb_std_32b8b_splitter_1_out0), .InB(norb_std_32b8b_splitter_2_out0), .CarryIn(1'b1),
    .CarryOverflow(norb_alu_8b_crs_1_carryoverflow), .OutASubtractB(norb_alu_8b_crs_1_outasubtractb));
  Norb_ALU_8B_CRS norb_alu_8b_crs_2 (
    .InA(norb_std_32b8b_splitter_1_out1), .InB(norb_std_32b8b_splitter_2_out1),
    .CarryIn(norb_alu_8b_crs_1_carryoverflow), .CarryOverflow(norb_alu_8b_crs_2_carryoverflow),
    .OutASubtractB(norb_alu_8b_crs_2_outasubtractb));
  Norb_ALU_8B_CRS norb_alu_8b_crs_3 (
    .InA(norb_std_32b8b_splitter_1_out2), .InB(norb_std_32b8b_splitter_2_out2),
    .CarryIn(norb_alu_8b_crs_2_carryoverflow), .CarryOverflow(norb_alu_8b_crs_3_carryoverflow),
    .OutASubtractB(norb_alu_8b_crs_3_outasubtractb));
  Norb_ALU_8B_CRS norb_alu_8b_crs_4 (
    .InA(norb_std_32b8b_splitter_1_out3), .InB(norb_std_32b8b_splitter_2_out3),
    .CarryIn(norb_alu_8b_crs_3_carryoverflow), .CarryOverflow(FlagOverflow),
    .OutASubtractB(norb_alu_8b_crs_4_outasubtractb));
  Norb_STD_8B32B_Splitter norb_std_8b32b_splitter_1 (
    .In0(norb_alu_8b_crs_1_outasubtractb), .In1(norb_alu_8b_crs_2_outasubtractb),
    .In2(norb_alu_8b_crs_3_outasubtractb), .In3(norb_alu_8b_crs_4_outasubtractb), .Out32B(OutASubtractB));

  // Notes on the sheet:
  //   CRS: Carry Ripple Subtractor
endmodule

module Norb_ALU_32B_SSLL (
  input  [31:0] InNum,
  output [31:0] OutLS1
);


  assign OutLS1 = {InNum[30:0], 1'b0};

  // Notes on the sheet:
  //   SSLL: Single Shift Left Logical Unit
endmodule

module Norb_ALU_32B_SLL (
  input  [4:0] InShamt,
  input  [31:0] InNum,
  output [31:0] OutShifted
);

  wire norb_std_5b_matcher_1_outaeqb, norb_std_5b_matcher_2_outaeqb, norb_std_5b_matcher_3_outaeqb,
       norb_std_5b_matcher_4_outaeqb, norb_std_5b_matcher_5_outaeqb, norb_std_5b_matcher_6_outaeqb,
       norb_std_5b_matcher_7_outaeqb, norb_std_5b_matcher_8_outaeqb, norb_std_5b_matcher_9_outaeqb,
       norb_std_5b_matcher_10_outaeqb, norb_std_5b_matcher_11_outaeqb, norb_std_5b_matcher_12_outaeqb,
       norb_std_5b_matcher_13_outaeqb, norb_std_5b_matcher_14_outaeqb, norb_std_5b_matcher_15_outaeqb,
       norb_std_5b_matcher_16_outaeqb, norb_std_5b_matcher_17_outaeqb, norb_std_5b_matcher_18_outaeqb,
       norb_std_5b_matcher_19_outaeqb, norb_std_5b_matcher_20_outaeqb, norb_std_5b_matcher_21_outaeqb,
       norb_std_5b_matcher_22_outaeqb, norb_std_5b_matcher_23_outaeqb, norb_std_5b_matcher_24_outaeqb,
       norb_std_5b_matcher_25_outaeqb, norb_std_5b_matcher_26_outaeqb, norb_std_5b_matcher_27_outaeqb,
       norb_std_5b_matcher_28_outaeqb, norb_std_5b_matcher_29_outaeqb, norb_std_5b_matcher_30_outaeqb,
       norb_std_5b_matcher_31_outaeqb, norb_std_5b_matcher_32_outaeqb;
  wire [31:0] norb_alu_32b_ssll_1_outls1, norb_alu_32b_ssll_2_outls1, norb_alu_32b_ssll_3_outls1,
       norb_alu_32b_ssll_4_outls1, norb_alu_32b_ssll_5_outls1, norb_alu_32b_ssll_6_outls1,
       norb_alu_32b_ssll_7_outls1, norb_alu_32b_ssll_8_outls1, norb_alu_32b_ssll_9_outls1,
       norb_alu_32b_ssll_10_outls1, norb_alu_32b_ssll_11_outls1, norb_alu_32b_ssll_12_outls1,
       norb_alu_32b_ssll_13_outls1, norb_alu_32b_ssll_14_outls1, norb_alu_32b_ssll_15_outls1,
       norb_alu_32b_ssll_16_outls1, norb_alu_32b_ssll_17_outls1, norb_alu_32b_ssll_18_outls1,
       norb_alu_32b_ssll_19_outls1, norb_alu_32b_ssll_20_outls1, norb_alu_32b_ssll_21_outls1,
       norb_alu_32b_ssll_22_outls1, norb_alu_32b_ssll_23_outls1, norb_alu_32b_ssll_24_outls1,
       norb_alu_32b_ssll_25_outls1, norb_alu_32b_ssll_26_outls1, norb_alu_32b_ssll_27_outls1,
       norb_alu_32b_ssll_28_outls1, norb_alu_32b_ssll_29_outls1, norb_alu_32b_ssll_30_outls1,
       norb_alu_32b_ssll_31_outls1, norb_std_32b_selector_1_out32b, norb_std_32b_selector_2_out32b,
       norb_std_32b_selector_3_out32b, norb_std_32b_selector_4_out32b, norb_std_32b_selector_5_out32b,
       norb_std_32b_selector_6_out32b, norb_std_32b_selector_7_out32b, norb_std_32b_selector_8_out32b,
       norb_std_32b_selector_9_out32b, norb_std_32b_selector_10_out32b, norb_std_32b_selector_11_out32b,
       norb_std_32b_selector_12_out32b, norb_std_32b_selector_13_out32b, norb_std_32b_selector_14_out32b,
       norb_std_32b_selector_15_out32b, norb_std_32b_selector_16_out32b, norb_std_32b_selector_17_out32b,
       norb_std_32b_selector_18_out32b, norb_std_32b_selector_19_out32b, norb_std_32b_selector_20_out32b,
       norb_std_32b_selector_21_out32b, norb_std_32b_selector_22_out32b, norb_std_32b_selector_23_out32b,
       norb_std_32b_selector_24_out32b, norb_std_32b_selector_25_out32b, norb_std_32b_selector_26_out32b,
       norb_std_32b_selector_27_out32b, norb_std_32b_selector_28_out32b, norb_std_32b_selector_29_out32b,
       norb_std_32b_selector_30_out32b, norb_std_32b_selector_31_out32b, norb_std_32b_selector_32_out32b;

  Norb_ALU_32B_SSLL norb_alu_32b_ssll_1 (.InNum(InNum), .OutLS1(norb_alu_32b_ssll_1_outls1));
  Norb_ALU_32B_SSLL norb_alu_32b_ssll_2 (.InNum(norb_alu_32b_ssll_1_outls1), .OutLS1(norb_alu_32b_ssll_2_outls1));
  Norb_ALU_32B_SSLL norb_alu_32b_ssll_3 (.InNum(norb_alu_32b_ssll_2_outls1), .OutLS1(norb_alu_32b_ssll_3_outls1));
  Norb_ALU_32B_SSLL norb_alu_32b_ssll_4 (.InNum(norb_alu_32b_ssll_3_outls1), .OutLS1(norb_alu_32b_ssll_4_outls1));
  Norb_ALU_32B_SSLL norb_alu_32b_ssll_5 (.InNum(norb_alu_32b_ssll_4_outls1), .OutLS1(norb_alu_32b_ssll_5_outls1));
  Norb_ALU_32B_SSLL norb_alu_32b_ssll_6 (.InNum(norb_alu_32b_ssll_5_outls1), .OutLS1(norb_alu_32b_ssll_6_outls1));
  Norb_ALU_32B_SSLL norb_alu_32b_ssll_7 (.InNum(norb_alu_32b_ssll_6_outls1), .OutLS1(norb_alu_32b_ssll_7_outls1));
  Norb_ALU_32B_SSLL norb_alu_32b_ssll_8 (.InNum(norb_alu_32b_ssll_7_outls1), .OutLS1(norb_alu_32b_ssll_8_outls1));
  Norb_ALU_32B_SSLL norb_alu_32b_ssll_9 (.InNum(norb_alu_32b_ssll_8_outls1), .OutLS1(norb_alu_32b_ssll_9_outls1));
  Norb_ALU_32B_SSLL norb_alu_32b_ssll_10 (.InNum(norb_alu_32b_ssll_9_outls1), .OutLS1(norb_alu_32b_ssll_10_outls1));
  Norb_ALU_32B_SSLL norb_alu_32b_ssll_11 (.InNum(norb_alu_32b_ssll_10_outls1), .OutLS1(norb_alu_32b_ssll_11_outls1));
  Norb_ALU_32B_SSLL norb_alu_32b_ssll_12 (.InNum(norb_alu_32b_ssll_11_outls1), .OutLS1(norb_alu_32b_ssll_12_outls1));
  Norb_ALU_32B_SSLL norb_alu_32b_ssll_13 (.InNum(norb_alu_32b_ssll_12_outls1), .OutLS1(norb_alu_32b_ssll_13_outls1));
  Norb_ALU_32B_SSLL norb_alu_32b_ssll_14 (.InNum(norb_alu_32b_ssll_13_outls1), .OutLS1(norb_alu_32b_ssll_14_outls1));
  Norb_ALU_32B_SSLL norb_alu_32b_ssll_15 (.InNum(norb_alu_32b_ssll_14_outls1), .OutLS1(norb_alu_32b_ssll_15_outls1));
  Norb_ALU_32B_SSLL norb_alu_32b_ssll_16 (.InNum(norb_alu_32b_ssll_15_outls1), .OutLS1(norb_alu_32b_ssll_16_outls1));
  Norb_ALU_32B_SSLL norb_alu_32b_ssll_17 (.InNum(norb_alu_32b_ssll_16_outls1), .OutLS1(norb_alu_32b_ssll_17_outls1));
  Norb_ALU_32B_SSLL norb_alu_32b_ssll_18 (.InNum(norb_alu_32b_ssll_17_outls1), .OutLS1(norb_alu_32b_ssll_18_outls1));
  Norb_ALU_32B_SSLL norb_alu_32b_ssll_19 (.InNum(norb_alu_32b_ssll_18_outls1), .OutLS1(norb_alu_32b_ssll_19_outls1));
  Norb_ALU_32B_SSLL norb_alu_32b_ssll_20 (.InNum(norb_alu_32b_ssll_19_outls1), .OutLS1(norb_alu_32b_ssll_20_outls1));
  Norb_ALU_32B_SSLL norb_alu_32b_ssll_21 (.InNum(norb_alu_32b_ssll_20_outls1), .OutLS1(norb_alu_32b_ssll_21_outls1));
  Norb_ALU_32B_SSLL norb_alu_32b_ssll_22 (.InNum(norb_alu_32b_ssll_21_outls1), .OutLS1(norb_alu_32b_ssll_22_outls1));
  Norb_ALU_32B_SSLL norb_alu_32b_ssll_23 (.InNum(norb_alu_32b_ssll_22_outls1), .OutLS1(norb_alu_32b_ssll_23_outls1));
  Norb_ALU_32B_SSLL norb_alu_32b_ssll_24 (.InNum(norb_alu_32b_ssll_23_outls1), .OutLS1(norb_alu_32b_ssll_24_outls1));
  Norb_ALU_32B_SSLL norb_alu_32b_ssll_25 (.InNum(norb_alu_32b_ssll_24_outls1), .OutLS1(norb_alu_32b_ssll_25_outls1));
  Norb_ALU_32B_SSLL norb_alu_32b_ssll_26 (.InNum(norb_alu_32b_ssll_25_outls1), .OutLS1(norb_alu_32b_ssll_26_outls1));
  Norb_ALU_32B_SSLL norb_alu_32b_ssll_27 (.InNum(norb_alu_32b_ssll_26_outls1), .OutLS1(norb_alu_32b_ssll_27_outls1));
  Norb_ALU_32B_SSLL norb_alu_32b_ssll_28 (.InNum(norb_alu_32b_ssll_27_outls1), .OutLS1(norb_alu_32b_ssll_28_outls1));
  Norb_ALU_32B_SSLL norb_alu_32b_ssll_29 (.InNum(norb_alu_32b_ssll_28_outls1), .OutLS1(norb_alu_32b_ssll_29_outls1));
  Norb_ALU_32B_SSLL norb_alu_32b_ssll_30 (.InNum(norb_alu_32b_ssll_29_outls1), .OutLS1(norb_alu_32b_ssll_30_outls1));
  Norb_ALU_32B_SSLL norb_alu_32b_ssll_31 (.InNum(norb_alu_32b_ssll_30_outls1), .OutLS1(norb_alu_32b_ssll_31_outls1));
  Norb_STD_5B_Matcher norb_std_5b_matcher_1 (
    .In8B_A(InShamt), .In8B_B({5{1'b0}}), .OutAEqB(norb_std_5b_matcher_1_outaeqb));
  Norb_STD_5B_Matcher norb_std_5b_matcher_2 (
    .In8B_A(InShamt), .In8B_B(5'b00001), .OutAEqB(norb_std_5b_matcher_2_outaeqb));
  Norb_STD_5B_Matcher norb_std_5b_matcher_3 (
    .In8B_A(InShamt), .In8B_B(5'b00010), .OutAEqB(norb_std_5b_matcher_3_outaeqb));
  Norb_STD_5B_Matcher norb_std_5b_matcher_4 (
    .In8B_A(InShamt), .In8B_B(5'b00011), .OutAEqB(norb_std_5b_matcher_4_outaeqb));
  Norb_STD_5B_Matcher norb_std_5b_matcher_5 (
    .In8B_A(InShamt), .In8B_B(5'b00100), .OutAEqB(norb_std_5b_matcher_5_outaeqb));
  Norb_STD_5B_Matcher norb_std_5b_matcher_6 (
    .In8B_A(InShamt), .In8B_B(5'b00101), .OutAEqB(norb_std_5b_matcher_6_outaeqb));
  Norb_STD_5B_Matcher norb_std_5b_matcher_7 (
    .In8B_A(InShamt), .In8B_B(5'b00110), .OutAEqB(norb_std_5b_matcher_7_outaeqb));
  Norb_STD_5B_Matcher norb_std_5b_matcher_8 (
    .In8B_A(InShamt), .In8B_B(5'b00111), .OutAEqB(norb_std_5b_matcher_8_outaeqb));
  Norb_STD_5B_Matcher norb_std_5b_matcher_9 (
    .In8B_A(InShamt), .In8B_B(5'b01000), .OutAEqB(norb_std_5b_matcher_9_outaeqb));
  Norb_STD_5B_Matcher norb_std_5b_matcher_10 (
    .In8B_A(InShamt), .In8B_B(5'b01001), .OutAEqB(norb_std_5b_matcher_10_outaeqb));
  Norb_STD_5B_Matcher norb_std_5b_matcher_11 (
    .In8B_A(InShamt), .In8B_B(5'b01010), .OutAEqB(norb_std_5b_matcher_11_outaeqb));
  Norb_STD_5B_Matcher norb_std_5b_matcher_12 (
    .In8B_A(InShamt), .In8B_B(5'b01011), .OutAEqB(norb_std_5b_matcher_12_outaeqb));
  Norb_STD_5B_Matcher norb_std_5b_matcher_13 (
    .In8B_A(InShamt), .In8B_B(5'b01100), .OutAEqB(norb_std_5b_matcher_13_outaeqb));
  Norb_STD_5B_Matcher norb_std_5b_matcher_14 (
    .In8B_A(InShamt), .In8B_B(5'b01101), .OutAEqB(norb_std_5b_matcher_14_outaeqb));
  Norb_STD_5B_Matcher norb_std_5b_matcher_15 (
    .In8B_A(InShamt), .In8B_B(5'b01110), .OutAEqB(norb_std_5b_matcher_15_outaeqb));
  Norb_STD_5B_Matcher norb_std_5b_matcher_16 (
    .In8B_A(InShamt), .In8B_B(5'b01111), .OutAEqB(norb_std_5b_matcher_16_outaeqb));
  Norb_STD_5B_Matcher norb_std_5b_matcher_17 (
    .In8B_A(InShamt), .In8B_B(5'b01011), .OutAEqB(norb_std_5b_matcher_17_outaeqb));
  Norb_STD_5B_Matcher norb_std_5b_matcher_18 (
    .In8B_A(InShamt), .In8B_B(5'b00001), .OutAEqB(norb_std_5b_matcher_18_outaeqb));
  Norb_STD_5B_Matcher norb_std_5b_matcher_19 (
    .In8B_A(InShamt), .In8B_B(5'b01111), .OutAEqB(norb_std_5b_matcher_19_outaeqb));
  Norb_STD_5B_Matcher norb_std_5b_matcher_20 (
    .In8B_A(InShamt), .In8B_B(5'b10000), .OutAEqB(norb_std_5b_matcher_20_outaeqb));
  Norb_STD_5B_Matcher norb_std_5b_matcher_21 (
    .In8B_A(InShamt), .In8B_B(5'b10001), .OutAEqB(norb_std_5b_matcher_21_outaeqb));
  Norb_STD_5B_Matcher norb_std_5b_matcher_22 (
    .In8B_A(InShamt), .In8B_B(5'b10010), .OutAEqB(norb_std_5b_matcher_22_outaeqb));
  Norb_STD_5B_Matcher norb_std_5b_matcher_23 (
    .In8B_A(InShamt), .In8B_B(5'b10011), .OutAEqB(norb_std_5b_matcher_23_outaeqb));
  Norb_STD_5B_Matcher norb_std_5b_matcher_24 (
    .In8B_A(InShamt), .In8B_B(5'b10100), .OutAEqB(norb_std_5b_matcher_24_outaeqb));
  Norb_STD_5B_Matcher norb_std_5b_matcher_25 (
    .In8B_A(InShamt), .In8B_B(5'b10101), .OutAEqB(norb_std_5b_matcher_25_outaeqb));
  Norb_STD_5B_Matcher norb_std_5b_matcher_26 (
    .In8B_A(InShamt), .In8B_B(5'b10110), .OutAEqB(norb_std_5b_matcher_26_outaeqb));
  Norb_STD_5B_Matcher norb_std_5b_matcher_27 (
    .In8B_A(InShamt), .In8B_B(5'b10111), .OutAEqB(norb_std_5b_matcher_27_outaeqb));
  Norb_STD_5B_Matcher norb_std_5b_matcher_28 (
    .In8B_A(InShamt), .In8B_B(5'b11000), .OutAEqB(norb_std_5b_matcher_28_outaeqb));
  Norb_STD_5B_Matcher norb_std_5b_matcher_29 (
    .In8B_A(InShamt), .In8B_B(5'b11001), .OutAEqB(norb_std_5b_matcher_29_outaeqb));
  Norb_STD_5B_Matcher norb_std_5b_matcher_30 (
    .In8B_A(InShamt), .In8B_B(5'b11010), .OutAEqB(norb_std_5b_matcher_30_outaeqb));
  Norb_STD_5B_Matcher norb_std_5b_matcher_31 (
    .In8B_A(InShamt), .In8B_B(5'b11011), .OutAEqB(norb_std_5b_matcher_31_outaeqb));
  Norb_STD_5B_Matcher norb_std_5b_matcher_32 (
    .In8B_A(InShamt), .In8B_B(5'b11100), .OutAEqB(norb_std_5b_matcher_32_outaeqb));
  Norb_STD_32B_Selector norb_std_32b_selector_1 (
    .In32B(InNum), .InSelect(norb_std_5b_matcher_1_outaeqb), .Out32B(norb_std_32b_selector_1_out32b));
  Norb_STD_32B_Selector norb_std_32b_selector_2 (
    .In32B(norb_alu_32b_ssll_1_outls1), .InSelect(norb_std_5b_matcher_2_outaeqb),
    .Out32B(norb_std_32b_selector_2_out32b));
  Norb_STD_32B_Selector norb_std_32b_selector_3 (
    .In32B(norb_alu_32b_ssll_2_outls1), .InSelect(norb_std_5b_matcher_3_outaeqb),
    .Out32B(norb_std_32b_selector_3_out32b));
  Norb_STD_32B_Selector norb_std_32b_selector_4 (
    .In32B(norb_alu_32b_ssll_3_outls1), .InSelect(norb_std_5b_matcher_4_outaeqb),
    .Out32B(norb_std_32b_selector_4_out32b));
  Norb_STD_32B_Selector norb_std_32b_selector_5 (
    .In32B(norb_alu_32b_ssll_4_outls1), .InSelect(norb_std_5b_matcher_5_outaeqb),
    .Out32B(norb_std_32b_selector_5_out32b));
  Norb_STD_32B_Selector norb_std_32b_selector_6 (
    .In32B(norb_alu_32b_ssll_5_outls1), .InSelect(norb_std_5b_matcher_6_outaeqb),
    .Out32B(norb_std_32b_selector_6_out32b));
  Norb_STD_32B_Selector norb_std_32b_selector_7 (
    .In32B(norb_alu_32b_ssll_6_outls1), .InSelect(norb_std_5b_matcher_7_outaeqb),
    .Out32B(norb_std_32b_selector_7_out32b));
  Norb_STD_32B_Selector norb_std_32b_selector_8 (
    .In32B(norb_alu_32b_ssll_7_outls1), .InSelect(norb_std_5b_matcher_8_outaeqb),
    .Out32B(norb_std_32b_selector_8_out32b));
  Norb_STD_32B_Selector norb_std_32b_selector_9 (
    .In32B(norb_alu_32b_ssll_8_outls1), .InSelect(norb_std_5b_matcher_9_outaeqb),
    .Out32B(norb_std_32b_selector_9_out32b));
  Norb_STD_32B_Selector norb_std_32b_selector_10 (
    .In32B(norb_alu_32b_ssll_9_outls1), .InSelect(norb_std_5b_matcher_10_outaeqb),
    .Out32B(norb_std_32b_selector_10_out32b));
  Norb_STD_32B_Selector norb_std_32b_selector_11 (
    .In32B(norb_alu_32b_ssll_10_outls1), .InSelect(norb_std_5b_matcher_11_outaeqb),
    .Out32B(norb_std_32b_selector_11_out32b));
  Norb_STD_32B_Selector norb_std_32b_selector_12 (
    .In32B(norb_alu_32b_ssll_11_outls1), .InSelect(norb_std_5b_matcher_12_outaeqb),
    .Out32B(norb_std_32b_selector_12_out32b));
  Norb_STD_32B_Selector norb_std_32b_selector_13 (
    .In32B(norb_alu_32b_ssll_12_outls1), .InSelect(norb_std_5b_matcher_13_outaeqb),
    .Out32B(norb_std_32b_selector_13_out32b));
  Norb_STD_32B_Selector norb_std_32b_selector_14 (
    .In32B(norb_alu_32b_ssll_13_outls1), .InSelect(norb_std_5b_matcher_14_outaeqb),
    .Out32B(norb_std_32b_selector_14_out32b));
  Norb_STD_32B_Selector norb_std_32b_selector_15 (
    .In32B(norb_alu_32b_ssll_14_outls1), .InSelect(norb_std_5b_matcher_15_outaeqb),
    .Out32B(norb_std_32b_selector_15_out32b));
  Norb_STD_32B_Selector norb_std_32b_selector_16 (
    .In32B(norb_alu_32b_ssll_15_outls1), .InSelect(norb_std_5b_matcher_16_outaeqb),
    .Out32B(norb_std_32b_selector_16_out32b));
  Norb_STD_32B_Selector norb_std_32b_selector_17 (
    .In32B(norb_alu_32b_ssll_16_outls1), .InSelect(norb_std_5b_matcher_17_outaeqb),
    .Out32B(norb_std_32b_selector_17_out32b));
  Norb_STD_32B_Selector norb_std_32b_selector_18 (
    .In32B(norb_alu_32b_ssll_17_outls1), .InSelect(norb_std_5b_matcher_18_outaeqb),
    .Out32B(norb_std_32b_selector_18_out32b));
  Norb_STD_32B_Selector norb_std_32b_selector_19 (
    .In32B(norb_alu_32b_ssll_18_outls1), .InSelect(norb_std_5b_matcher_19_outaeqb),
    .Out32B(norb_std_32b_selector_19_out32b));
  Norb_STD_32B_Selector norb_std_32b_selector_20 (
    .In32B(norb_alu_32b_ssll_19_outls1), .InSelect(norb_std_5b_matcher_20_outaeqb),
    .Out32B(norb_std_32b_selector_20_out32b));
  Norb_STD_32B_Selector norb_std_32b_selector_21 (
    .In32B(norb_alu_32b_ssll_20_outls1), .InSelect(norb_std_5b_matcher_21_outaeqb),
    .Out32B(norb_std_32b_selector_21_out32b));
  Norb_STD_32B_Selector norb_std_32b_selector_22 (
    .In32B(norb_alu_32b_ssll_21_outls1), .InSelect(norb_std_5b_matcher_22_outaeqb),
    .Out32B(norb_std_32b_selector_22_out32b));
  Norb_STD_32B_Selector norb_std_32b_selector_23 (
    .In32B(norb_alu_32b_ssll_22_outls1), .InSelect(norb_std_5b_matcher_23_outaeqb),
    .Out32B(norb_std_32b_selector_23_out32b));
  Norb_STD_32B_Selector norb_std_32b_selector_24 (
    .In32B(norb_alu_32b_ssll_23_outls1), .InSelect(norb_std_5b_matcher_24_outaeqb),
    .Out32B(norb_std_32b_selector_24_out32b));
  Norb_STD_32B_Selector norb_std_32b_selector_25 (
    .In32B(norb_alu_32b_ssll_24_outls1), .InSelect(norb_std_5b_matcher_25_outaeqb),
    .Out32B(norb_std_32b_selector_25_out32b));
  Norb_STD_32B_Selector norb_std_32b_selector_26 (
    .In32B(norb_alu_32b_ssll_25_outls1), .InSelect(norb_std_5b_matcher_26_outaeqb),
    .Out32B(norb_std_32b_selector_26_out32b));
  Norb_STD_32B_Selector norb_std_32b_selector_27 (
    .In32B(norb_alu_32b_ssll_26_outls1), .InSelect(norb_std_5b_matcher_27_outaeqb),
    .Out32B(norb_std_32b_selector_27_out32b));
  Norb_STD_32B_Selector norb_std_32b_selector_28 (
    .In32B(norb_alu_32b_ssll_27_outls1), .InSelect(norb_std_5b_matcher_28_outaeqb),
    .Out32B(norb_std_32b_selector_28_out32b));
  Norb_STD_32B_Selector norb_std_32b_selector_29 (
    .In32B(norb_alu_32b_ssll_28_outls1), .InSelect(norb_std_5b_matcher_29_outaeqb),
    .Out32B(norb_std_32b_selector_29_out32b));
  Norb_STD_32B_Selector norb_std_32b_selector_30 (
    .In32B(norb_alu_32b_ssll_29_outls1), .InSelect(norb_std_5b_matcher_30_outaeqb),
    .Out32B(norb_std_32b_selector_30_out32b));
  Norb_STD_32B_Selector norb_std_32b_selector_31 (
    .In32B(norb_alu_32b_ssll_30_outls1), .InSelect(norb_std_5b_matcher_31_outaeqb),
    .Out32B(norb_std_32b_selector_31_out32b));
  Norb_STD_32B_Selector norb_std_32b_selector_32 (
    .In32B(norb_alu_32b_ssll_31_outls1), .InSelect(norb_std_5b_matcher_32_outaeqb),
    .Out32B(norb_std_32b_selector_32_out32b));
  assign OutShifted = norb_std_32b_selector_1_out32b | norb_std_32b_selector_2_out32b | norb_std_32b_selector_3_out32b | norb_std_32b_selector_4_out32b | norb_std_32b_selector_5_out32b | norb_std_32b_selector_6_out32b | norb_std_32b_selector_7_out32b | norb_std_32b_selector_8_out32b | norb_std_32b_selector_9_out32b | norb_std_32b_selector_10_out32b | norb_std_32b_selector_11_out32b | norb_std_32b_selector_12_out32b | norb_std_32b_selector_13_out32b | norb_std_32b_selector_14_out32b | norb_std_32b_selector_15_out32b | norb_std_32b_selector_16_out32b | norb_std_32b_selector_17_out32b | norb_std_32b_selector_18_out32b | norb_std_32b_selector_19_out32b | norb_std_32b_selector_20_out32b | norb_std_32b_selector_21_out32b | norb_std_32b_selector_22_out32b | norb_std_32b_selector_23_out32b | norb_std_32b_selector_24_out32b | norb_std_32b_selector_25_out32b | norb_std_32b_selector_26_out32b | norb_std_32b_selector_27_out32b | norb_std_32b_selector_28_out32b | norb_std_32b_selector_29_out32b | norb_std_32b_selector_30_out32b | norb_std_32b_selector_31_out32b | norb_std_32b_selector_32_out32b;  // OR_Gate or_1, 32 bits wide

  // Notes on the sheet:
  //   SLL: Shift Left Logical Unit
endmodule

module Norb_ALU_32B_SSRL (
  input  [31:0] InNum,
  output [31:0] OutRS1
);


  assign OutRS1 = {1'b0, InNum[31:1]};

  // Notes on the sheet:
  //   SSRL: Single Shift Right Logical Unit
endmodule

module Norb_ALU_32B_SRL (
  input  [4:0] InShamt,
  input  [31:0] InNum,
  output [31:0] OutShifted
);

  wire norb_std_5b_matcher_1_outaeqb, norb_std_5b_matcher_2_outaeqb, norb_std_5b_matcher_3_outaeqb,
       norb_std_5b_matcher_4_outaeqb, norb_std_5b_matcher_5_outaeqb, norb_std_5b_matcher_6_outaeqb,
       norb_std_5b_matcher_7_outaeqb, norb_std_5b_matcher_8_outaeqb, norb_std_5b_matcher_9_outaeqb,
       norb_std_5b_matcher_10_outaeqb, norb_std_5b_matcher_11_outaeqb, norb_std_5b_matcher_12_outaeqb,
       norb_std_5b_matcher_13_outaeqb, norb_std_5b_matcher_14_outaeqb, norb_std_5b_matcher_15_outaeqb,
       norb_std_5b_matcher_16_outaeqb, norb_std_5b_matcher_17_outaeqb, norb_std_5b_matcher_18_outaeqb,
       norb_std_5b_matcher_19_outaeqb, norb_std_5b_matcher_20_outaeqb, norb_std_5b_matcher_21_outaeqb,
       norb_std_5b_matcher_22_outaeqb, norb_std_5b_matcher_23_outaeqb, norb_std_5b_matcher_24_outaeqb,
       norb_std_5b_matcher_25_outaeqb, norb_std_5b_matcher_26_outaeqb, norb_std_5b_matcher_27_outaeqb,
       norb_std_5b_matcher_28_outaeqb, norb_std_5b_matcher_29_outaeqb, norb_std_5b_matcher_30_outaeqb,
       norb_std_5b_matcher_31_outaeqb, norb_std_5b_matcher_32_outaeqb;
  wire [31:0] norb_alu_32b_ssrl_1_outrs1, norb_alu_32b_ssrl_2_outrs1, norb_alu_32b_ssrl_3_outrs1,
       norb_alu_32b_ssrl_4_outrs1, norb_alu_32b_ssrl_5_outrs1, norb_alu_32b_ssrl_6_outrs1,
       norb_alu_32b_ssrl_7_outrs1, norb_alu_32b_ssrl_8_outrs1, norb_alu_32b_ssrl_9_outrs1,
       norb_alu_32b_ssrl_10_outrs1, norb_alu_32b_ssrl_11_outrs1, norb_alu_32b_ssrl_12_outrs1,
       norb_alu_32b_ssrl_13_outrs1, norb_alu_32b_ssrl_14_outrs1, norb_alu_32b_ssrl_15_outrs1,
       norb_alu_32b_ssrl_16_outrs1, norb_alu_32b_ssrl_17_outrs1, norb_alu_32b_ssrl_18_outrs1,
       norb_alu_32b_ssrl_19_outrs1, norb_alu_32b_ssrl_20_outrs1, norb_alu_32b_ssrl_21_outrs1,
       norb_alu_32b_ssrl_22_outrs1, norb_alu_32b_ssrl_23_outrs1, norb_alu_32b_ssrl_24_outrs1,
       norb_alu_32b_ssrl_25_outrs1, norb_alu_32b_ssrl_26_outrs1, norb_alu_32b_ssrl_27_outrs1,
       norb_alu_32b_ssrl_28_outrs1, norb_alu_32b_ssrl_29_outrs1, norb_alu_32b_ssrl_30_outrs1,
       norb_alu_32b_ssrl_31_outrs1, norb_std_32b_selector_1_out32b, norb_std_32b_selector_2_out32b,
       norb_std_32b_selector_3_out32b, norb_std_32b_selector_4_out32b, norb_std_32b_selector_5_out32b,
       norb_std_32b_selector_6_out32b, norb_std_32b_selector_7_out32b, norb_std_32b_selector_8_out32b,
       norb_std_32b_selector_9_out32b, norb_std_32b_selector_10_out32b, norb_std_32b_selector_11_out32b,
       norb_std_32b_selector_12_out32b, norb_std_32b_selector_13_out32b, norb_std_32b_selector_14_out32b,
       norb_std_32b_selector_15_out32b, norb_std_32b_selector_16_out32b, norb_std_32b_selector_17_out32b,
       norb_std_32b_selector_18_out32b, norb_std_32b_selector_19_out32b, norb_std_32b_selector_20_out32b,
       norb_std_32b_selector_21_out32b, norb_std_32b_selector_22_out32b, norb_std_32b_selector_23_out32b,
       norb_std_32b_selector_24_out32b, norb_std_32b_selector_25_out32b, norb_std_32b_selector_26_out32b,
       norb_std_32b_selector_27_out32b, norb_std_32b_selector_28_out32b, norb_std_32b_selector_29_out32b,
       norb_std_32b_selector_30_out32b, norb_std_32b_selector_31_out32b, norb_std_32b_selector_32_out32b;

  Norb_ALU_32B_SSRL norb_alu_32b_ssrl_1 (.InNum(InNum), .OutRS1(norb_alu_32b_ssrl_1_outrs1));
  Norb_ALU_32B_SSRL norb_alu_32b_ssrl_2 (.InNum(norb_alu_32b_ssrl_1_outrs1), .OutRS1(norb_alu_32b_ssrl_2_outrs1));
  Norb_ALU_32B_SSRL norb_alu_32b_ssrl_3 (.InNum(norb_alu_32b_ssrl_2_outrs1), .OutRS1(norb_alu_32b_ssrl_3_outrs1));
  Norb_ALU_32B_SSRL norb_alu_32b_ssrl_4 (.InNum(norb_alu_32b_ssrl_3_outrs1), .OutRS1(norb_alu_32b_ssrl_4_outrs1));
  Norb_ALU_32B_SSRL norb_alu_32b_ssrl_5 (.InNum(norb_alu_32b_ssrl_4_outrs1), .OutRS1(norb_alu_32b_ssrl_5_outrs1));
  Norb_ALU_32B_SSRL norb_alu_32b_ssrl_6 (.InNum(norb_alu_32b_ssrl_5_outrs1), .OutRS1(norb_alu_32b_ssrl_6_outrs1));
  Norb_ALU_32B_SSRL norb_alu_32b_ssrl_7 (.InNum(norb_alu_32b_ssrl_6_outrs1), .OutRS1(norb_alu_32b_ssrl_7_outrs1));
  Norb_ALU_32B_SSRL norb_alu_32b_ssrl_8 (.InNum(norb_alu_32b_ssrl_7_outrs1), .OutRS1(norb_alu_32b_ssrl_8_outrs1));
  Norb_ALU_32B_SSRL norb_alu_32b_ssrl_9 (.InNum(norb_alu_32b_ssrl_8_outrs1), .OutRS1(norb_alu_32b_ssrl_9_outrs1));
  Norb_ALU_32B_SSRL norb_alu_32b_ssrl_10 (.InNum(norb_alu_32b_ssrl_9_outrs1), .OutRS1(norb_alu_32b_ssrl_10_outrs1));
  Norb_ALU_32B_SSRL norb_alu_32b_ssrl_11 (.InNum(norb_alu_32b_ssrl_10_outrs1), .OutRS1(norb_alu_32b_ssrl_11_outrs1));
  Norb_ALU_32B_SSRL norb_alu_32b_ssrl_12 (.InNum(norb_alu_32b_ssrl_11_outrs1), .OutRS1(norb_alu_32b_ssrl_12_outrs1));
  Norb_ALU_32B_SSRL norb_alu_32b_ssrl_13 (.InNum(norb_alu_32b_ssrl_12_outrs1), .OutRS1(norb_alu_32b_ssrl_13_outrs1));
  Norb_ALU_32B_SSRL norb_alu_32b_ssrl_14 (.InNum(norb_alu_32b_ssrl_13_outrs1), .OutRS1(norb_alu_32b_ssrl_14_outrs1));
  Norb_ALU_32B_SSRL norb_alu_32b_ssrl_15 (.InNum(norb_alu_32b_ssrl_14_outrs1), .OutRS1(norb_alu_32b_ssrl_15_outrs1));
  Norb_ALU_32B_SSRL norb_alu_32b_ssrl_16 (.InNum(norb_alu_32b_ssrl_15_outrs1), .OutRS1(norb_alu_32b_ssrl_16_outrs1));
  Norb_ALU_32B_SSRL norb_alu_32b_ssrl_17 (.InNum(norb_alu_32b_ssrl_16_outrs1), .OutRS1(norb_alu_32b_ssrl_17_outrs1));
  Norb_ALU_32B_SSRL norb_alu_32b_ssrl_18 (.InNum(norb_alu_32b_ssrl_17_outrs1), .OutRS1(norb_alu_32b_ssrl_18_outrs1));
  Norb_ALU_32B_SSRL norb_alu_32b_ssrl_19 (.InNum(norb_alu_32b_ssrl_18_outrs1), .OutRS1(norb_alu_32b_ssrl_19_outrs1));
  Norb_ALU_32B_SSRL norb_alu_32b_ssrl_20 (.InNum(norb_alu_32b_ssrl_19_outrs1), .OutRS1(norb_alu_32b_ssrl_20_outrs1));
  Norb_ALU_32B_SSRL norb_alu_32b_ssrl_21 (.InNum(norb_alu_32b_ssrl_20_outrs1), .OutRS1(norb_alu_32b_ssrl_21_outrs1));
  Norb_ALU_32B_SSRL norb_alu_32b_ssrl_22 (.InNum(norb_alu_32b_ssrl_21_outrs1), .OutRS1(norb_alu_32b_ssrl_22_outrs1));
  Norb_ALU_32B_SSRL norb_alu_32b_ssrl_23 (.InNum(norb_alu_32b_ssrl_22_outrs1), .OutRS1(norb_alu_32b_ssrl_23_outrs1));
  Norb_ALU_32B_SSRL norb_alu_32b_ssrl_24 (.InNum(norb_alu_32b_ssrl_23_outrs1), .OutRS1(norb_alu_32b_ssrl_24_outrs1));
  Norb_ALU_32B_SSRL norb_alu_32b_ssrl_25 (.InNum(norb_alu_32b_ssrl_24_outrs1), .OutRS1(norb_alu_32b_ssrl_25_outrs1));
  Norb_ALU_32B_SSRL norb_alu_32b_ssrl_26 (.InNum(norb_alu_32b_ssrl_25_outrs1), .OutRS1(norb_alu_32b_ssrl_26_outrs1));
  Norb_ALU_32B_SSRL norb_alu_32b_ssrl_27 (.InNum(norb_alu_32b_ssrl_26_outrs1), .OutRS1(norb_alu_32b_ssrl_27_outrs1));
  Norb_ALU_32B_SSRL norb_alu_32b_ssrl_28 (.InNum(norb_alu_32b_ssrl_27_outrs1), .OutRS1(norb_alu_32b_ssrl_28_outrs1));
  Norb_ALU_32B_SSRL norb_alu_32b_ssrl_29 (.InNum(norb_alu_32b_ssrl_28_outrs1), .OutRS1(norb_alu_32b_ssrl_29_outrs1));
  Norb_ALU_32B_SSRL norb_alu_32b_ssrl_30 (.InNum(norb_alu_32b_ssrl_29_outrs1), .OutRS1(norb_alu_32b_ssrl_30_outrs1));
  Norb_ALU_32B_SSRL norb_alu_32b_ssrl_31 (.InNum(norb_alu_32b_ssrl_30_outrs1), .OutRS1(norb_alu_32b_ssrl_31_outrs1));
  Norb_STD_5B_Matcher norb_std_5b_matcher_1 (
    .In8B_A(InShamt), .In8B_B({5{1'b0}}), .OutAEqB(norb_std_5b_matcher_1_outaeqb));
  Norb_STD_5B_Matcher norb_std_5b_matcher_2 (
    .In8B_A(InShamt), .In8B_B(5'b00001), .OutAEqB(norb_std_5b_matcher_2_outaeqb));
  Norb_STD_5B_Matcher norb_std_5b_matcher_3 (
    .In8B_A(InShamt), .In8B_B(5'b00010), .OutAEqB(norb_std_5b_matcher_3_outaeqb));
  Norb_STD_5B_Matcher norb_std_5b_matcher_4 (
    .In8B_A(InShamt), .In8B_B(5'b00011), .OutAEqB(norb_std_5b_matcher_4_outaeqb));
  Norb_STD_5B_Matcher norb_std_5b_matcher_5 (
    .In8B_A(InShamt), .In8B_B(5'b00100), .OutAEqB(norb_std_5b_matcher_5_outaeqb));
  Norb_STD_5B_Matcher norb_std_5b_matcher_6 (
    .In8B_A(InShamt), .In8B_B(5'b00101), .OutAEqB(norb_std_5b_matcher_6_outaeqb));
  Norb_STD_5B_Matcher norb_std_5b_matcher_7 (
    .In8B_A(InShamt), .In8B_B(5'b00110), .OutAEqB(norb_std_5b_matcher_7_outaeqb));
  Norb_STD_5B_Matcher norb_std_5b_matcher_8 (
    .In8B_A(InShamt), .In8B_B(5'b00111), .OutAEqB(norb_std_5b_matcher_8_outaeqb));
  Norb_STD_5B_Matcher norb_std_5b_matcher_9 (
    .In8B_A(InShamt), .In8B_B(5'b01000), .OutAEqB(norb_std_5b_matcher_9_outaeqb));
  Norb_STD_5B_Matcher norb_std_5b_matcher_10 (
    .In8B_A(InShamt), .In8B_B(5'b01001), .OutAEqB(norb_std_5b_matcher_10_outaeqb));
  Norb_STD_5B_Matcher norb_std_5b_matcher_11 (
    .In8B_A(InShamt), .In8B_B(5'b01010), .OutAEqB(norb_std_5b_matcher_11_outaeqb));
  Norb_STD_5B_Matcher norb_std_5b_matcher_12 (
    .In8B_A(InShamt), .In8B_B(5'b01011), .OutAEqB(norb_std_5b_matcher_12_outaeqb));
  Norb_STD_5B_Matcher norb_std_5b_matcher_13 (
    .In8B_A(InShamt), .In8B_B(5'b01100), .OutAEqB(norb_std_5b_matcher_13_outaeqb));
  Norb_STD_5B_Matcher norb_std_5b_matcher_14 (
    .In8B_A(InShamt), .In8B_B(5'b01101), .OutAEqB(norb_std_5b_matcher_14_outaeqb));
  Norb_STD_5B_Matcher norb_std_5b_matcher_15 (
    .In8B_A(InShamt), .In8B_B(5'b01110), .OutAEqB(norb_std_5b_matcher_15_outaeqb));
  Norb_STD_5B_Matcher norb_std_5b_matcher_16 (
    .In8B_A(InShamt), .In8B_B(5'b01111), .OutAEqB(norb_std_5b_matcher_16_outaeqb));
  Norb_STD_5B_Matcher norb_std_5b_matcher_17 (
    .In8B_A(InShamt), .In8B_B(5'b01011), .OutAEqB(norb_std_5b_matcher_17_outaeqb));
  Norb_STD_5B_Matcher norb_std_5b_matcher_18 (
    .In8B_A(InShamt), .In8B_B(5'b00001), .OutAEqB(norb_std_5b_matcher_18_outaeqb));
  Norb_STD_5B_Matcher norb_std_5b_matcher_19 (
    .In8B_A(InShamt), .In8B_B(5'b01111), .OutAEqB(norb_std_5b_matcher_19_outaeqb));
  Norb_STD_5B_Matcher norb_std_5b_matcher_20 (
    .In8B_A(InShamt), .In8B_B(5'b10000), .OutAEqB(norb_std_5b_matcher_20_outaeqb));
  Norb_STD_5B_Matcher norb_std_5b_matcher_21 (
    .In8B_A(InShamt), .In8B_B(5'b10001), .OutAEqB(norb_std_5b_matcher_21_outaeqb));
  Norb_STD_5B_Matcher norb_std_5b_matcher_22 (
    .In8B_A(InShamt), .In8B_B(5'b10010), .OutAEqB(norb_std_5b_matcher_22_outaeqb));
  Norb_STD_5B_Matcher norb_std_5b_matcher_23 (
    .In8B_A(InShamt), .In8B_B(5'b10011), .OutAEqB(norb_std_5b_matcher_23_outaeqb));
  Norb_STD_5B_Matcher norb_std_5b_matcher_24 (
    .In8B_A(InShamt), .In8B_B(5'b10100), .OutAEqB(norb_std_5b_matcher_24_outaeqb));
  Norb_STD_5B_Matcher norb_std_5b_matcher_25 (
    .In8B_A(InShamt), .In8B_B(5'b10101), .OutAEqB(norb_std_5b_matcher_25_outaeqb));
  Norb_STD_5B_Matcher norb_std_5b_matcher_26 (
    .In8B_A(InShamt), .In8B_B(5'b10110), .OutAEqB(norb_std_5b_matcher_26_outaeqb));
  Norb_STD_5B_Matcher norb_std_5b_matcher_27 (
    .In8B_A(InShamt), .In8B_B(5'b10111), .OutAEqB(norb_std_5b_matcher_27_outaeqb));
  Norb_STD_5B_Matcher norb_std_5b_matcher_28 (
    .In8B_A(InShamt), .In8B_B(5'b11000), .OutAEqB(norb_std_5b_matcher_28_outaeqb));
  Norb_STD_5B_Matcher norb_std_5b_matcher_29 (
    .In8B_A(InShamt), .In8B_B(5'b11001), .OutAEqB(norb_std_5b_matcher_29_outaeqb));
  Norb_STD_5B_Matcher norb_std_5b_matcher_30 (
    .In8B_A(InShamt), .In8B_B(5'b11010), .OutAEqB(norb_std_5b_matcher_30_outaeqb));
  Norb_STD_5B_Matcher norb_std_5b_matcher_31 (
    .In8B_A(InShamt), .In8B_B(5'b11011), .OutAEqB(norb_std_5b_matcher_31_outaeqb));
  Norb_STD_5B_Matcher norb_std_5b_matcher_32 (
    .In8B_A(InShamt), .In8B_B(5'b11100), .OutAEqB(norb_std_5b_matcher_32_outaeqb));
  Norb_STD_32B_Selector norb_std_32b_selector_1 (
    .In32B(InNum), .InSelect(norb_std_5b_matcher_1_outaeqb), .Out32B(norb_std_32b_selector_1_out32b));
  Norb_STD_32B_Selector norb_std_32b_selector_2 (
    .In32B(norb_alu_32b_ssrl_1_outrs1), .InSelect(norb_std_5b_matcher_2_outaeqb),
    .Out32B(norb_std_32b_selector_2_out32b));
  Norb_STD_32B_Selector norb_std_32b_selector_3 (
    .In32B(norb_alu_32b_ssrl_2_outrs1), .InSelect(norb_std_5b_matcher_3_outaeqb),
    .Out32B(norb_std_32b_selector_3_out32b));
  Norb_STD_32B_Selector norb_std_32b_selector_4 (
    .In32B(norb_alu_32b_ssrl_3_outrs1), .InSelect(norb_std_5b_matcher_4_outaeqb),
    .Out32B(norb_std_32b_selector_4_out32b));
  Norb_STD_32B_Selector norb_std_32b_selector_5 (
    .In32B(norb_alu_32b_ssrl_4_outrs1), .InSelect(norb_std_5b_matcher_5_outaeqb),
    .Out32B(norb_std_32b_selector_5_out32b));
  Norb_STD_32B_Selector norb_std_32b_selector_6 (
    .In32B(norb_alu_32b_ssrl_5_outrs1), .InSelect(norb_std_5b_matcher_6_outaeqb),
    .Out32B(norb_std_32b_selector_6_out32b));
  Norb_STD_32B_Selector norb_std_32b_selector_7 (
    .In32B(norb_alu_32b_ssrl_6_outrs1), .InSelect(norb_std_5b_matcher_7_outaeqb),
    .Out32B(norb_std_32b_selector_7_out32b));
  Norb_STD_32B_Selector norb_std_32b_selector_8 (
    .In32B(norb_alu_32b_ssrl_7_outrs1), .InSelect(norb_std_5b_matcher_8_outaeqb),
    .Out32B(norb_std_32b_selector_8_out32b));
  Norb_STD_32B_Selector norb_std_32b_selector_9 (
    .In32B(norb_alu_32b_ssrl_8_outrs1), .InSelect(norb_std_5b_matcher_9_outaeqb),
    .Out32B(norb_std_32b_selector_9_out32b));
  Norb_STD_32B_Selector norb_std_32b_selector_10 (
    .In32B(norb_alu_32b_ssrl_9_outrs1), .InSelect(norb_std_5b_matcher_10_outaeqb),
    .Out32B(norb_std_32b_selector_10_out32b));
  Norb_STD_32B_Selector norb_std_32b_selector_11 (
    .In32B(norb_alu_32b_ssrl_10_outrs1), .InSelect(norb_std_5b_matcher_11_outaeqb),
    .Out32B(norb_std_32b_selector_11_out32b));
  Norb_STD_32B_Selector norb_std_32b_selector_12 (
    .In32B(norb_alu_32b_ssrl_11_outrs1), .InSelect(norb_std_5b_matcher_12_outaeqb),
    .Out32B(norb_std_32b_selector_12_out32b));
  Norb_STD_32B_Selector norb_std_32b_selector_13 (
    .In32B(norb_alu_32b_ssrl_12_outrs1), .InSelect(norb_std_5b_matcher_13_outaeqb),
    .Out32B(norb_std_32b_selector_13_out32b));
  Norb_STD_32B_Selector norb_std_32b_selector_14 (
    .In32B(norb_alu_32b_ssrl_13_outrs1), .InSelect(norb_std_5b_matcher_14_outaeqb),
    .Out32B(norb_std_32b_selector_14_out32b));
  Norb_STD_32B_Selector norb_std_32b_selector_15 (
    .In32B(norb_alu_32b_ssrl_14_outrs1), .InSelect(norb_std_5b_matcher_15_outaeqb),
    .Out32B(norb_std_32b_selector_15_out32b));
  Norb_STD_32B_Selector norb_std_32b_selector_16 (
    .In32B(norb_alu_32b_ssrl_15_outrs1), .InSelect(norb_std_5b_matcher_16_outaeqb),
    .Out32B(norb_std_32b_selector_16_out32b));
  Norb_STD_32B_Selector norb_std_32b_selector_17 (
    .In32B(norb_alu_32b_ssrl_16_outrs1), .InSelect(norb_std_5b_matcher_17_outaeqb),
    .Out32B(norb_std_32b_selector_17_out32b));
  Norb_STD_32B_Selector norb_std_32b_selector_18 (
    .In32B(norb_alu_32b_ssrl_17_outrs1), .InSelect(norb_std_5b_matcher_18_outaeqb),
    .Out32B(norb_std_32b_selector_18_out32b));
  Norb_STD_32B_Selector norb_std_32b_selector_19 (
    .In32B(norb_alu_32b_ssrl_18_outrs1), .InSelect(norb_std_5b_matcher_19_outaeqb),
    .Out32B(norb_std_32b_selector_19_out32b));
  Norb_STD_32B_Selector norb_std_32b_selector_20 (
    .In32B(norb_alu_32b_ssrl_19_outrs1), .InSelect(norb_std_5b_matcher_20_outaeqb),
    .Out32B(norb_std_32b_selector_20_out32b));
  Norb_STD_32B_Selector norb_std_32b_selector_21 (
    .In32B(norb_alu_32b_ssrl_20_outrs1), .InSelect(norb_std_5b_matcher_21_outaeqb),
    .Out32B(norb_std_32b_selector_21_out32b));
  Norb_STD_32B_Selector norb_std_32b_selector_22 (
    .In32B(norb_alu_32b_ssrl_21_outrs1), .InSelect(norb_std_5b_matcher_22_outaeqb),
    .Out32B(norb_std_32b_selector_22_out32b));
  Norb_STD_32B_Selector norb_std_32b_selector_23 (
    .In32B(norb_alu_32b_ssrl_22_outrs1), .InSelect(norb_std_5b_matcher_23_outaeqb),
    .Out32B(norb_std_32b_selector_23_out32b));
  Norb_STD_32B_Selector norb_std_32b_selector_24 (
    .In32B(norb_alu_32b_ssrl_23_outrs1), .InSelect(norb_std_5b_matcher_24_outaeqb),
    .Out32B(norb_std_32b_selector_24_out32b));
  Norb_STD_32B_Selector norb_std_32b_selector_25 (
    .In32B(norb_alu_32b_ssrl_24_outrs1), .InSelect(norb_std_5b_matcher_25_outaeqb),
    .Out32B(norb_std_32b_selector_25_out32b));
  Norb_STD_32B_Selector norb_std_32b_selector_26 (
    .In32B(norb_alu_32b_ssrl_25_outrs1), .InSelect(norb_std_5b_matcher_26_outaeqb),
    .Out32B(norb_std_32b_selector_26_out32b));
  Norb_STD_32B_Selector norb_std_32b_selector_27 (
    .In32B(norb_alu_32b_ssrl_26_outrs1), .InSelect(norb_std_5b_matcher_27_outaeqb),
    .Out32B(norb_std_32b_selector_27_out32b));
  Norb_STD_32B_Selector norb_std_32b_selector_28 (
    .In32B(norb_alu_32b_ssrl_27_outrs1), .InSelect(norb_std_5b_matcher_28_outaeqb),
    .Out32B(norb_std_32b_selector_28_out32b));
  Norb_STD_32B_Selector norb_std_32b_selector_29 (
    .In32B(norb_alu_32b_ssrl_28_outrs1), .InSelect(norb_std_5b_matcher_29_outaeqb),
    .Out32B(norb_std_32b_selector_29_out32b));
  Norb_STD_32B_Selector norb_std_32b_selector_30 (
    .In32B(norb_alu_32b_ssrl_29_outrs1), .InSelect(norb_std_5b_matcher_30_outaeqb),
    .Out32B(norb_std_32b_selector_30_out32b));
  Norb_STD_32B_Selector norb_std_32b_selector_31 (
    .In32B(norb_alu_32b_ssrl_30_outrs1), .InSelect(norb_std_5b_matcher_31_outaeqb),
    .Out32B(norb_std_32b_selector_31_out32b));
  Norb_STD_32B_Selector norb_std_32b_selector_32 (
    .In32B(norb_alu_32b_ssrl_31_outrs1), .InSelect(norb_std_5b_matcher_32_outaeqb),
    .Out32B(norb_std_32b_selector_32_out32b));
  assign OutShifted = norb_std_32b_selector_1_out32b | norb_std_32b_selector_2_out32b | norb_std_32b_selector_3_out32b | norb_std_32b_selector_4_out32b | norb_std_32b_selector_5_out32b | norb_std_32b_selector_6_out32b | norb_std_32b_selector_7_out32b | norb_std_32b_selector_8_out32b | norb_std_32b_selector_9_out32b | norb_std_32b_selector_10_out32b | norb_std_32b_selector_11_out32b | norb_std_32b_selector_12_out32b | norb_std_32b_selector_13_out32b | norb_std_32b_selector_14_out32b | norb_std_32b_selector_15_out32b | norb_std_32b_selector_16_out32b | norb_std_32b_selector_17_out32b | norb_std_32b_selector_18_out32b | norb_std_32b_selector_19_out32b | norb_std_32b_selector_20_out32b | norb_std_32b_selector_21_out32b | norb_std_32b_selector_22_out32b | norb_std_32b_selector_23_out32b | norb_std_32b_selector_24_out32b | norb_std_32b_selector_25_out32b | norb_std_32b_selector_26_out32b | norb_std_32b_selector_27_out32b | norb_std_32b_selector_28_out32b | norb_std_32b_selector_29_out32b | norb_std_32b_selector_30_out32b | norb_std_32b_selector_31_out32b | norb_std_32b_selector_32_out32b;  // OR_Gate or_1, 32 bits wide

  // Notes on the sheet:
  //   SRL: Shift Right Logical Unit
endmodule

module Norb_ALU_32B_SSRA (
  input  [31:0] InNum,
  output [31:0] OutLS1
);


  assign OutLS1 = {{2{InNum[31]}}, InNum[30:1]};

  // Notes on the sheet:
  //   SSRA: Single Shift Right Arithmetic Unit
endmodule

module Norb_ALU_32B_SRA (
  input  [4:0] InShamt,
  input  [31:0] InNum,
  output [31:0] OutShifted
);

  wire norb_std_5b_matcher_1_outaeqb, norb_std_5b_matcher_2_outaeqb, norb_std_5b_matcher_3_outaeqb,
       norb_std_5b_matcher_4_outaeqb, norb_std_5b_matcher_5_outaeqb, norb_std_5b_matcher_6_outaeqb,
       norb_std_5b_matcher_7_outaeqb, norb_std_5b_matcher_8_outaeqb, norb_std_5b_matcher_9_outaeqb,
       norb_std_5b_matcher_10_outaeqb, norb_std_5b_matcher_11_outaeqb, norb_std_5b_matcher_12_outaeqb,
       norb_std_5b_matcher_13_outaeqb, norb_std_5b_matcher_14_outaeqb, norb_std_5b_matcher_15_outaeqb,
       norb_std_5b_matcher_16_outaeqb, norb_std_5b_matcher_17_outaeqb, norb_std_5b_matcher_18_outaeqb,
       norb_std_5b_matcher_19_outaeqb, norb_std_5b_matcher_20_outaeqb, norb_std_5b_matcher_21_outaeqb,
       norb_std_5b_matcher_22_outaeqb, norb_std_5b_matcher_23_outaeqb, norb_std_5b_matcher_24_outaeqb,
       norb_std_5b_matcher_25_outaeqb, norb_std_5b_matcher_26_outaeqb, norb_std_5b_matcher_27_outaeqb,
       norb_std_5b_matcher_28_outaeqb, norb_std_5b_matcher_29_outaeqb, norb_std_5b_matcher_30_outaeqb,
       norb_std_5b_matcher_31_outaeqb, norb_std_5b_matcher_32_outaeqb;
  wire [31:0] norb_alu_32b_ssra_1_outls1, norb_alu_32b_ssra_2_outls1, norb_alu_32b_ssra_3_outls1,
       norb_alu_32b_ssra_4_outls1, norb_alu_32b_ssra_5_outls1, norb_alu_32b_ssra_6_outls1,
       norb_alu_32b_ssra_7_outls1, norb_alu_32b_ssra_8_outls1, norb_alu_32b_ssra_9_outls1,
       norb_alu_32b_ssra_10_outls1, norb_alu_32b_ssra_11_outls1, norb_alu_32b_ssra_12_outls1,
       norb_alu_32b_ssra_13_outls1, norb_alu_32b_ssra_14_outls1, norb_alu_32b_ssra_15_outls1,
       norb_alu_32b_ssra_16_outls1, norb_alu_32b_ssra_17_outls1, norb_alu_32b_ssra_18_outls1,
       norb_alu_32b_ssra_19_outls1, norb_alu_32b_ssra_20_outls1, norb_alu_32b_ssra_21_outls1,
       norb_alu_32b_ssra_22_outls1, norb_alu_32b_ssra_23_outls1, norb_alu_32b_ssra_24_outls1,
       norb_alu_32b_ssra_25_outls1, norb_alu_32b_ssra_26_outls1, norb_alu_32b_ssra_27_outls1,
       norb_alu_32b_ssra_28_outls1, norb_alu_32b_ssra_29_outls1, norb_alu_32b_ssra_30_outls1,
       norb_alu_32b_ssra_31_outls1, norb_std_32b_selector_1_out32b, norb_std_32b_selector_2_out32b,
       norb_std_32b_selector_3_out32b, norb_std_32b_selector_4_out32b, norb_std_32b_selector_5_out32b,
       norb_std_32b_selector_6_out32b, norb_std_32b_selector_7_out32b, norb_std_32b_selector_8_out32b,
       norb_std_32b_selector_9_out32b, norb_std_32b_selector_10_out32b, norb_std_32b_selector_11_out32b,
       norb_std_32b_selector_12_out32b, norb_std_32b_selector_13_out32b, norb_std_32b_selector_14_out32b,
       norb_std_32b_selector_15_out32b, norb_std_32b_selector_16_out32b, norb_std_32b_selector_17_out32b,
       norb_std_32b_selector_18_out32b, norb_std_32b_selector_19_out32b, norb_std_32b_selector_20_out32b,
       norb_std_32b_selector_21_out32b, norb_std_32b_selector_22_out32b, norb_std_32b_selector_23_out32b,
       norb_std_32b_selector_24_out32b, norb_std_32b_selector_25_out32b, norb_std_32b_selector_26_out32b,
       norb_std_32b_selector_27_out32b, norb_std_32b_selector_28_out32b, norb_std_32b_selector_29_out32b,
       norb_std_32b_selector_30_out32b, norb_std_32b_selector_31_out32b, norb_std_32b_selector_32_out32b;

  Norb_ALU_32B_SSRA norb_alu_32b_ssra_1 (.InNum(InNum), .OutLS1(norb_alu_32b_ssra_1_outls1));
  Norb_ALU_32B_SSRA norb_alu_32b_ssra_2 (.InNum(norb_alu_32b_ssra_1_outls1), .OutLS1(norb_alu_32b_ssra_2_outls1));
  Norb_ALU_32B_SSRA norb_alu_32b_ssra_3 (.InNum(norb_alu_32b_ssra_2_outls1), .OutLS1(norb_alu_32b_ssra_3_outls1));
  Norb_ALU_32B_SSRA norb_alu_32b_ssra_4 (.InNum(norb_alu_32b_ssra_3_outls1), .OutLS1(norb_alu_32b_ssra_4_outls1));
  Norb_ALU_32B_SSRA norb_alu_32b_ssra_5 (.InNum(norb_alu_32b_ssra_4_outls1), .OutLS1(norb_alu_32b_ssra_5_outls1));
  Norb_ALU_32B_SSRA norb_alu_32b_ssra_6 (.InNum(norb_alu_32b_ssra_5_outls1), .OutLS1(norb_alu_32b_ssra_6_outls1));
  Norb_ALU_32B_SSRA norb_alu_32b_ssra_7 (.InNum(norb_alu_32b_ssra_6_outls1), .OutLS1(norb_alu_32b_ssra_7_outls1));
  Norb_ALU_32B_SSRA norb_alu_32b_ssra_8 (.InNum(norb_alu_32b_ssra_7_outls1), .OutLS1(norb_alu_32b_ssra_8_outls1));
  Norb_ALU_32B_SSRA norb_alu_32b_ssra_9 (.InNum(norb_alu_32b_ssra_8_outls1), .OutLS1(norb_alu_32b_ssra_9_outls1));
  Norb_ALU_32B_SSRA norb_alu_32b_ssra_10 (.InNum(norb_alu_32b_ssra_9_outls1), .OutLS1(norb_alu_32b_ssra_10_outls1));
  Norb_ALU_32B_SSRA norb_alu_32b_ssra_11 (.InNum(norb_alu_32b_ssra_10_outls1), .OutLS1(norb_alu_32b_ssra_11_outls1));
  Norb_ALU_32B_SSRA norb_alu_32b_ssra_12 (.InNum(norb_alu_32b_ssra_11_outls1), .OutLS1(norb_alu_32b_ssra_12_outls1));
  Norb_ALU_32B_SSRA norb_alu_32b_ssra_13 (.InNum(norb_alu_32b_ssra_12_outls1), .OutLS1(norb_alu_32b_ssra_13_outls1));
  Norb_ALU_32B_SSRA norb_alu_32b_ssra_14 (.InNum(norb_alu_32b_ssra_13_outls1), .OutLS1(norb_alu_32b_ssra_14_outls1));
  Norb_ALU_32B_SSRA norb_alu_32b_ssra_15 (.InNum(norb_alu_32b_ssra_14_outls1), .OutLS1(norb_alu_32b_ssra_15_outls1));
  Norb_ALU_32B_SSRA norb_alu_32b_ssra_16 (.InNum(norb_alu_32b_ssra_15_outls1), .OutLS1(norb_alu_32b_ssra_16_outls1));
  Norb_ALU_32B_SSRA norb_alu_32b_ssra_17 (.InNum(norb_alu_32b_ssra_16_outls1), .OutLS1(norb_alu_32b_ssra_17_outls1));
  Norb_ALU_32B_SSRA norb_alu_32b_ssra_18 (.InNum(norb_alu_32b_ssra_17_outls1), .OutLS1(norb_alu_32b_ssra_18_outls1));
  Norb_ALU_32B_SSRA norb_alu_32b_ssra_19 (.InNum(norb_alu_32b_ssra_18_outls1), .OutLS1(norb_alu_32b_ssra_19_outls1));
  Norb_ALU_32B_SSRA norb_alu_32b_ssra_20 (.InNum(norb_alu_32b_ssra_19_outls1), .OutLS1(norb_alu_32b_ssra_20_outls1));
  Norb_ALU_32B_SSRA norb_alu_32b_ssra_21 (.InNum(norb_alu_32b_ssra_20_outls1), .OutLS1(norb_alu_32b_ssra_21_outls1));
  Norb_ALU_32B_SSRA norb_alu_32b_ssra_22 (.InNum(norb_alu_32b_ssra_21_outls1), .OutLS1(norb_alu_32b_ssra_22_outls1));
  Norb_ALU_32B_SSRA norb_alu_32b_ssra_23 (.InNum(norb_alu_32b_ssra_22_outls1), .OutLS1(norb_alu_32b_ssra_23_outls1));
  Norb_ALU_32B_SSRA norb_alu_32b_ssra_24 (.InNum(norb_alu_32b_ssra_23_outls1), .OutLS1(norb_alu_32b_ssra_24_outls1));
  Norb_ALU_32B_SSRA norb_alu_32b_ssra_25 (.InNum(norb_alu_32b_ssra_24_outls1), .OutLS1(norb_alu_32b_ssra_25_outls1));
  Norb_ALU_32B_SSRA norb_alu_32b_ssra_26 (.InNum(norb_alu_32b_ssra_25_outls1), .OutLS1(norb_alu_32b_ssra_26_outls1));
  Norb_ALU_32B_SSRA norb_alu_32b_ssra_27 (.InNum(norb_alu_32b_ssra_26_outls1), .OutLS1(norb_alu_32b_ssra_27_outls1));
  Norb_ALU_32B_SSRA norb_alu_32b_ssra_28 (.InNum(norb_alu_32b_ssra_27_outls1), .OutLS1(norb_alu_32b_ssra_28_outls1));
  Norb_ALU_32B_SSRA norb_alu_32b_ssra_29 (.InNum(norb_alu_32b_ssra_28_outls1), .OutLS1(norb_alu_32b_ssra_29_outls1));
  Norb_ALU_32B_SSRA norb_alu_32b_ssra_30 (.InNum(norb_alu_32b_ssra_29_outls1), .OutLS1(norb_alu_32b_ssra_30_outls1));
  Norb_ALU_32B_SSRA norb_alu_32b_ssra_31 (.InNum(norb_alu_32b_ssra_30_outls1), .OutLS1(norb_alu_32b_ssra_31_outls1));
  Norb_STD_5B_Matcher norb_std_5b_matcher_1 (
    .In8B_A(InShamt), .In8B_B({5{1'b0}}), .OutAEqB(norb_std_5b_matcher_1_outaeqb));
  Norb_STD_5B_Matcher norb_std_5b_matcher_2 (
    .In8B_A(InShamt), .In8B_B(5'b00001), .OutAEqB(norb_std_5b_matcher_2_outaeqb));
  Norb_STD_5B_Matcher norb_std_5b_matcher_3 (
    .In8B_A(InShamt), .In8B_B(5'b00010), .OutAEqB(norb_std_5b_matcher_3_outaeqb));
  Norb_STD_5B_Matcher norb_std_5b_matcher_4 (
    .In8B_A(InShamt), .In8B_B(5'b00011), .OutAEqB(norb_std_5b_matcher_4_outaeqb));
  Norb_STD_5B_Matcher norb_std_5b_matcher_5 (
    .In8B_A(InShamt), .In8B_B(5'b00100), .OutAEqB(norb_std_5b_matcher_5_outaeqb));
  Norb_STD_5B_Matcher norb_std_5b_matcher_6 (
    .In8B_A(InShamt), .In8B_B(5'b00101), .OutAEqB(norb_std_5b_matcher_6_outaeqb));
  Norb_STD_5B_Matcher norb_std_5b_matcher_7 (
    .In8B_A(InShamt), .In8B_B(5'b00110), .OutAEqB(norb_std_5b_matcher_7_outaeqb));
  Norb_STD_5B_Matcher norb_std_5b_matcher_8 (
    .In8B_A(InShamt), .In8B_B(5'b00111), .OutAEqB(norb_std_5b_matcher_8_outaeqb));
  Norb_STD_5B_Matcher norb_std_5b_matcher_9 (
    .In8B_A(InShamt), .In8B_B(5'b01000), .OutAEqB(norb_std_5b_matcher_9_outaeqb));
  Norb_STD_5B_Matcher norb_std_5b_matcher_10 (
    .In8B_A(InShamt), .In8B_B(5'b01001), .OutAEqB(norb_std_5b_matcher_10_outaeqb));
  Norb_STD_5B_Matcher norb_std_5b_matcher_11 (
    .In8B_A(InShamt), .In8B_B(5'b01010), .OutAEqB(norb_std_5b_matcher_11_outaeqb));
  Norb_STD_5B_Matcher norb_std_5b_matcher_12 (
    .In8B_A(InShamt), .In8B_B(5'b01011), .OutAEqB(norb_std_5b_matcher_12_outaeqb));
  Norb_STD_5B_Matcher norb_std_5b_matcher_13 (
    .In8B_A(InShamt), .In8B_B(5'b01100), .OutAEqB(norb_std_5b_matcher_13_outaeqb));
  Norb_STD_5B_Matcher norb_std_5b_matcher_14 (
    .In8B_A(InShamt), .In8B_B(5'b01101), .OutAEqB(norb_std_5b_matcher_14_outaeqb));
  Norb_STD_5B_Matcher norb_std_5b_matcher_15 (
    .In8B_A(InShamt), .In8B_B(5'b01110), .OutAEqB(norb_std_5b_matcher_15_outaeqb));
  Norb_STD_5B_Matcher norb_std_5b_matcher_16 (
    .In8B_A(InShamt), .In8B_B(5'b01111), .OutAEqB(norb_std_5b_matcher_16_outaeqb));
  Norb_STD_5B_Matcher norb_std_5b_matcher_17 (
    .In8B_A(InShamt), .In8B_B(5'b01011), .OutAEqB(norb_std_5b_matcher_17_outaeqb));
  Norb_STD_5B_Matcher norb_std_5b_matcher_18 (
    .In8B_A(InShamt), .In8B_B(5'b00001), .OutAEqB(norb_std_5b_matcher_18_outaeqb));
  Norb_STD_5B_Matcher norb_std_5b_matcher_19 (
    .In8B_A(InShamt), .In8B_B(5'b01111), .OutAEqB(norb_std_5b_matcher_19_outaeqb));
  Norb_STD_5B_Matcher norb_std_5b_matcher_20 (
    .In8B_A(InShamt), .In8B_B(5'b10000), .OutAEqB(norb_std_5b_matcher_20_outaeqb));
  Norb_STD_5B_Matcher norb_std_5b_matcher_21 (
    .In8B_A(InShamt), .In8B_B(5'b10001), .OutAEqB(norb_std_5b_matcher_21_outaeqb));
  Norb_STD_5B_Matcher norb_std_5b_matcher_22 (
    .In8B_A(InShamt), .In8B_B(5'b10010), .OutAEqB(norb_std_5b_matcher_22_outaeqb));
  Norb_STD_5B_Matcher norb_std_5b_matcher_23 (
    .In8B_A(InShamt), .In8B_B(5'b10011), .OutAEqB(norb_std_5b_matcher_23_outaeqb));
  Norb_STD_5B_Matcher norb_std_5b_matcher_24 (
    .In8B_A(InShamt), .In8B_B(5'b10100), .OutAEqB(norb_std_5b_matcher_24_outaeqb));
  Norb_STD_5B_Matcher norb_std_5b_matcher_25 (
    .In8B_A(InShamt), .In8B_B(5'b10101), .OutAEqB(norb_std_5b_matcher_25_outaeqb));
  Norb_STD_5B_Matcher norb_std_5b_matcher_26 (
    .In8B_A(InShamt), .In8B_B(5'b10110), .OutAEqB(norb_std_5b_matcher_26_outaeqb));
  Norb_STD_5B_Matcher norb_std_5b_matcher_27 (
    .In8B_A(InShamt), .In8B_B(5'b10111), .OutAEqB(norb_std_5b_matcher_27_outaeqb));
  Norb_STD_5B_Matcher norb_std_5b_matcher_28 (
    .In8B_A(InShamt), .In8B_B(5'b11000), .OutAEqB(norb_std_5b_matcher_28_outaeqb));
  Norb_STD_5B_Matcher norb_std_5b_matcher_29 (
    .In8B_A(InShamt), .In8B_B(5'b11001), .OutAEqB(norb_std_5b_matcher_29_outaeqb));
  Norb_STD_5B_Matcher norb_std_5b_matcher_30 (
    .In8B_A(InShamt), .In8B_B(5'b11010), .OutAEqB(norb_std_5b_matcher_30_outaeqb));
  Norb_STD_5B_Matcher norb_std_5b_matcher_31 (
    .In8B_A(InShamt), .In8B_B(5'b11011), .OutAEqB(norb_std_5b_matcher_31_outaeqb));
  Norb_STD_5B_Matcher norb_std_5b_matcher_32 (
    .In8B_A(InShamt), .In8B_B(5'b11100), .OutAEqB(norb_std_5b_matcher_32_outaeqb));
  Norb_STD_32B_Selector norb_std_32b_selector_1 (
    .In32B(InNum), .InSelect(norb_std_5b_matcher_1_outaeqb), .Out32B(norb_std_32b_selector_1_out32b));
  Norb_STD_32B_Selector norb_std_32b_selector_2 (
    .In32B(norb_alu_32b_ssra_1_outls1), .InSelect(norb_std_5b_matcher_2_outaeqb),
    .Out32B(norb_std_32b_selector_2_out32b));
  Norb_STD_32B_Selector norb_std_32b_selector_3 (
    .In32B(norb_alu_32b_ssra_2_outls1), .InSelect(norb_std_5b_matcher_3_outaeqb),
    .Out32B(norb_std_32b_selector_3_out32b));
  Norb_STD_32B_Selector norb_std_32b_selector_4 (
    .In32B(norb_alu_32b_ssra_3_outls1), .InSelect(norb_std_5b_matcher_4_outaeqb),
    .Out32B(norb_std_32b_selector_4_out32b));
  Norb_STD_32B_Selector norb_std_32b_selector_5 (
    .In32B(norb_alu_32b_ssra_4_outls1), .InSelect(norb_std_5b_matcher_5_outaeqb),
    .Out32B(norb_std_32b_selector_5_out32b));
  Norb_STD_32B_Selector norb_std_32b_selector_6 (
    .In32B(norb_alu_32b_ssra_5_outls1), .InSelect(norb_std_5b_matcher_6_outaeqb),
    .Out32B(norb_std_32b_selector_6_out32b));
  Norb_STD_32B_Selector norb_std_32b_selector_7 (
    .In32B(norb_alu_32b_ssra_6_outls1), .InSelect(norb_std_5b_matcher_7_outaeqb),
    .Out32B(norb_std_32b_selector_7_out32b));
  Norb_STD_32B_Selector norb_std_32b_selector_8 (
    .In32B(norb_alu_32b_ssra_7_outls1), .InSelect(norb_std_5b_matcher_8_outaeqb),
    .Out32B(norb_std_32b_selector_8_out32b));
  Norb_STD_32B_Selector norb_std_32b_selector_9 (
    .In32B(norb_alu_32b_ssra_8_outls1), .InSelect(norb_std_5b_matcher_9_outaeqb),
    .Out32B(norb_std_32b_selector_9_out32b));
  Norb_STD_32B_Selector norb_std_32b_selector_10 (
    .In32B(norb_alu_32b_ssra_9_outls1), .InSelect(norb_std_5b_matcher_10_outaeqb),
    .Out32B(norb_std_32b_selector_10_out32b));
  Norb_STD_32B_Selector norb_std_32b_selector_11 (
    .In32B(norb_alu_32b_ssra_10_outls1), .InSelect(norb_std_5b_matcher_11_outaeqb),
    .Out32B(norb_std_32b_selector_11_out32b));
  Norb_STD_32B_Selector norb_std_32b_selector_12 (
    .In32B(norb_alu_32b_ssra_11_outls1), .InSelect(norb_std_5b_matcher_12_outaeqb),
    .Out32B(norb_std_32b_selector_12_out32b));
  Norb_STD_32B_Selector norb_std_32b_selector_13 (
    .In32B(norb_alu_32b_ssra_12_outls1), .InSelect(norb_std_5b_matcher_13_outaeqb),
    .Out32B(norb_std_32b_selector_13_out32b));
  Norb_STD_32B_Selector norb_std_32b_selector_14 (
    .In32B(norb_alu_32b_ssra_13_outls1), .InSelect(norb_std_5b_matcher_14_outaeqb),
    .Out32B(norb_std_32b_selector_14_out32b));
  Norb_STD_32B_Selector norb_std_32b_selector_15 (
    .In32B(norb_alu_32b_ssra_14_outls1), .InSelect(norb_std_5b_matcher_15_outaeqb),
    .Out32B(norb_std_32b_selector_15_out32b));
  Norb_STD_32B_Selector norb_std_32b_selector_16 (
    .In32B(norb_alu_32b_ssra_15_outls1), .InSelect(norb_std_5b_matcher_16_outaeqb),
    .Out32B(norb_std_32b_selector_16_out32b));
  Norb_STD_32B_Selector norb_std_32b_selector_17 (
    .In32B(norb_alu_32b_ssra_16_outls1), .InSelect(norb_std_5b_matcher_17_outaeqb),
    .Out32B(norb_std_32b_selector_17_out32b));
  Norb_STD_32B_Selector norb_std_32b_selector_18 (
    .In32B(norb_alu_32b_ssra_17_outls1), .InSelect(norb_std_5b_matcher_18_outaeqb),
    .Out32B(norb_std_32b_selector_18_out32b));
  Norb_STD_32B_Selector norb_std_32b_selector_19 (
    .In32B(norb_alu_32b_ssra_18_outls1), .InSelect(norb_std_5b_matcher_19_outaeqb),
    .Out32B(norb_std_32b_selector_19_out32b));
  Norb_STD_32B_Selector norb_std_32b_selector_20 (
    .In32B(norb_alu_32b_ssra_19_outls1), .InSelect(norb_std_5b_matcher_20_outaeqb),
    .Out32B(norb_std_32b_selector_20_out32b));
  Norb_STD_32B_Selector norb_std_32b_selector_21 (
    .In32B(norb_alu_32b_ssra_20_outls1), .InSelect(norb_std_5b_matcher_21_outaeqb),
    .Out32B(norb_std_32b_selector_21_out32b));
  Norb_STD_32B_Selector norb_std_32b_selector_22 (
    .In32B(norb_alu_32b_ssra_21_outls1), .InSelect(norb_std_5b_matcher_22_outaeqb),
    .Out32B(norb_std_32b_selector_22_out32b));
  Norb_STD_32B_Selector norb_std_32b_selector_23 (
    .In32B(norb_alu_32b_ssra_22_outls1), .InSelect(norb_std_5b_matcher_23_outaeqb),
    .Out32B(norb_std_32b_selector_23_out32b));
  Norb_STD_32B_Selector norb_std_32b_selector_24 (
    .In32B(norb_alu_32b_ssra_23_outls1), .InSelect(norb_std_5b_matcher_24_outaeqb),
    .Out32B(norb_std_32b_selector_24_out32b));
  Norb_STD_32B_Selector norb_std_32b_selector_25 (
    .In32B(norb_alu_32b_ssra_24_outls1), .InSelect(norb_std_5b_matcher_25_outaeqb),
    .Out32B(norb_std_32b_selector_25_out32b));
  Norb_STD_32B_Selector norb_std_32b_selector_26 (
    .In32B(norb_alu_32b_ssra_25_outls1), .InSelect(norb_std_5b_matcher_26_outaeqb),
    .Out32B(norb_std_32b_selector_26_out32b));
  Norb_STD_32B_Selector norb_std_32b_selector_27 (
    .In32B(norb_alu_32b_ssra_26_outls1), .InSelect(norb_std_5b_matcher_27_outaeqb),
    .Out32B(norb_std_32b_selector_27_out32b));
  Norb_STD_32B_Selector norb_std_32b_selector_28 (
    .In32B(norb_alu_32b_ssra_27_outls1), .InSelect(norb_std_5b_matcher_28_outaeqb),
    .Out32B(norb_std_32b_selector_28_out32b));
  Norb_STD_32B_Selector norb_std_32b_selector_29 (
    .In32B(norb_alu_32b_ssra_28_outls1), .InSelect(norb_std_5b_matcher_29_outaeqb),
    .Out32B(norb_std_32b_selector_29_out32b));
  Norb_STD_32B_Selector norb_std_32b_selector_30 (
    .In32B(norb_alu_32b_ssra_29_outls1), .InSelect(norb_std_5b_matcher_30_outaeqb),
    .Out32B(norb_std_32b_selector_30_out32b));
  Norb_STD_32B_Selector norb_std_32b_selector_31 (
    .In32B(norb_alu_32b_ssra_30_outls1), .InSelect(norb_std_5b_matcher_31_outaeqb),
    .Out32B(norb_std_32b_selector_31_out32b));
  Norb_STD_32B_Selector norb_std_32b_selector_32 (
    .In32B(norb_alu_32b_ssra_31_outls1), .InSelect(norb_std_5b_matcher_32_outaeqb),
    .Out32B(norb_std_32b_selector_32_out32b));
  assign OutShifted = norb_std_32b_selector_1_out32b | norb_std_32b_selector_2_out32b | norb_std_32b_selector_3_out32b | norb_std_32b_selector_4_out32b | norb_std_32b_selector_5_out32b | norb_std_32b_selector_6_out32b | norb_std_32b_selector_7_out32b | norb_std_32b_selector_8_out32b | norb_std_32b_selector_9_out32b | norb_std_32b_selector_10_out32b | norb_std_32b_selector_11_out32b | norb_std_32b_selector_12_out32b | norb_std_32b_selector_13_out32b | norb_std_32b_selector_14_out32b | norb_std_32b_selector_15_out32b | norb_std_32b_selector_16_out32b | norb_std_32b_selector_17_out32b | norb_std_32b_selector_18_out32b | norb_std_32b_selector_19_out32b | norb_std_32b_selector_20_out32b | norb_std_32b_selector_21_out32b | norb_std_32b_selector_22_out32b | norb_std_32b_selector_23_out32b | norb_std_32b_selector_24_out32b | norb_std_32b_selector_25_out32b | norb_std_32b_selector_26_out32b | norb_std_32b_selector_27_out32b | norb_std_32b_selector_28_out32b | norb_std_32b_selector_29_out32b | norb_std_32b_selector_30_out32b | norb_std_32b_selector_31_out32b | norb_std_32b_selector_32_out32b;  // OR_Gate or_1, 32 bits wide

  // Notes on the sheet:
  //   SRL: Shift Right Logical Unit
endmodule

module Norb_ALU_32B_BWL (
  input  [31:0] InA,
  input  [31:0] InB,
  output [31:0] OutAAndB,
  output [31:0] OutAOrB,
  output [31:0] OutAXorB
);

  assign OutAAndB = InA & InB;  // AND_Gate and_1, 32 bits wide
  assign OutAOrB = InA | InB;  // OR_Gate or_1, 32 bits wide
  assign OutAXorB = InA ^ InB;  // XOR_Gate xor_1, 32 bits wide

  // Notes on the sheet:
  //   BWL: Bitwise Logic Unit
endmodule

module Norb_ALU_32B_SLT (
  input  [31:0] InA,
  input  [31:0] InB,
  output [31:0] OutFlag
);

  wire [31:0] norb_alu_32b_crs_1_outasubtractb;

  Norb_ALU_32B_CRS norb_alu_32b_crs_1 (
    .InA(InA), .InB(InB), .OutASubtractB(norb_alu_32b_crs_1_outasubtractb));  // open: FlagOverflow
  Norb_STD_1B32B_Padder norb_std_1b32b_padder_1 (.In1B(norb_alu_32b_crs_1_outasubtractb[31]), .Out32B(OutFlag));

  // Notes on the sheet:
  //   SLT: Set Less Than Unit
endmodule

module Norb_ALU_1B_SLTU (
  input  InA,
  input  InB,
  input  InSuppress,
  output OutGreater,
  output OutEQ,
  output OutLess
);

  wire and_1_out, and_2_out, and_3_out, and_4_out, norb_std_1t2_decoder_1_out0, norb_std_1t2_decoder_1_out1,
       norb_std_1t2_decoder_2_out0, norb_std_1t2_decoder_2_out1, or_1_out;

  Norb_STD_1T2_Decoder norb_std_1t2_decoder_1 (
    .In1B(InA), .Out1(norb_std_1t2_decoder_1_out1), .Out0(norb_std_1t2_decoder_1_out0));
  Norb_STD_1T2_Decoder norb_std_1t2_decoder_2 (
    .In1B(InB), .Out1(norb_std_1t2_decoder_2_out1), .Out0(norb_std_1t2_decoder_2_out0));
  and and_1 (and_1_out, norb_std_1t2_decoder_1_out1, norb_std_1t2_decoder_2_out0);
  and and_2 (and_2_out, norb_std_1t2_decoder_1_out0, norb_std_1t2_decoder_2_out0);
  or or_1 (or_1_out, and_2_out, and_3_out);
  Multiplexer multiplexer_1 (.in0(and_1_out), .in1(1'b0), .out(OutGreater), .sel(InSuppress));
  and and_3 (and_3_out, norb_std_1t2_decoder_1_out1, norb_std_1t2_decoder_2_out1);
  and and_4 (and_4_out, norb_std_1t2_decoder_1_out0, norb_std_1t2_decoder_2_out1);
  Multiplexer multiplexer_2 (.in0(or_1_out), .in1(1'b0), .out(OutEQ), .sel(InSuppress));
  Multiplexer multiplexer_3 (.in0(and_4_out), .in1(1'b0), .out(OutLess), .sel(InSuppress));

  // Notes on the sheet:
  //   SLTU: Set Less Than Unsigned Unit
endmodule

module Norb_ALU_8B_SLTU (
  input  InSuppress,
  input  [7:0] InA,
  input  [7:0] InB,
  output OutLess,
  output OutEQ,
  output OutGreater
);

  wire and_1_out, norb_alu_1b_sltu_1_outeq, norb_alu_1b_sltu_1_outgreater, norb_alu_1b_sltu_1_outless,
       norb_alu_1b_sltu_2_outeq, norb_alu_1b_sltu_2_outgreater, norb_alu_1b_sltu_2_outless,
       norb_alu_1b_sltu_3_outeq, norb_alu_1b_sltu_3_outgreater, norb_alu_1b_sltu_3_outless,
       norb_alu_1b_sltu_4_outeq, norb_alu_1b_sltu_4_outgreater, norb_alu_1b_sltu_4_outless,
       norb_alu_1b_sltu_5_outeq, norb_alu_1b_sltu_5_outgreater, norb_alu_1b_sltu_5_outless,
       norb_alu_1b_sltu_6_outeq, norb_alu_1b_sltu_6_outgreater, norb_alu_1b_sltu_6_outless,
       norb_alu_1b_sltu_7_outeq, norb_alu_1b_sltu_7_outgreater, norb_alu_1b_sltu_7_outless,
       norb_alu_1b_sltu_8_outeq, norb_alu_1b_sltu_8_outgreater, norb_alu_1b_sltu_8_outless, not_1_out,
       not_2_out, not_3_out, not_4_out, not_5_out, not_6_out, not_7_out, or_1_out, or_2_out;

  Norb_ALU_1B_SLTU norb_alu_1b_sltu_1 (
    .InA(InA[7]), .InB(InB[7]), .InSuppress(1'b0), .OutGreater(norb_alu_1b_sltu_1_outgreater),
    .OutEQ(norb_alu_1b_sltu_1_outeq), .OutLess(norb_alu_1b_sltu_1_outless));
  not not_1 (not_1_out, norb_alu_1b_sltu_1_outeq);
  Multiplexer multiplexer_1 (.in0(or_1_out), .in1(1'b0), .out(OutLess), .sel(InSuppress));
  or or_1 (or_1_out, norb_alu_1b_sltu_1_outless, norb_alu_1b_sltu_2_outless, norb_alu_1b_sltu_3_outless, norb_alu_1b_sltu_4_outless, norb_alu_1b_sltu_5_outless, norb_alu_1b_sltu_6_outless, norb_alu_1b_sltu_7_outless, norb_alu_1b_sltu_8_outless);
  Multiplexer multiplexer_2 (.in0(and_1_out), .in1(1'b0), .out(OutEQ), .sel(InSuppress));
  and and_1 (and_1_out, norb_alu_1b_sltu_1_outeq, norb_alu_1b_sltu_2_outeq, norb_alu_1b_sltu_3_outeq, norb_alu_1b_sltu_4_outeq, norb_alu_1b_sltu_5_outeq, norb_alu_1b_sltu_6_outeq, norb_alu_1b_sltu_7_outeq, norb_alu_1b_sltu_8_outeq);
  Norb_ALU_1B_SLTU norb_alu_1b_sltu_2 (
    .InA(InA[6]), .InB(InB[6]), .InSuppress(not_1_out), .OutGreater(norb_alu_1b_sltu_2_outgreater),
    .OutEQ(norb_alu_1b_sltu_2_outeq), .OutLess(norb_alu_1b_sltu_2_outless));
  not not_2 (not_2_out, norb_alu_1b_sltu_2_outeq);
  Multiplexer multiplexer_3 (.in0(or_2_out), .in1(1'b0), .out(OutGreater), .sel(InSuppress));
  or or_2 (or_2_out, norb_alu_1b_sltu_1_outgreater, norb_alu_1b_sltu_2_outgreater, norb_alu_1b_sltu_3_outgreater, norb_alu_1b_sltu_4_outgreater, norb_alu_1b_sltu_5_outgreater, norb_alu_1b_sltu_6_outgreater, norb_alu_1b_sltu_7_outgreater, norb_alu_1b_sltu_8_outgreater);
  Norb_ALU_1B_SLTU norb_alu_1b_sltu_3 (
    .InA(InA[5]), .InB(InB[5]), .InSuppress(not_2_out), .OutGreater(norb_alu_1b_sltu_3_outgreater),
    .OutEQ(norb_alu_1b_sltu_3_outeq), .OutLess(norb_alu_1b_sltu_3_outless));
  not not_3 (not_3_out, norb_alu_1b_sltu_3_outeq);
  Norb_ALU_1B_SLTU norb_alu_1b_sltu_4 (
    .InA(InA[4]), .InB(InB[4]), .InSuppress(not_3_out), .OutGreater(norb_alu_1b_sltu_4_outgreater),
    .OutEQ(norb_alu_1b_sltu_4_outeq), .OutLess(norb_alu_1b_sltu_4_outless));
  not not_4 (not_4_out, norb_alu_1b_sltu_4_outeq);
  Norb_ALU_1B_SLTU norb_alu_1b_sltu_5 (
    .InA(InA[3]), .InB(InB[3]), .InSuppress(not_4_out), .OutGreater(norb_alu_1b_sltu_5_outgreater),
    .OutEQ(norb_alu_1b_sltu_5_outeq), .OutLess(norb_alu_1b_sltu_5_outless));
  not not_5 (not_5_out, norb_alu_1b_sltu_5_outeq);
  Norb_ALU_1B_SLTU norb_alu_1b_sltu_6 (
    .InA(InA[2]), .InB(InB[2]), .InSuppress(not_5_out), .OutGreater(norb_alu_1b_sltu_6_outgreater),
    .OutEQ(norb_alu_1b_sltu_6_outeq), .OutLess(norb_alu_1b_sltu_6_outless));
  not not_6 (not_6_out, norb_alu_1b_sltu_6_outeq);
  Norb_ALU_1B_SLTU norb_alu_1b_sltu_7 (
    .InA(InA[1]), .InB(InB[1]), .InSuppress(not_6_out), .OutGreater(norb_alu_1b_sltu_7_outgreater),
    .OutEQ(norb_alu_1b_sltu_7_outeq), .OutLess(norb_alu_1b_sltu_7_outless));
  not not_7 (not_7_out, norb_alu_1b_sltu_7_outeq);
  Norb_ALU_1B_SLTU norb_alu_1b_sltu_8 (
    .InA(InA[0]), .InB(InB[0]), .InSuppress(not_7_out), .OutGreater(norb_alu_1b_sltu_8_outgreater),
    .OutEQ(norb_alu_1b_sltu_8_outeq), .OutLess(norb_alu_1b_sltu_8_outless));

  // Notes on the sheet:
  //   SLTU: Set Less Than Unsigned Unit
endmodule

module Norb_ALU_32B_SLTU (
  input  [31:0] InA,
  input  [31:0] InB,
  output [31:0] OutSLTU
);

  wire LessThan_out, norb_alu_8b_sltu_1_outeq, norb_alu_8b_sltu_1_outgreater, norb_alu_8b_sltu_1_outless,
       norb_alu_8b_sltu_2_outeq, norb_alu_8b_sltu_2_outgreater, norb_alu_8b_sltu_2_outless,
       norb_alu_8b_sltu_3_outeq, norb_alu_8b_sltu_3_outgreater, norb_alu_8b_sltu_3_outless,
       norb_alu_8b_sltu_4_outeq, norb_alu_8b_sltu_4_outless, not_1_out, not_2_out, not_3_out;
  wire [7:0] norb_std_32b8b_splitter_1_out0, norb_std_32b8b_splitter_1_out1, norb_std_32b8b_splitter_1_out2,
       norb_std_32b8b_splitter_1_out3, norb_std_32b8b_splitter_2_out0, norb_std_32b8b_splitter_2_out1,
       norb_std_32b8b_splitter_2_out2, norb_std_32b8b_splitter_2_out3;

  Norb_STD_32B8B_Splitter norb_std_32b8b_splitter_1 (
    .In32B(InA), .Out0(norb_std_32b8b_splitter_1_out0), .Out1(norb_std_32b8b_splitter_1_out1),
    .Out2(norb_std_32b8b_splitter_1_out2), .Out3(norb_std_32b8b_splitter_1_out3));
  Norb_STD_32B8B_Splitter norb_std_32b8b_splitter_2 (
    .In32B(InB), .Out0(norb_std_32b8b_splitter_2_out0), .Out1(norb_std_32b8b_splitter_2_out1),
    .Out2(norb_std_32b8b_splitter_2_out2), .Out3(norb_std_32b8b_splitter_2_out3));
  Norb_ALU_8B_SLTU norb_alu_8b_sltu_1 (
    .InSuppress(1'b0), .InA(norb_std_32b8b_splitter_1_out3), .InB(norb_std_32b8b_splitter_2_out3),
    .OutLess(norb_alu_8b_sltu_1_outless), .OutEQ(norb_alu_8b_sltu_1_outeq),
    .OutGreater(norb_alu_8b_sltu_1_outgreater));
  not not_1 (not_1_out, norb_alu_8b_sltu_1_outeq);
  or LessThan (LessThan_out, norb_alu_8b_sltu_1_outless, norb_alu_8b_sltu_2_outless, norb_alu_8b_sltu_3_outless, norb_alu_8b_sltu_4_outless);
  // AND_Gate and_1 has open pins: in0=norb_alu_8b_sltu_1_outeq, in1=norb_alu_8b_sltu_2_outeq, in2=norb_alu_8b_sltu_3_outeq, in3=norb_alu_8b_sltu_4_outeq, out=open
  // OR_Gate or_1 has open pins: in0=norb_alu_8b_sltu_1_outgreater, in1=norb_alu_8b_sltu_2_outgreater, in2=norb_alu_8b_sltu_3_outgreater, in3=norb_alu_8b_sltu_3_outgreater, out=open
  Norb_ALU_8B_SLTU norb_alu_8b_sltu_2 (
    .InSuppress(not_1_out), .InA(norb_std_32b8b_splitter_1_out2), .InB(norb_std_32b8b_splitter_2_out2),
    .OutLess(norb_alu_8b_sltu_2_outless), .OutEQ(norb_alu_8b_sltu_2_outeq),
    .OutGreater(norb_alu_8b_sltu_2_outgreater));
  not not_2 (not_2_out, norb_alu_8b_sltu_2_outeq);
  Norb_STD_1B32B_Padder norb_std_1b32b_padder_1 (.In1B(LessThan_out), .Out32B(OutSLTU));
  Norb_ALU_8B_SLTU norb_alu_8b_sltu_3 (
    .InSuppress(not_2_out), .InA(norb_std_32b8b_splitter_1_out1), .InB(norb_std_32b8b_splitter_2_out1),
    .OutLess(norb_alu_8b_sltu_3_outless), .OutEQ(norb_alu_8b_sltu_3_outeq),
    .OutGreater(norb_alu_8b_sltu_3_outgreater));
  not not_3 (not_3_out, norb_alu_8b_sltu_3_outeq);
  Norb_ALU_8B_SLTU norb_alu_8b_sltu_4 (
    .InSuppress(not_3_out), .InA(norb_std_32b8b_splitter_1_out0), .InB(norb_std_32b8b_splitter_2_out0),
    .OutLess(norb_alu_8b_sltu_4_outless), .OutEQ(norb_alu_8b_sltu_4_outeq),
    .OutGreater(norb_alu_8b_sltu_3_outgreater));

  // Notes on the sheet:
  //   SLTU: Set Less Than Unsigned Unit
endmodule

module Norb_STD_8B_Selector (
  input  [7:0] In8B,
  input  InSelect,
  output [7:0] OutResult
);

  and and_1 (OutResult[7], InSelect, In8B[7]);
  and and_2 (OutResult[6], InSelect, In8B[6]);
  and and_3 (OutResult[5], InSelect, In8B[5]);
  and and_4 (OutResult[4], InSelect, In8B[4]);
  and and_5 (OutResult[3], InSelect, In8B[3]);
  and and_6 (OutResult[2], InSelect, In8B[2]);
  and and_7 (OutResult[1], InSelect, In8B[1]);
  and and_8 (OutResult[0], InSelect, In8B[0]);
endmodule

module Norb_STD_32B_Selector (
  input  [31:0] In32B,
  input  InSelect,
  output [31:0] Out32B
);

  wire [7:0] norb_std_8b_selector_1_outresult, norb_std_8b_selector_2_outresult,
       norb_std_8b_selector_3_outresult, norb_std_8b_selector_4_outresult, norb_std_32b8b_splitter_1_out0,
       norb_std_32b8b_splitter_1_out1, norb_std_32b8b_splitter_1_out2, norb_std_32b8b_splitter_1_out3;

  Norb_STD_32B8B_Splitter norb_std_32b8b_splitter_1 (
    .In32B(In32B), .Out0(norb_std_32b8b_splitter_1_out0), .Out1(norb_std_32b8b_splitter_1_out1),
    .Out2(norb_std_32b8b_splitter_1_out2), .Out3(norb_std_32b8b_splitter_1_out3));
  Norb_STD_8B_Selector norb_std_8b_selector_1 (
    .In8B(norb_std_32b8b_splitter_1_out0), .InSelect(InSelect), .OutResult(norb_std_8b_selector_1_outresult));
  Norb_STD_8B_Selector norb_std_8b_selector_2 (
    .In8B(norb_std_32b8b_splitter_1_out1), .InSelect(InSelect), .OutResult(norb_std_8b_selector_2_outresult));
  Norb_STD_8B_Selector norb_std_8b_selector_3 (
    .In8B(norb_std_32b8b_splitter_1_out2), .InSelect(InSelect), .OutResult(norb_std_8b_selector_3_outresult));
  Norb_STD_8B_Selector norb_std_8b_selector_4 (
    .In8B(norb_std_32b8b_splitter_1_out3), .InSelect(InSelect), .OutResult(norb_std_8b_selector_4_outresult));
  Norb_STD_8B32B_Splitter norb_std_8b32b_splitter_1 (
    .In0(norb_std_8b_selector_1_outresult), .In1(norb_std_8b_selector_2_outresult),
    .In2(norb_std_8b_selector_3_outresult), .In3(norb_std_8b_selector_4_outresult), .Out32B(Out32B));
endmodule

module Norb_STD_1T2_Decoder (
  input  In1B,
  output Out1,
  output Out0
);

  not not_1 (Out0, In1B);

  assign Out1 = In1B;
endmodule

module Norb_STD_2T4_Decoder (
  input  [1:0] In2B,
  output Out3,
  output Out2,
  output Out1,
  output Out0
);

  wire norb_std_1t2_decoder_1_out0, norb_std_1t2_decoder_1_out1, norb_std_1t2_decoder_2_out0,
       norb_std_1t2_decoder_2_out1, not_1_out;

  Norb_STD_1T2_Decoder norb_std_1t2_decoder_1 (
    .In1B(In2B[0]), .Out1(norb_std_1t2_decoder_1_out1), .Out0(norb_std_1t2_decoder_1_out0));
  Norb_STD_1T2_Decoder norb_std_1t2_decoder_2 (
    .In1B(In2B[0]), .Out1(norb_std_1t2_decoder_2_out1), .Out0(norb_std_1t2_decoder_2_out0));
  and and_1 (Out3, In2B[1], norb_std_1t2_decoder_1_out1);
  and and_2 (Out2, norb_std_1t2_decoder_1_out0, In2B[1]);
  not not_1 (not_1_out, In2B[1]);
  and and_3 (Out1, not_1_out, norb_std_1t2_decoder_2_out1);
  and and_4 (Out0, norb_std_1t2_decoder_2_out0, not_1_out);
endmodule

module Norb_STD_3T8_Decoder (
  input  [2:0] In3B,
  output Out4,
  output Out5,
  output Out6,
  output Out7,
  output Out0,
  output Out1,
  output Out2,
  output Out3
);

  wire norb_std_2t4_decoder_1_out0, norb_std_2t4_decoder_1_out1, norb_std_2t4_decoder_1_out2,
       norb_std_2t4_decoder_1_out3, norb_std_2t4_decoder_2_out0, norb_std_2t4_decoder_2_out1,
       norb_std_2t4_decoder_2_out2, norb_std_2t4_decoder_2_out3, not_1_out;

  Norb_STD_2T4_Decoder norb_std_2t4_decoder_1 (
    .In2B(In3B[1:0]), .Out3(norb_std_2t4_decoder_1_out3), .Out2(norb_std_2t4_decoder_1_out2),
    .Out1(norb_std_2t4_decoder_1_out1), .Out0(norb_std_2t4_decoder_1_out0));
  Norb_STD_2T4_Decoder norb_std_2t4_decoder_2 (
    .In2B(In3B[1:0]), .Out3(norb_std_2t4_decoder_2_out3), .Out2(norb_std_2t4_decoder_2_out2),
    .Out1(norb_std_2t4_decoder_2_out1), .Out0(norb_std_2t4_decoder_2_out0));
  and and_1 (Out4, In3B[2], norb_std_2t4_decoder_1_out0);
  and and_2 (Out5, In3B[2], norb_std_2t4_decoder_1_out1);
  not not_1 (not_1_out, In3B[2]);
  and and_3 (Out0, not_1_out, norb_std_2t4_decoder_2_out0);
  and and_4 (Out1, not_1_out, norb_std_2t4_decoder_2_out1);
  and and_5 (Out6, In3B[2], norb_std_2t4_decoder_1_out2);
  and and_6 (Out7, In3B[2], norb_std_2t4_decoder_1_out3);
  and and_7 (Out2, not_1_out, norb_std_2t4_decoder_2_out2);
  and and_8 (Out3, not_1_out, norb_std_2t4_decoder_2_out3);
endmodule

module Norb_STD_8B_Matcher (
  input  [7:0] In8B_A,
  input  [7:0] In8B_B,
  output OutAEqB
);

  wire xor_1_out, xor_2_out, xor_3_out, xor_4_out, xor_5_out, xor_6_out, xor_7_out, xor_8_out;

  xor xor_1 (xor_1_out, In8B_A[7], In8B_B[7]);
  xor xor_2 (xor_2_out, In8B_A[6], In8B_B[6]);
  xor xor_3 (xor_3_out, In8B_A[5], In8B_B[5]);
  xor xor_4 (xor_4_out, In8B_A[4], In8B_B[4]);
  xor xor_5 (xor_5_out, In8B_A[3], In8B_B[3]);
  xor xor_6 (xor_6_out, In8B_A[2], In8B_B[2]);
  xor xor_7 (xor_7_out, In8B_A[1], In8B_B[1]);
  xor xor_8 (xor_8_out, In8B_A[0], In8B_B[0]);
  nor nor_1 (OutAEqB, xor_8_out, xor_7_out, xor_6_out, xor_5_out, xor_4_out, xor_3_out, xor_2_out, xor_1_out);
endmodule

module Norb_STD_5B_Matcher (
  input  [4:0] In8B_A,
  input  [4:0] In8B_B,
  output OutAEqB
);

  wire xor_1_out, xor_2_out, xor_3_out, xor_4_out, xor_5_out;

  xor xor_1 (xor_1_out, In8B_A[4], In8B_B[4]);
  xor xor_2 (xor_2_out, In8B_A[3], In8B_B[3]);
  xor xor_3 (xor_3_out, In8B_A[2], In8B_B[2]);
  xor xor_4 (xor_4_out, In8B_A[1], In8B_B[1]);
  xor xor_5 (xor_5_out, In8B_A[0], In8B_B[0]);
  nor nor_1 (OutAEqB, xor_5_out, xor_4_out, xor_3_out, xor_2_out, xor_1_out);
endmodule

module Norb_STD_3B_Matcher (
  input  [2:0] In8B_A,
  input  [2:0] In8B_B,
  output OutAEqB
);

  wire xor_1_out, xor_2_out, xor_3_out;

  xor xor_1 (xor_1_out, In8B_A[2], In8B_B[2]);
  xor xor_2 (xor_2_out, In8B_A[1], In8B_B[1]);
  xor xor_3 (xor_3_out, In8B_A[0], In8B_B[0]);
  nor nor_1 (OutAEqB, xor_3_out, xor_2_out, xor_1_out);
endmodule

module Norb_STD_7B_Matcher (
  input  [6:0] In8B_A,
  input  [6:0] In8B_B,
  output OutAEqB
);

  wire xor_1_out, xor_2_out, xor_3_out, xor_4_out, xor_5_out, xor_6_out, xor_7_out;

  xor xor_1 (xor_1_out, In8B_A[6], In8B_B[6]);
  xor xor_2 (xor_2_out, In8B_A[5], In8B_B[5]);
  xor xor_3 (xor_3_out, In8B_A[4], In8B_B[4]);
  xor xor_4 (xor_4_out, In8B_A[3], In8B_B[3]);
  xor xor_5 (xor_5_out, In8B_A[2], In8B_B[2]);
  xor xor_6 (xor_6_out, In8B_A[1], In8B_B[1]);
  xor xor_7 (xor_7_out, In8B_A[0], In8B_B[0]);
  nor nor_1 (OutAEqB, xor_7_out, xor_6_out, xor_5_out, xor_1_out, xor_4_out, xor_3_out, xor_2_out);
endmodule

module Norb_STD_RType_Splitter (
  input  [31:0] IN32B_INS,
  output [6:0] func7,
  output [6:0] opcode,
  output [4:0] rs2,
  output [4:0] rs1,
  output [4:0] rd,
  output [2:0] func3
);


  assign func3 = IN32B_INS[14:12];
  assign func7 = IN32B_INS[31:25];
  assign opcode = IN32B_INS[6:0];
  assign rd = IN32B_INS[11:7];
  assign rs1 = IN32B_INS[19:15];
  assign rs2 = IN32B_INS[24:20];
endmodule

module Norb_STD_IType_Splitter (
  input  [31:0] IN32B_INS,
  output [6:0] opcode,
  output [6:0] func7,
  output [31:0] imm,
  output [4:0] rs1,
  output [4:0] rd,
  output [2:0] func3
);

  wire norb_std_3b_matcher_1_outaeqb, norb_std_3b_matcher_2_outaeqb, or_1_out;
  wire [4:0] norb_std_12b5_7b_splitter_1_out_5b;
  wire [6:0] norb_std_12b5_7b_splitter_1_out_7b;
  wire [31:0] bit_extender_1_out, norb_std_5b32b_padder_1_out32b;

  assign bit_extender_1_out = {{20{IN32B_INS[31]}}, IN32B_INS[31:20]};  // Bit_Extender bit_extender_1
  Multiplexer #(.width(32)) multiplexer_1 (
    .in0(bit_extender_1_out), .in1(norb_std_5b32b_padder_1_out32b), .out(imm), .sel(or_1_out));
  Norb_STD_5B32B_Padder norb_std_5b32b_padder_1 (
    .In5B(norb_std_12b5_7b_splitter_1_out_5b), .Out32B(norb_std_5b32b_padder_1_out32b));
  Norb_STD_3B_Matcher norb_std_3b_matcher_1 (
    .In8B_A(IN32B_INS[14:12]), .In8B_B(3'b001), .OutAEqB(norb_std_3b_matcher_1_outaeqb));
  Norb_STD_3B_Matcher norb_std_3b_matcher_2 (
    .In8B_A(IN32B_INS[14:12]), .In8B_B(3'b101), .OutAEqB(norb_std_3b_matcher_2_outaeqb));
  Norb_STD_12B5_7B_Splitter norb_std_12b5_7b_splitter_1 (
    .IN32B_INS(IN32B_INS[31:20]), .OUT_7B(norb_std_12b5_7b_splitter_1_out_7b),
    .OUT_5B(norb_std_12b5_7b_splitter_1_out_5b));
  or or_1 (or_1_out, norb_std_3b_matcher_1_outaeqb, norb_std_3b_matcher_2_outaeqb);
  Multiplexer #(.width(7)) multiplexer_2 (
    .in0({7{1'b0}}), .in1(norb_std_12b5_7b_splitter_1_out_7b), .out(func7), .sel(or_1_out));

  assign func3 = IN32B_INS[14:12];
  assign opcode = IN32B_INS[6:0];
  assign rd = IN32B_INS[11:7];
  assign rs1 = IN32B_INS[19:15];
endmodule

module Norb_STD_SType_Splitter (
  input  [31:0] IN32B_INS,
  output [6:0] imm2,
  output [6:0] opcode,
  output [4:0] rs2,
  output [4:0] rs1,
  output [4:0] imm,
  output [2:0] func3
);


  assign func3 = IN32B_INS[14:12];
  assign imm = IN32B_INS[11:7];
  assign imm2 = IN32B_INS[31:25];
  assign opcode = IN32B_INS[6:0];
  assign rs1 = IN32B_INS[19:15];
  assign rs2 = IN32B_INS[24:20];
endmodule

module Norb_STD_BType_Splitter (
  input  [31:0] IN32B_INS,
  output [6:0] imm2,
  output [6:0] opcode,
  output [4:0] rs2,
  output [4:0] rs1,
  output [4:0] imm,
  output [2:0] func3
);


  assign func3 = IN32B_INS[14:12];
  assign imm = IN32B_INS[11:7];
  assign imm2 = IN32B_INS[31:25];
  assign opcode = IN32B_INS[6:0];
  assign rs1 = IN32B_INS[19:15];
  assign rs2 = IN32B_INS[24:20];
endmodule

module Norb_STD_UType_Splitter (
  input  [31:0] IN32B_INS,
  output [6:0] opcode,
  output [4:0] rd,
  output [19:0] imm
);


  assign imm = IN32B_INS[31:12];
  assign opcode = IN32B_INS[6:0];
  assign rd = IN32B_INS[11:7];
endmodule

module Norb_STD_JType_Splitter (
  input  [31:0] IN32B_INS,
  output [6:0] opcode,
  output [4:0] rd,
  output [19:0] imm
);


  assign imm = IN32B_INS[31:12];
  assign opcode = IN32B_INS[6:0];
  assign rd = IN32B_INS[11:7];
endmodule

module Norb_STD_8B32B_Splitter (
  input  [7:0] In0,
  input  [7:0] In1,
  input  [7:0] In2,
  input  [7:0] In3,
  output [31:0] Out32B
);


  assign Out32B = {In3, In2, In1, In0};
endmodule

module Norb_STD_32B8B_Splitter (
  input  [31:0] In32B,
  output [7:0] Out0,
  output [7:0] Out1,
  output [7:0] Out2,
  output [7:0] Out3
);


  assign Out0 = In32B[7:0];
  assign Out1 = In32B[15:8];
  assign Out2 = In32B[23:16];
  assign Out3 = In32B[31:24];
endmodule

module Norb_STD_12B5_7B_Splitter (
  input  [11:0] IN32B_INS,
  output [6:0] OUT_7B,
  output [4:0] OUT_5B
);


  assign OUT_5B = IN32B_INS[4:0];
  assign OUT_7B = IN32B_INS[11:5];
endmodule

module Norb_STD_1B8B_Padder (
  input  In1B,
  output [7:0] Out8B
);


  assign Out8B = {{7{1'b0}}, In1B};
endmodule

module Norb_STD_1B32B_Padder (
  input  In1B,
  output [31:0] Out32B
);


  assign Out32B = {{31{1'b0}}, In1B};
endmodule

module Norb_STD_5B32B_Padder (
  input  [4:0] In5B,
  output [31:0] Out32B
);


  assign Out32B = {{27{1'b0}}, In5B};
endmodule

module Norb_STD_12B32B_Padder (
  input  [11:0] In12B,
  output [31:0] Out32B
);


  assign Out32B = {{20{1'b0}}, In12B};
endmodule

module Norb_STD_OP_Splitter (
  input  [31:0] IN32B_INS,
  output [6:0] opcode
);


  assign opcode = IN32B_INS[6:0];
endmodule

module Norb_STD_32B_Matcher (
  input  [31:0] In32B_A,
  input  [31:0] In32B_B,
  output OutAEqB
);

  wire xor_1_out, xor_2_out, xor_3_out, xor_4_out, xor_5_out, xor_6_out, xor_7_out, xor_8_out, xor_9_out,
       xor_10_out, xor_11_out, xor_12_out, xor_13_out, xor_14_out, xor_15_out, xor_16_out, xor_17_out,
       xor_18_out, xor_19_out, xor_20_out, xor_21_out, xor_22_out, xor_23_out, xor_24_out, xor_25_out,
       xor_26_out, xor_27_out, xor_28_out, xor_29_out, xor_30_out, xor_31_out, xor_32_out;

  xor xor_1 (xor_1_out, In32B_A[31], In32B_B[31]);
  xor xor_2 (xor_2_out, In32B_A[30], In32B_B[30]);
  xor xor_3 (xor_3_out, In32B_A[29], In32B_B[29]);
  xor xor_4 (xor_4_out, In32B_A[28], In32B_B[28]);
  xor xor_5 (xor_5_out, In32B_A[27], In32B_B[27]);
  xor xor_6 (xor_6_out, In32B_A[26], In32B_B[26]);
  xor xor_7 (xor_7_out, In32B_A[25], In32B_B[25]);
  xor xor_8 (xor_8_out, In32B_A[24], In32B_B[24]);
  xor xor_9 (xor_9_out, In32B_A[23], In32B_B[23]);
  xor xor_10 (xor_10_out, In32B_A[22], In32B_B[22]);
  xor xor_11 (xor_11_out, In32B_A[21], In32B_B[21]);
  xor xor_12 (xor_12_out, In32B_A[20], In32B_B[20]);
  xor xor_13 (xor_13_out, In32B_A[19], In32B_B[19]);
  xor xor_14 (xor_14_out, In32B_A[18], In32B_B[18]);
  xor xor_15 (xor_15_out, In32B_A[17], In32B_B[17]);
  xor xor_16 (xor_16_out, In32B_A[16], In32B_B[16]);
  xor xor_17 (xor_17_out, In32B_A[14], In32B_B[14]);
  xor xor_18 (xor_18_out, In32B_A[15], In32B_B[15]);
  xor xor_19 (xor_19_out, In32B_A[13], In32B_B[13]);
  xor xor_20 (xor_20_out, In32B_A[12], In32B_B[12]);
  xor xor_21 (xor_21_out, In32B_A[11], In32B_B[11]);
  xor xor_22 (xor_22_out, In32B_A[10], In32B_B[10]);
  xor xor_23 (xor_23_out, In32B_A[9], In32B_B[9]);
  xor xor_24 (xor_24_out, In32B_A[8], In32B_B[8]);
  xor xor_25 (xor_25_out, In32B_A[7], In32B_B[7]);
  xor xor_26 (xor_26_out, In32B_A[6], In32B_B[6]);
  xor xor_27 (xor_27_out, In32B_A[5], In32B_B[5]);
  xor xor_28 (xor_28_out, In32B_A[4], In32B_B[4]);
  xor xor_29 (xor_29_out, In32B_A[3], In32B_B[3]);
  xor xor_30 (xor_30_out, In32B_A[2], In32B_B[2]);
  xor xor_31 (xor_31_out, In32B_A[1], In32B_B[1]);
  xor xor_32 (xor_32_out, In32B_A[0], In32B_B[0]);
  nor nor_1 (OutAEqB, xor_32_out, xor_31_out, xor_30_out, xor_29_out, xor_28_out, xor_27_out, xor_26_out, xor_25_out, xor_24_out, xor_23_out, xor_22_out, xor_21_out, xor_20_out, xor_19_out, xor_17_out, xor_18_out, xor_16_out, xor_15_out, xor_14_out, xor_13_out, xor_12_out, xor_11_out, xor_10_out, xor_9_out, xor_8_out, xor_7_out, xor_6_out, xor_5_out, xor_4_out, xor_3_out, xor_2_out, xor_1_out);
endmodule

module Norb_STD_1B2T_Delayer (
  input  SIGIN,
  input  CLOCK,
  output SIGOUT
);

  wire d_ff_1_q, not_1_out;

  D_Flip_Flop d_ff_1 (.D(SIGIN), .clk(CLOCK), .Q(d_ff_1_q));  // open: Qn, preset, reset
  D_Flip_Flop d_ff_2 (.D(d_ff_1_q), .clk(not_1_out), .Q(SIGOUT));  // open: Qn, preset, reset
  not not_1 (not_1_out, CLOCK);
endmodule

module Norb_STD_2B2T_Delayer (
  input  [1:0] SIGIN,
  input  CLOCK,
  output [1:0] SIGOUT
);

  Norb_STD_1B2T_Delayer norb_std_1b2t_delayer_1 (.SIGIN(SIGIN[0]), .CLOCK(CLOCK), .SIGOUT(SIGOUT[0]));
  Norb_STD_1B2T_Delayer norb_std_1b2t_delayer_2 (.SIGIN(SIGIN[1]), .CLOCK(CLOCK), .SIGOUT(SIGOUT[1]));
endmodule

module Norb_STD_8B2T_Delayer (
  input  [7:0] SIGIN,
  input  CLOCK,
  output [7:0] SIGOUT
);

  Norb_STD_2B2T_Delayer norb_std_2b2t_delayer_1 (.SIGIN(SIGIN[1:0]), .CLOCK(CLOCK), .SIGOUT(SIGOUT[1:0]));
  Norb_STD_2B2T_Delayer norb_std_2b2t_delayer_2 (.SIGIN(SIGIN[3:2]), .CLOCK(CLOCK), .SIGOUT(SIGOUT[3:2]));
  Norb_STD_2B2T_Delayer norb_std_2b2t_delayer_3 (.SIGIN(SIGIN[5:4]), .CLOCK(CLOCK), .SIGOUT(SIGOUT[5:4]));
  Norb_STD_2B2T_Delayer norb_std_2b2t_delayer_4 (.SIGIN(SIGIN[7:6]), .CLOCK(CLOCK), .SIGOUT(SIGOUT[7:6]));
endmodule

module Norb_STD_32B2T_Delayer (
  input  [31:0] SIGIN,
  input  CLOCK,
  output [31:0] SIGOUT
);

  Norb_STD_8B2T_Delayer norb_std_8b2t_delayer_1 (.SIGIN(SIGIN[7:0]), .CLOCK(CLOCK), .SIGOUT(SIGOUT[7:0]));
  Norb_STD_8B2T_Delayer norb_std_8b2t_delayer_2 (.SIGIN(SIGIN[15:8]), .CLOCK(CLOCK), .SIGOUT(SIGOUT[15:8]));
  Norb_STD_8B2T_Delayer norb_std_8b2t_delayer_3 (.SIGIN(SIGIN[23:16]), .CLOCK(CLOCK), .SIGOUT(SIGOUT[23:16]));
  Norb_STD_8B2T_Delayer norb_std_8b2t_delayer_4 (.SIGIN(SIGIN[31:24]), .CLOCK(CLOCK), .SIGOUT(SIGOUT[31:24]));
endmodule

module Norb_STD_1B1T_SFTDelayer (
  input  SIGIN,
  input  CLOCK,
  output SIGOUT
);

  wire d_ff_1_q, not_1_out;

  D_Flip_Flop d_ff_1 (.D(SIGIN), .clk(CLOCK), .Q(d_ff_1_q));  // open: Qn, preset, reset
  D_Flip_Flop d_ff_2 (.D(d_ff_1_q), .clk(not_1_out), .Q(SIGOUT));  // open: Qn, preset, reset
  not not_1 (not_1_out, CLOCK);
endmodule

module GRS_Register_Dtouch (
  input  ALLOW,
  input  Data,
  output Q,
  output out_4
);

  wire and_1_out, and_2_out, not_1_out;

  not not_1 (not_1_out, Data);
  and and_1 (and_1_out, not_1_out, ALLOW);
  and and_2 (and_2_out, ALLOW, Data);
  nor nor_1 (Q, and_1_out, out_4);
  nor nor_2 (out_4, Q, and_2_out);
endmodule
module GRS_Register_4B (
  input  [31:0] Data1,
  input  ALLOW,
  output [31:0] Output1
);

  GRS_Register_Dtouch grs_register_dtouch_1 (.ALLOW(ALLOW), .Data(Data1[31]), .Q(Output1[31]));  // open: out_4
  GRS_Register_Dtouch grs_register_dtouch_2 (.ALLOW(ALLOW), .Data(Data1[30]), .Q(Output1[30]));  // open: out_4
  GRS_Register_Dtouch grs_register_dtouch_3 (.ALLOW(ALLOW), .Data(Data1[29]), .Q(Output1[29]));  // open: out_4
  GRS_Register_Dtouch grs_register_dtouch_4 (.ALLOW(ALLOW), .Data(Data1[28]), .Q(Output1[28]));  // open: out_4
  GRS_Register_Dtouch grs_register_dtouch_5 (.ALLOW(ALLOW), .Data(Data1[27]), .Q(Output1[27]));  // open: out_4
  GRS_Register_Dtouch grs_register_dtouch_6 (.ALLOW(ALLOW), .Data(Data1[26]), .Q(Output1[26]));  // open: out_4
  GRS_Register_Dtouch grs_register_dtouch_7 (.ALLOW(ALLOW), .Data(Data1[25]), .Q(Output1[25]));  // open: out_4
  GRS_Register_Dtouch grs_register_dtouch_8 (.ALLOW(ALLOW), .Data(Data1[24]), .Q(Output1[24]));  // open: out_4
  GRS_Register_Dtouch grs_register_dtouch_9 (.ALLOW(ALLOW), .Data(Data1[23]), .Q(Output1[23]));  // open: out_4
  GRS_Register_Dtouch grs_register_dtouch_10 (.ALLOW(ALLOW), .Data(Data1[22]), .Q(Output1[22]));  // open: out_4
  GRS_Register_Dtouch grs_register_dtouch_11 (.ALLOW(ALLOW), .Data(Data1[21]), .Q(Output1[21]));  // open: out_4
  GRS_Register_Dtouch grs_register_dtouch_12 (.ALLOW(ALLOW), .Data(Data1[20]), .Q(Output1[20]));  // open: out_4
  GRS_Register_Dtouch grs_register_dtouch_13 (.ALLOW(ALLOW), .Data(Data1[19]), .Q(Output1[19]));  // open: out_4
  GRS_Register_Dtouch grs_register_dtouch_14 (.ALLOW(ALLOW), .Data(Data1[18]), .Q(Output1[18]));  // open: out_4
  GRS_Register_Dtouch grs_register_dtouch_15 (.ALLOW(ALLOW), .Data(Data1[17]), .Q(Output1[17]));  // open: out_4
  GRS_Register_Dtouch grs_register_dtouch_16 (.ALLOW(ALLOW), .Data(Data1[16]), .Q(Output1[16]));  // open: out_4
  GRS_Register_Dtouch grs_register_dtouch_17 (.ALLOW(ALLOW), .Data(Data1[15]), .Q(Output1[15]));  // open: out_4
  GRS_Register_Dtouch grs_register_dtouch_18 (.ALLOW(ALLOW), .Data(Data1[14]), .Q(Output1[14]));  // open: out_4
  GRS_Register_Dtouch grs_register_dtouch_19 (.ALLOW(ALLOW), .Data(Data1[13]), .Q(Output1[13]));  // open: out_4
  GRS_Register_Dtouch grs_register_dtouch_20 (.ALLOW(ALLOW), .Data(Data1[12]), .Q(Output1[12]));  // open: out_4
  GRS_Register_Dtouch grs_register_dtouch_21 (.ALLOW(ALLOW), .Data(Data1[11]), .Q(Output1[11]));  // open: out_4
  GRS_Register_Dtouch grs_register_dtouch_22 (.ALLOW(ALLOW), .Data(Data1[10]), .Q(Output1[10]));  // open: out_4
  GRS_Register_Dtouch grs_register_dtouch_23 (.ALLOW(ALLOW), .Data(Data1[9]), .Q(Output1[9]));  // open: out_4
  GRS_Register_Dtouch grs_register_dtouch_24 (.ALLOW(ALLOW), .Data(Data1[8]), .Q(Output1[8]));  // open: out_4
  GRS_Register_Dtouch grs_register_dtouch_25 (.ALLOW(ALLOW), .Data(Data1[7]), .Q(Output1[7]));  // open: out_4
  GRS_Register_Dtouch grs_register_dtouch_26 (.ALLOW(ALLOW), .Data(Data1[6]), .Q(Output1[6]));  // open: out_4
  GRS_Register_Dtouch grs_register_dtouch_27 (.ALLOW(ALLOW), .Data(Data1[5]), .Q(Output1[5]));  // open: out_4
  GRS_Register_Dtouch grs_register_dtouch_28 (.ALLOW(ALLOW), .Data(Data1[4]), .Q(Output1[4]));  // open: out_4
  GRS_Register_Dtouch grs_register_dtouch_29 (.ALLOW(ALLOW), .Data(Data1[3]), .Q(Output1[3]));  // open: out_4
  GRS_Register_Dtouch grs_register_dtouch_30 (.ALLOW(ALLOW), .Data(Data1[2]), .Q(Output1[2]));  // open: out_4
  GRS_Register_Dtouch grs_register_dtouch_31 (.ALLOW(ALLOW), .Data(Data1[1]), .Q(Output1[1]));  // open: out_4
  GRS_Register_Dtouch grs_register_dtouch_32 (.ALLOW(ALLOW), .Data(Data1[0]), .Q(Output1[0]));  // open: out_4
endmodule

module GRS_Registers32 (
  input  [4:0] Inputaddress,
  input  Allow,
  input  [4:0] Outputaddress1,
  input  [31:0] Data32,
  input  [1:0] Choose,
  input  [4:0] Outputaddress2,
  output [31:0] Output1,
  output [31:0] Output2
);

  wire grs_register_writeallow_1_out_3, grs_register_writeallow_1_out_4, grs_register_writeallow_1_out_5,
       grs_register_writeallow_1_out_6, grs_register_writeallow_1_out_7, grs_register_writeallow_1_out_8,
       grs_register_writeallow_1_out_9, grs_register_writeallow_1_out_10, grs_register_writeallow_1_out_11,
       grs_register_writeallow_1_out_12, grs_register_writeallow_1_out_13, grs_register_writeallow_1_out_14,
       grs_register_writeallow_1_out_15, grs_register_writeallow_1_out_16, grs_register_writeallow_1_out_17,
       grs_register_writeallow_1_out_18, grs_register_writeallow_1_out_19, grs_register_writeallow_1_out_20,
       grs_register_writeallow_1_out_21, grs_register_writeallow_1_out_22, grs_register_writeallow_1_out_23,
       grs_register_writeallow_1_out_24, grs_register_writeallow_1_out_25, grs_register_writeallow_1_out_26,
       grs_register_writeallow_1_out_27, grs_register_writeallow_1_out_28, grs_register_writeallow_1_out_29,
       grs_register_writeallow_1_out_30, grs_register_writeallow_1_out_31, grs_register_writeallow_1_out_32,
       grs_register_writeallow_1_out_33, grs_register_writeallow_1_out_34;
  wire [31:0] grs_register_4b_1_output1, grs_register_4b_2_output1, grs_register_4b_3_output1,
       grs_register_4b_4_output1, grs_register_4b_5_output1, grs_register_4b_6_output1,
       grs_register_4b_7_output1, grs_register_4b_8_output1, grs_register_4b_9_output1,
       grs_register_4b_10_output1, grs_register_4b_11_output1, grs_register_4b_12_output1,
       grs_register_4b_13_output1, grs_register_4b_14_output1, grs_register_4b_15_output1,
       grs_register_4b_16_output1, grs_register_4b_17_output1, grs_register_4b_18_output1,
       grs_register_4b_19_output1, grs_register_4b_20_output1, grs_register_4b_21_output1,
       grs_register_4b_22_output1, grs_register_4b_23_output1, grs_register_4b_24_output1,
       grs_register_4b_25_output1, grs_register_4b_26_output1, grs_register_4b_27_output1,
       grs_register_4b_28_output1, grs_register_4b_29_output1, grs_register_4b_30_output1,
       grs_register_4b_31_output1, grs_register_4b_32_output1, grs_register_printallow32_1_out_34,
       grs_register_printallow32_2_out_34;

  GRS_Register_Writeallow grs_register_writeallow_1 (
    .ADRESS(Inputaddress), .WRITEALLOW(Allow), .out_3(grs_register_writeallow_1_out_3),
    .out_4(grs_register_writeallow_1_out_4), .out_5(grs_register_writeallow_1_out_5),
    .out_6(grs_register_writeallow_1_out_6), .out_7(grs_register_writeallow_1_out_7),
    .out_8(grs_register_writeallow_1_out_8), .out_9(grs_register_writeallow_1_out_9),
    .out_10(grs_register_writeallow_1_out_10), .out_11(grs_register_writeallow_1_out_11),
    .out_12(grs_register_writeallow_1_out_12), .out_13(grs_register_writeallow_1_out_13),
    .out_14(grs_register_writeallow_1_out_14), .out_15(grs_register_writeallow_1_out_15),
    .out_16(grs_register_writeallow_1_out_16), .out_17(grs_register_writeallow_1_out_17),
    .out_18(grs_register_writeallow_1_out_18), .out_19(grs_register_writeallow_1_out_19),
    .out_20(grs_register_writeallow_1_out_20), .out_21(grs_register_writeallow_1_out_21),
    .out_22(grs_register_writeallow_1_out_22), .out_23(grs_register_writeallow_1_out_23),
    .out_24(grs_register_writeallow_1_out_24), .out_25(grs_register_writeallow_1_out_25),
    .out_26(grs_register_writeallow_1_out_26), .out_27(grs_register_writeallow_1_out_27),
    .out_28(grs_register_writeallow_1_out_28), .out_29(grs_register_writeallow_1_out_29),
    .out_30(grs_register_writeallow_1_out_30), .out_31(grs_register_writeallow_1_out_31),
    .out_32(grs_register_writeallow_1_out_32), .out_33(grs_register_writeallow_1_out_33),
    .out_34(grs_register_writeallow_1_out_34));
  GRS_Register_4B grs_register_4b_1 (
    .Data1(Data32), .ALLOW(grs_register_writeallow_1_out_3), .Output1(grs_register_4b_1_output1));
  GRS_Register_4B grs_register_4b_2 (
    .Data1(Data32), .ALLOW(grs_register_writeallow_1_out_4), .Output1(grs_register_4b_2_output1));
  GRS_Register_4B grs_register_4b_3 (
    .Data1(Data32), .ALLOW(grs_register_writeallow_1_out_5), .Output1(grs_register_4b_3_output1));
  GRS_Register_4B grs_register_4b_4 (
    .Data1(Data32), .ALLOW(grs_register_writeallow_1_out_6), .Output1(grs_register_4b_4_output1));
  GRS_Register_4B grs_register_4b_5 (
    .Data1(Data32), .ALLOW(grs_register_writeallow_1_out_7), .Output1(grs_register_4b_5_output1));
  GRS_Register_4B grs_register_4b_6 (
    .Data1(Data32), .ALLOW(grs_register_writeallow_1_out_8), .Output1(grs_register_4b_6_output1));
  GRS_Register_4B grs_register_4b_7 (
    .Data1(Data32), .ALLOW(grs_register_writeallow_1_out_9), .Output1(grs_register_4b_7_output1));
  GRS_Register_4B grs_register_4b_8 (
    .Data1(Data32), .ALLOW(grs_register_writeallow_1_out_10), .Output1(grs_register_4b_8_output1));
  GRS_Register_4B grs_register_4b_9 (
    .Data1(Data32), .ALLOW(grs_register_writeallow_1_out_11), .Output1(grs_register_4b_9_output1));
  GRS_Register_4B grs_register_4b_10 (
    .Data1(Data32), .ALLOW(grs_register_writeallow_1_out_12), .Output1(grs_register_4b_10_output1));
  GRS_Register_4B grs_register_4b_11 (
    .Data1(Data32), .ALLOW(grs_register_writeallow_1_out_13), .Output1(grs_register_4b_11_output1));
  GRS_Register_4B grs_register_4b_12 (
    .Data1(Data32), .ALLOW(grs_register_writeallow_1_out_14), .Output1(grs_register_4b_12_output1));
  GRS_Register_4B grs_register_4b_13 (
    .Data1(Data32), .ALLOW(grs_register_writeallow_1_out_15), .Output1(grs_register_4b_13_output1));
  GRS_Register_4B grs_register_4b_14 (
    .Data1(Data32), .ALLOW(grs_register_writeallow_1_out_16), .Output1(grs_register_4b_14_output1));
  GRS_Register_4B grs_register_4b_15 (
    .Data1(Data32), .ALLOW(grs_register_writeallow_1_out_17), .Output1(grs_register_4b_15_output1));
  GRS_Register_4B grs_register_4b_16 (
    .Data1(Data32), .ALLOW(grs_register_writeallow_1_out_18), .Output1(grs_register_4b_16_output1));
  GRS_Register_4B grs_register_4b_17 (
    .Data1(Data32), .ALLOW(grs_register_writeallow_1_out_19), .Output1(grs_register_4b_17_output1));
  GRS_Register_4B grs_register_4b_18 (
    .Data1(Data32), .ALLOW(grs_register_writeallow_1_out_20), .Output1(grs_register_4b_18_output1));
  GRS_Register_4B grs_register_4b_19 (
    .Data1(Data32), .ALLOW(grs_register_writeallow_1_out_21), .Output1(grs_register_4b_19_output1));
  GRS_Register_4B grs_register_4b_20 (
    .Data1(Data32), .ALLOW(grs_register_writeallow_1_out_22), .Output1(grs_register_4b_20_output1));
  GRS_Register_4B grs_register_4b_21 (
    .Data1(Data32), .ALLOW(grs_register_writeallow_1_out_23), .Output1(grs_register_4b_21_output1));
  GRS_Register_4B grs_register_4b_22 (
    .Data1(Data32), .ALLOW(grs_register_writeallow_1_out_24), .Output1(grs_register_4b_22_output1));
  GRS_Register_4B grs_register_4b_23 (
    .Data1(Data32), .ALLOW(grs_register_writeallow_1_out_25), .Output1(grs_register_4b_23_output1));
  GRS_Register_4B grs_register_4b_24 (
    .Data1(Data32), .ALLOW(grs_register_writeallow_1_out_26), .Output1(grs_register_4b_24_output1));
  GRS_Register_4B grs_register_4b_25 (
    .Data1(Data32), .ALLOW(grs_register_writeallow_1_out_27), .Output1(grs_register_4b_25_output1));
  GRS_Register_4B grs_register_4b_26 (
    .Data1(Data32), .ALLOW(grs_register_writeallow_1_out_28), .Output1(grs_register_4b_26_output1));
  GRS_Register_4B grs_register_4b_27 (
    .Data1(Data32), .ALLOW(grs_register_writeallow_1_out_29), .Output1(grs_register_4b_27_output1));
  GRS_Register_4B grs_register_4b_28 (
    .Data1(Data32), .ALLOW(grs_register_writeallow_1_out_30), .Output1(grs_register_4b_28_output1));
  GRS_Register_4B grs_register_4b_29 (
    .Data1(Data32), .ALLOW(grs_register_writeallow_1_out_31), .Output1(grs_register_4b_29_output1));
  GRS_Register_4B grs_register_4b_30 (
    .Data1(Data32), .ALLOW(grs_register_writeallow_1_out_32), .Output1(grs_register_4b_30_output1));
  GRS_Register_4B grs_register_4b_31 (
    .Data1(Data32), .ALLOW(grs_register_writeallow_1_out_33), .Output1(grs_register_4b_31_output1));
  GRS_Register_4B grs_register_4b_32 (
    .Data1(Data32), .ALLOW(grs_register_writeallow_1_out_34), .Output1(grs_register_4b_32_output1));
  GRS_Register_Printallow32 grs_register_printallow32_1 (
    .Address(Outputaddress1), .in_2(grs_register_4b_1_output1), .in_3(grs_register_4b_2_output1),
    .in_4(grs_register_4b_3_output1), .in_5(grs_register_4b_4_output1), .in_6(grs_register_4b_5_output1),
    .in_7(grs_register_4b_6_output1), .in_8(grs_register_4b_7_output1), .in_9(grs_register_4b_8_output1),
    .in_10(grs_register_4b_9_output1), .in_11(grs_register_4b_10_output1),
    .in_12(grs_register_4b_11_output1), .in_13(grs_register_4b_12_output1),
    .in_14(grs_register_4b_13_output1), .in_15(grs_register_4b_14_output1),
    .in_16(grs_register_4b_15_output1), .in_17(grs_register_4b_16_output1),
    .in_18(grs_register_4b_17_output1), .in_19(grs_register_4b_18_output1),
    .in_20(grs_register_4b_19_output1), .in_21(grs_register_4b_20_output1),
    .in_22(grs_register_4b_21_output1), .in_23(grs_register_4b_22_output1),
    .in_24(grs_register_4b_23_output1), .in_25(grs_register_4b_24_output1),
    .in_26(grs_register_4b_25_output1), .in_27(grs_register_4b_26_output1),
    .in_28(grs_register_4b_27_output1), .in_29(grs_register_4b_28_output1),
    .in_30(grs_register_4b_29_output1), .in_31(grs_register_4b_30_output1),
    .in_32(grs_register_4b_31_output1), .in_33(grs_register_4b_32_output1),
    .out_34(grs_register_printallow32_1_out_34));
  GRS_Register_Printallow32 grs_register_printallow32_2 (
    .Address(Outputaddress2), .in_2(grs_register_4b_1_output1), .in_3(grs_register_4b_2_output1),
    .in_4(grs_register_4b_3_output1), .in_5(grs_register_4b_4_output1), .in_6(grs_register_4b_5_output1),
    .in_7(grs_register_4b_6_output1), .in_8(grs_register_4b_7_output1), .in_9(grs_register_4b_8_output1),
    .in_10(grs_register_4b_9_output1), .in_11(grs_register_4b_10_output1),
    .in_12(grs_register_4b_11_output1), .in_13(grs_register_4b_12_output1),
    .in_14(grs_register_4b_13_output1), .in_15(grs_register_4b_14_output1),
    .in_16(grs_register_4b_15_output1), .in_17(grs_register_4b_16_output1),
    .in_18(grs_register_4b_17_output1), .in_19(grs_register_4b_18_output1),
    .in_20(grs_register_4b_19_output1), .in_21(grs_register_4b_20_output1),
    .in_22(grs_register_4b_21_output1), .in_23(grs_register_4b_22_output1),
    .in_24(grs_register_4b_23_output1), .in_25(grs_register_4b_24_output1),
    .in_26(grs_register_4b_25_output1), .in_27(grs_register_4b_26_output1),
    .in_28(grs_register_4b_27_output1), .in_29(grs_register_4b_28_output1),
    .in_30(grs_register_4b_29_output1), .in_31(grs_register_4b_30_output1),
    .in_32(grs_register_4b_31_output1), .in_33(grs_register_4b_32_output1),
    .out_34(grs_register_printallow32_2_out_34));
  GRS_Register_Printchoose2 grs_register_printchoose2_1 (
    .Choose1(grs_register_printallow32_1_out_34), .Outputchoose(Choose),
    .Choose2(grs_register_printallow32_2_out_34), .Print1(Output1), .Print2(Output2));
endmodule

module GRS_MUX_5to32 (
  input  [4:0] Input5,
  output K00000,
  output K00001,
  output K00010,
  output K00011,
  output K00100,
  output K00101,
  output K00110,
  output K00111,
  output K01000,
  output K01001,
  output K01010,
  output K01011,
  output K01100,
  output K01101,
  output K01110,
  output K01111,
  output K10000,
  output K10001,
  output K10010,
  output K10011,
  output K10100,
  output K10101,
  output K10110,
  output K10111,
  output K11000,
  output K11001,
  output K11010,
  output K11011,
  output K11100,
  output K11101,
  output K11110,
  output K11111
);

  wire not_1_out, not_2_out, not_3_out, not_4_out, not_5_out, not_6_out, not_7_out, not_8_out, not_9_out,
       not_10_out, not_11_out, not_12_out, not_13_out, not_14_out, not_15_out, not_16_out, not_17_out,
       not_18_out, not_19_out, not_20_out, not_21_out, not_22_out, not_23_out, not_24_out, not_25_out,
       not_26_out, not_27_out, not_28_out, not_29_out, not_30_out, not_31_out, not_32_out, not_33_out,
       not_34_out, not_35_out, not_36_out, not_37_out, not_38_out, not_39_out, not_40_out, not_41_out,
       not_42_out, not_43_out, not_44_out, not_45_out, not_46_out, not_47_out, not_48_out, not_49_out,
       not_50_out, not_51_out, not_52_out, not_53_out, not_54_out, not_55_out, not_56_out, not_57_out,
       not_58_out, not_59_out, not_60_out, not_61_out, not_62_out, not_63_out, not_64_out, not_65_out,
       not_66_out, not_67_out, not_68_out, not_69_out, not_70_out, not_71_out, not_72_out, not_73_out,
       not_74_out, not_75_out, not_76_out, not_77_out, not_78_out, not_79_out, not_80_out;

  not not_1 (not_1_out, Input5[0]);
  not not_2 (not_2_out, Input5[1]);
  not not_3 (not_3_out, Input5[2]);
  not not_4 (not_4_out, Input5[3]);
  not not_5 (not_5_out, Input5[4]);
  and and_1 (K00000, not_1_out, not_2_out, not_3_out, not_4_out, not_5_out);
  not not_6 (not_6_out, Input5[1]);
  not not_7 (not_7_out, Input5[2]);
  and and_2 (K00001, Input5[0], not_6_out, not_7_out, not_9_out, not_10_out);
  not not_8 (not_8_out, Input5[0]);
  not not_9 (not_9_out, Input5[3]);
  not not_10 (not_10_out, Input5[4]);
  not not_11 (not_11_out, Input5[2]);
  not not_12 (not_12_out, Input5[3]);
  not not_13 (not_13_out, Input5[4]);
  and and_3 (K00010, not_8_out, Input5[1], not_11_out, not_12_out, not_13_out);
  not not_14 (not_14_out, Input5[2]);
  not not_15 (not_15_out, Input5[3]);
  not not_16 (not_16_out, Input5[4]);
  and and_4 (K00011, Input5[0], Input5[1], not_14_out, not_15_out, not_16_out);
  not not_17 (not_17_out, Input5[0]);
  not not_18 (not_18_out, Input5[1]);
  not not_19 (not_19_out, Input5[3]);
  not not_20 (not_20_out, Input5[4]);
  and and_5 (K00100, not_17_out, not_18_out, Input5[2], not_19_out, not_20_out);
  not not_21 (not_21_out, Input5[1]);
  and and_6 (K00101, Input5[0], not_21_out, Input5[2], not_23_out, not_24_out);
  not not_22 (not_22_out, Input5[0]);
  not not_23 (not_23_out, Input5[3]);
  not not_24 (not_24_out, Input5[4]);
  not not_25 (not_25_out, Input5[3]);
  not not_26 (not_26_out, Input5[4]);
  and and_7 (K00110, not_22_out, Input5[1], Input5[2], not_25_out, not_26_out);
  not not_27 (not_27_out, Input5[3]);
  not not_28 (not_28_out, Input5[4]);
  and and_8 (K00111, Input5[0], Input5[1], Input5[2], not_27_out, not_28_out);
  not not_29 (not_29_out, Input5[0]);
  not not_30 (not_30_out, Input5[1]);
  not not_31 (not_31_out, Input5[2]);
  not not_32 (not_32_out, Input5[4]);
  and and_9 (K01000, not_29_out, not_30_out, not_31_out, Input5[3], not_32_out);
  not not_33 (not_33_out, Input5[1]);
  not not_34 (not_34_out, Input5[2]);
  and and_10 (K01001, Input5[0], not_33_out, not_34_out, Input5[3], not_36_out);
  not not_35 (not_35_out, Input5[0]);
  not not_36 (not_36_out, Input5[4]);
  not not_37 (not_37_out, Input5[2]);
  not not_38 (not_38_out, Input5[4]);
  and and_11 (K01010, not_35_out, Input5[1], not_37_out, Input5[3], not_38_out);
  not not_39 (not_39_out, Input5[2]);
  not not_40 (not_40_out, Input5[4]);
  and and_12 (K01011, Input5[0], Input5[1], not_39_out, Input5[3], not_40_out);
  not not_41 (not_41_out, Input5[0]);
  not not_42 (not_42_out, Input5[1]);
  not not_43 (not_43_out, Input5[4]);
  and and_13 (K01100, not_41_out, not_42_out, Input5[2], Input5[3], not_43_out);
  not not_44 (not_44_out, Input5[1]);
  and and_14 (K01101, Input5[0], not_44_out, Input5[2], Input5[3], not_46_out);
  not not_45 (not_45_out, Input5[0]);
  not not_46 (not_46_out, Input5[4]);
  not not_47 (not_47_out, Input5[4]);
  and and_15 (K01110, not_45_out, Input5[1], Input5[2], Input5[3], not_47_out);
  not not_48 (not_48_out, Input5[4]);
  and and_16 (K01111, Input5[0], Input5[1], Input5[2], Input5[3], not_48_out);
  not not_49 (not_49_out, Input5[0]);
  not not_50 (not_50_out, Input5[1]);
  not not_51 (not_51_out, Input5[2]);
  not not_52 (not_52_out, Input5[3]);
  and and_17 (K10000, not_49_out, not_50_out, not_51_out, not_52_out, Input5[4]);
  not not_53 (not_53_out, Input5[1]);
  not not_54 (not_54_out, Input5[2]);
  and and_18 (K10001, Input5[0], not_53_out, not_54_out, not_56_out, Input5[4]);
  not not_55 (not_55_out, Input5[0]);
  not not_56 (not_56_out, Input5[3]);
  not not_57 (not_57_out, Input5[2]);
  not not_58 (not_58_out, Input5[3]);
  and and_19 (K10010, not_55_out, Input5[1], not_57_out, not_58_out, Input5[4]);
  not not_59 (not_59_out, Input5[2]);
  not not_60 (not_60_out, Input5[3]);
  and and_20 (K10011, Input5[0], Input5[1], not_59_out, not_60_out, Input5[4]);
  not not_61 (not_61_out, Input5[0]);
  not not_62 (not_62_out, Input5[1]);
  not not_63 (not_63_out, Input5[3]);
  and and_21 (K10100, not_61_out, not_62_out, Input5[2], not_63_out, Input5[4]);
  not not_64 (not_64_out, Input5[1]);
  not not_65 (not_65_out, Input5[3]);
  and and_22 (K10101, Input5[0], not_64_out, Input5[2], not_65_out, Input5[4]);
  not not_66 (not_66_out, Input5[0]);
  not not_67 (not_67_out, Input5[3]);
  and and_23 (K10110, not_66_out, Input5[1], Input5[2], not_67_out, Input5[4]);
  not not_68 (not_68_out, Input5[3]);
  and and_24 (K10111, Input5[0], Input5[1], Input5[2], not_68_out, Input5[4]);
  not not_69 (not_69_out, Input5[0]);
  not not_70 (not_70_out, Input5[1]);
  not not_71 (not_71_out, Input5[2]);
  and and_25 (K11000, not_69_out, not_70_out, not_71_out, Input5[3], Input5[4]);
  not not_72 (not_72_out, Input5[1]);
  not not_73 (not_73_out, Input5[2]);
  and and_26 (K11001, Input5[0], not_72_out, not_73_out, Input5[3], Input5[4]);
  not not_74 (not_74_out, Input5[0]);
  not not_75 (not_75_out, Input5[2]);
  and and_27 (K11010, not_74_out, Input5[1], not_75_out, Input5[3], Input5[4]);
  not not_76 (not_76_out, Input5[2]);
  and and_28 (K11011, Input5[0], Input5[1], not_76_out, Input5[3], Input5[4]);
  not not_77 (not_77_out, Input5[0]);
  not not_78 (not_78_out, Input5[1]);
  and and_29 (K11100, not_77_out, not_78_out, Input5[2], Input5[3], Input5[4]);
  not not_79 (not_79_out, Input5[1]);
  and and_30 (K11101, Input5[0], not_79_out, Input5[2], Input5[3], Input5[4]);
  not not_80 (not_80_out, Input5[0]);
  and and_31 (K11110, not_80_out, Input5[1], Input5[2], Input5[3], Input5[4]);
  and and_32 (K11111, Input5[0], Input5[1], Input5[2], Input5[3], Input5[4]);
endmodule

module GRS_Register_Writeallow (
  input  [4:0] ADRESS,
  input  WRITEALLOW,
  output out_3,
  output out_4,
  output out_5,
  output out_6,
  output out_7,
  output out_8,
  output out_9,
  output out_10,
  output out_11,
  output out_12,
  output out_13,
  output out_14,
  output out_15,
  output out_16,
  output out_17,
  output out_18,
  output out_19,
  output out_20,
  output out_21,
  output out_22,
  output out_23,
  output out_24,
  output out_25,
  output out_26,
  output out_27,
  output out_28,
  output out_29,
  output out_30,
  output out_31,
  output out_32,
  output out_33,
  output out_34
);

  wire grs_mux_5to32_1_k00000, grs_mux_5to32_1_k00001, grs_mux_5to32_1_k00010, grs_mux_5to32_1_k00011,
       grs_mux_5to32_1_k00100, grs_mux_5to32_1_k00101, grs_mux_5to32_1_k00110, grs_mux_5to32_1_k00111,
       grs_mux_5to32_1_k01000, grs_mux_5to32_1_k01001, grs_mux_5to32_1_k01010, grs_mux_5to32_1_k01011,
       grs_mux_5to32_1_k01100, grs_mux_5to32_1_k01101, grs_mux_5to32_1_k01110, grs_mux_5to32_1_k01111,
       grs_mux_5to32_1_k10000, grs_mux_5to32_1_k10001, grs_mux_5to32_1_k10010, grs_mux_5to32_1_k10011,
       grs_mux_5to32_1_k10100, grs_mux_5to32_1_k10101, grs_mux_5to32_1_k10110, grs_mux_5to32_1_k10111,
       grs_mux_5to32_1_k11000, grs_mux_5to32_1_k11001, grs_mux_5to32_1_k11010, grs_mux_5to32_1_k11011,
       grs_mux_5to32_1_k11100, grs_mux_5to32_1_k11101, grs_mux_5to32_1_k11110, grs_mux_5to32_1_k11111;

  GRS_MUX_5to32 grs_mux_5to32_1 (
    .Input5(ADRESS), .K00000(grs_mux_5to32_1_k00000), .K00001(grs_mux_5to32_1_k00001),
    .K00010(grs_mux_5to32_1_k00010), .K00011(grs_mux_5to32_1_k00011), .K00100(grs_mux_5to32_1_k00100),
    .K00101(grs_mux_5to32_1_k00101), .K00110(grs_mux_5to32_1_k00110), .K00111(grs_mux_5to32_1_k00111),
    .K01000(grs_mux_5to32_1_k01000), .K01001(grs_mux_5to32_1_k01001), .K01010(grs_mux_5to32_1_k01010),
    .K01011(grs_mux_5to32_1_k01011), .K01100(grs_mux_5to32_1_k01100), .K01101(grs_mux_5to32_1_k01101),
    .K01110(grs_mux_5to32_1_k01110), .K01111(grs_mux_5to32_1_k01111), .K10000(grs_mux_5to32_1_k10000),
    .K10001(grs_mux_5to32_1_k10001), .K10010(grs_mux_5to32_1_k10010), .K10011(grs_mux_5to32_1_k10011),
    .K10100(grs_mux_5to32_1_k10100), .K10101(grs_mux_5to32_1_k10101), .K10110(grs_mux_5to32_1_k10110),
    .K10111(grs_mux_5to32_1_k10111), .K11000(grs_mux_5to32_1_k11000), .K11001(grs_mux_5to32_1_k11001),
    .K11010(grs_mux_5to32_1_k11010), .K11011(grs_mux_5to32_1_k11011), .K11100(grs_mux_5to32_1_k11100),
    .K11101(grs_mux_5to32_1_k11101), .K11110(grs_mux_5to32_1_k11110), .K11111(grs_mux_5to32_1_k11111));
  and and_1 (out_3, grs_mux_5to32_1_k00000, WRITEALLOW);
  and and_2 (out_4, grs_mux_5to32_1_k00001, WRITEALLOW);
  and and_3 (out_5, grs_mux_5to32_1_k00010, WRITEALLOW);
  and and_4 (out_6, grs_mux_5to32_1_k00011, WRITEALLOW);
  and and_5 (out_7, grs_mux_5to32_1_k00100, WRITEALLOW);
  and and_6 (out_8, grs_mux_5to32_1_k00101, WRITEALLOW);
  and and_7 (out_9, grs_mux_5to32_1_k00110, WRITEALLOW);
  and and_8 (out_10, grs_mux_5to32_1_k00111, WRITEALLOW);
  and and_9 (out_11, grs_mux_5to32_1_k01000, WRITEALLOW);
  and and_10 (out_12, grs_mux_5to32_1_k01001, WRITEALLOW);
  and and_11 (out_13, grs_mux_5to32_1_k01010, WRITEALLOW);
  and and_12 (out_14, grs_mux_5to32_1_k01011, WRITEALLOW);
  and and_13 (out_15, grs_mux_5to32_1_k01100, WRITEALLOW);
  and and_14 (out_16, grs_mux_5to32_1_k01101, WRITEALLOW);
  and and_15 (out_17, grs_mux_5to32_1_k01110, WRITEALLOW);
  and and_16 (out_18, grs_mux_5to32_1_k01111, WRITEALLOW);
  and and_17 (out_19, grs_mux_5to32_1_k10000, WRITEALLOW);
  and and_18 (out_20, grs_mux_5to32_1_k10001, WRITEALLOW);
  and and_19 (out_21, grs_mux_5to32_1_k10010, WRITEALLOW);
  and and_20 (out_22, grs_mux_5to32_1_k10011, WRITEALLOW);
  and and_21 (out_23, grs_mux_5to32_1_k10100, WRITEALLOW);
  and and_22 (out_24, grs_mux_5to32_1_k10101, WRITEALLOW);
  and and_23 (out_25, grs_mux_5to32_1_k10110, WRITEALLOW);
  and and_24 (out_26, grs_mux_5to32_1_k10111, WRITEALLOW);
  and and_25 (out_27, grs_mux_5to32_1_k11000, WRITEALLOW);
  and and_26 (out_28, grs_mux_5to32_1_k11001, WRITEALLOW);
  and and_27 (out_29, grs_mux_5to32_1_k11010, WRITEALLOW);
  and and_28 (out_30, grs_mux_5to32_1_k11011, WRITEALLOW);
  and and_29 (out_31, grs_mux_5to32_1_k11100, WRITEALLOW);
  and and_30 (out_32, grs_mux_5to32_1_k11101, WRITEALLOW);
  and and_31 (out_33, grs_mux_5to32_1_k11110, WRITEALLOW);
  and and_32 (out_34, grs_mux_5to32_1_k11111, WRITEALLOW);
endmodule

module GRS_Register_Printallow1 (
  input  [31:0] Input1,
  input  Allow1,
  output [31:0] Output1
);

  assign Output1 = Input1 & {32{Allow1}};  // AND_Gate and_1, 32 bits wide
endmodule

module GRS_Register_Printallow32 (
  input  [4:0] Address,
  input  [31:0] in_2,
  input  [31:0] in_3,
  input  [31:0] in_4,
  input  [31:0] in_5,
  input  [31:0] in_6,
  input  [31:0] in_7,
  input  [31:0] in_8,
  input  [31:0] in_9,
  input  [31:0] in_10,
  input  [31:0] in_11,
  input  [31:0] in_12,
  input  [31:0] in_13,
  input  [31:0] in_14,
  input  [31:0] in_15,
  input  [31:0] in_16,
  input  [31:0] in_17,
  input  [31:0] in_18,
  input  [31:0] in_19,
  input  [31:0] in_20,
  input  [31:0] in_21,
  input  [31:0] in_22,
  input  [31:0] in_23,
  input  [31:0] in_24,
  input  [31:0] in_25,
  input  [31:0] in_26,
  input  [31:0] in_27,
  input  [31:0] in_28,
  input  [31:0] in_29,
  input  [31:0] in_30,
  input  [31:0] in_31,
  input  [31:0] in_32,
  input  [31:0] in_33,
  output [31:0] out_34
);

  wire grs_mux_5to32_1_k00000, grs_mux_5to32_1_k00001, grs_mux_5to32_1_k00010, grs_mux_5to32_1_k00011,
       grs_mux_5to32_1_k00100, grs_mux_5to32_1_k00101, grs_mux_5to32_1_k00110, grs_mux_5to32_1_k00111,
       grs_mux_5to32_1_k01000, grs_mux_5to32_1_k01001, grs_mux_5to32_1_k01010, grs_mux_5to32_1_k01011,
       grs_mux_5to32_1_k01100, grs_mux_5to32_1_k01101, grs_mux_5to32_1_k01110, grs_mux_5to32_1_k01111,
       grs_mux_5to32_1_k10000, grs_mux_5to32_1_k10001, grs_mux_5to32_1_k10010, grs_mux_5to32_1_k10011,
       grs_mux_5to32_1_k10100, grs_mux_5to32_1_k10101, grs_mux_5to32_1_k10110, grs_mux_5to32_1_k10111,
       grs_mux_5to32_1_k11000, grs_mux_5to32_1_k11001, grs_mux_5to32_1_k11010, grs_mux_5to32_1_k11011,
       grs_mux_5to32_1_k11100, grs_mux_5to32_1_k11101, grs_mux_5to32_1_k11110, grs_mux_5to32_1_k11111;
  wire [31:0] grs_register_printallow1_1_output1, grs_register_printallow1_2_output1,
       grs_register_printallow1_3_output1, grs_register_printallow1_4_output1,
       grs_register_printallow1_5_output1, grs_register_printallow1_6_output1,
       grs_register_printallow1_7_output1, grs_register_printallow1_8_output1,
       grs_register_printallow1_9_output1, grs_register_printallow1_10_output1,
       grs_register_printallow1_11_output1, grs_register_printallow1_12_output1,
       grs_register_printallow1_13_output1, grs_register_printallow1_14_output1,
       grs_register_printallow1_15_output1, grs_register_printallow1_16_output1,
       grs_register_printallow1_17_output1, grs_register_printallow1_18_output1,
       grs_register_printallow1_19_output1, grs_register_printallow1_20_output1,
       grs_register_printallow1_21_output1, grs_register_printallow1_22_output1,
       grs_register_printallow1_23_output1, grs_register_printallow1_24_output1,
       grs_register_printallow1_25_output1, grs_register_printallow1_26_output1,
       grs_register_printallow1_27_output1, grs_register_printallow1_28_output1,
       grs_register_printallow1_29_output1, grs_register_printallow1_30_output1,
       grs_register_printallow1_31_output1, grs_register_printallow1_32_output1;

  GRS_MUX_5to32 grs_mux_5to32_1 (
    .Input5(Address), .K00000(grs_mux_5to32_1_k00000), .K00001(grs_mux_5to32_1_k00001),
    .K00010(grs_mux_5to32_1_k00010), .K00011(grs_mux_5to32_1_k00011), .K00100(grs_mux_5to32_1_k00100),
    .K00101(grs_mux_5to32_1_k00101), .K00110(grs_mux_5to32_1_k00110), .K00111(grs_mux_5to32_1_k00111),
    .K01000(grs_mux_5to32_1_k01000), .K01001(grs_mux_5to32_1_k01001), .K01010(grs_mux_5to32_1_k01010),
    .K01011(grs_mux_5to32_1_k01011), .K01100(grs_mux_5to32_1_k01100), .K01101(grs_mux_5to32_1_k01101),
    .K01110(grs_mux_5to32_1_k01110), .K01111(grs_mux_5to32_1_k01111), .K10000(grs_mux_5to32_1_k10000),
    .K10001(grs_mux_5to32_1_k10001), .K10010(grs_mux_5to32_1_k10010), .K10011(grs_mux_5to32_1_k10011),
    .K10100(grs_mux_5to32_1_k10100), .K10101(grs_mux_5to32_1_k10101), .K10110(grs_mux_5to32_1_k10110),
    .K10111(grs_mux_5to32_1_k10111), .K11000(grs_mux_5to32_1_k11000), .K11001(grs_mux_5to32_1_k11001),
    .K11010(grs_mux_5to32_1_k11010), .K11011(grs_mux_5to32_1_k11011), .K11100(grs_mux_5to32_1_k11100),
    .K11101(grs_mux_5to32_1_k11101), .K11110(grs_mux_5to32_1_k11110), .K11111(grs_mux_5to32_1_k11111));
  GRS_Register_Printallow1 grs_register_printallow1_1 (
    .Input1(in_2), .Allow1(grs_mux_5to32_1_k00000), .Output1(grs_register_printallow1_1_output1));
  GRS_Register_Printallow1 grs_register_printallow1_2 (
    .Input1(in_3), .Allow1(grs_mux_5to32_1_k00001), .Output1(grs_register_printallow1_2_output1));
  GRS_Register_Printallow1 grs_register_printallow1_3 (
    .Input1(in_4), .Allow1(grs_mux_5to32_1_k00010), .Output1(grs_register_printallow1_3_output1));
  GRS_Register_Printallow1 grs_register_printallow1_4 (
    .Input1(in_5), .Allow1(grs_mux_5to32_1_k00011), .Output1(grs_register_printallow1_4_output1));
  GRS_Register_Printallow1 grs_register_printallow1_5 (
    .Input1(in_6), .Allow1(grs_mux_5to32_1_k00100), .Output1(grs_register_printallow1_5_output1));
  GRS_Register_Printallow1 grs_register_printallow1_6 (
    .Input1(in_7), .Allow1(grs_mux_5to32_1_k00101), .Output1(grs_register_printallow1_6_output1));
  GRS_Register_Printallow1 grs_register_printallow1_7 (
    .Input1(in_8), .Allow1(grs_mux_5to32_1_k00110), .Output1(grs_register_printallow1_7_output1));
  GRS_Register_Printallow1 grs_register_printallow1_8 (
    .Input1(in_9), .Allow1(grs_mux_5to32_1_k00111), .Output1(grs_register_printallow1_8_output1));
  GRS_Register_Printallow1 grs_register_printallow1_9 (
    .Input1(in_10), .Allow1(grs_mux_5to32_1_k01000), .Output1(grs_register_printallow1_9_output1));
  GRS_Register_Printallow1 grs_register_printallow1_10 (
    .Input1(in_11), .Allow1(grs_mux_5to32_1_k01001), .Output1(grs_register_printallow1_10_output1));
  GRS_Register_Printallow1 grs_register_printallow1_11 (
    .Input1(in_12), .Allow1(grs_mux_5to32_1_k01010), .Output1(grs_register_printallow1_11_output1));
  GRS_Register_Printallow1 grs_register_printallow1_12 (
    .Input1(in_13), .Allow1(grs_mux_5to32_1_k01011), .Output1(grs_register_printallow1_12_output1));
  GRS_Register_Printallow1 grs_register_printallow1_13 (
    .Input1(in_14), .Allow1(grs_mux_5to32_1_k01100), .Output1(grs_register_printallow1_13_output1));
  GRS_Register_Printallow1 grs_register_printallow1_14 (
    .Input1(in_15), .Allow1(grs_mux_5to32_1_k01101), .Output1(grs_register_printallow1_14_output1));
  GRS_Register_Printallow1 grs_register_printallow1_15 (
    .Input1(in_16), .Allow1(grs_mux_5to32_1_k01110), .Output1(grs_register_printallow1_15_output1));
  GRS_Register_Printallow1 grs_register_printallow1_16 (
    .Input1(in_17), .Allow1(grs_mux_5to32_1_k01111), .Output1(grs_register_printallow1_16_output1));
  GRS_Register_Printallow1 grs_register_printallow1_17 (
    .Input1(in_18), .Allow1(grs_mux_5to32_1_k10000), .Output1(grs_register_printallow1_17_output1));
  GRS_Register_Printallow1 grs_register_printallow1_18 (
    .Input1(in_19), .Allow1(grs_mux_5to32_1_k10001), .Output1(grs_register_printallow1_18_output1));
  GRS_Register_Printallow1 grs_register_printallow1_19 (
    .Input1(in_20), .Allow1(grs_mux_5to32_1_k10010), .Output1(grs_register_printallow1_19_output1));
  GRS_Register_Printallow1 grs_register_printallow1_20 (
    .Input1(in_21), .Allow1(grs_mux_5to32_1_k10011), .Output1(grs_register_printallow1_20_output1));
  GRS_Register_Printallow1 grs_register_printallow1_21 (
    .Input1(in_22), .Allow1(grs_mux_5to32_1_k10100), .Output1(grs_register_printallow1_21_output1));
  GRS_Register_Printallow1 grs_register_printallow1_22 (
    .Input1(in_23), .Allow1(grs_mux_5to32_1_k10101), .Output1(grs_register_printallow1_22_output1));
  GRS_Register_Printallow1 grs_register_printallow1_23 (
    .Input1(in_24), .Allow1(grs_mux_5to32_1_k10110), .Output1(grs_register_printallow1_23_output1));
  GRS_Register_Printallow1 grs_register_printallow1_24 (
    .Input1(in_25), .Allow1(grs_mux_5to32_1_k10111), .Output1(grs_register_printallow1_24_output1));
  GRS_Register_Printallow1 grs_register_printallow1_25 (
    .Input1(in_26), .Allow1(grs_mux_5to32_1_k11000), .Output1(grs_register_printallow1_25_output1));
  GRS_Register_Printallow1 grs_register_printallow1_26 (
    .Input1(in_27), .Allow1(grs_mux_5to32_1_k11001), .Output1(grs_register_printallow1_26_output1));
  GRS_Register_Printallow1 grs_register_printallow1_27 (
    .Input1(in_28), .Allow1(grs_mux_5to32_1_k11010), .Output1(grs_register_printallow1_27_output1));
  GRS_Register_Printallow1 grs_register_printallow1_28 (
    .Input1(in_29), .Allow1(grs_mux_5to32_1_k11011), .Output1(grs_register_printallow1_28_output1));
  GRS_Register_Printallow1 grs_register_printallow1_29 (
    .Input1(in_30), .Allow1(grs_mux_5to32_1_k11100), .Output1(grs_register_printallow1_29_output1));
  GRS_Register_Printallow1 grs_register_printallow1_30 (
    .Input1(in_31), .Allow1(grs_mux_5to32_1_k11101), .Output1(grs_register_printallow1_30_output1));
  GRS_Register_Printallow1 grs_register_printallow1_31 (
    .Input1(in_32), .Allow1(grs_mux_5to32_1_k11110), .Output1(grs_register_printallow1_31_output1));
  GRS_Register_Printallow1 grs_register_printallow1_32 (
    .Input1(in_33), .Allow1(grs_mux_5to32_1_k11111), .Output1(grs_register_printallow1_32_output1));
  assign out_34 = grs_register_printallow1_1_output1 | grs_register_printallow1_2_output1 | grs_register_printallow1_3_output1 | grs_register_printallow1_4_output1 | grs_register_printallow1_5_output1 | grs_register_printallow1_6_output1 | grs_register_printallow1_7_output1 | grs_register_printallow1_8_output1 | grs_register_printallow1_9_output1 | grs_register_printallow1_10_output1 | grs_register_printallow1_11_output1 | grs_register_printallow1_12_output1 | grs_register_printallow1_13_output1 | grs_register_printallow1_14_output1 | grs_register_printallow1_15_output1 | grs_register_printallow1_16_output1 | grs_register_printallow1_17_output1 | grs_register_printallow1_18_output1 | grs_register_printallow1_19_output1 | grs_register_printallow1_20_output1 | grs_register_printallow1_21_output1 | grs_register_printallow1_22_output1 | grs_register_printallow1_23_output1 | grs_register_printallow1_24_output1 | grs_register_printallow1_25_output1 | grs_register_printallow1_26_output1 | grs_register_printallow1_27_output1 | grs_register_printallow1_28_output1 | grs_register_printallow1_29_output1 | grs_register_printallow1_30_output1 | grs_register_printallow1_31_output1 | grs_register_printallow1_32_output1;  // OR_Gate or_1, 32 bits wide
endmodule

module GRS_Register_Printchoose2 (
  input  [31:0] Choose1,
  input  [1:0] Outputchoose,
  input  [31:0] Choose2,
  output [31:0] Print1,
  output [31:0] Print2
);

  assign Print1 = Choose1 & {32{Outputchoose[0]}};  // AND_Gate and_1, 32 bits wide
  assign Print2 = {32{Outputchoose[1]}} & Choose2;  // AND_Gate and_2, 32 bits wide
endmodule

module Instance_12_to_32 (
  input  [11:0] in_1,
  input  [31:0] in_2,
  input  in_3,
  output [31:0] out_4
);

  and and_1 (out_4[0], in_2[0], in_1[0]);
  and and_2 (out_4[1], in_2[1], in_1[1]);
  and and_3 (out_4[2], in_2[2], in_1[2]);
  and and_4 (out_4[3], in_2[3], in_1[3]);
  and and_5 (out_4[4], in_2[4], in_1[4]);
  and and_6 (out_4[5], in_2[5], in_1[5]);
  and and_7 (out_4[6], in_2[6], in_1[6]);
  and and_8 (out_4[7], in_2[7], in_1[7]);
  and and_9 (out_4[8], in_2[8], in_1[8]);
  and and_10 (out_4[9], in_2[9], in_1[9]);
  and and_11 (out_4[10], in_2[10], in_1[10]);
  and and_12 (out_4[11], in_2[11], in_1[11]);
  buf and_13 (out_4[12], in_2[12]);  // AND_Gate
  and and_14 (out_4[13], in_2[13], in_3);
  and and_15 (out_4[14], in_2[14], in_3);
  and and_16 (out_4[15], in_2[15], in_3);
  and and_17 (out_4[16], in_2[16], in_3);
  and and_18 (out_4[17], in_2[17], in_3);
  and and_19 (out_4[18], in_2[18], in_3);
  and and_20 (out_4[19], in_2[19], in_3);
  and and_21 (out_4[20], in_2[20], in_3);
  and and_22 (out_4[21], in_2[21], in_3);
  and and_23 (out_4[22], in_2[22], in_3);
  and and_24 (out_4[23], in_2[23], in_3);
  and and_25 (out_4[24], in_2[24], in_3);
  and and_26 (out_4[25], in_2[25], in_3);
  and and_27 (out_4[26], in_2[26], in_3);
  and and_28 (out_4[27], in_2[27], in_3);
  and and_29 (out_4[28], in_2[28], in_3);
  and and_30 (out_4[29], in_2[29], in_3);
  and and_31 (out_4[30], in_2[30], in_3);
  and and_32 (out_4[31], in_2[31], in_3);
endmodule

module New_Register (
  input  [31:0] DATA_IN,
  input  [1:0] CHOOSE,
  input  [4:0] PRINT_ADDRESS1,
  input  [4:0] PRINT_ADDRESS2,
  input  WRITEALLOW,
  input  Clock_sign,
  input  [4:0] ADDRESS,
  output [31:0] PRINT_1,
  output [31:0] PRINT_2
);

  wire and_1_out, cl_out, grs_register_writeallow_1_out_3, grs_register_writeallow_1_out_4,
       grs_register_writeallow_1_out_5, grs_register_writeallow_1_out_6, grs_register_writeallow_1_out_7,
       grs_register_writeallow_1_out_8, grs_register_writeallow_1_out_9, grs_register_writeallow_1_out_10,
       grs_register_writeallow_1_out_11, grs_register_writeallow_1_out_12, grs_register_writeallow_1_out_13,
       grs_register_writeallow_1_out_14, grs_register_writeallow_1_out_15, grs_register_writeallow_1_out_16,
       grs_register_writeallow_1_out_17, grs_register_writeallow_1_out_18, grs_register_writeallow_1_out_19,
       grs_register_writeallow_1_out_20, grs_register_writeallow_1_out_21, grs_register_writeallow_1_out_22,
       grs_register_writeallow_1_out_23, grs_register_writeallow_1_out_24, grs_register_writeallow_1_out_25,
       grs_register_writeallow_1_out_26, grs_register_writeallow_1_out_27, grs_register_writeallow_1_out_28,
       grs_register_writeallow_1_out_29, grs_register_writeallow_1_out_30, grs_register_writeallow_1_out_31,
       grs_register_writeallow_1_out_32, grs_register_writeallow_1_out_33, grs_register_writeallow_1_out_34,
       norb_ext_1b_delayer_1_sigout;
  wire [4:0] register_2_q;
  wire [31:0] grs_register_printallow32_1_out_34, grs_register_printallow32_2_out_34, register_1_q,
       register_3_q, register_4_q, register_5_q, register_6_q, register_7_q, register_8_q, register_9_q,
       register_10_q, register_11_q, register_12_q, register_13_q, register_14_q, register_15_q,
       register_16_q, register_17_q, register_18_q, register_19_q, register_20_q, register_21_q,
       register_22_q, register_23_q, register_24_q, register_25_q, register_26_q, register_27_q,
       register_28_q, register_29_q, register_30_q, register_31_q, register_32_q, register_33_q, undriven;

  Norb_EXT_1B_Delayer norb_ext_1b_delayer_1 (
    .SIGIN(WRITEALLOW), .CLOCK_IN(Clock_sign), .SIGOUT(norb_ext_1b_delayer_1_sigout));
  Register #(.trigger("high"), .width(32)) register_1 (
    .D(DATA_IN), .en(WRITEALLOW), .clk(WRITEALLOW), .Q(register_1_q));  // open: clr
  Register #(.trigger("high"), .width(5)) register_2 (
    .D(ADDRESS), .en(WRITEALLOW), .clk(WRITEALLOW), .Q(register_2_q), .clr(cl_out));
  Clock #(.lowDuration(13), .phaseOffset(9)) cl (.out(cl_out));
  and and_1 (and_1_out, norb_ext_1b_delayer_1_sigout, Clock_sign);
  GRS_Register_Writeallow grs_register_writeallow_1 (
    .ADRESS(register_2_q), .WRITEALLOW(and_1_out), .out_3(grs_register_writeallow_1_out_3),
    .out_4(grs_register_writeallow_1_out_4), .out_5(grs_register_writeallow_1_out_5),
    .out_6(grs_register_writeallow_1_out_6), .out_7(grs_register_writeallow_1_out_7),
    .out_8(grs_register_writeallow_1_out_8), .out_9(grs_register_writeallow_1_out_9),
    .out_10(grs_register_writeallow_1_out_10), .out_11(grs_register_writeallow_1_out_11),
    .out_12(grs_register_writeallow_1_out_12), .out_13(grs_register_writeallow_1_out_13),
    .out_14(grs_register_writeallow_1_out_14), .out_15(grs_register_writeallow_1_out_15),
    .out_16(grs_register_writeallow_1_out_16), .out_17(grs_register_writeallow_1_out_17),
    .out_18(grs_register_writeallow_1_out_18), .out_19(grs_register_writeallow_1_out_19),
    .out_20(grs_register_writeallow_1_out_20), .out_21(grs_register_writeallow_1_out_21),
    .out_22(grs_register_writeallow_1_out_22), .out_23(grs_register_writeallow_1_out_23),
    .out_24(grs_register_writeallow_1_out_24), .out_25(grs_register_writeallow_1_out_25),
    .out_26(grs_register_writeallow_1_out_26), .out_27(grs_register_writeallow_1_out_27),
    .out_28(grs_register_writeallow_1_out_28), .out_29(grs_register_writeallow_1_out_29),
    .out_30(grs_register_writeallow_1_out_30), .out_31(grs_register_writeallow_1_out_31),
    .out_32(grs_register_writeallow_1_out_32), .out_33(grs_register_writeallow_1_out_33),
    .out_34(grs_register_writeallow_1_out_34));
  Register #(.trigger("high"), .width(32)) register_3 (
    .D(register_1_q), .en(grs_register_writeallow_1_out_4), .clk(grs_register_writeallow_1_out_4),
    .Q(register_3_q));  // open: clr
  Register #(.trigger("high"), .width(32)) register_4 (
    .D(register_1_q), .en(grs_register_writeallow_1_out_5), .clk(grs_register_writeallow_1_out_5),
    .Q(register_4_q));  // open: clr
  Register #(.trigger("high"), .width(32)) register_5 (
    .D(register_1_q), .en(grs_register_writeallow_1_out_6), .clk(grs_register_writeallow_1_out_6),
    .Q(register_5_q));  // open: clr
  Register #(.trigger("high"), .width(32)) register_6 (
    .D(register_1_q), .en(grs_register_writeallow_1_out_7), .clk(grs_register_writeallow_1_out_7),
    .Q(register_6_q));  // open: clr
  Register #(.trigger("high"), .width(32)) register_7 (
    .D(register_1_q), .en(grs_register_writeallow_1_out_8), .clk(grs_register_writeallow_1_out_8),
    .Q(register_7_q));  // open: clr
  Register #(.trigger("high"), .width(32)) register_8 (
    .D(register_1_q), .en(grs_register_writeallow_1_out_9), .clk(grs_register_writeallow_1_out_9),
    .Q(register_8_q));  // open: clr
  Register #(.trigger("high"), .width(32)) register_9 (
    .D(register_1_q), .en(grs_register_writeallow_1_out_10), .clk(grs_register_writeallow_1_out_10),
    .Q(register_9_q));  // open: clr
  Register #(.trigger("high"), .width(32)) register_10 (
    .D(register_1_q), .en(grs_register_writeallow_1_out_11), .clk(grs_register_writeallow_1_out_11),
    .Q(register_10_q));  // open: clr
  Register #(.trigger("high"), .width(32)) register_11 (
    .D(register_1_q), .en(grs_register_writeallow_1_out_12), .clk(grs_register_writeallow_1_out_12),
    .Q(register_11_q));  // open: clr
  Register #(.trigger("high"), .width(32)) register_12 (
    .D(register_1_q), .en(grs_register_writeallow_1_out_13), .clk(grs_register_writeallow_1_out_13),
    .Q(register_12_q));  // open: clr
  Register #(.trigger("high"), .width(32)) register_13 (
    .D(register_1_q), .en(grs_register_writeallow_1_out_14), .clk(grs_register_writeallow_1_out_14),
    .Q(register_13_q));  // open: clr
  Register #(.trigger("high"), .width(32)) register_14 (
    .D(register_1_q), .en(grs_register_writeallow_1_out_15), .clk(grs_register_writeallow_1_out_15),
    .Q(register_14_q));  // open: clr
  Register #(.trigger("high"), .width(32)) register_15 (
    .D(register_1_q), .en(grs_register_writeallow_1_out_16), .clk(grs_register_writeallow_1_out_16),
    .Q(register_15_q));  // open: clr
  Register #(.trigger("high"), .width(32)) register_16 (
    .D(register_1_q), .en(grs_register_writeallow_1_out_17), .clk(grs_register_writeallow_1_out_17),
    .Q(register_16_q));  // open: clr
  Register #(.trigger("high"), .width(32)) register_17 (
    .D(register_1_q), .en(grs_register_writeallow_1_out_18), .clk(grs_register_writeallow_1_out_18),
    .Q(register_17_q));  // open: clr
  Register #(.trigger("high"), .width(32)) register_18 (
    .D(register_1_q), .en(grs_register_writeallow_1_out_19), .clk(grs_register_writeallow_1_out_19),
    .Q(register_18_q));  // open: clr
  Register #(.trigger("high"), .width(32)) register_19 (
    .D(register_1_q), .en(grs_register_writeallow_1_out_20), .clk(grs_register_writeallow_1_out_20),
    .Q(register_19_q));  // open: clr
  Register #(.trigger("high"), .width(32)) register_20 (
    .D(register_1_q), .en(grs_register_writeallow_1_out_21), .clk(grs_register_writeallow_1_out_21),
    .Q(register_20_q));  // open: clr
  Register #(.trigger("high"), .width(32)) register_21 (
    .D(register_1_q), .en(grs_register_writeallow_1_out_22), .clk(grs_register_writeallow_1_out_22),
    .Q(register_21_q));  // open: clr
  Register #(.trigger("high"), .width(32)) register_22 (
    .D(register_1_q), .en(grs_register_writeallow_1_out_23), .clk(grs_register_writeallow_1_out_23),
    .Q(register_22_q));  // open: clr
  Register #(.trigger("high"), .width(32)) register_23 (
    .D(register_1_q), .en(grs_register_writeallow_1_out_24), .clk(grs_register_writeallow_1_out_24),
    .Q(register_23_q));  // open: clr
  Register #(.trigger("high"), .width(32)) register_24 (
    .D(register_1_q), .en(grs_register_writeallow_1_out_25), .clk(grs_register_writeallow_1_out_25),
    .Q(register_24_q));  // open: clr
  Register #(.trigger("high"), .width(32)) register_25 (
    .D(register_1_q), .en(grs_register_writeallow_1_out_26), .clk(grs_register_writeallow_1_out_26),
    .Q(register_25_q));  // open: clr
  Register #(.trigger("high"), .width(32)) register_26 (
    .D(register_1_q), .en(grs_register_writeallow_1_out_27), .clk(grs_register_writeallow_1_out_27),
    .Q(register_26_q));  // open: clr
  Register #(.trigger("high"), .width(32)) register_27 (
    .D(register_1_q), .en(grs_register_writeallow_1_out_28), .clk(grs_register_writeallow_1_out_28),
    .Q(register_27_q));  // open: clr
  Register #(.trigger("high"), .width(32)) register_28 (
    .D(register_1_q), .en(grs_register_writeallow_1_out_29), .clk(grs_register_writeallow_1_out_29),
    .Q(register_28_q));  // open: clr
  Register #(.trigger("high"), .width(32)) register_29 (
    .D(register_1_q), .en(grs_register_writeallow_1_out_30), .clk(grs_register_writeallow_1_out_30),
    .Q(register_29_q));  // open: clr
  Register #(.trigger("high"), .width(32)) register_30 (
    .D(register_1_q), .en(grs_register_writeallow_1_out_31), .clk(grs_register_writeallow_1_out_31),
    .Q(register_30_q));  // open: clr
  Register #(.trigger("high"), .width(32)) register_31 (
    .D(register_1_q), .en(grs_register_writeallow_1_out_32), .clk(grs_register_writeallow_1_out_32),
    .Q(register_31_q));  // open: clr
  Register #(.trigger("high"), .width(32)) register_32 (
    .D(register_1_q), .en(grs_register_writeallow_1_out_33), .clk(grs_register_writeallow_1_out_33),
    .Q(register_32_q));  // open: clr
  Register #(.trigger("high"), .width(32)) register_33 (
    .D(register_1_q), .en(grs_register_writeallow_1_out_34), .clk(grs_register_writeallow_1_out_34),
    .Q(register_33_q));  // open: clr
  Register #(.trigger("high"), .width(32)) register_34 (
    .D(register_1_q), .en(grs_register_writeallow_1_out_3), .clk(grs_register_writeallow_1_out_3));  // open: Q, clr
  GRS_Register_Printallow32 grs_register_printallow32_1 (
    .Address(PRINT_ADDRESS2), .in_2(undriven), .in_3(register_3_q), .in_4(register_4_q), .in_5(register_5_q),
    .in_6(register_6_q), .in_7(register_7_q), .in_8(register_8_q), .in_9(register_9_q),
    .in_10(register_10_q), .in_11(register_11_q), .in_12(register_12_q), .in_13(register_13_q),
    .in_14(register_14_q), .in_15(register_15_q), .in_16(register_16_q), .in_17(register_17_q),
    .in_18(register_18_q), .in_19(register_19_q), .in_20(register_20_q), .in_21(register_21_q),
    .in_22(register_22_q), .in_23(register_23_q), .in_24(register_24_q), .in_25(register_25_q),
    .in_26(register_26_q), .in_27(register_27_q), .in_28(register_28_q), .in_29(register_29_q),
    .in_30(register_30_q), .in_31(register_31_q), .in_32(register_32_q), .in_33(register_33_q),
    .out_34(grs_register_printallow32_1_out_34));
  GRS_Register_Printallow32 grs_register_printallow32_2 (
    .Address(PRINT_ADDRESS1), .in_2(undriven), .in_3(register_3_q), .in_4(register_4_q), .in_5(register_5_q),
    .in_6(register_6_q), .in_7(register_7_q), .in_8(register_8_q), .in_9(register_9_q),
    .in_10(register_10_q), .in_11(register_11_q), .in_12(register_12_q), .in_13(register_13_q),
    .in_14(register_14_q), .in_15(register_15_q), .in_16(register_16_q), .in_17(register_17_q),
    .in_18(register_18_q), .in_19(register_19_q), .in_20(register_20_q), .in_21(register_21_q),
    .in_22(register_22_q), .in_23(register_23_q), .in_24(register_24_q), .in_25(register_25_q),
    .in_26(register_26_q), .in_27(register_27_q), .in_28(register_28_q), .in_29(register_29_q),
    .in_30(register_30_q), .in_31(register_31_q), .in_32(register_32_q), .in_33(register_33_q),
    .out_34(grs_register_printallow32_2_out_34));
  GRS_Register_Printchoose2 grs_register_printchoose2_1 (
    .Choose1(grs_register_printallow32_2_out_34), .Outputchoose(CHOOSE),
    .Choose2(grs_register_printallow32_1_out_34), .Print1(PRINT_1), .Print2(PRINT_2));

  // Notes on the sheet:
  //   Last Output
endmodule

module Norb_EXT_1B_Delayer (
  input  SIGIN,
  input  CLOCK_IN,
  output SIGOUT
);

  wire d_ff_1_q, not_1_out;

  // OR_Gate or_1 has open pins: in0=SIGIN, in1=CLOCK_IN, out=open
  D_Flip_Flop #(.trigger("low")) d_ff_1 (.D(SIGIN), .clk(CLOCK_IN), .Q(d_ff_1_q));  // open: Qn, preset, reset
  D_Flip_Flop #(.trigger("falling")) d_ff_2 (.D(d_ff_1_q), .clk(not_1_out), .Q(SIGOUT));  // open: Qn, preset, reset
  not not_1 (not_1_out, CLOCK_IN);
endmodule

module Instance_20_to_32 (
  input  [19:0] in_1,
  input  [31:0] in_2,
  input  in_3,
  output [31:0] out_4
);

  and and_1 (out_4[0], in_2[0], in_1[0]);
  and and_2 (out_4[1], in_2[1], in_1[1]);
  and and_3 (out_4[2], in_2[2], in_1[2]);
  and and_4 (out_4[3], in_2[3], in_1[3]);
  and and_5 (out_4[4], in_2[4], in_1[4]);
  and and_6 (out_4[5], in_2[5], in_1[5]);
  and and_7 (out_4[6], in_2[6], in_1[6]);
  and and_8 (out_4[7], in_2[7], in_1[7]);
  and and_9 (out_4[8], in_2[8], in_1[8]);
  and and_10 (out_4[9], in_2[9], in_1[9]);
  and and_11 (out_4[10], in_2[10], in_1[10]);
  and and_12 (out_4[11], in_2[11], in_1[11]);
  and and_13 (out_4[12], in_2[12], in_1[12]);
  and and_14 (out_4[13], in_2[13], in_1[13]);
  and and_15 (out_4[14], in_2[14], in_1[14]);
  and and_16 (out_4[15], in_2[15], in_1[15]);
  and and_17 (out_4[16], in_2[16], in_1[16]);
  and and_18 (out_4[17], in_2[17], in_1[17]);
  and and_19 (out_4[18], in_2[18], in_1[18]);
  and and_20 (out_4[19], in_2[19], in_1[19]);
  and and_21 (out_4[20], in_2[20], in_3);
  and and_22 (out_4[21], in_2[21], in_3);
  and and_23 (out_4[22], in_2[22], in_3);
  and and_24 (out_4[23], in_2[23], in_3);
  and and_25 (out_4[24], in_2[24], in_3);
  and and_26 (out_4[25], in_2[25], in_3);
  and and_27 (out_4[26], in_2[26], in_3);
  and and_28 (out_4[27], in_2[27], in_3);
  and and_29 (out_4[28], in_2[28], in_3);
  and and_30 (out_4[29], in_2[29], in_3);
  and and_31 (out_4[30], in_2[30], in_3);
  and and_32 (out_4[31], in_2[31], in_3);
endmodule

module GRS_Register_Readallow (
  input  [31:0] Input1,
  input  Allow1,
  output [31:0] Output1
);

  assign Output1 = Input1 & {32{Allow1}};  // AND_Gate and_1, 32 bits wide
endmodule

module GRS_MUX_3to8 (
  input  [2:0] Input3,
  output K000,
  output K001,
  output K002,
  output K003,
  output K004,
  output K005,
  output K006,
  output K008
);

  wire not_1_out, not_2_out, not_3_out, not_4_out, not_5_out, not_6_out, not_7_out, not_8_out, not_9_out,
       not_10_out, not_11_out, not_12_out;

  not not_1 (not_1_out, Input3[0]);
  not not_2 (not_2_out, Input3[1]);
  and and_1 (K000, not_1_out, not_2_out, not_3_out);
  not not_3 (not_3_out, Input3[2]);
  not not_4 (not_4_out, Input3[1]);
  not not_5 (not_5_out, Input3[2]);
  and and_2 (K001, Input3[0], not_4_out, not_5_out);
  not not_6 (not_6_out, Input3[0]);
  not not_7 (not_7_out, Input3[2]);
  and and_3 (K002, not_6_out, Input3[1], not_7_out);
  not not_8 (not_8_out, Input3[2]);
  and and_4 (K003, Input3[0], Input3[1], not_8_out);
  not not_9 (not_9_out, Input3[0]);
  not not_10 (not_10_out, Input3[1]);
  and and_5 (K004, not_9_out, not_10_out, Input3[2]);
  not not_11 (not_11_out, Input3[1]);
  and and_6 (K005, Input3[0], not_11_out, Input3[2]);
  not not_12 (not_12_out, Input3[0]);
  and and_7 (K006, not_12_out, Input3[1], Input3[2]);
  and and_8 (K008, Input3[0], Input3[1], Input3[2]);
endmodule

module FL_CU_32B_Splitter (
  input  [31:0] In32B,
  output LUI,
  output JAL,
  output BEQ,
  output LW,
  output ALUI,
  output ALU,
  output SW,
  output NOOP
);

  wire [6:0] norb_std_op_splitter_1_opcode;

  Norb_STD_OP_Splitter norb_std_op_splitter_1 (.IN32B_INS(In32B), .opcode(norb_std_op_splitter_1_opcode));
  Norb_STD_7B_Matcher norb_std_7b_matcher_1 (
    .In8B_A(norb_std_op_splitter_1_opcode), .In8B_B(7'b0110111), .OutAEqB(LUI));
  Norb_STD_7B_Matcher norb_std_7b_matcher_2 (
    .In8B_A(norb_std_op_splitter_1_opcode), .In8B_B(7'b1101111), .OutAEqB(JAL));
  Norb_STD_7B_Matcher norb_std_7b_matcher_3 (
    .In8B_A(norb_std_op_splitter_1_opcode), .In8B_B(7'b1100011), .OutAEqB(BEQ));
  Norb_STD_7B_Matcher norb_std_7b_matcher_4 (.In8B_A(norb_std_op_splitter_1_opcode), .In8B_B(7'b0000011), .OutAEqB(LW));
  Norb_STD_7B_Matcher norb_std_7b_matcher_5 (
    .In8B_A(norb_std_op_splitter_1_opcode), .In8B_B(7'b0010011), .OutAEqB(ALUI));
  Norb_STD_7B_Matcher norb_std_7b_matcher_6 (
    .In8B_A(norb_std_op_splitter_1_opcode), .In8B_B(7'b0110011), .OutAEqB(ALU));
  Norb_STD_7B_Matcher norb_std_7b_matcher_7 (.In8B_A(norb_std_op_splitter_1_opcode), .In8B_B(7'b0100011), .OutAEqB(SW));
  Norb_STD_7B_Matcher norb_std_7b_matcher_8 (
    .In8B_A(norb_std_op_splitter_1_opcode), .In8B_B({7{1'b0}}), .OutAEqB(NOOP));
endmodule

module FL_CPU (
);

  wire clock_1_out, clock_2_out, clock_3_out, clock_4_out, fl_cu_32b_splitter_1_alu,
       fl_cu_32b_splitter_1_alui, fl_cu_32b_splitter_1_beq, fl_cu_32b_splitter_1_jal,
       fl_cu_32b_splitter_1_lui, fl_cu_32b_splitter_1_lw, fl_cu_32b_splitter_1_sw,
       norb_std_1t2_decoder_1_out0, norb_std_1t2_decoder_1_out1, norb_std_32b_matcher_1_outaeqb,
       norb_std_32b_matcher_2_outaeqb, or_5_out;
  wire [2:0] norb_std_itype_splitter_3_func3, norb_std_rtype_splitter_1_func3, or_9_out;
  wire [4:0] multiplexer_1_out, multiplexer_2_out, norb_std_itype_splitter_1_rd,
       norb_std_itype_splitter_1_rs1, norb_std_itype_splitter_2_rd, norb_std_itype_splitter_2_rs1,
       norb_std_itype_splitter_3_rd, norb_std_itype_splitter_3_rs1, norb_std_rtype_splitter_1_rd,
       norb_std_rtype_splitter_1_rs1, norb_std_rtype_splitter_1_rs2, norb_std_utype_splitter_1_rd, or_1_out,
       or_2_out, or_4_out;
  wire [6:0] norb_std_itype_splitter_3_func7, norb_std_rtype_splitter_1_func7, or_8_out;
  wire [7:0] norb_std_32b8b_splitter_1_out0;
  wire [19:0] norb_std_jtype_splitter_1_imm, norb_std_utype_splitter_1_imm;
  wire [31:0] and_1_out, instance_20_to_32_1_out_4, instance_20_to_32_2_out_4, new_register_1_print_1,
       new_register_1_print_2, norb_alu_32b_cra_1_outaaddb, norb_alu_32b_cra_2_outaaddb,
       norb_alu_riscv_alu_1_alu_output, norb_std_32b2t_delayer_1_sigout, norb_std_32b2t_delayer_2_sigout,
       norb_std_32b2t_delayer_3_sigout, norb_std_32b_selector_1_out32b, norb_std_32b_selector_2_out32b,
       norb_std_32b_selector_3_out32b, norb_std_32b_selector_4_out32b, norb_std_32b_selector_5_out32b,
       norb_std_32b_selector_6_out32b, norb_std_32b_selector_8_out32b, norb_std_32b_selector_9_out32b,
       norb_std_32b_selector_10_out32b, norb_std_itype_splitter_1_imm, norb_std_itype_splitter_2_imm,
       norb_std_itype_splitter_3_imm, or_3_out, or_6_out, or_7_out, or_10_out, or_11_out, rom_1_data;

  Clock #(.highDuration(2), .lowDuration(2)) clock_1 (.out(clock_1_out));
  Clock #(.highDuration(2), .lowDuration(10), .phaseOffset(8)) clock_2 (.out(clock_2_out));
  Clock #(.highDuration(2), .lowDuration(10), .phaseOffset(4)) clock_3 (.out(clock_3_out));
  Clock #(.highDuration(2), .lowDuration(10)) clock_4 (.out(clock_4_out));
  assign or_1_out = norb_std_utype_splitter_1_rd | norb_std_itype_splitter_3_rd | norb_std_itype_splitter_2_rd | norb_std_rtype_splitter_1_rd | {5{1'b0}};  // OR_Gate or_1, 5 bits wide
  assign or_2_out = {5{1'b0}} | norb_std_itype_splitter_3_rs1 | norb_std_itype_splitter_2_rs1 | norb_std_rtype_splitter_1_rs1 | norb_std_itype_splitter_1_rs1;  // OR_Gate or_2, 5 bits wide
  assign or_3_out = instance_20_to_32_2_out_4 | rom_1_data | {32{1'b0}} | norb_alu_riscv_alu_1_alu_output | norb_std_32b2t_delayer_3_sigout;  // OR_Gate or_3, 32 bits wide
  assign or_4_out = norb_std_itype_splitter_1_rd | norb_std_rtype_splitter_1_rs2;  // OR_Gate or_4, 5 bits wide
  Norb_STD_32B2T_Delayer norb_std_32b2t_delayer_1 (
    .SIGIN(rom_1_data), .CLOCK(clock_2_out), .SIGOUT(norb_std_32b2t_delayer_1_sigout));
  Instance_20_to_32 instance_20_to_32_1 (
    .in_1(norb_std_jtype_splitter_1_imm), .in_2({32{1'b1}}), .in_3(1'b0), .out_4(instance_20_to_32_1_out_4));
  Multiplexer #(.width(5)) multiplexer_1 (.in0(or_1_out), .in1({5{1'b1}}), .out(multiplexer_1_out), .sel(or_5_out));
  Multiplexer #(.width(5)) multiplexer_2 (.in0(or_2_out), .in1({5{1'b1}}), .out(multiplexer_2_out), .sel(clock_2_out));
  buf or_5 (or_5_out, clock_4_out);  // OR_Gate
  FL_CU_32B_Splitter fl_cu_32b_splitter_1 (
    .In32B(norb_std_32b2t_delayer_1_sigout), .LUI(fl_cu_32b_splitter_1_lui), .JAL(fl_cu_32b_splitter_1_jal),
    .BEQ(fl_cu_32b_splitter_1_beq), .LW(fl_cu_32b_splitter_1_lw), .ALUI(fl_cu_32b_splitter_1_alui),
    .ALU(fl_cu_32b_splitter_1_alu), .SW(fl_cu_32b_splitter_1_sw));  // open: NOOP
  assign or_6_out = instance_20_to_32_1_out_4 | and_1_out;  // OR_Gate or_6, 32 bits wide
  Norb_STD_32B_Selector norb_std_32b_selector_1 (
    .In32B(norb_std_32b2t_delayer_1_sigout), .InSelect(fl_cu_32b_splitter_1_lui),
    .Out32B(norb_std_32b_selector_1_out32b));
  Norb_STD_32B_Selector norb_std_32b_selector_2 (
    .In32B(norb_std_32b2t_delayer_1_sigout), .InSelect(fl_cu_32b_splitter_1_jal),
    .Out32B(norb_std_32b_selector_2_out32b));
  Norb_STD_32B_Selector norb_std_32b_selector_3 (
    .In32B(norb_std_32b2t_delayer_1_sigout), .InSelect(fl_cu_32b_splitter_1_beq),
    .Out32B(norb_std_32b_selector_3_out32b));
  Norb_STD_32B_Selector norb_std_32b_selector_4 (
    .In32B(norb_std_32b2t_delayer_1_sigout), .InSelect(fl_cu_32b_splitter_1_lw),
    .Out32B(norb_std_32b_selector_4_out32b));
  Norb_STD_32B_Selector norb_std_32b_selector_5 (
    .In32B(norb_std_32b2t_delayer_1_sigout), .InSelect(fl_cu_32b_splitter_1_alui),
    .Out32B(norb_std_32b_selector_5_out32b));
  Norb_STD_32B_Selector norb_std_32b_selector_6 (
    .In32B(norb_std_32b2t_delayer_1_sigout), .InSelect(fl_cu_32b_splitter_1_alu),
    .Out32B(norb_std_32b_selector_6_out32b));
  Norb_STD_32B_Selector norb_std_32b_selector_7 (
    .In32B(norb_std_32b2t_delayer_1_sigout), .InSelect(fl_cu_32b_splitter_1_sw));  // open: Out32B
  New_Register new_register_1 (
    .DATA_IN(or_3_out), .CHOOSE(2'b11), .PRINT_ADDRESS1(multiplexer_2_out), .PRINT_ADDRESS2(or_4_out),
    .WRITEALLOW(clock_4_out), .Clock_sign(clock_4_out), .ADDRESS(multiplexer_1_out),
    .PRINT_1(new_register_1_print_1), .PRINT_2(new_register_1_print_2));
  Norb_STD_32B_Matcher norb_std_32b_matcher_1 (
    .In32B_A({32{1'b0}}), .In32B_B(or_6_out), .OutAEqB(norb_std_32b_matcher_1_outaeqb));
  Instance_20_to_32 instance_20_to_32_2 (
    .in_1(norb_std_utype_splitter_1_imm), .in_2({32{1'b1}}), .in_3(1'b0), .out_4(instance_20_to_32_2_out_4));
  Norb_STD_32B_Selector norb_std_32b_selector_8 (
    .In32B(32'h1), .InSelect(norb_std_32b_matcher_1_outaeqb), .Out32B(norb_std_32b_selector_8_out32b));
  Norb_STD_UType_Splitter norb_std_utype_splitter_1 (
    .IN32B_INS(norb_std_32b_selector_1_out32b), .rd(norb_std_utype_splitter_1_rd),
    .imm(norb_std_utype_splitter_1_imm));  // open: opcode
  Norb_STD_JType_Splitter norb_std_jtype_splitter_1 (
    .IN32B_INS(norb_std_32b_selector_2_out32b), .imm(norb_std_jtype_splitter_1_imm));  // open: opcode, rd
  Norb_STD_IType_Splitter norb_std_itype_splitter_1 (
    .IN32B_INS(norb_std_32b_selector_3_out32b), .imm(norb_std_itype_splitter_1_imm),
    .rs1(norb_std_itype_splitter_1_rs1), .rd(norb_std_itype_splitter_1_rd));  // open: opcode, func7, func3
  Norb_STD_IType_Splitter norb_std_itype_splitter_2 (
    .IN32B_INS(norb_std_32b_selector_4_out32b), .imm(norb_std_itype_splitter_2_imm),
    .rs1(norb_std_itype_splitter_2_rs1), .rd(norb_std_itype_splitter_2_rd));  // open: opcode, func7, func3
  Norb_STD_IType_Splitter norb_std_itype_splitter_3 (
    .IN32B_INS(norb_std_32b_selector_5_out32b), .func7(norb_std_itype_splitter_3_func7),
    .imm(norb_std_itype_splitter_3_imm), .rs1(norb_std_itype_splitter_3_rs1),
    .rd(norb_std_itype_splitter_3_rd), .func3(norb_std_itype_splitter_3_func3));  // open: opcode
  Norb_STD_RType_Splitter norb_std_rtype_splitter_1 (
    .IN32B_INS(norb_std_32b_selector_6_out32b), .func7(norb_std_rtype_splitter_1_func7),
    .rs2(norb_std_rtype_splitter_1_rs2), .rs1(norb_std_rtype_splitter_1_rs1),
    .rd(norb_std_rtype_splitter_1_rd), .func3(norb_std_rtype_splitter_1_func3));  // open: opcode
  assign or_7_out = norb_std_32b_selector_8_out32b | or_6_out;  // OR_Gate or_7, 32 bits wide
  Norb_STD_32B2T_Delayer norb_std_32b2t_delayer_2 (
    .SIGIN(new_register_1_print_1), .CLOCK(clock_3_out), .SIGOUT(norb_std_32b2t_delayer_2_sigout));
  assign or_8_out = norb_std_itype_splitter_3_func7 | norb_std_rtype_splitter_1_func7;  // OR_Gate or_8, 7 bits wide
  assign or_9_out = norb_std_itype_splitter_3_func3 | norb_std_rtype_splitter_1_func3;  // OR_Gate or_9, 3 bits wide
  Norb_ALU_32B_CRA norb_alu_32b_cra_1 (
    .InA(or_7_out), .InB(new_register_1_print_1), .OutAAddB(norb_alu_32b_cra_1_outaaddb));  // open: FlagOverflow
  Norb_STD_32B8B_Splitter norb_std_32b8b_splitter_1 (
    .In32B(norb_std_32b2t_delayer_2_sigout), .Out0(norb_std_32b8b_splitter_1_out0));  // open: Out1, Out2, Out3
  Norb_STD_32B_Matcher norb_std_32b_matcher_2 (
    .In32B_A(new_register_1_print_1), .In32B_B(new_register_1_print_2),
    .OutAEqB(norb_std_32b_matcher_2_outaeqb));
  Norb_ALU_32B_CRA norb_alu_32b_cra_2 (
    .InA(norb_std_itype_splitter_2_imm), .InB(new_register_1_print_1), .OutAAddB(norb_alu_32b_cra_2_outaaddb));  // open: FlagOverflow
  assign or_10_out = new_register_1_print_2 | norb_std_itype_splitter_3_imm;  // OR_Gate or_10, 32 bits wide
  ROM #(.dataWidth(32)) rom_1 (.addr(norb_std_32b8b_splitter_1_out0), .data(rom_1_data));
  Norb_STD_32B2T_Delayer norb_std_32b2t_delayer_3 (
    .SIGIN(norb_alu_32b_cra_1_outaaddb), .CLOCK(clock_3_out), .SIGOUT(norb_std_32b2t_delayer_3_sigout));
  Norb_STD_1T2_Decoder norb_std_1t2_decoder_1 (
    .In1B(norb_std_32b_matcher_2_outaeqb), .Out1(norb_std_1t2_decoder_1_out1),
    .Out0(norb_std_1t2_decoder_1_out0));
  Norb_ALU_RISCV_ALU norb_alu_riscv_alu_1 (
    .InFunc7(or_8_out), .InFunc3(or_9_out), .InA(new_register_1_print_1), .InB(or_10_out),
    .ALU_OUTPUT(norb_alu_riscv_alu_1_alu_output));  // open: ZERO_FLAG
  Norb_STD_32B_Selector norb_std_32b_selector_9 (
    .In32B({32{1'b1}}), .InSelect(norb_std_1t2_decoder_1_out1), .Out32B(norb_std_32b_selector_9_out32b));
  Norb_STD_32B_Selector norb_std_32b_selector_10 (
    .In32B({32{1'b0}}), .InSelect(norb_std_1t2_decoder_1_out0), .Out32B(norb_std_32b_selector_10_out32b));
  assign or_11_out = norb_std_32b_selector_9_out32b | norb_std_32b_selector_10_out32b;  // OR_Gate or_11, 32 bits wide
  assign and_1_out = or_11_out & norb_std_itype_splitter_1_imm;  // AND_Gate and_1, 32 bits wide

  // Notes on the sheet:
  //   Global Clock
  //   PhaseA Clock
  //   PhaseB Clock
  //   PhaseC Clock
  //   ALUI 
endmodule

module FLU_CPU_Testbench (
);

  wire clock_1_out, clock_2_out, clock_3_out, clock_4_out, fl_cu_32b_splitter_1_alu,
       fl_cu_32b_splitter_1_alui, fl_cu_32b_splitter_1_beq, fl_cu_32b_splitter_1_jal,
       fl_cu_32b_splitter_1_lui, fl_cu_32b_splitter_1_lw, fl_cu_32b_splitter_1_sw,
       norb_std_1t2_decoder_1_out0, norb_std_1t2_decoder_1_out1, norb_std_32b_matcher_1_outaeqb,
       norb_std_32b_matcher_2_outaeqb, or_5_out;
  wire [2:0] norb_std_itype_splitter_3_func3, norb_std_rtype_splitter_1_func3, or_9_out;
  wire [4:0] multiplexer_1_out, multiplexer_2_out, norb_std_itype_splitter_1_rd,
       norb_std_itype_splitter_1_rs1, norb_std_itype_splitter_2_rd, norb_std_itype_splitter_2_rs1,
       norb_std_itype_splitter_3_rd, norb_std_itype_splitter_3_rs1, norb_std_rtype_splitter_1_rd,
       norb_std_rtype_splitter_1_rs1, norb_std_rtype_splitter_1_rs2, norb_std_utype_splitter_1_rd, or_1_out,
       or_2_out, or_4_out;
  wire [6:0] norb_std_itype_splitter_3_func7, norb_std_rtype_splitter_1_func7, or_8_out;
  wire [7:0] norb_std_32b8b_splitter_1_out0;
  wire [19:0] norb_std_jtype_splitter_1_imm, norb_std_utype_splitter_1_imm;
  wire [31:0] and_1_out, instance_20_to_32_1_out_4, instance_20_to_32_2_out_4, new_register_1_print_1,
       new_register_1_print_2, norb_alu_32b_cra_1_outaaddb, norb_alu_32b_cra_2_outaaddb,
       norb_alu_riscv_alu_1_alu_output, norb_std_32b2t_delayer_1_sigout, norb_std_32b2t_delayer_2_sigout,
       norb_std_32b2t_delayer_3_sigout, norb_std_32b_selector_1_out32b, norb_std_32b_selector_2_out32b,
       norb_std_32b_selector_3_out32b, norb_std_32b_selector_4_out32b, norb_std_32b_selector_5_out32b,
       norb_std_32b_selector_6_out32b, norb_std_32b_selector_8_out32b, norb_std_32b_selector_9_out32b,
       norb_std_32b_selector_10_out32b, norb_std_itype_splitter_1_imm, norb_std_itype_splitter_2_imm,
       norb_std_itype_splitter_3_imm, or_3_out, or_6_out, or_7_out, or_10_out, or_11_out, rom_1_data;

  Clock #(.highDuration(2), .lowDuration(2)) clock_1 (.out(clock_1_out));
  Clock #(.highDuration(2), .lowDuration(10), .phaseOffset(8)) clock_2 (.out(clock_2_out));
  Clock #(.highDuration(2), .lowDuration(10), .phaseOffset(4)) clock_3 (.out(clock_3_out));
  Clock #(.highDuration(2), .lowDuration(10)) clock_4 (.out(clock_4_out));
  assign or_1_out = norb_std_utype_splitter_1_rd | norb_std_itype_splitter_3_rd | norb_std_itype_splitter_2_rd | norb_std_rtype_splitter_1_rd | {5{1'b0}};  // OR_Gate or_1, 5 bits wide
  assign or_2_out = {5{1'b0}} | norb_std_itype_splitter_3_rs1 | norb_std_itype_splitter_2_rs1 | norb_std_rtype_splitter_1_rs1 | norb_std_itype_splitter_1_rs1;  // OR_Gate or_2, 5 bits wide
  assign or_3_out = instance_20_to_32_2_out_4 | rom_1_data | {32{1'b0}} | norb_alu_riscv_alu_1_alu_output | norb_std_32b2t_delayer_3_sigout;  // OR_Gate or_3, 32 bits wide
  assign or_4_out = norb_std_itype_splitter_1_rd | norb_std_rtype_splitter_1_rs2;  // OR_Gate or_4, 5 bits wide
  Norb_STD_32B2T_Delayer norb_std_32b2t_delayer_1 (
    .SIGIN(rom_1_data), .CLOCK(clock_2_out), .SIGOUT(norb_std_32b2t_delayer_1_sigout));
  Instance_20_to_32 instance_20_to_32_1 (
    .in_1(norb_std_jtype_splitter_1_imm), .in_2({32{1'b1}}), .in_3(1'b0), .out_4(instance_20_to_32_1_out_4));
  buf or_5 (or_5_out, clock_4_out);  // OR_Gate
  Multiplexer #(.width(5)) multiplexer_1 (.in0(or_1_out), .in1({5{1'b1}}), .out(multiplexer_1_out), .sel(or_5_out));
  Multiplexer #(.width(5)) multiplexer_2 (.in0(or_2_out), .in1({5{1'b1}}), .out(multiplexer_2_out), .sel(clock_2_out));
  FL_CU_32B_Splitter fl_cu_32b_splitter_1 (
    .In32B(norb_std_32b2t_delayer_1_sigout), .LUI(fl_cu_32b_splitter_1_lui), .JAL(fl_cu_32b_splitter_1_jal),
    .BEQ(fl_cu_32b_splitter_1_beq), .LW(fl_cu_32b_splitter_1_lw), .ALUI(fl_cu_32b_splitter_1_alui),
    .ALU(fl_cu_32b_splitter_1_alu), .SW(fl_cu_32b_splitter_1_sw));  // open: NOOP
  assign or_6_out = instance_20_to_32_1_out_4 | and_1_out;  // OR_Gate or_6, 32 bits wide
  Norb_STD_32B_Selector norb_std_32b_selector_1 (
    .In32B(norb_std_32b2t_delayer_1_sigout), .InSelect(fl_cu_32b_splitter_1_lui),
    .Out32B(norb_std_32b_selector_1_out32b));
  Norb_STD_32B_Selector norb_std_32b_selector_2 (
    .In32B(norb_std_32b2t_delayer_1_sigout), .InSelect(fl_cu_32b_splitter_1_jal),
    .Out32B(norb_std_32b_selector_2_out32b));
  Norb_STD_32B_Selector norb_std_32b_selector_3 (
    .In32B(norb_std_32b2t_delayer_1_sigout), .InSelect(fl_cu_32b_splitter_1_beq),
    .Out32B(norb_std_32b_selector_3_out32b));
  Norb_STD_32B_Selector norb_std_32b_selector_4 (
    .In32B(norb_std_32b2t_delayer_1_sigout), .InSelect(fl_cu_32b_splitter_1_lw),
    .Out32B(norb_std_32b_selector_4_out32b));
  Norb_STD_32B_Selector norb_std_32b_selector_5 (
    .In32B(norb_std_32b2t_delayer_1_sigout), .InSelect(fl_cu_32b_splitter_1_alui),
    .Out32B(norb_std_32b_selector_5_out32b));
  Norb_STD_32B_Selector norb_std_32b_selector_6 (
    .In32B(norb_std_32b2t_delayer_1_sigout), .InSelect(fl_cu_32b_splitter_1_alu),
    .Out32B(norb_std_32b_selector_6_out32b));
  Norb_STD_32B_Selector norb_std_32b_selector_7 (
    .In32B(norb_std_32b2t_delayer_1_sigout), .InSelect(fl_cu_32b_splitter_1_sw));  // open: Out32B
  New_Register new_register_1 (
    .DATA_IN(or_3_out), .CHOOSE(2'b11), .PRINT_ADDRESS1(multiplexer_2_out), .PRINT_ADDRESS2(or_4_out),
    .WRITEALLOW(clock_4_out), .Clock_sign(clock_4_out), .ADDRESS(multiplexer_1_out),
    .PRINT_1(new_register_1_print_1), .PRINT_2(new_register_1_print_2));
  Norb_STD_32B_Matcher norb_std_32b_matcher_1 (
    .In32B_A({32{1'b0}}), .In32B_B(or_6_out), .OutAEqB(norb_std_32b_matcher_1_outaeqb));
  Instance_20_to_32 instance_20_to_32_2 (
    .in_1(norb_std_utype_splitter_1_imm), .in_2({32{1'b1}}), .in_3(1'b0), .out_4(instance_20_to_32_2_out_4));
  Norb_STD_32B_Selector norb_std_32b_selector_8 (
    .In32B(32'h1), .InSelect(norb_std_32b_matcher_1_outaeqb), .Out32B(norb_std_32b_selector_8_out32b));
  Norb_STD_UType_Splitter norb_std_utype_splitter_1 (
    .IN32B_INS(norb_std_32b_selector_1_out32b), .rd(norb_std_utype_splitter_1_rd),
    .imm(norb_std_utype_splitter_1_imm));  // open: opcode
  Norb_STD_JType_Splitter norb_std_jtype_splitter_1 (
    .IN32B_INS(norb_std_32b_selector_2_out32b), .imm(norb_std_jtype_splitter_1_imm));  // open: opcode, rd
  Norb_STD_IType_Splitter norb_std_itype_splitter_1 (
    .IN32B_INS(norb_std_32b_selector_3_out32b), .imm(norb_std_itype_splitter_1_imm),
    .rs1(norb_std_itype_splitter_1_rs1), .rd(norb_std_itype_splitter_1_rd));  // open: opcode, func7, func3
  Norb_STD_IType_Splitter norb_std_itype_splitter_2 (
    .IN32B_INS(norb_std_32b_selector_4_out32b), .imm(norb_std_itype_splitter_2_imm),
    .rs1(norb_std_itype_splitter_2_rs1), .rd(norb_std_itype_splitter_2_rd));  // open: opcode, func7, func3
  Norb_STD_IType_Splitter norb_std_itype_splitter_3 (
    .IN32B_INS(norb_std_32b_selector_5_out32b), .func7(norb_std_itype_splitter_3_func7),
    .imm(norb_std_itype_splitter_3_imm), .rs1(norb_std_itype_splitter_3_rs1),
    .rd(norb_std_itype_splitter_3_rd), .func3(norb_std_itype_splitter_3_func3));  // open: opcode
  Norb_STD_RType_Splitter norb_std_rtype_splitter_1 (
    .IN32B_INS(norb_std_32b_selector_6_out32b), .func7(norb_std_rtype_splitter_1_func7),
    .rs2(norb_std_rtype_splitter_1_rs2), .rs1(norb_std_rtype_splitter_1_rs1),
    .rd(norb_std_rtype_splitter_1_rd), .func3(norb_std_rtype_splitter_1_func3));  // open: opcode
  assign or_7_out = norb_std_32b_selector_8_out32b | or_6_out;  // OR_Gate or_7, 32 bits wide
  Norb_STD_32B2T_Delayer norb_std_32b2t_delayer_2 (
    .SIGIN(new_register_1_print_1), .CLOCK(clock_3_out), .SIGOUT(norb_std_32b2t_delayer_2_sigout));
  assign or_8_out = norb_std_itype_splitter_3_func7 | norb_std_rtype_splitter_1_func7;  // OR_Gate or_8, 7 bits wide
  assign or_9_out = norb_std_itype_splitter_3_func3 | norb_std_rtype_splitter_1_func3;  // OR_Gate or_9, 3 bits wide
  Norb_ALU_32B_CRA norb_alu_32b_cra_1 (
    .InA(or_7_out), .InB(new_register_1_print_1), .OutAAddB(norb_alu_32b_cra_1_outaaddb));  // open: FlagOverflow
  Norb_STD_32B8B_Splitter norb_std_32b8b_splitter_1 (
    .In32B(norb_std_32b2t_delayer_2_sigout), .Out0(norb_std_32b8b_splitter_1_out0));  // open: Out1, Out2, Out3
  Norb_ALU_32B_CRA norb_alu_32b_cra_2 (
    .InA(norb_std_itype_splitter_2_imm), .InB(new_register_1_print_1), .OutAAddB(norb_alu_32b_cra_2_outaaddb));  // open: FlagOverflow
  assign or_10_out = new_register_1_print_2 | norb_std_itype_splitter_3_imm;  // OR_Gate or_10, 32 bits wide
  ROM #(.dataWidth(32)) rom_1 (.addr(norb_std_32b8b_splitter_1_out0), .data(rom_1_data));
  Norb_STD_32B_Matcher norb_std_32b_matcher_2 (
    .In32B_A(new_register_1_print_1), .In32B_B(new_register_1_print_2),
    .OutAEqB(norb_std_32b_matcher_2_outaeqb));
  Norb_STD_32B2T_Delayer norb_std_32b2t_delayer_3 (
    .SIGIN(norb_alu_32b_cra_1_outaaddb), .CLOCK(clock_3_out), .SIGOUT(norb_std_32b2t_delayer_3_sigout));
  Norb_STD_1T2_Decoder norb_std_1t2_decoder_1 (
    .In1B(norb_std_32b_matcher_2_outaeqb), .Out1(norb_std_1t2_decoder_1_out1),
    .Out0(norb_std_1t2_decoder_1_out0));
  Norb_ALU_RISCV_ALU norb_alu_riscv_alu_1 (
    .InFunc7(or_8_out), .InFunc3(or_9_out), .InA(new_register_1_print_1), .InB(or_10_out),
    .ALU_OUTPUT(norb_alu_riscv_alu_1_alu_output));  // open: ZERO_FLAG
  Norb_STD_32B_Selector norb_std_32b_selector_9 (
    .In32B({32{1'b1}}), .InSelect(norb_std_1t2_decoder_1_out1), .Out32B(norb_std_32b_selector_9_out32b));
  Norb_STD_32B_Selector norb_std_32b_selector_10 (
    .In32B({32{1'b0}}), .InSelect(norb_std_1t2_decoder_1_out0), .Out32B(norb_std_32b_selector_10_out32b));
  assign or_11_out = norb_std_32b_selector_9_out32b | norb_std_32b_selector_10_out32b;  // OR_Gate or_11, 32 bits wide
  assign and_1_out = or_11_out & norb_std_itype_splitter_1_imm;  // AND_Gate and_1, 32 bits wide

  // Notes on the sheet:
  //   Global Clock
  //   PhaseA Clock
  //   PhaseB Clock
  //   PhaseC Clock
  //   ALUI 
endmodule

module clock_test (
);

  wire clock_1_out, clock_2_out, clock_3_out, clock_4_out;

  Clock #(.highDuration(2), .lowDuration(2)) clock_1 (.out(clock_1_out));
  Clock #(.highDuration(2), .lowDuration(10), .phaseOffset(8)) clock_2 (.out(clock_2_out));
  Clock #(.highDuration(2), .lowDuration(10), .phaseOffset(4)) clock_3 (.out(clock_3_out));
  Clock #(.highDuration(2), .lowDuration(10)) clock_4 (.out(clock_4_out));

  // Notes on the sheet:
  //   Global Clock
  //   PhaseA Clock
  //   PhaseB Clock
  //   PhaseC Clock
endmodule

module Norb_CPU (
  input  Reboot,
  input  [7:0] in_2,
  input  in_3
);

  wire adder_1_cout, and_1_out, and_2_out, and_3_out, clock_1_out, clock_2_out, clock_3_out, clock_4_out,
       clock_5_out, clock_6_out, clock_7_out, clock_8_out, clock_9_out, clock_10_out,
       fl_cu_32b_splitter_1_alu, fl_cu_32b_splitter_1_alui, fl_cu_32b_splitter_1_beq,
       fl_cu_32b_splitter_1_jal, fl_cu_32b_splitter_1_lui, fl_cu_32b_splitter_1_lw,
       fl_cu_32b_splitter_1_noop, fl_cu_32b_splitter_1_sw, multiplexer_18_out, multiplexer_19_out,
       norb_alu_riscv_alu_1_zero_flag, norb_std_1b2t_delayer_1_sigout, not_1_out, not_2_out, or_1_out,
       or_2_out, or_3_out, or_4_out, or_5_out, or_7_out, or_9_out, or_10_out, or_11_out, or_14_out,
       or_15_out, RAM_AD_out, REG_RE_out, REG_WE_out;
  wire [1:0] multiplexer_17_out;
  wire [2:0] ALU_func3, ALUI_func3, BEQ_func3, F3_out, LW_func3;
  wire [4:0] ALU_rd, ALU_rs1, ALU_rs2, ALUI_rd, ALUI_rs1, BEQ_rd, BEQ_rs1, JAL_rd, LUI_rd, LW_rd, LW_rs1,
       multiplexer_12_out, multiplexer_15_out, multiplexer_16_out, RD_out, RS1_out, RS2_out, SW_rd, SW_rs1;
  wire [6:0] ALU_func7, ALUI_func7, BEQ_func7, F7_out;
  wire [7:0] adder_1_out, bit_extender_1_out, multiplexer_20_out, norb_std_8b2t_delayer_1_sigout;
  wire [19:0] JAL_imm, LUI_imm;
  wire [31:0] ALUI_imm, BEQ_imm, bit_extender_2_out, bit_extender_3_out, IMM_out, LW_imm, multiplexer_1_out,
       multiplexer_2_out, multiplexer_3_out, multiplexer_4_out, multiplexer_5_out, multiplexer_6_out,
       multiplexer_7_out, multiplexer_8_out, multiplexer_9_out, multiplexer_10_out, multiplexer_11_out,
       multiplexer_13_out, multiplexer_14_out, multiplexer_21_out, multiplexer_22_out, multiplexer_23_out,
       multiplexer_24_out, new_register_1_print_1, new_register_1_print_2, norb_alu_32b_cra_1_outaaddb,
       norb_alu_32b_cra_2_outaaddb, norb_alu_riscv_alu_1_alu_output, norb_std_32b2t_delayer_1_sigout,
       norb_std_32b2t_delayer_2_sigout, or_6_out, or_8_out, or_12_out, or_13_out, ram_1_dout, register_1_q,
       rom_1_data, rom_2_data, SW_imm;

  ROM #(.dataWidth(32)) rom_1 (.addr(in_2), .data(rom_1_data));
  Clock #(.highDuration(2), .lowDuration(12), .phaseOffset(8)) clock_1 (.out(clock_1_out));
  Clock #(.highDuration(2), .lowDuration(12), .phaseOffset(4)) clock_2 (.out(clock_2_out));
  Clock #(.highDuration(2), .lowDuration(12)) clock_3 (.out(clock_3_out));
  Clock #(.highDuration(2), .lowDuration(12), .phaseOffset(7)) clock_4 (.out(clock_4_out));
  Clock #(.highDuration(2), .lowDuration(12), .phaseOffset(3)) clock_5 (.out(clock_5_out));
  Clock #(.highDuration(2), .lowDuration(12), .phaseOffset(13)) clock_6 (.out(clock_6_out));
  Register #(.trigger("high"), .width(32)) register_1 (
    .D(ram_1_dout), .en(clock_1_out), .clk(clock_1_out), .Q(register_1_q), .clr(clock_3_out));
  Multiplexer #(.width(32)) multiplexer_1 (.in0(rom_1_data), .in1(register_1_q), .out(multiplexer_1_out), .sel(in_3));
  and and_1 (and_1_out, clock_2_out, ~Reboot);  // AND_Gate
  Multiplexer #(.width(32)) multiplexer_2 (
    .in0({32{1'b0}}), .in1(multiplexer_1_out), .out(multiplexer_2_out), .sel(and_1_out));
  FL_CU_32B_Splitter fl_cu_32b_splitter_1 (
    .In32B(multiplexer_2_out), .LUI(fl_cu_32b_splitter_1_lui), .JAL(fl_cu_32b_splitter_1_jal),
    .BEQ(fl_cu_32b_splitter_1_beq), .LW(fl_cu_32b_splitter_1_lw), .ALUI(fl_cu_32b_splitter_1_alui),
    .ALU(fl_cu_32b_splitter_1_alu), .SW(fl_cu_32b_splitter_1_sw), .NOOP(fl_cu_32b_splitter_1_noop));
  or REG_RE (REG_RE_out, fl_cu_32b_splitter_1_jal, fl_cu_32b_splitter_1_beq, fl_cu_32b_splitter_1_lw, fl_cu_32b_splitter_1_alui, fl_cu_32b_splitter_1_alu);
  or REG_WE (REG_WE_out, fl_cu_32b_splitter_1_lui, fl_cu_32b_splitter_1_jal, fl_cu_32b_splitter_1_beq, fl_cu_32b_splitter_1_alui, fl_cu_32b_splitter_1_alu);
  or RAM_AD (RAM_AD_out, fl_cu_32b_splitter_1_lw, fl_cu_32b_splitter_1_sw);
  or or_1 (or_1_out, RAM_AD_out, clock_1_out);
  or or_2 (or_2_out, fl_cu_32b_splitter_1_alui, fl_cu_32b_splitter_1_jal);
  Multiplexer #(.width(32)) multiplexer_3 (
    .in0({32{1'b0}}), .in1(multiplexer_2_out), .out(multiplexer_3_out), .sel(fl_cu_32b_splitter_1_lui));
  Multiplexer #(.width(32)) multiplexer_4 (
    .in0({32{1'b0}}), .in1(multiplexer_2_out), .out(multiplexer_4_out), .sel(fl_cu_32b_splitter_1_jal));
  Multiplexer #(.width(32)) multiplexer_5 (
    .in0({32{1'b0}}), .in1(multiplexer_2_out), .out(multiplexer_5_out), .sel(fl_cu_32b_splitter_1_beq));
  Multiplexer #(.width(32)) multiplexer_6 (
    .in0({32{1'b0}}), .in1(multiplexer_2_out), .out(multiplexer_6_out), .sel(fl_cu_32b_splitter_1_lw));
  Multiplexer #(.width(32)) multiplexer_7 (
    .in0({32{1'b0}}), .in1(multiplexer_2_out), .out(multiplexer_7_out), .sel(fl_cu_32b_splitter_1_alui));
  Multiplexer #(.width(32)) multiplexer_8 (
    .in0({32{1'b0}}), .in1(multiplexer_2_out), .out(multiplexer_8_out), .sel(fl_cu_32b_splitter_1_alu));
  Multiplexer #(.width(32)) multiplexer_9 (
    .in0({32{1'b0}}), .in1(multiplexer_2_out), .out(multiplexer_9_out), .sel(fl_cu_32b_splitter_1_sw));
  or or_3 (or_3_out, REG_RE_out, or_5_out);
  and and_2 (and_2_out, fl_cu_32b_splitter_1_beq, norb_alu_riscv_alu_1_zero_flag);
  or or_4 (or_4_out, and_2_out, fl_cu_32b_splitter_1_jal);
  or or_5 (or_5_out, clock_3_out, clock_1_out, clock_6_out);
  Multiplexer #(.width(32)) multiplexer_10 (
    .in0({32{1'b0}}), .in1(new_register_1_print_1), .out(multiplexer_10_out), .sel(or_1_out));
  Norb_STD_UType_Splitter LUI (.IN32B_INS(multiplexer_3_out), .rd(LUI_rd), .imm(LUI_imm));  // open: opcode
  Norb_STD_JType_Splitter JAL (.IN32B_INS(multiplexer_4_out), .rd(JAL_rd), .imm(JAL_imm));  // open: opcode
  Norb_STD_IType_Splitter BEQ (
    .IN32B_INS(multiplexer_5_out), .func7(BEQ_func7), .imm(BEQ_imm), .rs1(BEQ_rs1), .rd(BEQ_rd),
    .func3(BEQ_func3));  // open: opcode
  Norb_STD_IType_Splitter LW (
    .IN32B_INS(multiplexer_6_out), .imm(LW_imm), .rs1(LW_rs1), .rd(LW_rd), .func3(LW_func3));  // open: opcode, func7
  Norb_STD_IType_Splitter ALUI (
    .IN32B_INS(multiplexer_7_out), .func7(ALUI_func7), .imm(ALUI_imm), .rs1(ALUI_rs1), .rd(ALUI_rd),
    .func3(ALUI_func3));  // open: opcode
  Norb_STD_RType_Splitter ALU (
    .IN32B_INS(multiplexer_8_out), .func7(ALU_func7), .rs2(ALU_rs2), .rs1(ALU_rs1), .rd(ALU_rd),
    .func3(ALU_func3));  // open: opcode
  Norb_STD_IType_Splitter SW (
    .IN32B_INS(multiplexer_9_out), .imm(SW_imm), .rs1(SW_rs1), .rd(SW_rd));  // open: opcode, func7, func3
  assign RD_out = LUI_rd | JAL_rd | BEQ_rd | SW_rd | LW_rd | ALUI_rd | ALU_rd;  // OR_Gate RD, 5 bits wide
  Norb_ALU_32B_CRA norb_alu_32b_cra_1 (
    .InA(multiplexer_10_out), .InB(IMM_out), .OutAAddB(norb_alu_32b_cra_1_outaaddb));  // open: FlagOverflow
  Bit_Extender #(.in_width(32), .out_width(8), .\type ("zero")) bit_extender_1 (
    .in(norb_alu_32b_cra_1_outaaddb), .out(bit_extender_1_out));
  Multiplexer #(.width(32)) multiplexer_11 (.in0(IMM_out), .in1({32{1'b0}}), .out(multiplexer_11_out), .sel(or_2_out));
  assign IMM_out = bit_extender_2_out | bit_extender_3_out | BEQ_imm | or_6_out | ALUI_imm;  // OR_Gate IMM, 32 bits wide
  assign bit_extender_2_out = {{12{LUI_imm[19]}}, LUI_imm};  // Bit_Extender bit_extender_2
  assign bit_extender_3_out = {{12{JAL_imm[19]}}, JAL_imm};  // Bit_Extender bit_extender_3
  assign or_6_out = LW_imm | SW_imm;  // OR_Gate or_6, 32 bits wide
  Multiplexer #(.width(5)) multiplexer_12 (
    .in0(RS1_out), .in1({5{1'b1}}), .out(multiplexer_12_out), .sel(fl_cu_32b_splitter_1_jal));
  assign RS1_out = BEQ_rs1 | LW_rs1 | SW_rs1 | ALUI_rs1 | ALU_rs1;  // OR_Gate RS1, 5 bits wide
  Multiplexer #(.width(32)) multiplexer_13 (
    .in0(IMM_out), .in1(new_register_1_print_2), .out(multiplexer_13_out), .sel(fl_cu_32b_splitter_1_alu));
  assign RS2_out = {5{1'b0}} | ALU_rs2;  // OR_Gate RS2, 5 bits wide
  assign F7_out = BEQ_func7 | ALUI_func7 | ALU_func7;  // OR_Gate F7, 7 bits wide
  Multiplexer #(.width(32)) multiplexer_14 (
    .in0({32{1'b0}}), .in1(ram_1_dout), .out(multiplexer_14_out), .sel(fl_cu_32b_splitter_1_sw));
  assign F3_out = BEQ_func3 | LW_func3 | ALUI_func3 | ALU_func3;  // OR_Gate F3, 3 bits wide
  or or_7 (or_7_out, clock_1_out, clock_3_out, clock_6_out);
  assign or_8_out = norb_alu_riscv_alu_1_alu_output | multiplexer_11_out | multiplexer_14_out;  // OR_Gate or_8, 32 bits wide
  or or_9 (or_9_out, clock_3_out, clock_6_out, or_14_out);
  Multiplexer #(.width(5)) multiplexer_15 (
    .in0(multiplexer_12_out), .in1({5{1'b1}}), .out(multiplexer_15_out), .sel(or_7_out));
  or or_10 (or_10_out, or_9_out, fl_cu_32b_splitter_1_jal);
  Multiplexer #(.width(5)) multiplexer_16 (.in0(RD_out), .in1({5{1'b1}}), .out(multiplexer_16_out), .sel(or_10_out));
  Clock #(.lowDuration(13), .phaseOffset(11)) clock_7 (.out(clock_7_out));
  Multiplexer #(.width(2)) multiplexer_17 (.in0(2'b00), .in1(2'b11), .out(multiplexer_17_out), .sel(or_3_out));
  Multiplexer multiplexer_18 (.in0(REG_WE_out), .in1(1'b1), .out(multiplexer_18_out), .sel(or_9_out));
  Clock #(.lowDuration(13), .phaseOffset(13)) clock_8 (.out(clock_8_out));
  or or_11 (or_11_out, clock_5_out, clock_7_out);
  assign or_12_out = or_8_out | multiplexer_24_out;  // OR_Gate or_12, 32 bits wide
  assign or_13_out = norb_alu_riscv_alu_1_alu_output | IMM_out;  // OR_Gate or_13, 32 bits wide
  Multiplexer multiplexer_19 (.in0(fl_cu_32b_splitter_1_sw), .in1(and_3_out), .out(multiplexer_19_out), .sel(Reboot));
  not not_1 (not_1_out, Reboot);
  RAM #(.dataWidth(32), .trigger("high")) ram_1 (
    .addr(multiplexer_20_out), .we(multiplexer_19_out), .oe(not_1_out), .din(multiplexer_21_out),
    .dout(ram_1_dout));
  Multiplexer #(.width(8)) multiplexer_20 (
    .in0(bit_extender_1_out), .in1(adder_1_out), .out(multiplexer_20_out), .sel(Reboot));
  Multiplexer #(.width(32)) multiplexer_21 (
    .in0(new_register_1_print_1), .in1(rom_2_data), .out(multiplexer_21_out), .sel(Reboot));
  New_Register new_register_1 (
    .DATA_IN(or_12_out), .CHOOSE(multiplexer_17_out), .PRINT_ADDRESS1(multiplexer_15_out),
    .PRINT_ADDRESS2(RS2_out), .WRITEALLOW(multiplexer_18_out), .Clock_sign(or_11_out),
    .ADDRESS(multiplexer_16_out), .PRINT_1(new_register_1_print_1), .PRINT_2(new_register_1_print_2));
  Norb_ALU_RISCV_ALU norb_alu_riscv_alu_1 (
    .InFunc7(F7_out), .InFunc3(F3_out), .InA(new_register_1_print_1), .InB(multiplexer_13_out),
    .ZERO_FLAG(norb_alu_riscv_alu_1_zero_flag), .ALU_OUTPUT(norb_alu_riscv_alu_1_alu_output));
  Multiplexer #(.width(32)) multiplexer_22 (.in0(32'h1), .in1({32{1'b0}}), .out(multiplexer_22_out), .sel(Reboot));
  Norb_STD_1B2T_Delayer norb_std_1b2t_delayer_1 (
    .SIGIN(or_4_out), .CLOCK(clock_8_out), .SIGOUT(norb_std_1b2t_delayer_1_sigout));
  Norb_STD_32B2T_Delayer norb_std_32b2t_delayer_1 (
    .SIGIN(or_13_out), .CLOCK(clock_8_out), .SIGOUT(norb_std_32b2t_delayer_1_sigout));
  Norb_STD_32B2T_Delayer norb_std_32b2t_delayer_2 (
    .SIGIN(new_register_1_print_1), .CLOCK(clock_8_out), .SIGOUT(norb_std_32b2t_delayer_2_sigout));
  Multiplexer #(.width(32)) multiplexer_23 (
    .in0(multiplexer_22_out), .in1(norb_std_32b2t_delayer_1_sigout), .out(multiplexer_23_out),
    .sel(norb_std_1b2t_delayer_1_sigout));
  or or_14 (or_14_out, clock_6_out, clock_9_out);
  Norb_ALU_32B_CRA norb_alu_32b_cra_2 (
    .InA(multiplexer_23_out), .InB(norb_std_32b2t_delayer_2_sigout), .OutAAddB(norb_alu_32b_cra_2_outaaddb));  // open: FlagOverflow
  or or_15 (or_15_out, clock_6_out, clock_9_out, clock_3_out);
  Multiplexer #(.width(32)) multiplexer_24 (
    .in0({32{1'b0}}), .in1(norb_alu_32b_cra_2_outaaddb), .out(multiplexer_24_out), .sel(or_15_out));
  Clock #(.lowDuration(13), .phaseOffset(12)) clock_9 (.out(clock_9_out));
  ROM #(.dataWidth(32)) rom_2 (.addr(adder_1_out), .data(rom_2_data));
  Clock clock_10 (.out(clock_10_out));
  and and_3 (and_3_out, clock_10_out, not_2_out);
  not not_2 (not_2_out, adder_1_cout);
  Norb_STD_8B2T_Delayer norb_std_8b2t_delayer_1 (
    .SIGIN(adder_1_out), .CLOCK(and_3_out), .SIGOUT(norb_std_8b2t_delayer_1_sigout));
  Adder adder_1 (.a(norb_std_8b2t_delayer_1_sigout), .b(8'h1), .out(adder_1_out), .cout(adder_1_cout));  // open: cin

  // Notes on the sheet:
  //   Clock
  //   Data
  //   Global Clock
  //   PhaseA Clock
  //   PhaseB Clock
  //   PhaseC Clock
  //   PhaseA Clock
  //   PhaseB Clock
  //   PhaseC Clock
  //   contents of rom_1 (hex, n*v repeats v):
  //   0 10b7 1137 2081b3 10093 18113 f8f13 ffcf0f93
  //   Instruction_Memory_Test_Purposes
  //   RAM_READ
  //   ALU_OUT
  //   ZERO_FLAG
  //   PRINT2
  //   PRINT1
  //   RAM_WE
  //   RAM_RE
  //   32B
  //   RAM_ADDR
  //   ALU2
  //   ALU1
  //   REG_IN
  //   RAM_VAL
  //   FLAG
  //   OFFSET
  //   contents of rom_2 (hex, n*v repeats v):
  //   0 10b7 1137 2081b3 10093 18113 f8f13 ffcf0f93 15*0 1 44*0 1 4*0 1 1
  //   Flashboot
endmodule

module Norb_ALU_RISCV_ALU_Dummy (
  input  [6:0] InFunc7,
  input  [2:0] InFunc3,
  input  [31:0] InA,
  input  [31:0] InB,
  output ZERO_FLAG,
  output [31:0] ALU_OUTPUT
);


  assign ALU_OUTPUT = {32{1'b0}};
  assign ZERO_FLAG = 1'b0;
endmodule

module GRS_Delayer (
  input  SIGIN,
  input  CLOCK_IN,
  input  A,
  input  in_4,
  output SIGOUT,
  output out_6
);

  wire d_ff_2_q, not_1_out;

  // OR_Gate or_1 has open pins: in0=SIGIN, in1=CLOCK_IN, out=open
  D_Flip_Flop d_ff_1 (.D(A), .clk(in_4), .Q(out_6));  // open: Qn, preset, reset
  D_Flip_Flop #(.trigger("low")) d_ff_2 (.D(SIGIN), .clk(CLOCK_IN), .Q(d_ff_2_q));  // open: Qn, preset, reset
  D_Flip_Flop #(.trigger("falling")) d_ff_3 (.D(d_ff_2_q), .clk(not_1_out), .Q(SIGOUT));  // open: Qn, preset, reset
  not not_1 (not_1_out, CLOCK_IN);
endmodule

module GRS_BOOT (
  input  [7:0] in_1
);

  wire adder_1_cout, and_1_out, clock_1_out, not_1_out;
  wire [7:0] adder_1_out, norb_std_8b2t_delayer_1_sigout;

  Clock clock_1 (.out(clock_1_out));
  and and_1 (and_1_out, clock_1_out, not_1_out);
  not not_1 (not_1_out, adder_1_cout);
  Norb_STD_8B2T_Delayer norb_std_8b2t_delayer_1 (
    .SIGIN(adder_1_out), .CLOCK(and_1_out), .SIGOUT(norb_std_8b2t_delayer_1_sigout));
  Adder adder_1 (.a(norb_std_8b2t_delayer_1_sigout), .b(in_1), .out(adder_1_out), .cout(adder_1_cout));  // open: cin
  ROM #(.dataWidth(32)) rom_1 (.addr(adder_1_out));  // open: data

  // Notes on the sheet:
  //   contents of rom_1 (hex, n*v repeats v):
  //   1 22*0 1 44*0 1 4*0 1 1
endmodule
