// Logisim project GRS_Register.circ as structural Verilog: 17 circuits, main circuit GRS_Register_Dtouch
module Norb_STD_1B2T_Delayer (
  input  SIGIN,
  input  CLOCK,
  output SIGOUT
);

  wire d_ff_1_q, not_1_out;

  D_Flip_Flop d_ff_1 (.D(SIGIN), .clk(CLOCK), .Q(d_ff_1_q));  // open: Qn, preset, reset
  D_Flip_Flop d_ff_2 (.D(d_ff_1_q), .clk(not_1_out), .Q(SIGOUT));  // open: Qn, preset, reset
  not not_1 (not_1_out, CLOCK);
endmodule

module Norb_STD_2B2T_Delayer (
  input  [1:0] SIGIN,
  input  CLOCK,
  output [1:0] SIGOUT
);

  Norb_STD_1B2T_Delayer norb_std_1b2t_delayer_1 (.SIGIN(SIGIN[0]), .CLOCK(CLOCK), .SIGOUT(SIGOUT[0]));
  Norb_STD_1B2T_Delayer norb_std_1b2t_delayer_2 (.SIGIN(SIGIN[1]), .CLOCK(CLOCK), .SIGOUT(SIGOUT[1]));
endmodule

module Norb_STD_8B2T_Delayer (
  input  [7:0] SIGIN,
  input  CLOCK,
  output [7:0] SIGOUT
);

  Norb_STD_2B2T_Delayer norb_std_2b2t_delayer_1 (.SIGIN(SIGIN[1:0]), .CLOCK(CLOCK), .SIGOUT(SIGOUT[1:0]));
  Norb_STD_2B2T_Delayer norb_std_2b2t_delayer_2 (.SIGIN(SIGIN[3:2]), .CLOCK(CLOCK), .SIGOUT(SIGOUT[3:2]));
  Norb_STD_2B2T_Delayer norb_std_2b2t_delayer_3 (.SIGIN(SIGIN[5:4]), .CLOCK(CLOCK), .SIGOUT(SIGOUT[5:4]));
  Norb_STD_2B2T_Delayer norb_std_2b2t_delayer_4 (.SIGIN(SIGIN[7:6]), .CLOCK(CLOCK), .SIGOUT(SIGOUT[7:6]));
endmodule

module Norb_STD_32B2T_Delayer (
  input  [31:0] SIGIN,
  input  CLOCK,
  output [31:0] SIGOUT
);

  Norb_STD_8B2T_Delayer norb_std_8b2t_delayer_1 (.SIGIN(SIGIN[7:0]), .CLOCK(CLOCK), .SIGOUT(SIGOUT[7:0]));
  Norb_STD_8B2T_Delayer norb_std_8b2t_delayer_2 (.SIGIN(SIGIN[15:8]), .CLOCK(CLOCK), .SIGOUT(SIGOUT[15:8]));
  Norb_STD_8B2T_Delayer norb_std_8b2t_delayer_3 (.SIGIN(SIGIN[23:16]), .CLOCK(CLOCK), .SIGOUT(SIGOUT[23:16]));
  Norb_STD_8B2T_Delayer norb_std_8b2t_delayer_4 (.SIGIN(SIGIN[31:24]), .CLOCK(CLOCK), .SIGOUT(SIGOUT[31:24]));
endmodule

module GRS_Register_Dtouch (
  input  ALLOW,
  input  Data,
  output Q,
  output out_4
);

  wire and_1_out, and_2_out, not_1_out;

  not not_1 (not_1_out, Data);
  and and_1 (and_1_out, not_1_out, ALLOW);
  and and_2 (and_2_out, ALLOW, Data);
  nor nor_1 (Q, and_1_out, out_4);
  nor nor_2 (out_4, Q, and_2_out);
endmodule

module GRS_Register_4B (
  input  [31:0] Data1,
  input  ALLOW,
  output [31:0] Output1
);

  GRS_Register_Dtouch grs_register_dtouch_1 (.ALLOW(ALLOW), .Data(Data1[31]), .Q(Output1[31]));  // open: out_4
  GRS_Register_Dtouch grs_register_dtouch_2 (.ALLOW(ALLOW), .Data(Data1[30]), .Q(Output1[30]));  // open: out_4
  GRS_Register_Dtouch grs_register_dtouch_3 (.ALLOW(ALLOW), .Data(Data1[29]), .Q(Output1[29]));  // open: out_4
  GRS_Register_Dtouch grs_register_dtouch_4 (.ALLOW(ALLOW), .Data(Data1[28]), .Q(Output1[28]));  // open: out_4
  GRS_Register_Dtouch grs_register_dtouch_5 (.ALLOW(ALLOW), .Data(Data1[27]), .Q(Output1[27]));  // open: out_4
  GRS_Register_Dtouch grs_register_dtouch_6 (.ALLOW(ALLOW), .Data(Data1[26]), .Q(Output1[26]));  // open: out_4
  GRS_Register_Dtouch grs_register_dtouch_7 (.ALLOW(ALLOW), .Data(Data1[25]), .Q(Output1[25]));  // open: out_4
  GRS_Register_Dtouch grs_register_dtouch_8 (.ALLOW(ALLOW), .Data(Data1[24]), .Q(Output1[24]));  // open: out_4
  GRS_Register_Dtouch grs_register_dtouch_9 (.ALLOW(ALLOW), .Data(Data1[23]), .Q(Output1[23]));  // open: out_4
  GRS_Register_Dtouch grs_register_dtouch_10 (.ALLOW(ALLOW), .Data(Data1[22]), .Q(Output1[22]));  // open: out_4
  GRS_Register_Dtouch grs_register_dtouch_11 (.ALLOW(ALLOW), .Data(Data1[21]), .Q(Output1[21]));  // open: out_4
  GRS_Register_Dtouch grs_register_dtouch_12 (.ALLOW(ALLOW), .Data(Data1[20]), .Q(Output1[20]));  // open: out_4
  GRS_Register_Dtouch grs_register_dtouch_13 (.ALLOW(ALLOW), .Data(Data1[19]), .Q(Output1[19]));  // open: out_4
  GRS_Register_Dtouch grs_register_dtouch_14 (.ALLOW(ALLOW), .Data(Data1[18]), .Q(Output1[18]));  // open: out_4
  GRS_Register_Dtouch grs_register_dtouch_15 (.ALLOW(ALLOW), .Data(Data1[17]), .Q(Output1[17]));  // open: out_4
  GRS_Register_Dtouch grs_register_dtouch_16 (.ALLOW(ALLOW), .Data(Data1[16]), .Q(Output1[16]));  // open: out_4
  GRS_Register_Dtouch grs_register_dtouch_17 (.ALLOW(ALLOW), .Data(Data1[15]), .Q(Output1[15]));  // open: out_4
  GRS_Register_Dtouch grs_register_dtouch_18 (.ALLOW(ALLOW), .Data(Data1[14]), .Q(Output1[14]));  // open: out_4
  GRS_Register_Dtouch grs_register_dtouch_19 (.ALLOW(ALLOW), .Data(Data1[13]), .Q(Output1[13]));  // open: out_4
  GRS_Register_Dtouch grs_register_dtouch_20 (.ALLOW(ALLOW), .Data(Data1[12]), .Q(Output1[12]));  // open: out_4
  GRS_Register_Dtouch grs_register_dtouch_21 (.ALLOW(ALLOW), .Data(Data1[11]), .Q(Output1[11]));  // open: out_4
  GRS_Register_Dtouch grs_register_dtouch_22 (.ALLOW(ALLOW), .Data(Data1[10]), .Q(Output1[10]));  // open: out_4
  GRS_Register_Dtouch grs_register_dtouch_23 (.ALLOW(ALLOW), .Data(Data1[9]), .Q(Output1[9]));  // open: out_4
  GRS_Register_Dtouch grs_register_dtouch_24 (.ALLOW(ALLOW), .Data(Data1[8]), .Q(Output1[8]));  // open: out_4
  GRS_Register_Dtouch grs_register_dtouch_25 (.ALLOW(ALLOW), .Data(Data1[7]), .Q(Output1[7]));  // open: out_4
  GRS_Register_Dtouch grs_register_dtouch_26 (.ALLOW(ALLOW), .Data(Data1[6]), .Q(Output1[6]));  // open: out_4
  GRS_Register_Dtouch grs_register_dtouch_27 (.ALLOW(ALLOW), .Data(Data1[5]), .Q(Output1[5]));  // open: out_4
  GRS_Register_Dtouch grs_register_dtouch_28 (.ALLOW(ALLOW), .Data(Data1[4]), .Q(Output1[4]));  // open: out_4
  GRS_Register_Dtouch grs_register_dtouch_29 (.ALLOW(ALLOW), .Data(Data1[3]), .Q(Output1[3]));  // open: out_4
  GRS_Register_Dtouch grs_register_dtouch_30 (.ALLOW(ALLOW), .Data(Data1[2]), .Q(Output1[2]));  // open: out_4
  GRS_Register_Dtouch grs_register_dtouch_31 (.ALLOW(ALLOW), .Data(Data1[1]), .Q(Output1[1]));  // open: out_4
  GRS_Register_Dtouch grs_register_dtouch_32 (.ALLOW(ALLOW), .Data(Data1[0]), .Q(Output1[0]));  // open: out_4
endmodule

module GRS_Registers32 (
  input  [4:0] Inputaddress,
  input  Allow,
  input  [4:0] Outputaddress1,
  input  [31:0] Data32,
  input  [1:0] Choose,
  input  [4:0] Outputaddress2,
  output [31:0] Output1,
  output [31:0] Output2
);

  wire grs_register_writeallow_1_out_3, grs_register_writeallow_1_out_4, grs_register_writeallow_1_out_5,
       grs_register_writeallow_1_out_6, grs_register_writeallow_1_out_7, grs_register_writeallow_1_out_8,
       grs_register_writeallow_1_out_9, grs_register_writeallow_1_out_10, grs_register_writeallow_1_out_11,
       grs_register_writeallow_1_out_12, grs_register_writeallow_1_out_13, grs_register_writeallow_1_out_14,
       grs_register_writeallow_1_out_15, grs_register_writeallow_1_out_16, grs_register_writeallow_1_out_17,
       grs_register_writeallow_1_out_18, grs_register_writeallow_1_out_19, grs_register_writeallow_1_out_20,
       grs_register_writeallow_1_out_21, grs_register_writeallow_1_out_22, grs_register_writeallow_1_out_23,
       grs_register_writeallow_1_out_24, grs_register_writeallow_1_out_25, grs_register_writeallow_1_out_26,
       grs_register_writeallow_1_out_27, grs_register_writeallow_1_out_28, grs_register_writeallow_1_out_29,
       grs_register_writeallow_1_out_30, grs_register_writeallow_1_out_31, grs_register_writeallow_1_out_32,
       grs_register_writeallow_1_out_33, grs_register_writeallow_1_out_34;
  wire [31:0] grs_register_4b_1_output1, grs_register_4b_2_output1, grs_register_4b_3_output1,
       grs_register_4b_4_output1, grs_register_4b_5_output1, grs_register_4b_6_output1,
       grs_register_4b_7_output1, grs_register_4b_8_output1, grs_register_4b_9_output1,
       grs_register_4b_10_output1, grs_register_4b_11_output1, grs_register_4b_12_output1,
       grs_register_4b_13_output1, grs_register_4b_14_output1, grs_register_4b_15_output1,
       grs_register_4b_16_output1, grs_register_4b_17_output1, grs_register_4b_18_output1,
       grs_register_4b_19_output1, grs_register_4b_20_output1, grs_register_4b_21_output1,
       grs_register_4b_22_output1, grs_register_4b_23_output1, grs_register_4b_24_output1,
       grs_register_4b_25_output1, grs_register_4b_26_output1, grs_register_4b_27_output1,
       grs_register_4b_28_output1, grs_register_4b_29_output1, grs_register_4b_30_output1,
       grs_register_4b_31_output1, grs_register_4b_32_output1, grs_register_printallow32_1_out_34,
       grs_register_printallow32_2_out_34;

  Register #(.width(32)) register_1 ();  // open: D, en, clk, Q, clr
  GRS_Register_Writeallow grs_register_writeallow_1 (
    .ADRESS(Inputaddress), .WRITEALLOW(Allow), .out_3(grs_register_writeallow_1_out_3),
    .out_4(grs_register_writeallow_1_out_4), .out_5(grs_register_writeallow_1_out_5),
    .out_6(grs_register_writeallow_1_out_6), .out_7(grs_register_writeallow_1_out_7),
    .out_8(grs_register_writeallow_1_out_8), .out_9(grs_register_writeallow_1_out_9),
    .out_10(grs_register_writeallow_1_out_10), .out_11(grs_register_writeallow_1_out_11),
    .out_12(grs_register_writeallow_1_out_12), .out_13(grs_register_writeallow_1_out_13),
    .out_14(grs_register_writeallow_1_out_14), .out_15(grs_register_writeallow_1_out_15),
    .out_16(grs_register_writeallow_1_out_16), .out_17(grs_register_writeallow_1_out_17),
    .out_18(grs_register_writeallow_1_out_18), .out_19(grs_register_writeallow_1_out_19),
    .out_20(grs_register_writeallow_1_out_20), .out_21(grs_register_writeallow_1_out_21),
    .out_22(grs_register_writeallow_1_out_22), .out_23(grs_register_writeallow_1_out_23),
    .out_24(grs_register_writeallow_1_out_24), .out_25(grs_register_writeallow_1_out_25),
    .out_26(grs_register_writeallow_1_out_26), .out_27(grs_register_writeallow_1_out_27),
    .out_28(grs_register_writeallow_1_out_28), .out_29(grs_register_writeallow_1_out_29),
    .out_30(grs_register_writeallow_1_out_30), .out_31(grs_register_writeallow_1_out_31),
    .out_32(grs_register_writeallow_1_out_32), .out_33(grs_register_writeallow_1_out_33),
    .out_34(grs_register_writeallow_1_out_34));
  GRS_Register_4B grs_register_4b_1 (
    .Data1(Data32), .ALLOW(grs_register_writeallow_1_out_3), .Output1(grs_register_4b_1_output1));
  GRS_Register_4B grs_register_4b_2 (
    .Data1(Data32), .ALLOW(grs_register_writeallow_1_out_4), .Output1(grs_register_4b_2_output1));
  GRS_Register_4B grs_register_4b_3 (
    .Data1(Data32), .ALLOW(grs_register_writeallow_1_out_5), .Output1(grs_register_4b_3_output1));
  GRS_Register_4B grs_register_4b_4 (
    .Data1(Data32), .ALLOW(grs_register_writeallow_1_out_6), .Output1(grs_register_4b_4_output1));
  GRS_Register_4B grs_register_4b_5 (
    .Data1(Data32), .ALLOW(grs_register_writeallow_1_out_7), .Output1(grs_register_4b_5_output1));
  GRS_Register_4B grs_register_4b_6 (
    .Data1(Data32), .ALLOW(grs_register_writeallow_1_out_8), .Output1(grs_register_4b_6_output1));
  GRS_Register_4B grs_register_4b_7 (
    .Data1(Data32), .ALLOW(grs_register_writeallow_1_out_9), .Output1(grs_register_4b_7_output1));
  GRS_Register_4B grs_register_4b_8 (
    .Data1(Data32), .ALLOW(grs_register_writeallow_1_out_10), .Output1(grs_register_4b_8_output1));
  GRS_Register_4B grs_register_4b_9 (
    .Data1(Data32), .ALLOW(grs_register_writeallow_1_out_11), .Output1(grs_register_4b_9_output1));
  GRS_Register_4B grs_register_4b_10 (
    .Data1(Data32), .ALLOW(grs_register_writeallow_1_out_12), .Output1(grs_register_4b_10_output1));
  GRS_Register_4B grs_register_4b_11 (
    .Data1(Data32), .ALLOW(grs_register_writeallow_1_out_13), .Output1(grs_register_4b_11_output1));
  GRS_Register_4B grs_register_4b_12 (
    .Data1(Data32), .ALLOW(grs_register_writeallow_1_out_14), .Output1(grs_register_4b_12_output1));
  GRS_Register_4B grs_register_4b_13 (
    .Data1(Data32), .ALLOW(grs_register_writeallow_1_out_15), .Output1(grs_register_4b_13_output1));
  GRS_Register_4B grs_register_4b_14 (
    .Data1(Data32), .ALLOW(grs_register_writeallow_1_out_16), .Output1(grs_register_4b_14_output1));
  GRS_Register_4B grs_register_4b_15 (
    .Data1(Data32), .ALLOW(grs_register_writeallow_1_out_17), .Output1(grs_register_4b_15_output1));
  GRS_Register_4B grs_register_4b_16 (
    .Data1(Data32), .ALLOW(grs_register_writeallow_1_out_18), .Output1(grs_register_4b_16_output1));
  GRS_Register_4B grs_register_4b_17 (
    .Data1(Data32), .ALLOW(grs_register_writeallow_1_out_19), .Output1(grs_register_4b_17_output1));
  GRS_Register_4B grs_register_4b_18 (
    .Data1(Data32), .ALLOW(grs_register_writeallow_1_out_20), .Output1(grs_register_4b_18_output1));
  GRS_Register_4B grs_register_4b_19 (
    .Data1(Data32), .ALLOW(grs_register_writeallow_1_out_21), .Output1(grs_register_4b_19_output1));
  GRS_Register_4B grs_register_4b_20 (
    .Data1(Data32), .ALLOW(grs_register_writeallow_1_out_22), .Output1(grs_register_4b_20_output1));
  GRS_Register_4B grs_register_4b_21 (
    .Data1(Data32), .ALLOW(grs_register_writeallow_1_out_23), .Output1(grs_register_4b_21_output1));
  GRS_Register_4B grs_register_4b_22 (
    .Data1(Data32), .ALLOW(grs_register_writeallow_1_out_24), .Output1(grs_register_4b_22_output1));
  GRS_Register_4B grs_register_4b_23 (
    .Data1(Data32), .ALLOW(grs_register_writeallow_1_out_25), .Output1(grs_register_4b_23_output1));
  GRS_Register_4B grs_register_4b_24 (
    .Data1(Data32), .ALLOW(grs_register_writeallow_1_out_26), .Output1(grs_register_4b_24_output1));
  GRS_Register_4B grs_register_4b_25 (
    .Data1(Data32), .ALLOW(grs_register_writeallow_1_out_27), .Output1(grs_register_4b_25_output1));
  GRS_Register_4B grs_register_4b_26 (
    .Data1(Data32), .ALLOW(grs_register_writeallow_1_out_28), .Output1(grs_register_4b_26_output1));
  GRS_Register_4B grs_register_4b_27 (
    .Data1(Data32), .ALLOW(grs_register_writeallow_1_out_29), .Output1(grs_register_4b_27_output1));
  GRS_Register_4B grs_register_4b_28 (
    .Data1(Data32), .ALLOW(grs_register_writeallow_1_out_30), .Output1(grs_register_4b_28_output1));
  GRS_Register_4B grs_register_4b_29 (
    .Data1(Data32), .ALLOW(grs_register_writeallow_1_out_31), .Output1(grs_register_4b_29_output1));
  GRS_Register_4B grs_register_4b_30 (
    .Data1(Data32), .ALLOW(grs_register_writeallow_1_out_32), .Output1(grs_register_4b_30_output1));
  GRS_Register_4B grs_register_4b_31 (
    .Data1(Data32), .ALLOW(grs_register_writeallow_1_out_33), .Output1(grs_register_4b_31_output1));
  GRS_Register_4B grs_register_4b_32 (
    .Data1(Data32), .ALLOW(grs_register_writeallow_1_out_34), .Output1(grs_register_4b_32_output1));
  GRS_Register_Printallow32 grs_register_printallow32_1 (
    .Address(Outputaddress1), .in_2(grs_register_4b_1_output1), .in_3(grs_register_4b_2_output1),
    .in_4(grs_register_4b_3_output1), .in_5(grs_register_4b_4_output1), .in_6(grs_register_4b_5_output1),
    .in_7(grs_register_4b_6_output1), .in_8(grs_register_4b_7_output1), .in_9(grs_register_4b_8_output1),
    .in_10(grs_register_4b_9_output1), .in_11(grs_register_4b_10_output1),
    .in_12(grs_register_4b_11_output1), .in_13(grs_register_4b_12_output1),
    .in_14(grs_register_4b_13_output1), .in_15(grs_register_4b_14_output1),
    .in_16(grs_register_4b_15_output1), .in_17(grs_register_4b_16_output1),
    .in_18(grs_register_4b_17_output1), .in_19(grs_register_4b_18_output1),
    .in_20(grs_register_4b_19_output1), .in_21(grs_register_4b_20_output1),
    .in_22(grs_register_4b_21_output1), .in_23(grs_register_4b_22_output1),
    .in_24(grs_register_4b_23_output1), .in_25(grs_register_4b_24_output1),
    .in_26(grs_register_4b_25_output1), .in_27(grs_register_4b_26_output1),
    .in_28(grs_register_4b_27_output1), .in_29(grs_register_4b_28_output1),
    .in_30(grs_register_4b_29_output1), .in_31(grs_register_4b_30_output1),
    .in_32(grs_register_4b_31_output1), .in_33(grs_register_4b_32_output1),
    .out_34(grs_register_printallow32_1_out_34));
  GRS_Register_Printallow32 grs_register_printallow32_2 (
    .Address(Outputaddress2), .in_2(grs_register_4b_1_output1), .in_3(grs_register_4b_2_output1),
    .in_4(grs_register_4b_3_output1), .in_5(grs_register_4b_4_output1), .in_6(grs_register_4b_5_output1),
    .in_7(grs_register_4b_6_output1), .in_8(grs_register_4b_7_output1), .in_9(grs_register_4b_8_output1),
    .in_10(grs_register_4b_9_output1), .in_11(grs_register_4b_10_output1),
    .in_12(grs_register_4b_11_output1), .in_13(grs_register_4b_12_output1),
    .in_14(grs_register_4b_13_output1), .in_15(grs_register_4b_14_output1),
    .in_16(grs_register_4b_15_output1), .in_17(grs_register_4b_16_output1),
    .in_18(grs_register_4b_17_output1), .in_19(grs_register_4b_18_output1),
    .in_20(grs_register_4b_19_output1), .in_21(grs_register_4b_20_output1),
    .in_22(grs_register_4b_21_output1), .in_23(grs_register_4b_22_output1),
    .in_24(grs_register_4b_23_output1), .in_25(grs_register_4b_24_output1),
    .in_26(grs_register_4b_25_output1), .in_27(grs_register_4b_26_output1),
    .in_28(grs_register_4b_27_output1), .in_29(grs_register_4b_28_output1),
    .in_30(grs_register_4b_29_output1), .in_31(grs_register_4b_30_output1),
    .in_32(grs_register_4b_31_output1), .in_33(grs_register_4b_32_output1),
    .out_34(grs_register_printallow32_2_out_34));
  GRS_Register_Printchoose2 grs_register_printchoose2_1 (
    .Choose1(grs_register_printallow32_1_out_34), .Outputchoose(Choose),
    .Choose2(grs_register_printallow32_2_out_34), .Print1(Output1), .Print2(Output2));
endmodule

module GRS_MUX_5to32 (
  input  [4:0] Input5,
  output K00000,
  output K00001,
  output K00010,
  output K00011,
  output K00100,
  output K00101,
  output K00110,
  output K00111,
  output K01000,
  output K01001,
  output K01010,
  output K01011,
  output K01100,
  output K01101,
  output K01110,
  output K01111,
  output K10000,
  output K10001,
  output K10010,
  output K10011,
  output K10100,
  output K10101,
  output K10110,
  output K10111,
  output K11000,
  output K11001,
  output K11010,
  output K11011,
  output K11100,
  output K11101,
  output K11110,
  output K11111
);

  wire not_1_out, not_2_out, not_3_out, not_4_out, not_5_out, not_6_out, not_7_out, not_8_out, not_9_out,
       not_10_out, not_11_out, not_12_out, not_13_out, not_14_out, not_15_out, not_16_out, not_17_out,
       not_18_out, not_19_out, not_20_out, not_21_out, not_22_out, not_23_out, not_24_out, not_25_out,
       not_26_out, not_27_out, not_28_out, not_29_out, not_30_out, not_31_out, not_32_out, not_33_out,
       not_34_out, not_35_out, not_36_out, not_37_out, not_38_out, not_39_out, not_40_out, not_41_out,
       not_42_out, not_43_out, not_44_out, not_45_out, not_46_out, not_47_out, not_48_out, not_49_out,
       not_50_out, not_51_out, not_52_out, not_53_out, not_54_out, not_55_out, not_56_out, not_57_out,
       not_58_out, not_59_out, not_60_out, not_61_out, not_62_out, not_63_out, not_64_out, not_65_out,
       not_66_out, not_67_out, not_68_out, not_69_out, not_70_out, not_71_out, not_72_out, not_73_out,
       not_74_out, not_75_out, not_76_out, not_77_out, not_78_out, not_79_out, not_80_out;

  not not_1 (not_1_out, Input5[0]);
  not not_2 (not_2_out, Input5[1]);
  not not_3 (not_3_out, Input5[2]);
  not not_4 (not_4_out, Input5[3]);
  not not_5 (not_5_out, Input5[4]);
  and and_1 (K00000, not_1_out, not_2_out, not_3_out, not_4_out, not_5_out);
  not not_6 (not_6_out, Input5[1]);
  not not_7 (not_7_out, Input5[2]);
  and and_2 (K00001, Input5[0], not_6_out, not_7_out, not_9_out, not_10_out);
  not not_8 (not_8_out, Input5[0]);
  not not_9 (not_9_out, Input5[3]);
  not not_10 (not_10_out, Input5[4]);
  not not_11 (not_11_out, Input5[2]);
  not not_12 (not_12_out, Input5[3]);
  not not_13 (not_13_out, Input5[4]);
  and and_3 (K00010, not_8_out, Input5[1], not_11_out, not_12_out, not_13_out);
  not not_14 (not_14_out, Input5[2]);
  not not_15 (not_15_out, Input5[3]);
  not not_16 (not_16_out, Input5[4]);
  and and_4 (K00011, Input5[0], Input5[1], not_14_out, not_15_out, not_16_out);
  not not_17 (not_17_out, Input5[0]);
  not not_18 (not_18_out, Input5[1]);
  not not_19 (not_19_out, Input5[3]);
  not not_20 (not_20_out, Input5[4]);
  and and_5 (K00100, not_17_out, not_18_out, Input5[2], not_19_out, not_20_out);
  not not_21 (not_21_out, Input5[1]);
  and and_6 (K00101, Input5[0], not_21_out, Input5[2], not_23_out, not_24_out);
  not not_22 (not_22_out, Input5[0]);
  not not_23 (not_23_out, Input5[3]);
  not not_24 (not_24_out, Input5[4]);
  not not_25 (not_25_out, Input5[3]);
  not not_26 (not_26_out, Input5[4]);
  and and_7 (K00110, not_22_out, Input5[1], Input5[2], not_25_out, not_26_out);
  not not_27 (not_27_out, Input5[3]);
  not not_28 (not_28_out, Input5[4]);
  and and_8 (K00111, Input5[0], Input5[1], Input5[2], not_27_out, not_28_out);
  not not_29 (not_29_out, Input5[0]);
  not not_30 (not_30_out, Input5[1]);
  not not_31 (not_31_out, Input5[2]);
  not not_32 (not_32_out, Input5[4]);
  and and_9 (K01000, not_29_out, not_30_out, not_31_out, Input5[3], not_32_out);
  not not_33 (not_33_out, Input5[1]);
  not not_34 (not_34_out, Input5[2]);
  and and_10 (K01001, Input5[0], not_33_out, not_34_out, Input5[3], not_36_out);
  not not_35 (not_35_out, Input5[0]);
  not not_36 (not_36_out, Input5[4]);
  not not_37 (not_37_out, Input5[2]);
  not not_38 (not_38_out, Input5[4]);
  and and_11 (K01010, not_35_out, Input5[1], not_37_out, Input5[3], not_38_out);
  not not_39 (not_39_out, Input5[2]);
  not not_40 (not_40_out, Input5[4]);
  and and_12 (K01011, Input5[0], Input5[1], not_39_out, Input5[3], not_40_out);
  not not_41 (not_41_out, Input5[0]);
  not not_42 (not_42_out, Input5[1]);
  not not_43 (not_43_out, Input5[4]);
  and and_13 (K01100, not_41_out, not_42_out, Input5[2], Input5[3], not_43_out);
  not not_44 (not_44_out, Input5[1]);
  and and_14 (K01101, Input5[0], not_44_out, Input5[2], Input5[3], not_46_out);
  not not_45 (not_45_out, Input5[0]);
  not not_46 (not_46_out, Input5[4]);
  not not_47 (not_47_out, Input5[4]);
  and and_15 (K01110, not_45_out, Input5[1], Input5[2], Input5[3], not_47_out);
  not not_48 (not_48_out, Input5[4]);
  and and_16 (K01111, Input5[0], Input5[1], Input5[2], Input5[3], not_48_out);
  not not_49 (not_49_out, Input5[0]);
  not not_50 (not_50_out, Input5[1]);
  not not_51 (not_51_out, Input5[2]);
  not not_52 (not_52_out, Input5[3]);
  and and_17 (K10000, not_49_out, not_50_out, not_51_out, not_52_out, Input5[4]);
  not not_53 (not_53_out, Input5[1]);
  not not_54 (not_54_out, Input5[2]);
  and and_18 (K10001, Input5[0], not_53_out, not_54_out, not_56_out, Input5[4]);
  not not_55 (not_55_out, Input5[0]);
  not not_56 (not_56_out, Input5[3]);
  not not_57 (not_57_out, Input5[2]);
  not not_58 (not_58_out, Input5[3]);
  and and_19 (K10010, not_55_out, Input5[1], not_57_out, not_58_out, Input5[4]);
  not not_59 (not_59_out, Input5[2]);
  not not_60 (not_60_out, Input5[3]);
  and and_20 (K10011, Input5[0], Input5[1], not_59_out, not_60_out, Input5[4]);
  not not_61 (not_61_out, Input5[0]);
  not not_62 (not_62_out, Input5[1]);
  not not_63 (not_63_out, Input5[3]);
  and and_21 (K10100, not_61_out, not_62_out, Input5[2], not_63_out, Input5[4]);
  not not_64 (not_64_out, Input5[1]);
  not not_65 (not_65_out, Input5[3]);
  and and_22 (K10101, Input5[0], not_64_out, Input5[2], not_65_out, Input5[4]);
  not not_66 (not_66_out, Input5[0]);
  not not_67 (not_67_out, Input5[3]);
  and and_23 (K10110, not_66_out, Input5[1], Input5[2], not_67_out, Input5[4]);
  not not_68 (not_68_out, Input5[3]);
  and and_24 (K10111, Input5[0], Input5[1], Input5[2], not_68_out, Input5[4]);
  not not_69 (not_69_out, Input5[0]);
  not not_70 (not_70_out, Input5[1]);
  not not_71 (not_71_out, Input5[2]);
  and and_25 (K11000, not_69_out, not_70_out, not_71_out, Input5[3], Input5[4]);
  not not_72 (not_72_out, Input5[1]);
  not not_73 (not_73_out, Input5[2]);
  and and_26 (K11001, Input5[0], not_72_out, not_73_out, Input5[3], Input5[4]);
  not not_74 (not_74_out, Input5[0]);
  not not_75 (not_75_out, Input5[2]);
  and and_27 (K11010, not_74_out, Input5[1], not_75_out, Input5[3], Input5[4]);
  not not_76 (not_76_out, Input5[2]);
  and and_28 (K11011, Input5[0], Input5[1], not_76_out, Input5[3], Input5[4]);
  not not_77 (not_77_out, Input5[0]);
  not not_78 (not_78_out, Input5[1]);
  and and_29 (K11100, not_77_out, not_78_out, Input5[2], Input5[3], Input5[4]);
  not not_79 (not_79_out, Input5[1]);
  and and_30 (K11101, Input5[0], not_79_out, Input5[2], Input5[3], Input5[4]);
  not not_80 (not_80_out, Input5[0]);
  and and_31 (K11110, not_80_out, Input5[1], Input5[2], Input5[3], Input5[4]);
  and and_32 (K11111, Input5[0], Input5[1], Input5[2], Input5[3], Input5[4]);
endmodule

module GRS_Register_Writeallow (
  input  [4:0] ADRESS,
  input  WRITEALLOW,
  output out_3,
  output out_4,
  output out_5,
  output out_6,
  output out_7,
  output out_8,
  output out_9,
  output out_10,
  output out_11,
  output out_12,
  output out_13,
  output out_14,
  output out_15,
  output out_16,
  output out_17,
  output out_18,
  output out_19,
  output out_20,
  output out_21,
  output out_22,
  output out_23,
  output out_24,
  output out_25,
  output out_26,
  output out_27,
  output out_28,
  output out_29,
  output out_30,
  output out_31,
  output out_32,
  output out_33,
  output out_34
);

  wire grs_mux_5to32_1_k00000, grs_mux_5to32_1_k00001, grs_mux_5to32_1_k00010, grs_mux_5to32_1_k00011,
       grs_mux_5to32_1_k00100, grs_mux_5to32_1_k00101, grs_mux_5to32_1_k00110, grs_mux_5to32_1_k00111,
       grs_mux_5to32_1_k01000, grs_mux_5to32_1_k01001, grs_mux_5to32_1_k01010, grs_mux_5to32_1_k01011,
       grs_mux_5to32_1_k01100, grs_mux_5to32_1_k01101, grs_mux_5to32_1_k01110, grs_mux_5to32_1_k01111,
       grs_mux_5to32_1_k10000, grs_mux_5to32_1_k10001, grs_mux_5to32_1_k10010, grs_mux_5to32_1_k10011,
       grs_mux_5to32_1_k10100, grs_mux_5to32_1_k10101, grs_mux_5to32_1_k10110, grs_mux_5to32_1_k10111,
       grs_mux_5to32_1_k11000, grs_mux_5to32_1_k11001, grs_mux_5to32_1_k11010, grs_mux_5to32_1_k11011,
       grs_mux_5to32_1_k11100, grs_mux_5to32_1_k11101, grs_mux_5to32_1_k11110, grs_mux_5to32_1_k11111;

  GRS_MUX_5to32 grs_mux_5to32_1 (
    .Input5(ADRESS), .K00000(grs_mux_5to32_1_k00000), .K00001(grs_mux_5to32_1_k00001),
    .K00010(grs_mux_5to32_1_k00010), .K00011(grs_mux_5to32_1_k00011), .K00100(grs_mux_5to32_1_k00100),
    .K00101(grs_mux_5to32_1_k00101), .K00110(grs_mux_5to32_1_k00110), .K00111(grs_mux_5to32_1_k00111),
    .K01000(grs_mux_5to32_1_k01000), .K01001(grs_mux_5to32_1_k01001), .K01010(grs_mux_5to32_1_k01010),
    .K01011(grs_mux_5to32_1_k01011), .K01100(grs_mux_5to32_1_k01100), .K01101(grs_mux_5to32_1_k01101),
    .K01110(grs_mux_5to32_1_k01110), .K01111(grs_mux_5to32_1_k01111), .K10000(grs_mux_5to32_1_k10000),
    .K10001(grs_mux_5to32_1_k10001), .K10010(grs_mux_5to32_1_k10010), .K10011(grs_mux_5to32_1_k10011),
    .K10100(grs_mux_5to32_1_k10100), .K10101(grs_mux_5to32_1_k10101), .K10110(grs_mux_5to32_1_k10110),
    .K10111(grs_mux_5to32_1_k10111), .K11000(grs_mux_5to32_1_k11000), .K11001(grs_mux_5to32_1_k11001),
    .K11010(grs_mux_5to32_1_k11010), .K11011(grs_mux_5to32_1_k11011), .K11100(grs_mux_5to32_1_k11100),
    .K11101(grs_mux_5to32_1_k11101), .K11110(grs_mux_5to32_1_k11110), .K11111(grs_mux_5to32_1_k11111));
  and and_1 (out_3, grs_mux_5to32_1_k00000, WRITEALLOW);
  and and_2 (out_4, grs_mux_5to32_1_k00001, WRITEALLOW);
  and and_3 (out_5, grs_mux_5to32_1_k00010, WRITEALLOW);
  and and_4 (out_6, grs_mux_5to32_1_k00011, WRITEALLOW);
  and and_5 (out_7, grs_mux_5to32_1_k00100, WRITEALLOW);
  and and_6 (out_8, grs_mux_5to32_1_k00101, WRITEALLOW);
  and and_7 (out_9, grs_mux_5to32_1_k00110, WRITEALLOW);
  and and_8 (out_10, grs_mux_5to32_1_k00111, WRITEALLOW);
  and and_9 (out_11, grs_mux_5to32_1_k01000, WRITEALLOW);
  and and_10 (out_12, grs_mux_5to32_1_k01001, WRITEALLOW);
  and and_11 (out_13, grs_mux_5to32_1_k01010, WRITEALLOW);
  and and_12 (out_14, grs_mux_5to32_1_k01011, WRITEALLOW);
  and and_13 (out_15, grs_mux_5to32_1_k01100, WRITEALLOW);
  and and_14 (out_16, grs_mux_5to32_1_k01101, WRITEALLOW);
  and and_15 (out_17, grs_mux_5to32_1_k01110, WRITEALLOW);
  and and_16 (out_18, grs_mux_5to32_1_k01111, WRITEALLOW);
  and and_17 (out_19, grs_mux_5to32_1_k10000, WRITEALLOW);
  and and_18 (out_20, grs_mux_5to32_1_k10001, WRITEALLOW);
  and and_19 (out_21, grs_mux_5to32_1_k10010, WRITEALLOW);
  and and_20 (out_22, grs_mux_5to32_1_k10011, WRITEALLOW);
  and and_21 (out_23, grs_mux_5to32_1_k10100, WRITEALLOW);
  and and_22 (out_24, grs_mux_5to32_1_k10101, WRITEALLOW);
  and and_23 (out_25, grs_mux_5to32_1_k10110, WRITEALLOW);
  and and_24 (out_26, grs_mux_5to32_1_k10111, WRITEALLOW);
  and and_25 (out_27, grs_mux_5to32_1_k11000, WRITEALLOW);
  and and_26 (out_28, grs_mux_5to32_1_k11001, WRITEALLOW);
  and and_27 (out_29, grs_mux_5to32_1_k11010, WRITEALLOW);
  and and_28 (out_30, grs_mux_5to32_1_k11011, WRITEALLOW);
  and and_29 (out_31, grs_mux_5to32_1_k11100, WRITEALLOW);
  and and_30 (out_32, grs_mux_5to32_1_k11101, WRITEALLOW);
  and and_31 (out_33, grs_mux_5to32_1_k11110, WRITEALLOW);
  and and_32 (out_34, grs_mux_5to32_1_k11111, WRITEALLOW);
endmodule

module GRS_Register_Printallow1 (
  input  [31:0] Input1,
  input  Allow1,
  output [31:0] Output1
);

  assign Output1 = Input1 & {32{Allow1}};  // AND_Gate and_1, 32 bits wide
endmodule

module GRS_Register_Printallow32 (
  input  [4:0] Address,
  input  [31:0] in_2,
  input  [31:0] in_3,
  input  [31:0] in_4,
  input  [31:0] in_5,
  input  [31:0] in_6,
  input  [31:0] in_7,
  input  [31:0] in_8,
  input  [31:0] in_9,
  input  [31:0] in_10,
  input  [31:0] in_11,
  input  [31:0] in_12,
  input  [31:0] in_13,
  input  [31:0] in_14,
  input  [31:0] in_15,
  input  [31:0] in_16,
  input  [31:0] in_17,
  input  [31:0] in_18,
  input  [31:0] in_19,
  input  [31:0] in_20,
  input  [31:0] in_21,
  input  [31:0] in_22,
  input  [31:0] in_23,
  input  [31:0] in_24,
  input  [31:0] in_25,
  input  [31:0] in_26,
  input  [31:0] in_27,
  input  [31:0] in_28,
  input  [31:0] in_29,
  input  [31:0] in_30,
  input  [31:0] in_31,
  input  [31:0] in_32,
  input  [31:0] in_33,
  output [31:0] out_34
);

  wire grs_mux_5to32_1_k00000, grs_mux_5to32_1_k00001, grs_mux_5to32_1_k00010, grs_mux_5to32_1_k00011,
       grs_mux_5to32_1_k00100, grs_mux_5to32_1_k00101, grs_mux_5to32_1_k00110, grs_mux_5to32_1_k00111,
       grs_mux_5to32_1_k01000, grs_mux_5to32_1_k01001, grs_mux_5to32_1_k01010, grs_mux_5to32_1_k01011,
       grs_mux_5to32_1_k01100, grs_mux_5to32_1_k01101, grs_mux_5to32_1_k01110, grs_mux_5to32_1_k01111,
       grs_mux_5to32_1_k10000, grs_mux_5to32_1_k10001, grs_mux_5to32_1_k10010, grs_mux_5to32_1_k10011,
       grs_mux_5to32_1_k10100, grs_mux_5to32_1_k10101, grs_mux_5to32_1_k10110, grs_mux_5to32_1_k10111,
       grs_mux_5to32_1_k11000, grs_mux_5to32_1_k11001, grs_mux_5to32_1_k11010, grs_mux_5to32_1_k11011,
       grs_mux_5to32_1_k11100, grs_mux_5to32_1_k11101, grs_mux_5to32_1_k11110, grs_mux_5to32_1_k11111;
  wire [31:0] grs_register_printallow1_1_output1, grs_register_printallow1_2_output1,
       grs_register_printallow1_3_output1, grs_register_printallow1_4_output1,
       grs_register_printallow1_5_output1, grs_register_printallow1_6_output1,
       grs_register_printallow1_7_output1, grs_register_printallow1_8_output1,
       grs_register_printallow1_9_output1, grs_register_printallow1_10_output1,
       grs_register_printallow1_11_output1, grs_register_printallow1_12_output1,
       grs_register_printallow1_13_output1, grs_register_printallow1_14_output1,
       grs_register_printallow1_15_output1, grs_register_printallow1_16_output1,
       grs_register_printallow1_17_output1, grs_register_printallow1_18_output1,
       grs_register_printallow1_19_output1, grs_register_printallow1_20_output1,
       grs_register_printallow1_21_output1, grs_register_printallow1_22_output1,
       grs_register_printallow1_23_output1, grs_register_printallow1_24_output1,
       grs_register_printallow1_25_output1, grs_register_printallow1_26_output1,
       grs_register_printallow1_27_output1, grs_register_printallow1_28_output1,
       grs_register_printallow1_29_output1, grs_register_printallow1_30_output1,
       grs_register_printallow1_31_output1, grs_register_printallow1_32_output1;

  GRS_MUX_5to32 grs_mux_5to32_1 (
    .Input5(Address), .K00000(grs_mux_5to32_1_k00000), .K00001(grs_mux_5to32_1_k00001),
    .K00010(grs_mux_5to32_1_k00010), .K00011(grs_mux_5to32_1_k00011), .K00100(grs_mux_5to32_1_k00100),
    .K00101(grs_mux_5to32_1_k00101), .K00110(grs_mux_5to32_1_k00110), .K00111(grs_mux_5to32_1_k00111),
    .K01000(grs_mux_5to32_1_k01000), .K01001(grs_mux_5to32_1_k01001), .K01010(grs_mux_5to32_1_k01010),
    .K01011(grs_mux_5to32_1_k01011), .K01100(grs_mux_5to32_1_k01100), .K01101(grs_mux_5to32_1_k01101),
    .K01110(grs_mux_5to32_1_k01110), .K01111(grs_mux_5to32_1_k01111), .K10000(grs_mux_5to32_1_k10000),
    .K10001(grs_mux_5to32_1_k10001), .K10010(grs_mux_5to32_1_k10010), .K10011(grs_mux_5to32_1_k10011),
    .K10100(grs_mux_5to32_1_k10100), .K10101(grs_mux_5to32_1_k10101), .K10110(grs_mux_5to32_1_k10110),
    .K10111(grs_mux_5to32_1_k10111), .K11000(grs_mux_5to32_1_k11000), .K11001(grs_mux_5to32_1_k11001),
    .K11010(grs_mux_5to32_1_k11010), .K11011(grs_mux_5to32_1_k11011), .K11100(grs_mux_5to32_1_k11100),
    .K11101(grs_mux_5to32_1_k11101), .K11110(grs_mux_5to32_1_k11110), .K11111(grs_mux_5to32_1_k11111));
  GRS_Register_Printallow1 grs_register_printallow1_1 (
    .Input1(in_2), .Allow1(grs_mux_5to32_1_k00000), .Output1(grs_register_printallow1_1_output1));
  GRS_Register_Printallow1 grs_register_printallow1_2 (
    .Input1(in_3), .Allow1(grs_mux_5to32_1_k00001), .Output1(grs_register_printallow1_2_output1));
  GRS_Register_Printallow1 grs_register_printallow1_3 (
    .Input1(in_4), .Allow1(grs_mux_5to32_1_k00010), .Output1(grs_register_printallow1_3_output1));
  GRS_Register_Printallow1 grs_register_printallow1_4 (
    .Input1(in_5), .Allow1(grs_mux_5to32_1_k00011), .Output1(grs_register_printallow1_4_output1));
  GRS_Register_Printallow1 grs_register_printallow1_5 (
    .Input1(in_6), .Allow1(grs_mux_5to32_1_k00100), .Output1(grs_register_printallow1_5_output1));
  GRS_Register_Printallow1 grs_register_printallow1_6 (
    .Input1(in_7), .Allow1(grs_mux_5to32_1_k00101), .Output1(grs_register_printallow1_6_output1));
  GRS_Register_Printallow1 grs_register_printallow1_7 (
    .Input1(in_8), .Allow1(grs_mux_5to32_1_k00110), .Output1(grs_register_printallow1_7_output1));
  GRS_Register_Printallow1 grs_register_printallow1_8 (
    .Input1(in_9), .Allow1(grs_mux_5to32_1_k00111), .Output1(grs_register_printallow1_8_output1));
  GRS_Register_Printallow1 grs_register_printallow1_9 (
    .Input1(in_10), .Allow1(grs_mux_5to32_1_k01000), .Output1(grs_register_printallow1_9_output1));
  GRS_Register_Printallow1 grs_register_printallow1_10 (
    .Input1(in_11), .Allow1(grs_mux_5to32_1_k01001), .Output1(grs_register_printallow1_10_output1));
  GRS_Register_Printallow1 grs_register_printallow1_11 (
    .Input1(in_12), .Allow1(grs_mux_5to32_1_k01010), .Output1(grs_register_printallow1_11_output1));
  GRS_Register_Printallow1 grs_register_printallow1_12 (
    .Input1(in_13), .Allow1(grs_mux_5to32_1_k01011), .Output1(grs_register_printallow1_12_output1));
  GRS_Register_Printallow1 grs_register_printallow1_13 (
    .Input1(in_14), .Allow1(grs_mux_5to32_1_k01100), .Output1(grs_register_printallow1_13_output1));
  GRS_Register_Printallow1 grs_register_printallow1_14 (
    .Input1(in_15), .Allow1(grs_mux_5to32_1_k01101), .Output1(grs_register_printallow1_14_output1));
  GRS_Register_Printallow1 grs_register_printallow1_15 (
    .Input1(in_16), .Allow1(grs_mux_5to32_1_k01110), .Output1(grs_register_printallow1_15_output1));
  GRS_Register_Printallow1 grs_register_printallow1_16 (
    .Input1(in_17), .Allow1(grs_mux_5to32_1_k01111), .Output1(grs_register_printallow1_16_output1));
  GRS_Register_Printallow1 grs_register_printallow1_17 (
    .Input1(in_18), .Allow1(grs_mux_5to32_1_k10000), .Output1(grs_register_printallow1_17_output1));
  GRS_Register_Printallow1 grs_register_printallow1_18 (
    .Input1(in_19), .Allow1(grs_mux_5to32_1_k10001), .Output1(grs_register_printallow1_18_output1));
  GRS_Register_Printallow1 grs_register_printallow1_19 (
    .Input1(in_20), .Allow1(grs_mux_5to32_1_k10010), .Output1(grs_register_printallow1_19_output1));
  GRS_Register_Printallow1 grs_register_printallow1_20 (
    .Input1(in_21), .Allow1(grs_mux_5to32_1_k10011), .Output1(grs_register_printallow1_20_output1));
  GRS_Register_Printallow1 grs_register_printallow1_21 (
    .Input1(in_22), .Allow1(grs_mux_5to32_1_k10100), .Output1(grs_register_printallow1_21_output1));
  GRS_Register_Printallow1 grs_register_printallow1_22 (
    .Input1(in_23), .Allow1(grs_mux_5to32_1_k10101), .Output1(grs_register_printallow1_22_output1));
  GRS_Register_Printallow1 grs_register_printallow1_23 (
    .Input1(in_24), .Allow1(grs_mux_5to32_1_k10110), .Output1(grs_register_printallow1_23_output1));
  GRS_Register_Printallow1 grs_register_printallow1_24 (
    .Input1(in_25), .Allow1(grs_mux_5to32_1_k10111), .Output1(grs_register_printallow1_24_output1));
  GRS_Register_Printallow1 grs_register_printallow1_25 (
    .Input1(in_26), .Allow1(grs_mux_5to32_1_k11000), .Output1(grs_register_printallow1_25_output1));
  GRS_Register_Printallow1 grs_register_printallow1_26 (
    .Input1(in_27), .Allow1(grs_mux_5to32_1_k11001), .Output1(grs_register_printallow1_26_output1));
  GRS_Register_Printallow1 grs_register_printallow1_27 (
    .Input1(in_28), .Allow1(grs_mux_5to32_1_k11010), .Output1(grs_register_printallow1_27_output1));
  GRS_Register_Printallow1 grs_register_printallow1_28 (
    .Input1(in_29), .Allow1(grs_mux_5to32_1_k11011), .Output1(grs_register_printallow1_28_output1));
  GRS_Register_Printallow1 grs_register_printallow1_29 (
    .Input1(in_30), .Allow1(grs_mux_5to32_1_k11100), .Output1(grs_register_printallow1_29_output1));
  GRS_Register_Printallow1 grs_register_printallow1_30 (
    .Input1(in_31), .Allow1(grs_mux_5to32_1_k11101), .Output1(grs_register_printallow1_30_output1));
  GRS_Register_Printallow1 grs_register_printallow1_31 (
    .Input1(in_32), .Allow1(grs_mux_5to32_1_k11110), .Output1(grs_register_printallow1_31_output1));
  GRS_Register_Printallow1 grs_register_printallow1_32 (
    .Input1(in_33), .Allow1(grs_mux_5to32_1_k11111), .Output1(grs_register_printallow1_32_output1));
  assign out_34 = grs_register_printallow1_1_output1 | grs_register_printallow1_2_output1 | grs_register_printallow1_3_output1 | grs_register_printallow1_4_output1 | grs_register_printallow1_5_output1 | grs_register_printallow1_6_output1 | grs_register_printallow1_7_output1 | grs_register_printallow1_8_output1 | grs_register_printallow1_9_output1 | grs_register_printallow1_10_output1 | grs_register_printallow1_11_output1 | grs_register_printallow1_12_output1 | grs_register_printallow1_13_output1 | grs_register_printallow1_14_output1 | grs_register_printallow1_15_output1 | grs_register_printallow1_16_output1 | grs_register_printallow1_17_output1 | grs_register_printallow1_18_output1 | grs_register_printallow1_19_output1 | grs_register_printallow1_20_output1 | grs_register_printallow1_21_output1 | grs_register_printallow1_22_output1 | grs_register_printallow1_23_output1 | grs_register_printallow1_24_output1 | grs_register_printallow1_25_output1 | grs_register_printallow1_26_output1 | grs_register_printallow1_27_output1 | grs_register_printallow1_28_output1 | grs_register_printallow1_29_output1 | grs_register_printallow1_30_output1 | grs_register_printallow1_31_output1 | grs_register_printallow1_32_output1;  // OR_Gate or_1, 32 bits wide
endmodule

module GRS_Register_Printchoose2 (
  input  [31:0] Choose1,
  input  [1:0] Outputchoose,
  input  [31:0] Choose2,
  output [31:0] Print1,
  output [31:0] Print2
);

  assign Print1 = Choose1 & {32{Outputchoose[0]}};  // AND_Gate and_1, 32 bits wide
  assign Print2 = {32{Outputchoose[1]}} & Choose2;  // AND_Gate and_2, 32 bits wide
endmodule

module Instance_to_32 (
  input  [19:0] in_1,
  input  [31:0] in_2,
  input  in_3,
  output [31:0] out_4
);

  and and_1 (out_4[0], in_2[0], in_1[0]);
  and and_2 (out_4[1], in_2[1], in_1[1]);
  and and_3 (out_4[2], in_2[2], in_1[2]);
  and and_4 (out_4[3], in_2[3], in_1[3]);
  and and_5 (out_4[4], in_2[4], in_1[4]);
  and and_6 (out_4[5], in_2[5], in_1[5]);
  and and_7 (out_4[6], in_2[6], in_1[6]);
  and and_8 (out_4[7], in_2[7], in_1[7]);
  and and_9 (out_4[8], in_2[8], in_1[8]);
  and and_10 (out_4[9], in_2[9], in_1[9]);
  and and_11 (out_4[10], in_2[10], in_1[10]);
  and and_12 (out_4[11], in_2[11], in_1[11]);
  and and_13 (out_4[12], in_2[12], in_1[12]);
  and and_14 (out_4[13], in_2[13], in_1[13]);
  and and_15 (out_4[14], in_2[14], in_1[14]);
  and and_16 (out_4[15], in_2[15], in_1[15]);
  and and_17 (out_4[16], in_2[16], in_1[16]);
  and and_18 (out_4[17], in_2[17], in_1[17]);
  and and_19 (out_4[18], in_2[18], in_1[18]);
  and and_20 (out_4[19], in_2[19], in_1[19]);
  and and_21 (out_4[20], in_2[20], in_3);
  and and_22 (out_4[21], in_2[21], in_3);
  and and_23 (out_4[22], in_2[22], in_3);
  and and_24 (out_4[23], in_2[23], in_3);
  and and_25 (out_4[24], in_2[24], in_3);
  and and_26 (out_4[25], in_2[25], in_3);
  and and_27 (out_4[26], in_2[26], in_3);
  and and_28 (out_4[27], in_2[27], in_3);
  and and_29 (out_4[28], in_2[28], in_3);
  and and_30 (out_4[29], in_2[29], in_3);
  and and_31 (out_4[30], in_2[30], in_3);
  and and_32 (out_4[31], in_2[31], in_3);
endmodule

module New_Register (
  input  [31:0] DATA_IN,
  input  [1:0] CHOOSE,
  input  [4:0] PRINT_ADDRESS1,
  input  [4:0] PRINT_ADDRESS2,
  input  WRITEALLOW,
  input  CLOCK,
  input  [4:0] ADDRESS,
  output [31:0] out_8,
  output [31:0] out_9
);

  wire and_3_out, grs_register_writeallow_1_out_3, grs_register_writeallow_1_out_4,
       grs_register_writeallow_1_out_5, grs_register_writeallow_1_out_6, grs_register_writeallow_1_out_7,
       grs_register_writeallow_1_out_8, grs_register_writeallow_1_out_9, grs_register_writeallow_1_out_10,
       grs_register_writeallow_1_out_11, grs_register_writeallow_1_out_12, grs_register_writeallow_1_out_13,
       grs_register_writeallow_1_out_14, grs_register_writeallow_1_out_15, grs_register_writeallow_1_out_16,
       grs_register_writeallow_1_out_17, grs_register_writeallow_1_out_18, grs_register_writeallow_1_out_19,
       grs_register_writeallow_1_out_20, grs_register_writeallow_1_out_21, grs_register_writeallow_1_out_22,
       grs_register_writeallow_1_out_23, grs_register_writeallow_1_out_24, grs_register_writeallow_1_out_25,
       grs_register_writeallow_1_out_26, grs_register_writeallow_1_out_27, grs_register_writeallow_1_out_28,
       grs_register_writeallow_1_out_29, grs_register_writeallow_1_out_30, grs_register_writeallow_1_out_31,
       grs_register_writeallow_1_out_32, grs_register_writeallow_1_out_33, grs_register_writeallow_1_out_34,
       norb_ext_1b_delayer_1_sigout, not_1_out;
  wire [1:0] and_1_out;
  wire [4:0] register_2_q;
  wire [31:0] grs_register_printallow32_1_out_34, grs_register_printallow32_2_out_34, register_1_q,
       register_3_q, register_4_q, register_5_q, register_6_q, register_7_q, register_8_q, register_9_q,
       register_10_q, register_11_q, register_12_q, register_13_q, register_14_q, register_15_q,
       register_16_q, register_17_q, register_18_q, register_19_q, register_20_q, register_21_q,
       register_22_q, register_23_q, register_24_q, register_25_q, register_26_q, register_27_q,
       register_28_q, register_29_q, register_30_q, register_31_q, register_32_q, register_33_q,
       register_34_q;

  Norb_EXT_1B_Delayer norb_ext_1b_delayer_1 (
    .SIGIN(WRITEALLOW), .CLOCK_IN(CLOCK), .SIGOUT(norb_ext_1b_delayer_1_sigout));
  not not_1 (not_1_out, CLOCK);
  and and_1 (and_1_out[0], CHOOSE[0], CLOCK);
  and and_2 (and_1_out[1], CHOOSE[1], CLOCK);
  Register #(.trigger("high"), .width(32)) register_1 (
    .D(DATA_IN), .en(CLOCK), .clk(CLOCK), .Q(register_1_q));  // open: clr
  and and_3 (and_3_out, norb_ext_1b_delayer_1_sigout, not_1_out);
  Register #(.trigger("high"), .width(5)) register_2 (
    .D(ADDRESS), .en(CLOCK), .clk(CLOCK), .Q(register_2_q));  // open: clr
  GRS_Register_Writeallow grs_register_writeallow_1 (
    .ADRESS(register_2_q), .WRITEALLOW(and_3_out), .out_3(grs_register_writeallow_1_out_3),
    .out_4(grs_register_writeallow_1_out_4), .out_5(grs_register_writeallow_1_out_5),
    .out_6(grs_register_writeallow_1_out_6), .out_7(grs_register_writeallow_1_out_7),
    .out_8(grs_register_writeallow_1_out_8), .out_9(grs_register_writeallow_1_out_9),
    .out_10(grs_register_writeallow_1_out_10), .out_11(grs_register_writeallow_1_out_11),
    .out_12(grs_register_writeallow_1_out_12), .out_13(grs_register_writeallow_1_out_13),
    .out_14(grs_register_writeallow_1_out_14), .out_15(grs_register_writeallow_1_out_15),
    .out_16(grs_register_writeallow_1_out_16), .out_17(grs_register_writeallow_1_out_17),
    .out_18(grs_register_writeallow_1_out_18), .out_19(grs_register_writeallow_1_out_19),
    .out_20(grs_register_writeallow_1_out_20), .out_21(grs_register_writeallow_1_out_21),
    .out_22(grs_register_writeallow_1_out_22), .out_23(grs_register_writeallow_1_out_23),
    .out_24(grs_register_writeallow_1_out_24), .out_25(grs_register_writeallow_1_out_25),
    .out_26(grs_register_writeallow_1_out_26), .out_27(grs_register_writeallow_1_out_27),
    .out_28(grs_register_writeallow_1_out_28), .out_29(grs_register_writeallow_1_out_29),
    .out_30(grs_register_writeallow_1_out_30), .out_31(grs_register_writeallow_1_out_31),
    .out_32(grs_register_writeallow_1_out_32), .out_33(grs_register_writeallow_1_out_33),
    .out_34(grs_register_writeallow_1_out_34));
  Register #(.trigger("high"), .width(32)) register_3 (
    .D(register_1_q), .en(grs_register_writeallow_1_out_3), .clk(grs_register_writeallow_1_out_3),
    .Q(register_3_q));  // open: clr
  Register #(.trigger("high"), .width(32)) register_4 (
    .D(register_1_q), .en(grs_register_writeallow_1_out_4), .clk(grs_register_writeallow_1_out_4),
    .Q(register_4_q));  // open: clr
  Register #(.trigger("high"), .width(32)) register_5 (
    .D(register_1_q), .en(grs_register_writeallow_1_out_5), .clk(grs_register_writeallow_1_out_5),
    .Q(register_5_q));  // open: clr
  Register #(.trigger("high"), .width(32)) register_6 (
    .D(register_1_q), .en(grs_register_writeallow_1_out_6), .clk(grs_register_writeallow_1_out_6),
    .Q(register_6_q));  // open: clr
  Register #(.trigger("high"), .width(32)) register_7 (
    .D(register_1_q), .en(grs_register_writeallow_1_out_7), .clk(grs_register_writeallow_1_out_7),
    .Q(register_7_q));  // open: clr
  Register #(.trigger("high"), .width(32)) register_8 (
    .D(register_1_q), .en(grs_register_writeallow_1_out_8), .clk(grs_register_writeallow_1_out_8),
    .Q(register_8_q));  // open: clr
  Register #(.trigger("high"), .width(32)) register_9 (
    .D(register_1_q), .en(grs_register_writeallow_1_out_9), .clk(grs_register_writeallow_1_out_9),
    .Q(register_9_q));  // open: clr
  Register #(.trigger("high"), .width(32)) register_10 (
    .D(register_1_q), .en(grs_register_writeallow_1_out_10), .clk(grs_register_writeallow_1_out_10),
    .Q(register_10_q));  // open: clr
  Register #(.trigger("high"), .width(32)) register_11 (
    .D(register_1_q), .en(grs_register_writeallow_1_out_11), .clk(grs_register_writeallow_1_out_11),
    .Q(register_11_q));  // open: clr
  Register #(.trigger("high"), .width(32)) register_12 (
    .D(register_1_q), .en(grs_register_writeallow_1_out_12), .clk(grs_register_writeallow_1_out_12),
    .Q(register_12_q));  // open: clr
  Register #(.trigger("high"), .width(32)) register_13 (
    .D(register_1_q), .en(grs_register_writeallow_1_out_13), .clk(grs_register_writeallow_1_out_13),
    .Q(register_13_q));  // open: clr
  Register #(.trigger("high"), .width(32)) register_14 (
    .D(register_1_q), .en(grs_register_writeallow_1_out_14), .clk(grs_register_writeallow_1_out_14),
    .Q(register_14_q));  // open: clr
  Register #(.trigger("high"), .width(32)) register_15 (
    .D(register_1_q), .en(grs_register_writeallow_1_out_15), .clk(grs_register_writeallow_1_out_15),
    .Q(register_15_q));  // open: clr
  Register #(.trigger("high"), .width(32)) register_16 (
    .D(register_1_q), .en(grs_register_writeallow_1_out_16), .clk(grs_register_writeallow_1_out_16),
    .Q(register_16_q));  // open: clr
  Register #(.trigger("high"), .width(32)) register_17 (
    .D(register_1_q), .en(grs_register_writeallow_1_out_17), .clk(grs_register_writeallow_1_out_17),
    .Q(register_17_q));  // open: clr
  Register #(.trigger("high"), .width(32)) register_18 (
    .D(register_1_q), .en(grs_register_writeallow_1_out_18), .clk(grs_register_writeallow_1_out_18),
    .Q(register_18_q));  // open: clr
  Register #(.trigger("high"), .width(32)) register_19 (
    .D(register_1_q), .en(grs_register_writeallow_1_out_19), .clk(grs_register_writeallow_1_out_19),
    .Q(register_19_q));  // open: clr
  Register #(.trigger("high"), .width(32)) register_20 (
    .D(register_1_q), .en(grs_register_writeallow_1_out_20), .clk(grs_register_writeallow_1_out_20),
    .Q(register_20_q));  // open: clr
  Register #(.trigger("high"), .width(32)) register_21 (
    .D(register_1_q), .en(grs_register_writeallow_1_out_21), .clk(grs_register_writeallow_1_out_21),
    .Q(register_21_q));  // open: clr
  Register #(.trigger("high"), .width(32)) register_22 (
    .D(register_1_q), .en(grs_register_writeallow_1_out_22), .clk(grs_register_writeallow_1_out_22),
    .Q(register_22_q));  // open: clr
  Register #(.trigger("high"), .width(32)) register_23 (
    .D(register_1_q), .en(grs_register_writeallow_1_out_23), .clk(grs_register_writeallow_1_out_23),
    .Q(register_23_q));  // open: clr
  Register #(.trigger("high"), .width(32)) register_24 (
    .D(register_1_q), .en(grs_register_writeallow_1_out_24), .clk(grs_register_writeallow_1_out_24),
    .Q(register_24_q));  // open: clr
  Register #(.trigger("high"), .width(32)) register_25 (
    .D(register_1_q), .en(grs_register_writeallow_1_out_25), .clk(grs_register_writeallow_1_out_25),
    .Q(register_25_q));  // open: clr
  Register #(.trigger("high"), .width(32)) register_26 (
    .D(register_1_q), .en(grs_register_writeallow_1_out_26), .clk(grs_register_writeallow_1_out_26),
    .Q(register_26_q));  // open: clr
  Register #(.trigger("high"), .width(32)) register_27 (
    .D(register_1_q), .en(grs_register_writeallow_1_out_27), .clk(grs_register_writeallow_1_out_27),
    .Q(register_27_q));  // open: clr
  Register #(.trigger("high"), .width(32)) register_28 (
    .D(register_1_q), .en(grs_register_writeallow_1_out_28), .clk(grs_register_writeallow_1_out_28),
    .Q(register_28_q));  // open: clr
  Register #(.trigger("high"), .width(32)) register_29 (
    .D(register_1_q), .en(grs_register_writeallow_1_out_29), .clk(grs_register_writeallow_1_out_29),
    .Q(register_29_q));  // open: clr
  Register #(.trigger("high"), .width(32)) register_30 (
    .D(register_1_q), .en(grs_register_writeallow_1_out_30), .clk(grs_register_writeallow_1_out_30),
    .Q(register_30_q));  // open: clr
  Register #(.trigger("high"), .width(32)) register_31 (
    .D(register_1_q), .en(grs_register_writeallow_1_out_31), .clk(grs_register_writeallow_1_out_31),
    .Q(register_31_q));  // open: clr
  Register #(.trigger("high"), .width(32)) register_32 (
    .D(register_1_q), .en(grs_register_writeallow_1_out_32), .clk(grs_register_writeallow_1_out_32),
    .Q(register_32_q));  // open: clr
  Register #(.trigger("high"), .width(32)) register_33 (
    .D(register_1_q), .en(grs_register_writeallow_1_out_33), .clk(grs_register_writeallow_1_out_33),
    .Q(register_33_q));  // open: clr
  Register #(.trigger("high"), .width(32)) register_34 (
    .D(register_1_q), .en(grs_register_writeallow_1_out_34), .clk(grs_register_writeallow_1_out_34),
    .Q(register_34_q));  // open: clr
  GRS_Register_Printallow32 grs_register_printallow32_1 (
    .Address(PRINT_ADDRESS2), .in_2(register_3_q), .in_3(register_4_q), .in_4(register_5_q),
    .in_5(register_6_q), .in_6(register_7_q), .in_7(register_8_q), .in_8(register_9_q), .in_9(register_10_q),
    .in_10(register_11_q), .in_11(register_12_q), .in_12(register_13_q), .in_13(register_14_q),
    .in_14(register_15_q), .in_15(register_16_q), .in_16(register_17_q), .in_17(register_18_q),
    .in_18(register_19_q), .in_19(register_20_q), .in_20(register_21_q), .in_21(register_22_q),
    .in_22(register_23_q), .in_23(register_24_q), .in_24(register_25_q), .in_25(register_26_q),
    .in_26(register_27_q), .in_27(register_28_q), .in_28(register_29_q), .in_29(register_30_q),
    .in_30(register_31_q), .in_31(register_32_q), .in_32(register_33_q), .in_33(register_34_q),
    .out_34(grs_register_printallow32_1_out_34));
  GRS_Register_Printallow32 grs_register_printallow32_2 (
    .Address(PRINT_ADDRESS1), .in_2(register_3_q), .in_3(register_4_q), .in_4(register_5_q),
    .in_5(register_6_q), .in_6(register_7_q), .in_7(register_8_q), .in_8(register_9_q), .in_9(register_10_q),
    .in_10(register_11_q), .in_11(register_12_q), .in_12(register_13_q), .in_13(register_14_q),
    .in_14(register_15_q), .in_15(register_16_q), .in_16(register_17_q), .in_17(register_18_q),
    .in_18(register_19_q), .in_19(register_20_q), .in_20(register_21_q), .in_21(register_22_q),
    .in_22(register_23_q), .in_23(register_24_q), .in_24(register_25_q), .in_25(register_26_q),
    .in_26(register_27_q), .in_27(register_28_q), .in_28(register_29_q), .in_29(register_30_q),
    .in_30(register_31_q), .in_31(register_32_q), .in_32(register_33_q), .in_33(register_34_q),
    .out_34(grs_register_printallow32_2_out_34));
  GRS_Register_Printchoose2 grs_register_printchoose2_1 (
    .Choose1(grs_register_printallow32_1_out_34), .Outputchoose(and_1_out),
    .Choose2(grs_register_printallow32_2_out_34), .Print1(out_8), .Print2(out_9));
endmodule

module Norb_EXT_1B_Delayer (
  input  SIGIN,
  input  CLOCK_IN,
  output SIGOUT
);

  wire d_ff_1_q, not_1_out;

  D_Flip_Flop d_ff_1 (.D(SIGIN), .clk(CLOCK_IN), .Q(d_ff_1_q));  // open: Qn, preset, reset
  D_Flip_Flop d_ff_2 (.D(d_ff_1_q), .clk(not_1_out), .Q(SIGOUT));  // open: Qn, preset, reset
  not not_1 (not_1_out, CLOCK_IN);
endmodule

module Locked (
  input  in_1,
  input  RESET,
  input  in_3,
  input  ALLOW,
  input  SET,
  output out_6,
  output Q,
  output out_8,
  output out_9
);

  wire and_1_out, and_2_out;

  and and_1 (and_1_out, RESET, ALLOW);
  and and_2 (and_2_out, ALLOW, SET);
  and and_3 (out_6, in_1, out_6);
  nor nor_1 (Q, and_1_out, out_9);
  nor nor_2 (out_9, Q, and_2_out);
  or or_1 (out_8, in_3, out_8);
endmodule

module GRS_BOOT (
  input  [7:0] ADDRESS,
  input  Write_Enable,
  input  Output_enable,
  input  [7:0] in_4
);

  wire adder_1_cout, and_1_out, clock_1_out, not_1_out, or_1_out, or_2_out;
  wire [7:0] adder_1_out, norb_std_8b2t_delayer_1_sigout, or_3_out;
  wire [31:0] ram_1_dout, rom_1_data;

  Clock clock_1 (.out(clock_1_out));
  and and_1 (and_1_out, clock_1_out, not_1_out);
  not not_1 (not_1_out, adder_1_cout);
  Norb_STD_8B2T_Delayer norb_std_8b2t_delayer_1 (
    .SIGIN(adder_1_out), .CLOCK(and_1_out), .SIGOUT(norb_std_8b2t_delayer_1_sigout));
  Adder adder_1 (.a(norb_std_8b2t_delayer_1_sigout), .b(in_4), .out(adder_1_out), .cout(adder_1_cout));  // open: cin
  or or_1 (or_1_out, Output_enable, and_1_out);
  or or_2 (or_2_out, Write_Enable, and_1_out);
  assign or_3_out = ADDRESS | adder_1_out;  // OR_Gate or_3, 8 bits wide
  ROM #(.dataWidth(32)) rom_1 (.addr(or_3_out), .data(rom_1_data));
  RAM #(.dataWidth(32), .trigger("high")) ram_1 (
    .addr(or_3_out), .we(or_1_out), .oe(or_2_out), .din(rom_1_data), .dout(ram_1_dout));

  // Notes on the sheet:
  //   contents of rom_1 (hex, n*v repeats v):
  //   1 22*0 1 44*0 1 4*0 1 1
endmodule
