// Logisim project GRS_Storage.circ as structural Verilog: 8 circuits, main circuit GRS_Storage_64_4B
module GRS_Storage_64_4B (
  input  [31:0] ALLINPUT,
  input  ALLOWTOINPUT,
  input  [2:0] INPUTADDRESS2,
  input  [2:0] INPUTADDRESS1,
  input  [2:0] READADDRESS1,
  input  [2:0] READADDRESS2,
  input  READALLOW,
  output [31:0] ALLOUTPUT
);

  wire grs_storage_readallowfor8_1_out_3, grs_storage_readallowfor8_1_out_4,
       grs_storage_readallowfor8_1_out_5, grs_storage_readallowfor8_1_out_6,
       grs_storage_readallowfor8_1_out_7, grs_storage_readallowfor8_1_out_8,
       grs_storage_readallowfor8_1_out_9, grs_storage_readallowfor8_1_out_10,
       grs_storage_readallowfor8_2_out_3, grs_storage_readallowfor8_2_out_4,
       grs_storage_readallowfor8_2_out_5, grs_storage_readallowfor8_2_out_6,
       grs_storage_readallowfor8_2_out_7, grs_storage_readallowfor8_2_out_8,
       grs_storage_readallowfor8_2_out_9, grs_storage_readallowfor8_2_out_10,
       grs_storage_writeallowfor8_1_out_3, grs_storage_writeallowfor8_1_out_4,
       grs_storage_writeallowfor8_1_out_5, grs_storage_writeallowfor8_1_out_6,
       grs_storage_writeallowfor8_1_out_7, grs_storage_writeallowfor8_1_out_8,
       grs_storage_writeallowfor8_1_out_9, grs_storage_writeallowfor8_1_out_10,
       grs_storage_writeallowfor8_2_out_3, grs_storage_writeallowfor8_2_out_4,
       grs_storage_writeallowfor8_2_out_5, grs_storage_writeallowfor8_2_out_6,
       grs_storage_writeallowfor8_2_out_7, grs_storage_writeallowfor8_2_out_8,
       grs_storage_writeallowfor8_2_out_9, grs_storage_writeallowfor8_2_out_10;
  wire [31:0] grs_register_4b_1_output1, grs_register_4b_2_output1, grs_register_4b_3_output1,
       grs_register_4b_4_output1, grs_register_4b_5_output1, grs_register_4b_6_output1,
       grs_register_4b_7_output1, grs_register_4b_8_output1, grs_register_4b_9_output1,
       grs_register_4b_10_output1, grs_register_4b_11_output1, grs_register_4b_12_output1,
       grs_register_4b_13_output1, grs_register_4b_14_output1, grs_register_4b_15_output1,
       grs_register_4b_16_output1, grs_register_4b_17_output1, grs_register_4b_18_output1,
       grs_register_4b_19_output1, grs_register_4b_20_output1, grs_register_4b_21_output1,
       grs_register_4b_22_output1, grs_register_4b_23_output1, grs_register_4b_24_output1,
       grs_register_4b_25_output1, grs_register_4b_26_output1, grs_register_4b_27_output1,
       grs_register_4b_28_output1, grs_register_4b_29_output1, grs_register_4b_30_output1,
       grs_register_4b_31_output1, grs_register_4b_32_output1, grs_register_4b_33_output1,
       grs_register_4b_34_output1, grs_register_4b_35_output1, grs_register_4b_36_output1,
       grs_register_4b_37_output1, grs_register_4b_38_output1, grs_register_4b_39_output1,
       grs_register_4b_40_output1, grs_register_4b_41_output1, grs_register_4b_42_output1,
       grs_register_4b_43_output1, grs_register_4b_44_output1, grs_register_4b_45_output1,
       grs_register_4b_46_output1, grs_register_4b_47_output1, grs_register_4b_48_output1,
       grs_register_4b_49_output1, grs_register_4b_50_output1, grs_register_4b_51_output1,
       grs_register_4b_52_output1, grs_register_4b_53_output1, grs_register_4b_54_output1,
       grs_register_4b_55_output1, grs_register_4b_56_output1, grs_register_4b_57_output1,
       grs_register_4b_58_output1, grs_register_4b_59_output1, grs_register_4b_60_output1,
       grs_register_4b_61_output1, grs_register_4b_62_output1, grs_register_4b_63_output1,
       grs_register_4b_64_output1, or_2_out;

  GRS_Storage_Readallowfor8 grs_storage_readallowfor8_1 (
    .ADDRESS(READADDRESS2), .Readallow(READALLOW), .out_3(grs_storage_readallowfor8_1_out_3),
    .out_4(grs_storage_readallowfor8_1_out_4), .out_5(grs_storage_readallowfor8_1_out_5),
    .out_6(grs_storage_readallowfor8_1_out_6), .out_7(grs_storage_readallowfor8_1_out_7),
    .out_8(grs_storage_readallowfor8_1_out_8), .out_9(grs_storage_readallowfor8_1_out_9),
    .out_10(grs_storage_readallowfor8_1_out_10));
  GRS_Register_4B grs_register_4b_1 (
    .ReadAllow2(grs_storage_readallowfor8_1_out_3), .ReadAllow1(grs_storage_readallowfor8_2_out_3),
    .Data1(ALLINPUT), .WriteAllow1(grs_storage_writeallowfor8_1_out_3),
    .WriteAllow2(grs_storage_writeallowfor8_2_out_3), .Output1(grs_register_4b_1_output1));
  GRS_Register_4B grs_register_4b_2 (
    .ReadAllow2(grs_storage_readallowfor8_1_out_4), .ReadAllow1(grs_storage_readallowfor8_2_out_3),
    .Data1(ALLINPUT), .WriteAllow1(grs_storage_writeallowfor8_1_out_3),
    .WriteAllow2(grs_storage_writeallowfor8_2_out_4), .Output1(grs_register_4b_2_output1));
  GRS_Register_4B grs_register_4b_3 (
    .ReadAllow2(grs_storage_readallowfor8_1_out_5), .ReadAllow1(grs_storage_readallowfor8_2_out_3),
    .Data1(ALLINPUT), .WriteAllow1(grs_storage_writeallowfor8_1_out_3),
    .WriteAllow2(grs_storage_writeallowfor8_2_out_5), .Output1(grs_register_4b_3_output1));
  GRS_Register_4B grs_register_4b_4 (
    .ReadAllow2(grs_storage_readallowfor8_1_out_6), .ReadAllow1(grs_storage_readallowfor8_2_out_3),
    .Data1(ALLINPUT), .WriteAllow1(grs_storage_writeallowfor8_1_out_3),
    .WriteAllow2(grs_storage_writeallowfor8_2_out_6), .Output1(grs_register_4b_4_output1));
  GRS_Register_4B grs_register_4b_5 (
    .ReadAllow2(grs_storage_readallowfor8_1_out_7), .ReadAllow1(grs_storage_readallowfor8_2_out_3),
    .Data1(ALLINPUT), .WriteAllow1(grs_storage_writeallowfor8_1_out_3),
    .WriteAllow2(grs_storage_writeallowfor8_2_out_7), .Output1(grs_register_4b_5_output1));
  GRS_Register_4B grs_register_4b_6 (
    .ReadAllow2(grs_storage_readallowfor8_1_out_8), .ReadAllow1(grs_storage_readallowfor8_2_out_3),
    .Data1(ALLINPUT), .WriteAllow1(grs_storage_writeallowfor8_1_out_3),
    .WriteAllow2(grs_storage_writeallowfor8_2_out_8), .Output1(grs_register_4b_6_output1));
  GRS_Register_4B grs_register_4b_7 (
    .ReadAllow2(grs_storage_readallowfor8_1_out_9), .ReadAllow1(grs_storage_readallowfor8_2_out_3),
    .Data1(ALLINPUT), .WriteAllow1(grs_storage_writeallowfor8_1_out_3),
    .WriteAllow2(grs_storage_writeallowfor8_2_out_9), .Output1(grs_register_4b_7_output1));
  GRS_Register_4B grs_register_4b_8 (
    .ReadAllow2(grs_storage_readallowfor8_1_out_10), .ReadAllow1(grs_storage_readallowfor8_2_out_3),
    .Data1(ALLINPUT), .WriteAllow1(grs_storage_writeallowfor8_1_out_3),
    .WriteAllow2(grs_storage_writeallowfor8_2_out_10), .Output1(grs_register_4b_8_output1));
  assign ALLOUTPUT = grs_register_4b_1_output1 | grs_register_4b_2_output1 | grs_register_4b_3_output1 | grs_register_4b_4_output1 | grs_register_4b_5_output1 | grs_register_4b_6_output1 | grs_register_4b_7_output1 | grs_register_4b_8_output1;  // OR_Gate or_1, 32 bits wide
  GRS_Register_4B grs_register_4b_9 (
    .ReadAllow2(grs_storage_readallowfor8_1_out_3), .ReadAllow1(grs_storage_readallowfor8_2_out_4),
    .Data1(ALLINPUT), .WriteAllow1(grs_storage_writeallowfor8_1_out_4),
    .WriteAllow2(grs_storage_writeallowfor8_2_out_3), .Output1(grs_register_4b_9_output1));
  GRS_Register_4B grs_register_4b_10 (
    .ReadAllow2(grs_storage_readallowfor8_1_out_4), .ReadAllow1(grs_storage_readallowfor8_2_out_4),
    .Data1(ALLINPUT), .WriteAllow1(grs_storage_writeallowfor8_1_out_4),
    .WriteAllow2(grs_storage_writeallowfor8_2_out_4), .Output1(grs_register_4b_10_output1));
  GRS_Register_4B grs_register_4b_11 (
    .ReadAllow2(grs_storage_readallowfor8_1_out_5), .ReadAllow1(grs_storage_readallowfor8_2_out_4),
    .Data1(ALLINPUT), .WriteAllow1(grs_storage_writeallowfor8_1_out_4),
    .WriteAllow2(grs_storage_writeallowfor8_2_out_5), .Output1(grs_register_4b_11_output1));
  GRS_Register_4B grs_register_4b_12 (
    .ReadAllow2(grs_storage_readallowfor8_1_out_6), .ReadAllow1(grs_storage_readallowfor8_2_out_4),
    .Data1(ALLINPUT), .WriteAllow1(grs_storage_writeallowfor8_1_out_4),
    .WriteAllow2(grs_storage_writeallowfor8_2_out_6), .Output1(grs_register_4b_12_output1));
  GRS_Register_4B grs_register_4b_13 (
    .ReadAllow2(grs_storage_readallowfor8_1_out_7), .ReadAllow1(grs_storage_readallowfor8_2_out_4),
    .Data1(ALLINPUT), .WriteAllow1(grs_storage_writeallowfor8_1_out_4),
    .WriteAllow2(grs_storage_writeallowfor8_2_out_7), .Output1(grs_register_4b_13_output1));
  GRS_Register_4B grs_register_4b_14 (
    .ReadAllow2(grs_storage_readallowfor8_1_out_8), .ReadAllow1(grs_storage_readallowfor8_2_out_4),
    .Data1(ALLINPUT), .WriteAllow1(grs_storage_writeallowfor8_1_out_4),
    .WriteAllow2(grs_storage_writeallowfor8_2_out_8), .Output1(grs_register_4b_14_output1));
  GRS_Register_4B grs_register_4b_15 (
    .ReadAllow2(grs_storage_readallowfor8_1_out_9), .ReadAllow1(grs_storage_readallowfor8_2_out_4),
    .Data1(ALLINPUT), .WriteAllow1(grs_storage_writeallowfor8_1_out_4),
    .WriteAllow2(grs_storage_writeallowfor8_2_out_9), .Output1(grs_register_4b_15_output1));
  GRS_Register_4B grs_register_4b_16 (
    .ReadAllow2(grs_storage_readallowfor8_1_out_10), .ReadAllow1(grs_storage_readallowfor8_2_out_4),
    .Data1(ALLINPUT), .WriteAllow1(grs_storage_writeallowfor8_1_out_4),
    .WriteAllow2(grs_storage_writeallowfor8_2_out_10), .Output1(grs_register_4b_16_output1));
  assign or_2_out = grs_register_4b_9_output1 | grs_register_4b_10_output1 | grs_register_4b_11_output1 | grs_register_4b_12_output1 | grs_register_4b_13_output1 | grs_register_4b_14_output1 | grs_register_4b_15_output1 | grs_register_4b_16_output1;  // OR_Gate or_2, 32 bits wide
  GRS_Register_4B grs_register_4b_17 (
    .ReadAllow2(grs_storage_readallowfor8_1_out_3), .ReadAllow1(grs_storage_readallowfor8_2_out_5),
    .Data1(ALLINPUT), .WriteAllow1(grs_storage_writeallowfor8_1_out_5),
    .WriteAllow2(grs_storage_writeallowfor8_2_out_3), .Output1(grs_register_4b_17_output1));
  GRS_Register_4B grs_register_4b_18 (
    .ReadAllow2(grs_storage_readallowfor8_1_out_4), .ReadAllow1(grs_storage_readallowfor8_2_out_5),
    .Data1(ALLINPUT), .WriteAllow1(grs_storage_writeallowfor8_1_out_5),
    .WriteAllow2(grs_storage_writeallowfor8_2_out_4), .Output1(grs_register_4b_18_output1));
  GRS_Register_4B grs_register_4b_19 (
    .ReadAllow2(grs_storage_readallowfor8_1_out_5), .ReadAllow1(grs_storage_readallowfor8_2_out_5),
    .Data1(ALLINPUT), .WriteAllow1(grs_storage_writeallowfor8_1_out_5),
    .WriteAllow2(grs_storage_writeallowfor8_2_out_5), .Output1(grs_register_4b_19_output1));
  GRS_Register_4B grs_register_4b_20 (
    .ReadAllow2(grs_storage_readallowfor8_1_out_6), .ReadAllow1(grs_storage_readallowfor8_2_out_5),
    .Data1(ALLINPUT), .WriteAllow1(grs_storage_writeallowfor8_1_out_5),
    .WriteAllow2(grs_storage_writeallowfor8_2_out_6), .Output1(grs_register_4b_20_output1));
  GRS_Register_4B grs_register_4b_21 (
    .ReadAllow2(grs_storage_readallowfor8_1_out_7), .ReadAllow1(grs_storage_readallowfor8_2_out_5),
    .Data1(ALLINPUT), .WriteAllow1(grs_storage_writeallowfor8_1_out_5),
    .WriteAllow2(grs_storage_writeallowfor8_2_out_7), .Output1(grs_register_4b_21_output1));
  GRS_Register_4B grs_register_4b_22 (
    .ReadAllow2(grs_storage_readallowfor8_1_out_8), .ReadAllow1(grs_storage_readallowfor8_2_out_5),
    .Data1(ALLINPUT), .WriteAllow1(grs_storage_writeallowfor8_1_out_5),
    .WriteAllow2(grs_storage_writeallowfor8_2_out_8), .Output1(grs_register_4b_22_output1));
  GRS_Register_4B grs_register_4b_23 (
    .ReadAllow2(grs_storage_readallowfor8_1_out_9), .ReadAllow1(grs_storage_readallowfor8_2_out_5),
    .Data1(ALLINPUT), .WriteAllow1(grs_storage_writeallowfor8_1_out_5),
    .WriteAllow2(grs_storage_writeallowfor8_2_out_9), .Output1(grs_register_4b_23_output1));
  GRS_Register_4B grs_register_4b_24 (
    .ReadAllow2(grs_storage_readallowfor8_1_out_10), .ReadAllow1(grs_storage_readallowfor8_2_out_5),
    .Data1(ALLINPUT), .WriteAllow1(grs_storage_writeallowfor8_1_out_5),
    .WriteAllow2(grs_storage_writeallowfor8_2_out_10), .Output1(grs_register_4b_24_output1));
  assign ALLOUTPUT = grs_register_4b_17_output1 | grs_register_4b_18_output1 | grs_register_4b_19_output1 | grs_register_4b_20_output1 | grs_register_4b_21_output1 | grs_register_4b_22_output1 | grs_register_4b_23_output1 | grs_register_4b_24_output1;  // OR_Gate or_3, 32 bits wide
  GRS_Register_4B grs_register_4b_25 (
    .ReadAllow2(grs_storage_readallowfor8_1_out_3), .ReadAllow1(grs_storage_readallowfor8_2_out_6),
    .Data1(ALLINPUT), .WriteAllow1(grs_storage_writeallowfor8_1_out_6),
    .WriteAllow2(grs_storage_writeallowfor8_2_out_3), .Output1(grs_register_4b_25_output1));
  GRS_Register_4B grs_register_4b_26 (
    .ReadAllow2(grs_storage_readallowfor8_1_out_4), .ReadAllow1(grs_storage_readallowfor8_2_out_6),
    .Data1(ALLINPUT), .WriteAllow1(grs_storage_writeallowfor8_1_out_6),
    .WriteAllow2(grs_storage_writeallowfor8_2_out_4), .Output1(grs_register_4b_26_output1));
  GRS_Register_4B grs_register_4b_27 (
    .ReadAllow2(grs_storage_readallowfor8_1_out_5), .ReadAllow1(grs_storage_readallowfor8_2_out_6),
    .Data1(ALLINPUT), .WriteAllow1(grs_storage_writeallowfor8_1_out_6),
    .WriteAllow2(grs_storage_writeallowfor8_2_out_5), .Output1(grs_register_4b_27_output1));
  GRS_Register_4B grs_register_4b_28 (
    .ReadAllow2(grs_storage_readallowfor8_1_out_6), .ReadAllow1(grs_storage_readallowfor8_2_out_6),
    .Data1(ALLINPUT), .WriteAllow1(grs_storage_writeallowfor8_1_out_6),
    .WriteAllow2(grs_storage_writeallowfor8_2_out_6), .Output1(grs_register_4b_28_output1));
  GRS_Register_4B grs_register_4b_29 (
    .ReadAllow2(grs_storage_readallowfor8_1_out_7), .ReadAllow1(grs_storage_readallowfor8_2_out_6),
    .Data1(ALLINPUT), .WriteAllow1(grs_storage_writeallowfor8_1_out_6),
    .WriteAllow2(grs_storage_writeallowfor8_2_out_7), .Output1(grs_register_4b_29_output1));
  GRS_Register_4B grs_register_4b_30 (
    .ReadAllow2(grs_storage_readallowfor8_1_out_8), .ReadAllow1(grs_storage_readallowfor8_2_out_6),
    .Data1(ALLINPUT), .WriteAllow1(grs_storage_writeallowfor8_1_out_6),
    .WriteAllow2(grs_storage_writeallowfor8_2_out_8), .Output1(grs_register_4b_30_output1));
  GRS_Register_4B grs_register_4b_31 (
    .ReadAllow2(grs_storage_readallowfor8_1_out_9), .ReadAllow1(grs_storage_readallowfor8_2_out_6),
    .Data1(ALLINPUT), .WriteAllow1(grs_storage_writeallowfor8_1_out_6),
    .WriteAllow2(grs_storage_writeallowfor8_2_out_9), .Output1(grs_register_4b_31_output1));
  GRS_Register_4B grs_register_4b_32 (
    .ReadAllow2(grs_storage_readallowfor8_1_out_10), .ReadAllow1(grs_storage_readallowfor8_2_out_6),
    .Data1(ALLINPUT), .WriteAllow1(grs_storage_writeallowfor8_1_out_6),
    .WriteAllow2(grs_storage_writeallowfor8_2_out_10), .Output1(grs_register_4b_32_output1));
  GRS_Storage_Writeallowfor8 grs_storage_writeallowfor8_1 (
    .ADDRESS(INPUTADDRESS1), .Writeallow(ALLOWTOINPUT), .out_3(grs_storage_writeallowfor8_1_out_3),
    .out_4(grs_storage_writeallowfor8_1_out_4), .out_5(grs_storage_writeallowfor8_1_out_5),
    .out_6(grs_storage_writeallowfor8_1_out_6), .out_7(grs_storage_writeallowfor8_1_out_7),
    .out_8(grs_storage_writeallowfor8_1_out_8), .out_9(grs_storage_writeallowfor8_1_out_9),
    .out_10(grs_storage_writeallowfor8_1_out_10));
  GRS_Storage_Readallowfor8 grs_storage_readallowfor8_2 (
    .ADDRESS(READADDRESS1), .Readallow(READALLOW), .out_3(grs_storage_readallowfor8_2_out_3),
    .out_4(grs_storage_readallowfor8_2_out_4), .out_5(grs_storage_readallowfor8_2_out_5),
    .out_6(grs_storage_readallowfor8_2_out_6), .out_7(grs_storage_readallowfor8_2_out_7),
    .out_8(grs_storage_readallowfor8_2_out_8), .out_9(grs_storage_readallowfor8_2_out_9),
    .out_10(grs_storage_readallowfor8_2_out_10));
  assign ALLOUTPUT = grs_register_4b_25_output1 | grs_register_4b_26_output1 | grs_register_4b_27_output1 | grs_register_4b_28_output1 | grs_register_4b_29_output1 | grs_register_4b_30_output1 | grs_register_4b_31_output1 | grs_register_4b_32_output1;  // OR_Gate or_4, 32 bits wide
  GRS_Register_4B grs_register_4b_33 (
    .ReadAllow2(grs_storage_readallowfor8_1_out_3), .ReadAllow1(grs_storage_readallowfor8_2_out_7),
    .Data1(ALLINPUT), .WriteAllow1(grs_storage_writeallowfor8_1_out_7),
    .WriteAllow2(grs_storage_writeallowfor8_2_out_3), .Output1(grs_register_4b_33_output1));
  GRS_Register_4B grs_register_4b_34 (
    .ReadAllow2(grs_storage_readallowfor8_1_out_4), .ReadAllow1(grs_storage_readallowfor8_2_out_7),
    .Data1(ALLINPUT), .WriteAllow1(grs_storage_writeallowfor8_1_out_7),
    .WriteAllow2(grs_storage_writeallowfor8_2_out_4), .Output1(grs_register_4b_34_output1));
  GRS_Register_4B grs_register_4b_35 (
    .ReadAllow2(grs_storage_readallowfor8_1_out_5), .ReadAllow1(grs_storage_readallowfor8_2_out_7),
    .Data1(ALLINPUT), .WriteAllow1(grs_storage_writeallowfor8_1_out_7),
    .WriteAllow2(grs_storage_writeallowfor8_2_out_5), .Output1(grs_register_4b_35_output1));
  GRS_Register_4B grs_register_4b_36 (
    .ReadAllow2(grs_storage_readallowfor8_1_out_6), .ReadAllow1(grs_storage_readallowfor8_2_out_7),
    .Data1(ALLINPUT), .WriteAllow1(grs_storage_writeallowfor8_1_out_7),
    .WriteAllow2(grs_storage_writeallowfor8_2_out_6), .Output1(grs_register_4b_36_output1));
  GRS_Register_4B grs_register_4b_37 (
    .ReadAllow2(grs_storage_readallowfor8_1_out_7), .ReadAllow1(grs_storage_readallowfor8_2_out_7),
    .Data1(ALLINPUT), .WriteAllow1(grs_storage_writeallowfor8_1_out_7),
    .WriteAllow2(grs_storage_writeallowfor8_2_out_7), .Output1(grs_register_4b_37_output1));
  GRS_Register_4B grs_register_4b_38 (
    .ReadAllow2(grs_storage_readallowfor8_1_out_8), .ReadAllow1(grs_storage_readallowfor8_2_out_7),
    .Data1(ALLINPUT), .WriteAllow1(grs_storage_writeallowfor8_1_out_7),
    .WriteAllow2(grs_storage_writeallowfor8_2_out_8), .Output1(grs_register_4b_38_output1));
  GRS_Register_4B grs_register_4b_39 (
    .ReadAllow2(grs_storage_readallowfor8_1_out_9), .ReadAllow1(grs_storage_readallowfor8_2_out_7),
    .Data1(ALLINPUT), .WriteAllow1(grs_storage_writeallowfor8_1_out_7),
    .WriteAllow2(grs_storage_writeallowfor8_2_out_9), .Output1(grs_register_4b_39_output1));
  GRS_Register_4B grs_register_4b_40 (
    .ReadAllow2(grs_storage_readallowfor8_1_out_10), .ReadAllow1(grs_storage_readallowfor8_2_out_7),
    .Data1(ALLINPUT), .WriteAllow1(grs_storage_writeallowfor8_1_out_7),
    .WriteAllow2(grs_storage_writeallowfor8_2_out_10), .Output1(grs_register_4b_40_output1));
  assign ALLOUTPUT = grs_register_4b_33_output1 | grs_register_4b_34_output1 | grs_register_4b_35_output1 | grs_register_4b_36_output1 | grs_register_4b_37_output1 | grs_register_4b_38_output1 | grs_register_4b_39_output1 | grs_register_4b_40_output1;  // OR_Gate or_5, 32 bits wide
  GRS_Register_4B grs_register_4b_41 (
    .ReadAllow2(grs_storage_readallowfor8_1_out_3), .ReadAllow1(grs_storage_readallowfor8_2_out_8),
    .Data1(ALLINPUT), .WriteAllow1(grs_storage_writeallowfor8_1_out_8),
    .WriteAllow2(grs_storage_writeallowfor8_2_out_3), .Output1(grs_register_4b_41_output1));
  GRS_Register_4B grs_register_4b_42 (
    .ReadAllow2(grs_storage_readallowfor8_1_out_4), .ReadAllow1(grs_storage_readallowfor8_2_out_8),
    .Data1(ALLINPUT), .WriteAllow1(grs_storage_writeallowfor8_1_out_8),
    .WriteAllow2(grs_storage_writeallowfor8_2_out_4), .Output1(grs_register_4b_42_output1));
  GRS_Register_4B grs_register_4b_43 (
    .ReadAllow2(grs_storage_readallowfor8_1_out_5), .ReadAllow1(grs_storage_readallowfor8_2_out_8),
    .Data1(ALLINPUT), .WriteAllow1(grs_storage_writeallowfor8_1_out_8),
    .WriteAllow2(grs_storage_writeallowfor8_2_out_5), .Output1(grs_register_4b_43_output1));
  GRS_Register_4B grs_register_4b_44 (
    .ReadAllow2(grs_storage_readallowfor8_1_out_6), .ReadAllow1(grs_storage_readallowfor8_2_out_8),
    .Data1(ALLINPUT), .WriteAllow1(grs_storage_writeallowfor8_1_out_8),
    .WriteAllow2(grs_storage_writeallowfor8_2_out_6), .Output1(grs_register_4b_44_output1));
  GRS_Register_4B grs_register_4b_45 (
    .ReadAllow2(grs_storage_readallowfor8_1_out_7), .ReadAllow1(grs_storage_readallowfor8_2_out_8),
    .Data1(ALLINPUT), .WriteAllow1(grs_storage_writeallowfor8_1_out_8),
    .WriteAllow2(grs_storage_writeallowfor8_2_out_7), .Output1(grs_register_4b_45_output1));
  GRS_Register_4B grs_register_4b_46 (
    .ReadAllow2(grs_storage_readallowfor8_1_out_8), .ReadAllow1(grs_storage_readallowfor8_2_out_8),
    .Data1(ALLINPUT), .WriteAllow1(grs_storage_writeallowfor8_1_out_8),
    .WriteAllow2(grs_storage_writeallowfor8_2_out_8), .Output1(grs_register_4b_46_output1));
  GRS_Register_4B grs_register_4b_47 (
    .ReadAllow2(grs_storage_readallowfor8_1_out_9), .ReadAllow1(grs_storage_readallowfor8_2_out_8),
    .Data1(ALLINPUT), .WriteAllow1(grs_storage_writeallowfor8_1_out_8),
    .WriteAllow2(grs_storage_writeallowfor8_2_out_9), .Output1(grs_register_4b_47_output1));
  GRS_Register_4B grs_register_4b_48 (
    .ReadAllow2(grs_storage_readallowfor8_1_out_10), .ReadAllow1(grs_storage_readallowfor8_2_out_8),
    .Data1(ALLINPUT), .WriteAllow1(grs_storage_writeallowfor8_1_out_8),
    .WriteAllow2(grs_storage_writeallowfor8_2_out_10), .Output1(grs_register_4b_48_output1));
  assign ALLOUTPUT = grs_register_4b_41_output1 | grs_register_4b_42_output1 | grs_register_4b_43_output1 | grs_register_4b_44_output1 | grs_register_4b_45_output1 | grs_register_4b_46_output1 | grs_register_4b_47_output1 | grs_register_4b_48_output1;  // OR_Gate or_6, 32 bits wide
  GRS_Register_4B grs_register_4b_49 (
    .ReadAllow2(grs_storage_readallowfor8_1_out_3), .ReadAllow1(grs_storage_readallowfor8_2_out_9),
    .Data1(ALLINPUT), .WriteAllow1(grs_storage_writeallowfor8_1_out_9),
    .WriteAllow2(grs_storage_writeallowfor8_2_out_3), .Output1(grs_register_4b_49_output1));
  GRS_Register_4B grs_register_4b_50 (
    .ReadAllow2(grs_storage_readallowfor8_1_out_4), .ReadAllow1(grs_storage_readallowfor8_2_out_9),
    .Data1(ALLINPUT), .WriteAllow1(grs_storage_writeallowfor8_1_out_9),
    .WriteAllow2(grs_storage_writeallowfor8_2_out_4), .Output1(grs_register_4b_50_output1));
  GRS_Register_4B grs_register_4b_51 (
    .ReadAllow2(grs_storage_readallowfor8_1_out_5), .ReadAllow1(grs_storage_readallowfor8_2_out_9),
    .Data1(ALLINPUT), .WriteAllow1(grs_storage_writeallowfor8_1_out_9),
    .WriteAllow2(grs_storage_writeallowfor8_2_out_5), .Output1(grs_register_4b_51_output1));
  GRS_Register_4B grs_register_4b_52 (
    .ReadAllow2(grs_storage_readallowfor8_1_out_6), .ReadAllow1(grs_storage_readallowfor8_2_out_9),
    .Data1(ALLINPUT), .WriteAllow1(grs_storage_writeallowfor8_1_out_9),
    .WriteAllow2(grs_storage_writeallowfor8_2_out_6), .Output1(grs_register_4b_52_output1));
  GRS_Register_4B grs_register_4b_53 (
    .ReadAllow2(grs_storage_readallowfor8_1_out_7), .ReadAllow1(grs_storage_readallowfor8_2_out_9),
    .Data1(ALLINPUT), .WriteAllow1(grs_storage_writeallowfor8_1_out_9),
    .WriteAllow2(grs_storage_writeallowfor8_2_out_7), .Output1(grs_register_4b_53_output1));
  GRS_Register_4B grs_register_4b_54 (
    .ReadAllow2(grs_storage_readallowfor8_1_out_8), .ReadAllow1(grs_storage_readallowfor8_2_out_9),
    .Data1(ALLINPUT), .WriteAllow1(grs_storage_writeallowfor8_1_out_9),
    .WriteAllow2(grs_storage_writeallowfor8_2_out_8), .Output1(grs_register_4b_54_output1));
  GRS_Register_4B grs_register_4b_55 (
    .ReadAllow2(grs_storage_readallowfor8_1_out_9), .ReadAllow1(grs_storage_readallowfor8_2_out_9),
    .Data1(ALLINPUT), .WriteAllow1(grs_storage_writeallowfor8_1_out_9),
    .WriteAllow2(grs_storage_writeallowfor8_2_out_9), .Output1(grs_register_4b_55_output1));
  GRS_Register_4B grs_register_4b_56 (
    .ReadAllow2(grs_storage_readallowfor8_1_out_10), .ReadAllow1(grs_storage_readallowfor8_2_out_9),
    .Data1(ALLINPUT), .WriteAllow1(grs_storage_writeallowfor8_1_out_9),
    .WriteAllow2(grs_storage_writeallowfor8_2_out_10), .Output1(grs_register_4b_56_output1));
  assign ALLOUTPUT = grs_register_4b_49_output1 | grs_register_4b_50_output1 | grs_register_4b_51_output1 | grs_register_4b_52_output1 | grs_register_4b_53_output1 | grs_register_4b_54_output1 | grs_register_4b_55_output1 | grs_register_4b_56_output1;  // OR_Gate or_7, 32 bits wide
  GRS_Register_4B grs_register_4b_57 (
    .ReadAllow2(grs_storage_readallowfor8_1_out_3), .ReadAllow1(grs_storage_readallowfor8_2_out_10),
    .Data1(ALLINPUT), .WriteAllow1(grs_storage_writeallowfor8_1_out_10),
    .WriteAllow2(grs_storage_writeallowfor8_2_out_3), .Output1(grs_register_4b_57_output1));
  GRS_Register_4B grs_register_4b_58 (
    .ReadAllow2(grs_storage_readallowfor8_1_out_4), .ReadAllow1(grs_storage_readallowfor8_2_out_10),
    .Data1(ALLINPUT), .WriteAllow1(grs_storage_writeallowfor8_1_out_10),
    .WriteAllow2(grs_storage_writeallowfor8_2_out_4), .Output1(grs_register_4b_58_output1));
  GRS_Register_4B grs_register_4b_59 (
    .ReadAllow2(grs_storage_readallowfor8_1_out_5), .ReadAllow1(grs_storage_readallowfor8_2_out_10),
    .Data1(ALLINPUT), .WriteAllow1(grs_storage_writeallowfor8_1_out_10),
    .WriteAllow2(grs_storage_writeallowfor8_2_out_5), .Output1(grs_register_4b_59_output1));
  GRS_Register_4B grs_register_4b_60 (
    .ReadAllow2(grs_storage_readallowfor8_1_out_6), .ReadAllow1(grs_storage_readallowfor8_2_out_10),
    .Data1(ALLINPUT), .WriteAllow1(grs_storage_writeallowfor8_1_out_10),
    .WriteAllow2(grs_storage_writeallowfor8_2_out_6), .Output1(grs_register_4b_60_output1));
  GRS_Register_4B grs_register_4b_61 (
    .ReadAllow2(grs_storage_readallowfor8_1_out_7), .ReadAllow1(grs_storage_readallowfor8_2_out_10),
    .Data1(ALLINPUT), .WriteAllow1(grs_storage_writeallowfor8_1_out_10),
    .WriteAllow2(grs_storage_writeallowfor8_2_out_7), .Output1(grs_register_4b_61_output1));
  GRS_Register_4B grs_register_4b_62 (
    .ReadAllow2(grs_storage_readallowfor8_1_out_8), .ReadAllow1(grs_storage_readallowfor8_2_out_10),
    .Data1(ALLINPUT), .WriteAllow1(grs_storage_writeallowfor8_1_out_10),
    .WriteAllow2(grs_storage_writeallowfor8_2_out_8), .Output1(grs_register_4b_62_output1));
  GRS_Register_4B grs_register_4b_63 (
    .ReadAllow2(grs_storage_readallowfor8_1_out_9), .ReadAllow1(grs_storage_readallowfor8_2_out_10),
    .Data1(ALLINPUT), .WriteAllow1(grs_storage_writeallowfor8_1_out_10),
    .WriteAllow2(grs_storage_writeallowfor8_2_out_9), .Output1(grs_register_4b_63_output1));
  GRS_Register_4B grs_register_4b_64 (
    .ReadAllow2(grs_storage_readallowfor8_1_out_10), .ReadAllow1(grs_storage_readallowfor8_2_out_10),
    .Data1(ALLINPUT), .WriteAllow1(grs_storage_writeallowfor8_1_out_10),
    .WriteAllow2(grs_storage_writeallowfor8_2_out_10), .Output1(grs_register_4b_64_output1));
  assign ALLOUTPUT = grs_register_4b_57_output1 | grs_register_4b_58_output1 | grs_register_4b_59_output1 | grs_register_4b_60_output1 | grs_register_4b_61_output1 | grs_register_4b_62_output1 | grs_register_4b_63_output1 | grs_register_4b_64_output1;  // OR_Gate or_8, 32 bits wide
  GRS_Storage_Writeallowfor8 grs_storage_writeallowfor8_2 (
    .ADDRESS(INPUTADDRESS2), .Writeallow(ALLOWTOINPUT), .out_3(grs_storage_writeallowfor8_2_out_3),
    .out_4(grs_storage_writeallowfor8_2_out_4), .out_5(grs_storage_writeallowfor8_2_out_5),
    .out_6(grs_storage_writeallowfor8_2_out_6), .out_7(grs_storage_writeallowfor8_2_out_7),
    .out_8(grs_storage_writeallowfor8_2_out_8), .out_9(grs_storage_writeallowfor8_2_out_9),
    .out_10(grs_storage_writeallowfor8_2_out_10));
endmodule

module GRS_Storage_Dtouch (
  input  ALLOW,
  input  Data,
  output Q,
  output out_4
);

  wire and_1_out, and_2_out, not_1_out;

  not not_1 (not_1_out, Data);
  and and_1 (and_1_out, not_1_out, ALLOW);
  and and_2 (and_2_out, ALLOW, Data);
  nor nor_1 (Q, and_1_out, out_4);
  nor nor_2 (out_4, Q, and_2_out);
endmodule

module GRS_Register_4B (
  input  ReadAllow2,
  input  ReadAllow1,
  input  [31:0] Data1,
  input  WriteAllow1,
  input  WriteAllow2,
  output [31:0] Output1
);

  wire and_1_out, and_2_out;
  wire [31:0] grs_storage_dtouch_32_q;

  and and_1 (and_1_out, WriteAllow1, WriteAllow2);
  GRS_Storage_Dtouch grs_storage_dtouch_1 (
    .ALLOW(and_1_out), .Data(Data1[31]), .Q(grs_storage_dtouch_32_q[31]));  // open: out_4
  GRS_Storage_Dtouch grs_storage_dtouch_2 (
    .ALLOW(and_1_out), .Data(Data1[30]), .Q(grs_storage_dtouch_32_q[30]));  // open: out_4
  GRS_Storage_Dtouch grs_storage_dtouch_3 (
    .ALLOW(and_1_out), .Data(Data1[29]), .Q(grs_storage_dtouch_32_q[29]));  // open: out_4
  GRS_Storage_Dtouch grs_storage_dtouch_4 (
    .ALLOW(and_1_out), .Data(Data1[28]), .Q(grs_storage_dtouch_32_q[28]));  // open: out_4
  GRS_Storage_Dtouch grs_storage_dtouch_5 (
    .ALLOW(and_1_out), .Data(Data1[27]), .Q(grs_storage_dtouch_32_q[27]));  // open: out_4
  GRS_Storage_Dtouch grs_storage_dtouch_6 (
    .ALLOW(and_1_out), .Data(Data1[26]), .Q(grs_storage_dtouch_32_q[26]));  // open: out_4
  GRS_Storage_Dtouch grs_storage_dtouch_7 (
    .ALLOW(and_1_out), .Data(Data1[25]), .Q(grs_storage_dtouch_32_q[25]));  // open: out_4
  GRS_Storage_Dtouch grs_storage_dtouch_8 (
    .ALLOW(and_1_out), .Data(Data1[24]), .Q(grs_storage_dtouch_32_q[24]));  // open: out_4
  GRS_Storage_Dtouch grs_storage_dtouch_9 (
    .ALLOW(and_1_out), .Data(Data1[23]), .Q(grs_storage_dtouch_32_q[23]));  // open: out_4
  GRS_Storage_Dtouch grs_storage_dtouch_10 (
    .ALLOW(and_1_out), .Data(Data1[22]), .Q(grs_storage_dtouch_32_q[22]));  // open: out_4
  GRS_Storage_Dtouch grs_storage_dtouch_11 (
    .ALLOW(and_1_out), .Data(Data1[21]), .Q(grs_storage_dtouch_32_q[21]));  // open: out_4
  GRS_Storage_Dtouch grs_storage_dtouch_12 (
    .ALLOW(and_1_out), .Data(Data1[20]), .Q(grs_storage_dtouch_32_q[20]));  // open: out_4
  GRS_Storage_Dtouch grs_storage_dtouch_13 (
    .ALLOW(and_1_out), .Data(Data1[19]), .Q(grs_storage_dtouch_32_q[19]));  // open: out_4
  GRS_Storage_Dtouch grs_storage_dtouch_14 (
    .ALLOW(and_1_out), .Data(Data1[18]), .Q(grs_storage_dtouch_32_q[18]));  // open: out_4
  GRS_Storage_Dtouch grs_storage_dtouch_15 (
    .ALLOW(and_1_out), .Data(Data1[17]), .Q(grs_storage_dtouch_32_q[17]));  // open: out_4
  GRS_Storage_Dtouch grs_storage_dtouch_16 (
    .ALLOW(and_1_out), .Data(Data1[16]), .Q(grs_storage_dtouch_32_q[16]));  // open: out_4
  GRS_Storage_Dtouch grs_storage_dtouch_17 (
    .ALLOW(and_1_out), .Data(Data1[15]), .Q(grs_storage_dtouch_32_q[15]));  // open: out_4
  GRS_Storage_Dtouch grs_storage_dtouch_18 (
    .ALLOW(and_1_out), .Data(Data1[14]), .Q(grs_storage_dtouch_32_q[14]));  // open: out_4
  GRS_Storage_Dtouch grs_storage_dtouch_19 (
    .ALLOW(and_1_out), .Data(Data1[13]), .Q(grs_storage_dtouch_32_q[13]));  // open: out_4
  GRS_Storage_Dtouch grs_storage_dtouch_20 (
    .ALLOW(and_1_out), .Data(Data1[12]), .Q(grs_storage_dtouch_32_q[12]));  // open: out_4
  GRS_Storage_Dtouch grs_storage_dtouch_21 (
    .ALLOW(and_1_out), .Data(Data1[11]), .Q(grs_storage_dtouch_32_q[11]));  // open: out_4
  GRS_Storage_Dtouch grs_storage_dtouch_22 (
    .ALLOW(and_1_out), .Data(Data1[10]), .Q(grs_storage_dtouch_32_q[10]));  // open: out_4
  GRS_Storage_Dtouch grs_storage_dtouch_23 (
    .ALLOW(and_1_out), .Data(Data1[9]), .Q(grs_storage_dtouch_32_q[9]));  // open: out_4
  GRS_Storage_Dtouch grs_storage_dtouch_24 (
    .ALLOW(and_1_out), .Data(Data1[8]), .Q(grs_storage_dtouch_32_q[8]));  // open: out_4
  GRS_Storage_Dtouch grs_storage_dtouch_25 (
    .ALLOW(and_1_out), .Data(Data1[7]), .Q(grs_storage_dtouch_32_q[7]));  // open: out_4
  GRS_Storage_Dtouch grs_storage_dtouch_26 (
    .ALLOW(and_1_out), .Data(Data1[6]), .Q(grs_storage_dtouch_32_q[6]));  // open: out_4
  GRS_Storage_Dtouch grs_storage_dtouch_27 (
    .ALLOW(and_1_out), .Data(Data1[5]), .Q(grs_storage_dtouch_32_q[5]));  // open: out_4
  GRS_Storage_Dtouch grs_storage_dtouch_28 (
    .ALLOW(and_1_out), .Data(Data1[4]), .Q(grs_storage_dtouch_32_q[4]));  // open: out_4
  GRS_Storage_Dtouch grs_storage_dtouch_29 (
    .ALLOW(and_1_out), .Data(Data1[3]), .Q(grs_storage_dtouch_32_q[3]));  // open: out_4
  GRS_Storage_Dtouch grs_storage_dtouch_30 (
    .ALLOW(and_1_out), .Data(Data1[2]), .Q(grs_storage_dtouch_32_q[2]));  // open: out_4
  GRS_Storage_Dtouch grs_storage_dtouch_31 (
    .ALLOW(and_1_out), .Data(Data1[1]), .Q(grs_storage_dtouch_32_q[1]));  // open: out_4
  GRS_Storage_Dtouch grs_storage_dtouch_32 (
    .ALLOW(and_1_out), .Data(Data1[0]), .Q(grs_storage_dtouch_32_q[0]));  // open: out_4
  and and_2 (and_2_out, ReadAllow2, ReadAllow1);
  GRS_Register_Readallow grs_register_readallow_1 (
    .Input1(grs_storage_dtouch_32_q), .Allow1(and_2_out), .Output1(Output1));
endmodule

module GRS_Register_Readallow (
  input  [31:0] Input1,
  input  Allow1,
  output [31:0] Output1
);

  assign Output1 = Input1 & {32{Allow1}};  // AND_Gate and_1, 32 bits wide
endmodule

module GRS_MUX_5to32 (
  input  [4:0] Input5,
  output K00000,
  output K00001,
  output K00010,
  output K00011,
  output K00100,
  output K00101,
  output K00110,
  output K00111,
  output K01000,
  output K01001,
  output K01010,
  output K01011,
  output K01100,
  output K01101,
  output K01110,
  output K01111,
  output K10000,
  output K10001,
  output K10010,
  output K10011,
  output K10100,
  output K10101,
  output K10110,
  output K10111,
  output K11000,
  output K11001,
  output K11010,
  output K11011,
  output K11100,
  output K11101,
  output K11110,
  output K11111
);

  wire not_1_out, not_2_out, not_3_out, not_4_out, not_5_out, not_6_out, not_7_out, not_8_out, not_9_out,
       not_10_out, not_11_out, not_12_out, not_13_out, not_14_out, not_15_out, not_16_out, not_17_out,
       not_18_out, not_19_out, not_20_out, not_21_out, not_22_out, not_23_out, not_24_out, not_25_out,
       not_26_out, not_27_out, not_28_out, not_29_out, not_30_out, not_31_out, not_32_out, not_33_out,
       not_34_out, not_35_out, not_36_out, not_37_out, not_38_out, not_39_out, not_40_out, not_41_out,
       not_42_out, not_43_out, not_44_out, not_45_out, not_46_out, not_47_out, not_48_out, not_49_out,
       not_50_out, not_51_out, not_52_out, not_53_out, not_54_out, not_55_out, not_56_out, not_57_out,
       not_58_out, not_59_out, not_60_out, not_61_out, not_62_out, not_63_out, not_64_out, not_65_out,
       not_66_out, not_67_out, not_68_out, not_69_out, not_70_out, not_71_out, not_72_out, not_73_out,
       not_74_out, not_75_out, not_76_out, not_77_out, not_78_out, not_79_out, not_80_out;

  not not_1 (not_1_out, Input5[0]);
  not not_2 (not_2_out, Input5[1]);
  not not_3 (not_3_out, Input5[2]);
  not not_4 (not_4_out, Input5[3]);
  not not_5 (not_5_out, Input5[4]);
  and and_1 (K00000, not_1_out, not_2_out, not_3_out, not_4_out, not_5_out);
  not not_6 (not_6_out, Input5[1]);
  not not_7 (not_7_out, Input5[2]);
  and and_2 (K00001, Input5[0], not_6_out, not_7_out, not_9_out, not_10_out);
  not not_8 (not_8_out, Input5[0]);
  not not_9 (not_9_out, Input5[3]);
  not not_10 (not_10_out, Input5[4]);
  not not_11 (not_11_out, Input5[2]);
  not not_12 (not_12_out, Input5[3]);
  not not_13 (not_13_out, Input5[4]);
  and and_3 (K00010, not_8_out, Input5[1], not_11_out, not_12_out, not_13_out);
  not not_14 (not_14_out, Input5[2]);
  not not_15 (not_15_out, Input5[3]);
  not not_16 (not_16_out, Input5[4]);
  and and_4 (K00011, Input5[0], Input5[1], not_14_out, not_15_out, not_16_out);
  not not_17 (not_17_out, Input5[0]);
  not not_18 (not_18_out, Input5[1]);
  not not_19 (not_19_out, Input5[3]);
  not not_20 (not_20_out, Input5[4]);
  and and_5 (K00100, not_17_out, not_18_out, Input5[2], not_19_out, not_20_out);
  not not_21 (not_21_out, Input5[1]);
  and and_6 (K00101, Input5[0], not_21_out, Input5[2], not_23_out, not_24_out);
  not not_22 (not_22_out, Input5[0]);
  not not_23 (not_23_out, Input5[3]);
  not not_24 (not_24_out, Input5[4]);
  not not_25 (not_25_out, Input5[3]);
  not not_26 (not_26_out, Input5[4]);
  and and_7 (K00110, not_22_out, Input5[1], Input5[2], not_25_out, not_26_out);
  not not_27 (not_27_out, Input5[3]);
  not not_28 (not_28_out, Input5[4]);
  and and_8 (K00111, Input5[0], Input5[1], Input5[2], not_27_out, not_28_out);
  not not_29 (not_29_out, Input5[0]);
  not not_30 (not_30_out, Input5[1]);
  not not_31 (not_31_out, Input5[2]);
  not not_32 (not_32_out, Input5[4]);
  and and_9 (K01000, not_29_out, not_30_out, not_31_out, Input5[3], not_32_out);
  not not_33 (not_33_out, Input5[1]);
  not not_34 (not_34_out, Input5[2]);
  and and_10 (K01001, Input5[0], not_33_out, not_34_out, Input5[3], not_36_out);
  not not_35 (not_35_out, Input5[0]);
  not not_36 (not_36_out, Input5[4]);
  not not_37 (not_37_out, Input5[2]);
  not not_38 (not_38_out, Input5[4]);
  and and_11 (K01010, not_35_out, Input5[1], not_37_out, Input5[3], not_38_out);
  not not_39 (not_39_out, Input5[2]);
  not not_40 (not_40_out, Input5[4]);
  and and_12 (K01011, Input5[0], Input5[1], not_39_out, Input5[3], not_40_out);
  not not_41 (not_41_out, Input5[0]);
  not not_42 (not_42_out, Input5[1]);
  not not_43 (not_43_out, Input5[4]);
  and and_13 (K01100, not_41_out, not_42_out, Input5[2], Input5[3], not_43_out);
  not not_44 (not_44_out, Input5[1]);
  and and_14 (K01101, Input5[0], not_44_out, Input5[2], Input5[3], not_46_out);
  not not_45 (not_45_out, Input5[0]);
  not not_46 (not_46_out, Input5[4]);
  not not_47 (not_47_out, Input5[4]);
  and and_15 (K01110, not_45_out, Input5[1], Input5[2], Input5[3], not_47_out);
  not not_48 (not_48_out, Input5[4]);
  and and_16 (K01111, Input5[0], Input5[1], Input5[2], Input5[3], not_48_out);
  not not_49 (not_49_out, Input5[0]);
  not not_50 (not_50_out, Input5[1]);
  not not_51 (not_51_out, Input5[2]);
  not not_52 (not_52_out, Input5[3]);
  and and_17 (K10000, not_49_out, not_50_out, not_51_out, not_52_out, Input5[4]);
  not not_53 (not_53_out, Input5[1]);
  not not_54 (not_54_out, Input5[2]);
  and and_18 (K10001, Input5[0], not_53_out, not_54_out, not_56_out, Input5[4]);
  not not_55 (not_55_out, Input5[0]);
  not not_56 (not_56_out, Input5[3]);
  not not_57 (not_57_out, Input5[2]);
  not not_58 (not_58_out, Input5[3]);
  and and_19 (K10010, not_55_out, Input5[1], not_57_out, not_58_out, Input5[4]);
  not not_59 (not_59_out, Input5[2]);
  not not_60 (not_60_out, Input5[3]);
  and and_20 (K10011, Input5[0], Input5[1], not_59_out, not_60_out, Input5[4]);
  not not_61 (not_61_out, Input5[0]);
  not not_62 (not_62_out, Input5[1]);
  not not_63 (not_63_out, Input5[3]);
  and and_21 (K10100, not_61_out, not_62_out, Input5[2], not_63_out, Input5[4]);
  not not_64 (not_64_out, Input5[1]);
  not not_65 (not_65_out, Input5[3]);
  and and_22 (K10101, Input5[0], not_64_out, Input5[2], not_65_out, Input5[4]);
  not not_66 (not_66_out, Input5[0]);
  not not_67 (not_67_out, Input5[3]);
  and and_23 (K10110, not_66_out, Input5[1], Input5[2], not_67_out, Input5[4]);
  not not_68 (not_68_out, Input5[3]);
  and and_24 (K10111, Input5[0], Input5[1], Input5[2], not_68_out, Input5[4]);
  not not_69 (not_69_out, Input5[0]);
  not not_70 (not_70_out, Input5[1]);
  not not_71 (not_71_out, Input5[2]);
  and and_25 (K11000, not_69_out, not_70_out, not_71_out, Input5[3], Input5[4]);
  not not_72 (not_72_out, Input5[1]);
  not not_73 (not_73_out, Input5[2]);
  and and_26 (K11001, Input5[0], not_72_out, not_73_out, Input5[3], Input5[4]);
  not not_74 (not_74_out, Input5[0]);
  not not_75 (not_75_out, Input5[2]);
  and and_27 (K11010, not_74_out, Input5[1], not_75_out, Input5[3], Input5[4]);
  not not_76 (not_76_out, Input5[2]);
  and and_28 (K11011, Input5[0], Input5[1], not_76_out, Input5[3], Input5[4]);
  not not_77 (not_77_out, Input5[0]);
  not not_78 (not_78_out, Input5[1]);
  and and_29 (K11100, not_77_out, not_78_out, Input5[2], Input5[3], Input5[4]);
  not not_79 (not_79_out, Input5[1]);
  and and_30 (K11101, Input5[0], not_79_out, Input5[2], Input5[3], Input5[4]);
  not not_80 (not_80_out, Input5[0]);
  and and_31 (K11110, not_80_out, Input5[1], Input5[2], Input5[3], Input5[4]);
  and and_32 (K11111, Input5[0], Input5[1], Input5[2], Input5[3], Input5[4]);
endmodule

module GRS_MUX_3to8 (
  input  [2:0] Input3,
  output K000,
  output K001,
  output K002,
  output K003,
  output K004,
  output K005,
  output K006,
  output K008
);

  wire not_1_out, not_2_out, not_3_out, not_4_out, not_5_out, not_6_out, not_7_out, not_8_out, not_9_out,
       not_10_out, not_11_out, not_12_out;

  not not_1 (not_1_out, Input3[0]);
  not not_2 (not_2_out, Input3[1]);
  and and_1 (K000, not_1_out, not_2_out, not_3_out);
  not not_3 (not_3_out, Input3[2]);
  not not_4 (not_4_out, Input3[1]);
  not not_5 (not_5_out, Input3[2]);
  and and_2 (K001, Input3[0], not_4_out, not_5_out);
  not not_6 (not_6_out, Input3[0]);
  not not_7 (not_7_out, Input3[2]);
  and and_3 (K002, not_6_out, Input3[1], not_7_out);
  not not_8 (not_8_out, Input3[2]);
  and and_4 (K003, Input3[0], Input3[1], not_8_out);
  not not_9 (not_9_out, Input3[0]);
  not not_10 (not_10_out, Input3[1]);
  and and_5 (K004, not_9_out, not_10_out, Input3[2]);
  not not_11 (not_11_out, Input3[1]);
  and and_6 (K005, Input3[0], not_11_out, Input3[2]);
  not not_12 (not_12_out, Input3[0]);
  and and_7 (K006, not_12_out, Input3[1], Input3[2]);
  and and_8 (K008, Input3[0], Input3[1], Input3[2]);
endmodule

module GRS_Storage_Writeallowfor8 (
  input  [2:0] ADDRESS,
  input  Writeallow,
  output out_3,
  output out_4,
  output out_5,
  output out_6,
  output out_7,
  output out_8,
  output out_9,
  output out_10
);

  wire grs_mux_3to8_1_k000, grs_mux_3to8_1_k001, grs_mux_3to8_1_k002, grs_mux_3to8_1_k003,
       grs_mux_3to8_1_k004, grs_mux_3to8_1_k005, grs_mux_3to8_1_k006, grs_mux_3to8_1_k008;

  GRS_MUX_3to8 grs_mux_3to8_1 (
    .Input3(ADDRESS), .K000(grs_mux_3to8_1_k000), .K001(grs_mux_3to8_1_k001), .K002(grs_mux_3to8_1_k002),
    .K003(grs_mux_3to8_1_k003), .K004(grs_mux_3to8_1_k004), .K005(grs_mux_3to8_1_k005),
    .K006(grs_mux_3to8_1_k006), .K008(grs_mux_3to8_1_k008));
  and and_1 (out_3, grs_mux_3to8_1_k000, Writeallow);
  and and_2 (out_4, grs_mux_3to8_1_k001, Writeallow);
  and and_3 (out_5, grs_mux_3to8_1_k002, Writeallow);
  and and_4 (out_6, grs_mux_3to8_1_k003, Writeallow);
  and and_5 (out_7, grs_mux_3to8_1_k004, Writeallow);
  and and_6 (out_8, grs_mux_3to8_1_k005, Writeallow);
  and and_7 (out_9, grs_mux_3to8_1_k006, Writeallow);
  and and_8 (out_10, grs_mux_3to8_1_k008, Writeallow);
endmodule

module GRS_Storage_Readallowfor8 (
  input  [2:0] ADDRESS,
  input  Readallow,
  output out_3,
  output out_4,
  output out_5,
  output out_6,
  output out_7,
  output out_8,
  output out_9,
  output out_10
);

  wire grs_mux_3to8_1_k000, grs_mux_3to8_1_k001, grs_mux_3to8_1_k002, grs_mux_3to8_1_k003,
       grs_mux_3to8_1_k004, grs_mux_3to8_1_k005, grs_mux_3to8_1_k006, grs_mux_3to8_1_k008;

  GRS_MUX_3to8 grs_mux_3to8_1 (
    .Input3(ADDRESS), .K000(grs_mux_3to8_1_k000), .K001(grs_mux_3to8_1_k001), .K002(grs_mux_3to8_1_k002),
    .K003(grs_mux_3to8_1_k003), .K004(grs_mux_3to8_1_k004), .K005(grs_mux_3to8_1_k005),
    .K006(grs_mux_3to8_1_k006), .K008(grs_mux_3to8_1_k008));
  and and_1 (out_3, grs_mux_3to8_1_k000, Readallow);
  and and_2 (out_4, grs_mux_3to8_1_k001, Readallow);
  and and_3 (out_5, grs_mux_3to8_1_k002, Readallow);
  and and_4 (out_6, grs_mux_3to8_1_k003, Readallow);
  and and_5 (out_7, grs_mux_3to8_1_k004, Readallow);
  and and_6 (out_8, grs_mux_3to8_1_k005, Readallow);
  and and_7 (out_9, grs_mux_3to8_1_k006, Readallow);
  and and_8 (out_10, grs_mux_3to8_1_k008, Readallow);
endmodule
