// Logisim project Norb_RISCV_ALU.circ as structural Verilog: 6 circuits, main circuit Norb_8B_CRA
module Norb_8B_CRA (
  input  [7:0] InA,
  input  [7:0] InB,
  input  CarryIn,
  output CarryOverflow,
  output [7:0] OutAPlusB
);

  wire and_1_out, and_2_out, and_3_out, and_4_out, and_5_out, and_6_out, and_7_out, and_8_out, and_9_out,
       and_10_out, and_11_out, and_12_out, and_13_out, and_14_out, and_15_out, and_16_out, or_1_out,
       or_2_out, or_3_out, or_4_out, or_5_out, or_6_out, or_7_out, xor_1_out, xor_3_out, xor_5_out,
       xor_7_out, xor_9_out, xor_11_out, xor_13_out, xor_15_out;

  xor xor_1 (xor_1_out, InA[0], CarryIn);
  and and_1 (and_1_out, InA[0], CarryIn);
  xor xor_2 (OutAPlusB[0], InB[0], xor_1_out);
  and and_2 (and_2_out, InB[0], xor_1_out);
  or or_1 (or_1_out, and_2_out, and_1_out);
  xor xor_3 (xor_3_out, InA[1], or_1_out);
  and and_3 (and_3_out, InA[1], or_1_out);
  xor xor_4 (OutAPlusB[1], InB[1], xor_3_out);
  and and_4 (and_4_out, InB[1], xor_3_out);
  or or_2 (or_2_out, and_4_out, and_3_out);
  xor xor_5 (xor_5_out, InA[2], or_2_out);
  and and_5 (and_5_out, InA[2], or_2_out);
  xor xor_6 (OutAPlusB[2], InB[2], xor_5_out);
  or or_3 (or_3_out, and_6_out, and_5_out);
  and and_6 (and_6_out, InB[2], xor_5_out);
  and and_7 (and_7_out, InA[3], or_3_out);
  xor xor_7 (xor_7_out, InA[3], or_3_out);
  and and_8 (and_8_out, InB[3], xor_7_out);
  xor xor_8 (OutAPlusB[3], InB[3], xor_7_out);
  or or_4 (or_4_out, and_8_out, and_7_out);
  xor xor_9 (xor_9_out, InA[4], or_4_out);
  and and_9 (and_9_out, InA[4], or_4_out);
  xor xor_10 (OutAPlusB[4], InB[4], xor_9_out);
  and and_10 (and_10_out, InB[4], xor_9_out);
  or or_5 (or_5_out, and_10_out, and_9_out);
  xor xor_11 (xor_11_out, InA[5], or_5_out);
  and and_11 (and_11_out, InA[5], or_5_out);
  xor xor_12 (OutAPlusB[5], InB[5], xor_11_out);
  and and_12 (and_12_out, InB[5], xor_11_out);
  or or_6 (or_6_out, and_12_out, and_11_out);
  xor xor_13 (xor_13_out, InA[6], or_6_out);
  and and_13 (and_13_out, InA[6], or_6_out);
  xor xor_14 (OutAPlusB[6], InB[6], xor_13_out);
  and and_14 (and_14_out, InB[6], xor_13_out);
  or or_7 (or_7_out, and_14_out, and_13_out);
  xor xor_15 (xor_15_out, InA[7], or_7_out);
  and and_15 (and_15_out, InA[7], or_7_out);
  xor xor_16 (OutAPlusB[7], InB[7], xor_15_out);
  and and_16 (and_16_out, InB[7], xor_15_out);
  or or_8 (CarryOverflow, and_16_out, and_15_out);
endmodule

module Norb_8B_CRS (
  input  [7:0] InA,
  input  [7:0] InB,
  input  CarryIn,
  output CarryOverflow,
  output [7:0] OutASubtractB
);

  wire and_1_out, and_2_out, and_3_out, and_4_out, and_5_out, and_6_out, and_7_out, and_8_out, and_9_out,
       and_10_out, and_11_out, and_12_out, and_13_out, and_14_out, and_15_out, and_16_out, not_1_out,
       not_2_out, not_3_out, not_4_out, not_5_out, not_6_out, not_7_out, not_8_out, or_1_out, or_2_out,
       or_3_out, or_4_out, or_5_out, or_6_out, or_7_out, xor_1_out, xor_3_out, xor_5_out, xor_7_out,
       xor_9_out, xor_11_out, xor_13_out, xor_15_out;

  xor xor_1 (xor_1_out, InA[0], CarryIn);
  and and_1 (and_1_out, InA[0], CarryIn);
  xor xor_2 (OutASubtractB[0], not_1_out, xor_1_out);
  and and_2 (and_2_out, not_1_out, xor_1_out);
  or or_1 (or_1_out, and_2_out, and_1_out);
  not not_1 (not_1_out, InB[0]);
  not not_2 (not_2_out, InB[1]);
  not not_3 (not_3_out, InB[2]);
  not not_4 (not_4_out, InB[3]);
  xor xor_3 (xor_3_out, InA[1], or_1_out);
  and and_3 (and_3_out, InA[1], or_1_out);
  not not_5 (not_5_out, InB[4]);
  not not_6 (not_6_out, InB[5]);
  not not_7 (not_7_out, InB[6]);
  not not_8 (not_8_out, InB[7]);
  xor xor_4 (OutASubtractB[1], not_2_out, xor_3_out);
  and and_4 (and_4_out, not_2_out, xor_3_out);
  or or_2 (or_2_out, and_4_out, and_3_out);
  xor xor_5 (xor_5_out, InA[2], or_2_out);
  and and_5 (and_5_out, InA[2], or_2_out);
  xor xor_6 (OutASubtractB[2], not_3_out, xor_5_out);
  or or_3 (or_3_out, and_6_out, and_5_out);
  and and_6 (and_6_out, not_3_out, xor_5_out);
  and and_7 (and_7_out, InA[3], or_3_out);
  xor xor_7 (xor_7_out, InA[3], or_3_out);
  and and_8 (and_8_out, not_4_out, xor_7_out);
  xor xor_8 (OutASubtractB[3], not_4_out, xor_7_out);
  or or_4 (or_4_out, and_8_out, and_7_out);
  xor xor_9 (xor_9_out, InA[4], or_4_out);
  and and_9 (and_9_out, InA[4], or_4_out);
  xor xor_10 (OutASubtractB[4], not_5_out, xor_9_out);
  and and_10 (and_10_out, not_5_out, xor_9_out);
  or or_5 (or_5_out, and_10_out, and_9_out);
  xor xor_11 (xor_11_out, InA[5], or_5_out);
  and and_11 (and_11_out, InA[5], or_5_out);
  xor xor_12 (OutASubtractB[5], not_6_out, xor_11_out);
  and and_12 (and_12_out, not_6_out, xor_11_out);
  or or_6 (or_6_out, and_12_out, and_11_out);
  xor xor_13 (xor_13_out, InA[6], or_6_out);
  and and_13 (and_13_out, InA[6], or_6_out);
  xor xor_14 (OutASubtractB[6], not_7_out, xor_13_out);
  and and_14 (and_14_out, not_7_out, xor_13_out);
  or or_7 (or_7_out, and_14_out, and_13_out);
  xor xor_15 (xor_15_out, InA[7], or_7_out);
  and and_15 (and_15_out, InA[7], or_7_out);
  xor xor_16 (OutASubtractB[7], not_8_out, xor_15_out);
  and and_16 (and_16_out, not_8_out, xor_15_out);
  or or_8 (CarryOverflow, and_16_out, and_15_out);

  // Notes on the sheet:
  //   CarryIn: initial=0x1
endmodule

module Norb_RISCV_ALU (
  input  [7:0] InA,
  input  [7:0] InB
);

  Norb_8B_CRA norb_8b_cra_1 (.InA(InA), .InB(InB));  // open: CarryIn, CarryOverflow, OutAPlusB
  Norb_8B_CRS norb_8b_crs_1 (.InA(InA), .InB(InB));  // open: CarryIn, CarryOverflow, OutASubtractB
  // AND_Gate and_1 has open pins: in0=InA, in1=InB, out=open
  // OR_Gate or_1 has open pins: in0=InA, in1=InB, out=open
  // XOR_Gate xor_1 has open pins: in0=InA, in1=InB, out=open
endmodule

module Norb_32B_CRA (
  input  [31:0] InA,
  input  [31:0] InB,
  output FlagOverflow,
  output [31:0] OutAAddB
);

  wire norb_8b_cra_1_carryoverflow, norb_8b_cra_2_carryoverflow, norb_8b_cra_3_carryoverflow;
  wire [7:0] norb_8b_cra_1_outaplusb, norb_8b_cra_2_outaplusb, norb_8b_cra_3_outaplusb,
       norb_8b_cra_4_outaplusb, norb_32b8b_splitter_1_out0, norb_32b8b_splitter_1_out1,
       norb_32b8b_splitter_1_out2, norb_32b8b_splitter_1_out3, norb_32b8b_splitter_2_out0,
       norb_32b8b_splitter_2_out1, norb_32b8b_splitter_2_out2, norb_32b8b_splitter_2_out3;

  Norb_32B8B_Splitter norb_32b8b_splitter_1 (
    .In32B(InA), .Out0(norb_32b8b_splitter_1_out0), .Out1(norb_32b8b_splitter_1_out1),
    .Out2(norb_32b8b_splitter_1_out2), .Out3(norb_32b8b_splitter_1_out3));
  Norb_32B8B_Splitter norb_32b8b_splitter_2 (
    .In32B(InB), .Out0(norb_32b8b_splitter_2_out0), .Out1(norb_32b8b_splitter_2_out1),
    .Out2(norb_32b8b_splitter_2_out2), .Out3(norb_32b8b_splitter_2_out3));
  Norb_8B_CRA norb_8b_cra_1 (
    .InA(norb_32b8b_splitter_1_out0), .InB(norb_32b8b_splitter_2_out0), .CarryIn(1'b0),
    .CarryOverflow(norb_8b_cra_1_carryoverflow), .OutAPlusB(norb_8b_cra_1_outaplusb));
  Norb_8B_CRA norb_8b_cra_2 (
    .InA(norb_32b8b_splitter_1_out1), .InB(norb_32b8b_splitter_2_out1),
    .CarryIn(norb_8b_cra_1_carryoverflow), .CarryOverflow(norb_8b_cra_2_carryoverflow),
    .OutAPlusB(norb_8b_cra_2_outaplusb));
  Norb_8B_CRA norb_8b_cra_3 (
    .InA(norb_32b8b_splitter_1_out2), .InB(norb_32b8b_splitter_2_out2),
    .CarryIn(norb_8b_cra_2_carryoverflow), .CarryOverflow(norb_8b_cra_3_carryoverflow),
    .OutAPlusB(norb_8b_cra_3_outaplusb));
  Norb_8B_CRA norb_8b_cra_4 (
    .InA(norb_32b8b_splitter_1_out3), .InB(norb_32b8b_splitter_2_out3),
    .CarryIn(norb_8b_cra_3_carryoverflow), .CarryOverflow(FlagOverflow), .OutAPlusB(norb_8b_cra_4_outaplusb));
  Norb_8B32B_Splitter norb_8b32b_splitter_1 (
    .In0(norb_8b_cra_1_outaplusb), .In1(norb_8b_cra_2_outaplusb), .In2(norb_8b_cra_3_outaplusb),
    .In3(norb_8b_cra_4_outaplusb), .Out32B(OutAAddB));
endmodule

module Norb_32B_CRS (
  input  [31:0] InA,
  input  [31:0] InB,
  output FlagOverflow,
  output [31:0] OutASubtractB
);

  wire norb_8b_crs_1_carryoverflow, norb_8b_crs_2_carryoverflow, norb_8b_crs_3_carryoverflow;
  wire [7:0] norb_8b_crs_1_outasubtractb, norb_8b_crs_2_outasubtractb, norb_8b_crs_3_outasubtractb,
       norb_8b_crs_4_outasubtractb, norb_32b8b_splitter_1_out0, norb_32b8b_splitter_1_out1,
       norb_32b8b_splitter_1_out2, norb_32b8b_splitter_1_out3, norb_32b8b_splitter_2_out0,
       norb_32b8b_splitter_2_out1, norb_32b8b_splitter_2_out2, norb_32b8b_splitter_2_out3;

  Norb_32B8B_Splitter norb_32b8b_splitter_1 (
    .In32B(InA), .Out0(norb_32b8b_splitter_1_out0), .Out1(norb_32b8b_splitter_1_out1),
    .Out2(norb_32b8b_splitter_1_out2), .Out3(norb_32b8b_splitter_1_out3));
  Norb_32B8B_Splitter norb_32b8b_splitter_2 (
    .In32B(InB), .Out0(norb_32b8b_splitter_2_out0), .Out1(norb_32b8b_splitter_2_out1),
    .Out2(norb_32b8b_splitter_2_out2), .Out3(norb_32b8b_splitter_2_out3));
  Norb_8B_CRS norb_8b_crs_1 (
    .InA(norb_32b8b_splitter_1_out0), .InB(norb_32b8b_splitter_2_out0), .CarryIn(1'b1),
    .CarryOverflow(norb_8b_crs_1_carryoverflow), .OutASubtractB(norb_8b_crs_1_outasubtractb));
  Norb_8B_CRS norb_8b_crs_2 (
    .InA(norb_32b8b_splitter_1_out1), .InB(norb_32b8b_splitter_2_out1),
    .CarryIn(norb_8b_crs_1_carryoverflow), .CarryOverflow(norb_8b_crs_2_carryoverflow),
    .OutASubtractB(norb_8b_crs_2_outasubtractb));
  Norb_8B_CRS norb_8b_crs_3 (
    .InA(norb_32b8b_splitter_1_out2), .InB(norb_32b8b_splitter_2_out2),
    .CarryIn(norb_8b_crs_2_carryoverflow), .CarryOverflow(norb_8b_crs_3_carryoverflow),
    .OutASubtractB(norb_8b_crs_3_outasubtractb));
  Norb_8B_CRS norb_8b_crs_4 (
    .InA(norb_32b8b_splitter_1_out3), .InB(norb_32b8b_splitter_2_out3),
    .CarryIn(norb_8b_crs_3_carryoverflow), .CarryOverflow(FlagOverflow),
    .OutASubtractB(norb_8b_crs_4_outasubtractb));
  Norb_8B32B_Splitter norb_8b32b_splitter_1 (
    .In0(norb_8b_crs_1_outasubtractb), .In1(norb_8b_crs_2_outasubtractb), .In2(norb_8b_crs_3_outasubtractb),
    .In3(norb_8b_crs_4_outasubtractb), .Out32B(OutASubtractB));
endmodule

module Norb_32B_SLT (
  input  [31:0] InNum
);
endmodule
