// Logisim project Norb_StdLib.circ as structural Verilog: 25 circuits, main circuit Norb_STD_8B_Selector
module Norb_STD_8B_Selector (
  input  [7:0] In8B,
  input  InSelect,
  output [7:0] OutResult
);

  and and_1 (OutResult[7], InSelect, In8B[7]);
  and and_2 (OutResult[6], InSelect, In8B[6]);
  and and_3 (OutResult[5], InSelect, In8B[5]);
  and and_4 (OutResult[4], InSelect, In8B[4]);
  and and_5 (OutResult[3], InSelect, In8B[3]);
  and and_6 (OutResult[2], InSelect, In8B[2]);
  and and_7 (OutResult[1], InSelect, In8B[1]);
  and and_8 (OutResult[0], InSelect, In8B[0]);
endmodule

module Norb_STD_32B_Selector (
  input  [31:0] In32B,
  input  InSelect,
  output [31:0] Out32B
);

  wire [7:0] norb_std_8b_selector_1_outresult, norb_std_8b_selector_2_outresult,
       norb_std_8b_selector_3_outresult, norb_std_8b_selector_4_outresult, norb_std_32b8b_splitter_1_out0,
       norb_std_32b8b_splitter_1_out1, norb_std_32b8b_splitter_1_out2, norb_std_32b8b_splitter_1_out3;

  Norb_STD_32B8B_Splitter norb_std_32b8b_splitter_1 (
    .In32B(In32B), .Out0(norb_std_32b8b_splitter_1_out0), .Out1(norb_std_32b8b_splitter_1_out1),
    .Out2(norb_std_32b8b_splitter_1_out2), .Out3(norb_std_32b8b_splitter_1_out3));
  Norb_STD_8B_Selector norb_std_8b_selector_1 (
    .In8B(norb_std_32b8b_splitter_1_out0), .InSelect(InSelect), .OutResult(norb_std_8b_selector_1_outresult));
  Norb_STD_8B_Selector norb_std_8b_selector_2 (
    .In8B(norb_std_32b8b_splitter_1_out1), .InSelect(InSelect), .OutResult(norb_std_8b_selector_2_outresult));
  Norb_STD_8B_Selector norb_std_8b_selector_3 (
    .In8B(norb_std_32b8b_splitter_1_out2), .InSelect(InSelect), .OutResult(norb_std_8b_selector_3_outresult));
  Norb_STD_8B_Selector norb_std_8b_selector_4 (
    .In8B(norb_std_32b8b_splitter_1_out3), .InSelect(InSelect), .OutResult(norb_std_8b_selector_4_outresult));
  Norb_STD_8B32B_Splitter norb_std_8b32b_splitter_1 (
    .In0(norb_std_8b_selector_1_outresult), .In1(norb_std_8b_selector_2_outresult),
    .In2(norb_std_8b_selector_3_outresult), .In3(norb_std_8b_selector_4_outresult), .Out32B(Out32B));
endmodule

module Norb_STD_1T2_Decoder (
  input  In1B,
  output Out1,
  output Out0
);

  not not_1 (Out0, In1B);

  assign Out1 = In1B;
endmodule

module Norb_STD_2T4_Decoder (
  input  [1:0] In2B,
  output Out3,
  output Out2,
  output Out1,
  output Out0
);

  wire norb_std_1t2_decoder_1_out0, norb_std_1t2_decoder_1_out1, norb_std_1t2_decoder_2_out0,
       norb_std_1t2_decoder_2_out1, not_1_out;

  Norb_STD_1T2_Decoder norb_std_1t2_decoder_1 (
    .In1B(In2B[0]), .Out1(norb_std_1t2_decoder_1_out1), .Out0(norb_std_1t2_decoder_1_out0));
  Norb_STD_1T2_Decoder norb_std_1t2_decoder_2 (
    .In1B(In2B[0]), .Out1(norb_std_1t2_decoder_2_out1), .Out0(norb_std_1t2_decoder_2_out0));
  and and_1 (Out3, In2B[1], norb_std_1t2_decoder_1_out1);
  and and_2 (Out2, norb_std_1t2_decoder_1_out0, In2B[1]);
  not not_1 (not_1_out, In2B[1]);
  and and_3 (Out1, not_1_out, norb_std_1t2_decoder_2_out1);
  and and_4 (Out0, norb_std_1t2_decoder_2_out0, not_1_out);
endmodule

module Norb_STD_3T8_Decoder (
  input  [2:0] In3B,
  output Out4,
  output Out5,
  output Out6,
  output Out7,
  output Out0,
  output Out1,
  output Out2,
  output Out3
);

  wire norb_std_2t4_decoder_1_out0, norb_std_2t4_decoder_1_out1, norb_std_2t4_decoder_1_out2,
       norb_std_2t4_decoder_1_out3, norb_std_2t4_decoder_2_out0, norb_std_2t4_decoder_2_out1,
       norb_std_2t4_decoder_2_out2, norb_std_2t4_decoder_2_out3, not_1_out;

  Norb_STD_2T4_Decoder norb_std_2t4_decoder_1 (
    .In2B(In3B[1:0]), .Out3(norb_std_2t4_decoder_1_out3), .Out2(norb_std_2t4_decoder_1_out2),
    .Out1(norb_std_2t4_decoder_1_out1), .Out0(norb_std_2t4_decoder_1_out0));
  Norb_STD_2T4_Decoder norb_std_2t4_decoder_2 (
    .In2B(In3B[1:0]), .Out3(norb_std_2t4_decoder_2_out3), .Out2(norb_std_2t4_decoder_2_out2),
    .Out1(norb_std_2t4_decoder_2_out1), .Out0(norb_std_2t4_decoder_2_out0));
  and and_1 (Out4, In3B[2], norb_std_2t4_decoder_1_out0);
  and and_2 (Out5, In3B[2], norb_std_2t4_decoder_1_out1);
  not not_1 (not_1_out, In3B[2]);
  and and_3 (Out0, not_1_out, norb_std_2t4_decoder_2_out0);
  and and_4 (Out1, not_1_out, norb_std_2t4_decoder_2_out1);
  and and_5 (Out6, In3B[2], norb_std_2t4_decoder_1_out2);
  and and_6 (Out7, In3B[2], norb_std_2t4_decoder_1_out3);
  and and_7 (Out2, not_1_out, norb_std_2t4_decoder_2_out2);
  and and_8 (Out3, not_1_out, norb_std_2t4_decoder_2_out3);
endmodule

module Norb_STD_8B_Matcher (
  input  [7:0] In8B_A,
  input  [7:0] In8B_B,
  output OutAEqB
);

  wire xor_1_out, xor_2_out, xor_3_out, xor_4_out, xor_5_out, xor_6_out, xor_7_out, xor_8_out;

  xor xor_1 (xor_1_out, In8B_A[7], In8B_B[7]);
  xor xor_2 (xor_2_out, In8B_A[6], In8B_B[6]);
  xor xor_3 (xor_3_out, In8B_A[5], In8B_B[5]);
  xor xor_4 (xor_4_out, In8B_A[4], In8B_B[4]);
  xor xor_5 (xor_5_out, In8B_A[3], In8B_B[3]);
  xor xor_6 (xor_6_out, In8B_A[2], In8B_B[2]);
  xor xor_7 (xor_7_out, In8B_A[1], In8B_B[1]);
  xor xor_8 (xor_8_out, In8B_A[0], In8B_B[0]);
  nor nor_1 (OutAEqB, xor_8_out, xor_7_out, xor_6_out, xor_5_out, xor_4_out, xor_3_out, xor_2_out, xor_1_out);
endmodule

module Norb_STD_5B_Matcher (
  input  [4:0] In8B_A,
  input  [4:0] In8B_B,
  output OutAEqB
);

  wire xor_1_out, xor_2_out, xor_3_out, xor_4_out, xor_5_out;

  xor xor_1 (xor_1_out, In8B_A[4], In8B_B[4]);
  xor xor_2 (xor_2_out, In8B_A[3], In8B_B[3]);
  xor xor_3 (xor_3_out, In8B_A[2], In8B_B[2]);
  xor xor_4 (xor_4_out, In8B_A[1], In8B_B[1]);
  xor xor_5 (xor_5_out, In8B_A[0], In8B_B[0]);
  nor nor_1 (OutAEqB, xor_5_out, xor_4_out, xor_3_out, xor_2_out, xor_1_out);
endmodule

module Norb_STD_3B_Matcher (
  input  [2:0] In8B_A,
  input  [2:0] In8B_B,
  output OutAEqB
);

  wire xor_1_out, xor_2_out, xor_3_out;

  xor xor_1 (xor_1_out, In8B_A[2], In8B_B[2]);
  xor xor_2 (xor_2_out, In8B_A[1], In8B_B[1]);
  xor xor_3 (xor_3_out, In8B_A[0], In8B_B[0]);
  nor nor_1 (OutAEqB, xor_3_out, xor_2_out, xor_1_out);
endmodule

module Norb_STD_7B_Matcher (
  input  [6:0] In8B_A,
  input  [6:0] In8B_B,
  output OutAEqB
);

  wire xor_1_out, xor_2_out, xor_3_out, xor_4_out, xor_5_out, xor_6_out, xor_7_out;

  xor xor_1 (xor_1_out, In8B_A[6], In8B_B[6]);
  xor xor_2 (xor_2_out, In8B_A[5], In8B_B[5]);
  xor xor_3 (xor_3_out, In8B_A[4], In8B_B[4]);
  xor xor_4 (xor_4_out, In8B_A[3], In8B_B[3]);
  xor xor_5 (xor_5_out, In8B_A[2], In8B_B[2]);
  xor xor_6 (xor_6_out, In8B_A[1], In8B_B[1]);
  xor xor_7 (xor_7_out, In8B_A[0], In8B_B[0]);
  nor nor_1 (OutAEqB, xor_7_out, xor_6_out, xor_5_out, xor_1_out, xor_4_out, xor_3_out, xor_2_out);
endmodule

module Norb_STD_OP_Splitter (
  input  [31:0] IN32B_INS,
  output [6:0] opcode
);


  assign opcode = IN32B_INS[6:0];
endmodule

module Norb_STD_32B_Matcher (
  input  [31:0] In8B_A,
  input  [31:0] In8B_B,
  output OutAEqB
);

  wire xor_1_out, xor_2_out, xor_3_out, xor_4_out, xor_5_out, xor_6_out, xor_7_out, xor_8_out, xor_9_out,
       xor_10_out, xor_11_out, xor_12_out, xor_13_out, xor_14_out, xor_15_out, xor_16_out, xor_17_out,
       xor_18_out, xor_19_out, xor_20_out, xor_21_out, xor_22_out, xor_23_out, xor_24_out, xor_25_out,
       xor_26_out, xor_27_out, xor_28_out, xor_29_out, xor_30_out, xor_31_out, xor_32_out;

  xor xor_1 (xor_1_out, In8B_A[31], In8B_B[31]);
  xor xor_2 (xor_2_out, In8B_A[30], In8B_B[30]);
  xor xor_3 (xor_3_out, In8B_A[29], In8B_B[29]);
  xor xor_4 (xor_4_out, In8B_A[28], In8B_B[28]);
  xor xor_5 (xor_5_out, In8B_A[27], In8B_B[27]);
  xor xor_6 (xor_6_out, In8B_A[26], In8B_B[26]);
  xor xor_7 (xor_7_out, In8B_A[25], In8B_B[25]);
  xor xor_8 (xor_8_out, In8B_A[24], In8B_B[24]);
  xor xor_9 (xor_9_out, In8B_A[23], In8B_B[23]);
  xor xor_10 (xor_10_out, In8B_A[22], In8B_B[22]);
  xor xor_11 (xor_11_out, In8B_A[21], In8B_B[21]);
  xor xor_12 (xor_12_out, In8B_A[20], In8B_B[20]);
  xor xor_13 (xor_13_out, In8B_A[19], In8B_B[19]);
  xor xor_14 (xor_14_out, In8B_A[18], In8B_B[18]);
  xor xor_15 (xor_15_out, In8B_A[17], In8B_B[17]);
  xor xor_16 (xor_16_out, In8B_A[16], In8B_B[16]);
  xor xor_17 (xor_17_out, In8B_A[14], In8B_B[14]);
  xor xor_18 (xor_18_out, In8B_A[15], In8B_B[15]);
  xor xor_19 (xor_19_out, In8B_A[13], In8B_B[13]);
  xor xor_20 (xor_20_out, In8B_A[12], In8B_B[12]);
  xor xor_21 (xor_21_out, In8B_A[11], In8B_B[11]);
  xor xor_22 (xor_22_out, In8B_A[10], In8B_B[10]);
  xor xor_23 (xor_23_out, In8B_A[9], In8B_B[9]);
  xor xor_24 (xor_24_out, In8B_A[8], In8B_B[8]);
  xor xor_25 (xor_25_out, In8B_A[7], In8B_B[7]);
  xor xor_26 (xor_26_out, In8B_A[6], In8B_B[6]);
  xor xor_27 (xor_27_out, In8B_A[5], In8B_B[5]);
  xor xor_28 (xor_28_out, In8B_A[4], In8B_B[4]);
  xor xor_29 (xor_29_out, In8B_A[3], In8B_B[3]);
  xor xor_30 (xor_30_out, In8B_A[2], In8B_B[2]);
  xor xor_31 (xor_31_out, In8B_A[1], In8B_B[1]);
  xor xor_32 (xor_32_out, In8B_A[0], In8B_B[0]);
  nor nor_1 (OutAEqB, xor_32_out, xor_31_out, xor_30_out, xor_29_out, xor_28_out, xor_27_out, xor_26_out, xor_25_out, xor_24_out, xor_23_out, xor_22_out, xor_21_out, xor_20_out, xor_19_out, xor_17_out, xor_18_out, xor_16_out, xor_15_out, xor_14_out, xor_13_out, xor_12_out, xor_11_out, xor_10_out, xor_9_out, xor_8_out, xor_7_out, xor_6_out, xor_5_out, xor_4_out, xor_3_out, xor_2_out, xor_1_out);
endmodule

module Norb_STD_RType_Splitter (
  input  [31:0] IN32B_INS,
  output [6:0] func7,
  output [6:0] opcode,
  output [4:0] rs2,
  output [4:0] rs1,
  output [4:0] rd,
  output [2:0] func3
);


  assign func3 = IN32B_INS[14:12];
  assign func7 = IN32B_INS[31:25];
  assign opcode = IN32B_INS[6:0];
  assign rd = IN32B_INS[11:7];
  assign rs1 = IN32B_INS[19:15];
  assign rs2 = IN32B_INS[24:20];
endmodule

module Norb_STD_IType_Splitter (
  input  [31:0] IN32B_INS,
  output [6:0] opcode,
  output [4:0] rs1,
  output [4:0] rd,
  output [2:0] func3,
  output [11:0] imm
);


  assign func3 = IN32B_INS[14:12];
  assign imm = IN32B_INS[31:20];
  assign opcode = IN32B_INS[6:0];
  assign rd = IN32B_INS[11:7];
  assign rs1 = IN32B_INS[19:15];
endmodule

module Norb_STD_SType_Splitter (
  input  [31:0] IN32B_INS,
  output [6:0] imm2,
  output [6:0] opcode,
  output [4:0] rs2,
  output [4:0] rs1,
  output [4:0] imm,
  output [2:0] func3
);


  assign func3 = IN32B_INS[14:12];
  assign imm = IN32B_INS[11:7];
  assign imm2 = IN32B_INS[31:25];
  assign opcode = IN32B_INS[6:0];
  assign rs1 = IN32B_INS[19:15];
  assign rs2 = IN32B_INS[24:20];
endmodule

module Norb_STD_BType_Splitter (
  input  [31:0] IN32B_INS,
  output [6:0] imm2,
  output [6:0] opcode,
  output [4:0] rs2,
  output [4:0] rs1,
  output [4:0] imm,
  output [2:0] func3
);


  assign func3 = IN32B_INS[14:12];
  assign imm = IN32B_INS[11:7];
  assign imm2 = IN32B_INS[31:25];
  assign opcode = IN32B_INS[6:0];
  assign rs1 = IN32B_INS[19:15];
  assign rs2 = IN32B_INS[24:20];
endmodule

module Norb_STD_UType_Splitter (
  input  [31:0] IN32B_INS,
  output [6:0] opcode,
  output [4:0] rd,
  output [19:0] imm
);


  assign imm = IN32B_INS[31:12];
  assign opcode = IN32B_INS[6:0];
  assign rd = IN32B_INS[11:7];
endmodule

module Norb_STD_JType_Splitter (
  input  [31:0] IN32B_INS,
  output [6:0] opcode,
  output [4:0] rd,
  output [19:0] imm
);


  assign imm = IN32B_INS[31:12];
  assign opcode = IN32B_INS[6:0];
  assign rd = IN32B_INS[11:7];
endmodule

module Norb_STD_8B32B_Splitter (
  input  [7:0] In0,
  input  [7:0] In1,
  input  [7:0] In2,
  input  [7:0] In3,
  output [31:0] Out32B
);


  assign Out32B = {In3, In2, In1, In0};
endmodule

module Norb_STD_32B8B_Splitter (
  input  [31:0] In32B,
  output [7:0] Out0,
  output [7:0] Out1,
  output [7:0] Out2,
  output [7:0] Out3
);


  assign Out0 = In32B[7:0];
  assign Out1 = In32B[15:8];
  assign Out2 = In32B[23:16];
  assign Out3 = In32B[31:24];
endmodule

module Norb_STD_1B2T_Delayer (
  input  SIGIN,
  input  CLOCK,
  output SIGOUT
);

  wire d_ff_1_q, not_1_out;

  D_Flip_Flop d_ff_1 (.D(SIGIN), .clk(CLOCK), .Q(d_ff_1_q));  // open: Qn, preset, reset
  D_Flip_Flop d_ff_2 (.D(d_ff_1_q), .clk(not_1_out), .Q(SIGOUT));  // open: Qn, preset, reset
  not not_1 (not_1_out, CLOCK);
endmodule

module Norb_STD_2B2T_Delayer (
  input  [1:0] SIGIN,
  input  CLOCK,
  output [1:0] SIGOUT
);

  Norb_STD_1B2T_Delayer norb_std_1b2t_delayer_1 (.SIGIN(SIGIN[0]), .CLOCK(CLOCK), .SIGOUT(SIGOUT[0]));
  Norb_STD_1B2T_Delayer norb_std_1b2t_delayer_2 (.SIGIN(SIGIN[1]), .CLOCK(CLOCK), .SIGOUT(SIGOUT[1]));
endmodule

module Norb_STD_8B2T_Delayer (
  input  [7:0] SIGIN,
  input  CLOCK,
  output [7:0] SIGOUT
);

  Norb_STD_2B2T_Delayer norb_std_2b2t_delayer_1 (.SIGIN(SIGIN[1:0]), .CLOCK(CLOCK), .SIGOUT(SIGOUT[1:0]));
  Norb_STD_2B2T_Delayer norb_std_2b2t_delayer_2 (.SIGIN(SIGIN[3:2]), .CLOCK(CLOCK), .SIGOUT(SIGOUT[3:2]));
  Norb_STD_2B2T_Delayer norb_std_2b2t_delayer_3 (.SIGIN(SIGIN[5:4]), .CLOCK(CLOCK), .SIGOUT(SIGOUT[5:4]));
  Norb_STD_2B2T_Delayer norb_std_2b2t_delayer_4 (.SIGIN(SIGIN[7:6]), .CLOCK(CLOCK), .SIGOUT(SIGOUT[7:6]));
endmodule

module Norb_STD_32B2T_Delayer (
  input  [31:0] SIGIN,
  input  CLOCK,
  output [31:0] SIGOUT
);

  Norb_STD_8B2T_Delayer norb_std_8b2t_delayer_1 (.SIGIN(SIGIN[7:0]), .CLOCK(CLOCK), .SIGOUT(SIGOUT[7:0]));
  Norb_STD_8B2T_Delayer norb_std_8b2t_delayer_2 (.SIGIN(SIGIN[15:8]), .CLOCK(CLOCK), .SIGOUT(SIGOUT[15:8]));
  Norb_STD_8B2T_Delayer norb_std_8b2t_delayer_3 (.SIGIN(SIGIN[23:16]), .CLOCK(CLOCK), .SIGOUT(SIGOUT[23:16]));
  Norb_STD_8B2T_Delayer norb_std_8b2t_delayer_4 (.SIGIN(SIGIN[31:24]), .CLOCK(CLOCK), .SIGOUT(SIGOUT[31:24]));
endmodule

module Norb_STD_1B8B_Padder (
  input  In1B,
  output [7:0] Out8B
);


  assign Out8B = {{7{1'b0}}, In1B};
endmodule

module Norb_STD_1B32B_Padder (
  input  In1B,
  output [31:0] Out32B
);


  assign Out32B = {{31{1'b0}}, In1B};
endmodule
